// Logisim project cpu24_team.circ as structural Verilog: 24 circuits, main circuit ◇单周期MIPS
module \单周期MIPS_团队任务  (
  input  IR1,
  input  IR2,
  input  IR3,
  output RegWrite,
  output MemWrite,
  output [31:0] PC,
  output [31:0] IR,
  output [31:0] RDin,
  output [31:0] MDin,
  output [31:0] LedData
);

  wire _1_out, _2_out, _3_out, and_2_out, and_3_out, and_4_out, and_5_out, and_6_out, and_8_out, beq, BGEZ,
       bne, CLK, clock_2_out, comparator_1_eq, comparator_2_eq, comparator_3_eq, comparator_4_eq,
       comparator_5_eq, comparator_5_lt, comparator_6_eq, counter_3_carry, d_ff_2_q, ERET, Go, Halt, IE,
       INT1, INT2, INT3, IR1_t, IR2_t, IR3_t, IRA, IRB, IRC, JAL, JMP, LH, LUI, mips_alu_1_equal, nand_1_out,
       not_1_out, or_1_out, or_2_out, or_3_out, or_7_out, or_8_out, or_9_out, or_10_out, or_11_out,
       or_12_out, or_14_out, priority_encoder_1_gs, RESET, RST1, RST2, RST3, show, SignedExt, Syscall,
       undriven, W1, W2, W3, \中断请求 , \单周期硬布线控制器_1_alu_src , \单周期硬布线控制器_1_jr , \单周期硬布线控制器_1_memtoreg ,
       \单周期硬布线控制器_1_regdst , \右 , \左 ;
  wire [1:0] priority_encoder_1_out, register_1_q;
  wire [3:0] adder_1_out_2, \单周期硬布线控制器_1_alu_op ;
  wire [4:0] mips_probe_1_p3, multiplexer_8_out, multiplexer_9_out, multiplexer_10_out, shamt;
  wire [6:0] x, y;
  wire [12:0] CNT_num;
  wire [15:0] lcd_video_1_p6, \总周期数 ;
  wire [16:0] adder_3_out, adder_4_out, mips_alu_1_result_2, multiplier_1_out, multiplier_2_out;
  wire [27:0] adder_1_out;
  wire [31:0] adder_2_out, bit_extender_1_out, bit_extender_2_out, EPCAddress, INTAddress, mips_alu_1_result,
       multiplexer_1_out, multiplexer_2_out, multiplexer_4_out, multiplexer_5_out, multiplexer_12_out,
       multiplexer_14_out, multiplexer_15_out, multiplexer_16_out, multiplexer_17_out, NextPC, PC_JR,
       ram_1_data, shifter_1_out, shifter_2_out, shifter_3_out, shifter_4_out;
  wire [31:16] rom_2_data;

  Clock #(.highDuration(1), .lowDuration(1)) clock_1 ();  // open: out
  Button _1 (.out(_1_out));
  Button _2 (.out(_2_out));
  Button _3 (.out(_3_out));
  Button \u_继续运行  (.out(Go));
  LED #(.active("true")) led_1 (.in(W1));
  LED #(.active("true")) led_2 (.in(W2));
  LED #(.active("true")) led_3 (.in(W3));
  Multiplexer #(.select(1), .width(32), .disabled("Z"), .enable("false")) multiplexer_1 (
    .in0({adder_1_out_2, adder_1_out}), .in1(adder_2_out), .out(multiplexer_1_out), .sel(or_8_out));
  Hex_Digit_Display hex_digit_display_1 (.value(LedData[31:28]));  // open: dp
  Comparator #(.width(16), .mode("twosComplement")) comparator_1 (
    .a(16'h23b), .b(\总周期数 ), .eq(comparator_1_eq));  // open: gt, lt
  Comparator #(.width(16), .mode("twosComplement")) comparator_2 (
    .a(\总周期数 ), .b(16'h1), .eq(comparator_2_eq));  // open: gt, lt
  Comparator #(.width(16), .mode("twosComplement")) comparator_3 (
    .a(\总周期数 ), .b(16'h4), .eq(comparator_3_eq));  // open: gt, lt
  Comparator #(.width(16), .mode("twosComplement")) comparator_4 (
    .a(\总周期数 ), .b(16'h7), .eq(comparator_4_eq));  // open: gt, lt
  or or_1 (or_1_out, JAL, JMP);
  Multiplexer #(.select(1), .width(32), .disabled("Z"), .enable("false")) multiplexer_2 (
    .in0(multiplexer_1_out), .in1({adder_1_out_2, IR[25:0], 2'b00}), .out(multiplexer_2_out), .sel(or_1_out));
  Hex_Digit_Display hex_digit_display_2 (.value(LedData[23:20]));  // open: dp
  Hex_Digit_Display hex_digit_display_3 (.value(LedData[27:24]));  // open: dp
  or or_2 (or_2_out, comparator_1_eq, comparator_2_eq);
  assign IRA = or_2_out ? ~CLK : 1'bz;  // Controlled_Inverter controlled_inverter_1
  assign IRB = comparator_3_eq ? ~CLK : 1'bz;  // Controlled_Inverter controlled_inverter_2
  assign IRC = comparator_4_eq ? ~CLK : 1'bz;  // Controlled_Inverter controlled_inverter_3
  Multiplexer #(.select(1), .width(32), .disabled("Z"), .enable("false")) multiplexer_3 (
    .in0(multiplexer_2_out), .in1(PC_JR), .out(NextPC), .sel(\单周期硬布线控制器_1_jr ));
  Hex_Digit_Display hex_digit_display_4 (.value(LedData[15:12]));  // open: dp
  Hex_Digit_Display hex_digit_display_5 (.value(LedData[19:16]));  // open: dp
  Pull_Resistor #(.pull(0)) pull_resistor_1 (.node(IRA));
  Pull_Resistor #(.pull(0)) pull_resistor_2 (.node(IRB));
  Pull_Resistor #(.pull(0)) pull_resistor_3 (.node(IRC));
  Multiplexer #(.select(1), .width(32), .disabled("Z"), .enable("false")) multiplexer_4 (
    .in0(NextPC), .in1(INTAddress), .out(multiplexer_4_out), .sel(\中断请求 ));
  Hex_Digit_Display hex_digit_display_6 (.value(LedData[7:4]));  // open: dp
  Hex_Digit_Display hex_digit_display_7 (.value(LedData[11:8]));  // open: dp
  // Probe on \总周期数 
  // Probe on multiplexer_5_out
  Multiplexer #(.select(1), .width(32), .disabled("Z"), .enable("false")) multiplexer_5 (
    .in0(multiplexer_4_out), .in1(EPCAddress), .out(multiplexer_5_out), .sel(ERET));
  or or_3 (or_3_out, ~Halt, W1, Go, W2);  // OR_Gate
  Hex_Digit_Display hex_digit_display_8 (.value(LedData[3:0]));  // open: dp
  Register #(.width(32), .trigger("rising"), .Select("low")) u_PC (
    .D(multiplexer_5_out), .en(or_3_out), .Q(PC), .clk(CLK));  // open: clr
  // Probe on PC
  Counter #(.width(16), .max('hffff), .ongoal("wrap"), .trigger("rising"), .behavior("new")) counter_1 (
    .count(or_3_out), .Q(\总周期数 ), .clk(CLK), .clr(RESET));  // open: load, D, carry, preset, down
  or or_4 (IR1_t, IR1, IRA);
  \中断按键参考电路  \u_中断按键参考电路_1  (.\与中断屏蔽位与 (INT1), .\同步清零信号 (RST1), .CLK(CLK), .INT(\左 ), .\中断等待指示灯 (W1));
  \中断按键参考电路  \u_中断按键参考电路_2  (.\与中断屏蔽位与 (INT2), .\同步清零信号 (RST2), .CLK(CLK), .INT(\右 ), .\中断等待指示灯 (W2));
  \中断按键参考电路  \u_中断按键参考电路_3  (.\与中断屏蔽位与 (INT3), .\同步清零信号 (RST3), .CLK(CLK), .INT(IRC), .\中断等待指示灯 (W3));
  Adder #(.width(32)) adder_1 (.a(PC), .b(32'h4), .out({adder_1_out_2, adder_1_out}));  // open: cin, cout
  Multiplexer #(.select(1), .width(5), .disabled("Z"), .enable("false")) multiplexer_6 (
    .in0(IR[10:6]), .in1(5'b10000), .out(shamt), .sel(LUI));
  or or_5 (IR2_t, IR2, IRB);
  // Mips_Probe mips_probe_1: pin names not known; wires that end beside it: IR, Syscall, mips_probe_1_p3
  ROM #(.addrWidth(10), .dataWidth(32), .Select("high")) rom_1 (.addr(PC[11:2]), .data(IR));
  or or_6 (IR3_t, IR3, IRC);
  \单周期硬布线控制器  \u_单周期硬布线控制器_1  (
    .Func(IR[5:0]), .OP(IR[31:26]), .ALU_OP(\单周期硬布线控制器_1_alu_op ), .MemToReg(\单周期硬布线控制器_1_memtoreg ),
    .MemWrite(MemWrite), .ALU_SRC(\单周期硬布线控制器_1_alu_src ), .RegWrite(RegWrite), .SysCALL(Syscall),
    .SignedExt(SignedExt), .RegDst(\单周期硬布线控制器_1_regdst ), .JR(\单周期硬布线控制器_1_jr ), .JMP(JMP), .Beq(beq),
    .JAL(JAL), .Bne(bne), .LUI(LUI), .LH(LH), .BGEZ(BGEZ), .ERET(ERET));  // open: rs, rt, INTO, INTC
  Multiplexer #(.select(1), .width(5), .disabled("Z"), .enable("false")) multiplexer_7 (
    .in0(IR[25:21]), .in1(5'b00010), .out(mips_probe_1_p3), .sel(Syscall));
  Multiplexer #(.select(1), .width(5), .disabled("Z"), .enable("false")) multiplexer_8 (
    .in0(IR[20:16]), .in1(5'b00100), .out(multiplexer_8_out), .sel(Syscall));
  Multiplexer #(.select(1), .width(5), .disabled("Z"), .enable("false")) multiplexer_9 (
    .in0(IR[20:16]), .in1(IR[15:11]), .out(multiplexer_9_out), .sel(\单周期硬布线控制器_1_regdst ));
  Priority_Encoder #(.select(2), .disabled("Z")) priority_encoder_1 (
    .in0(INT1), .in1(INT2), .in2(undriven), .out(priority_encoder_1_out), .gs(priority_encoder_1_gs));  // open: in3, en_out, en_in
  Multiplexer #(.select(1), .width(5), .disabled("Z"), .enable("false")) multiplexer_10 (
    .in0(multiplexer_9_out), .in1({5{1'b1}}), .out(multiplexer_10_out), .sel(JAL));
  Multiplexer #(.select(1), .width(32), .disabled("Z"), .enable("false")) multiplexer_11 (
    .in0(multiplexer_17_out), .in1({adder_1_out_2, adder_1_out}), .out(RDin), .sel(JAL));
  MIPS_Regifile mips_regifile_1 (
    .Din(RDin), .Clk(CLK), .R1(PC_JR), .R2(MDin), .WE(RegWrite), .W_num(multiplexer_10_out),
    .R1_num(mips_probe_1_p3), .R2_num(multiplexer_8_out));
  assign bit_extender_1_out = {{16{1'b0}}, IR[15:0]};  // Bit_Extender bit_extender_1
  Multiplexer #(.select(1), .width(32), .disabled("Z"), .enable("false")) multiplexer_12 (
    .in0(bit_extender_1_out), .in1(bit_extender_2_out), .out(multiplexer_12_out), .sel(or_7_out));
  assign bit_extender_2_out = {{16{IR[15]}}, IR[15:0]};  // Bit_Extender bit_extender_2
  or or_7 (or_7_out, beq, SignedExt, bne, BGEZ);
  Multiplexer #(.select(2), .width(32), .disabled("Z"), .enable("false")) multiplexer_13 (
    .in0(32'h3024), .in1(32'h3030), .out(INTAddress), .sel(priority_encoder_1_out));  // open: in2, in3
  and and_1 (\中断请求 , priority_encoder_1_gs, IE);
  Multiplexer #(.select(1), .width(32), .disabled("Z"), .enable("false")) multiplexer_14 (
    .in0(MDin), .in1(multiplexer_12_out), .out(multiplexer_14_out), .sel(\单周期硬布线控制器_1_alu_src ));
  Multiplexer #(.select(1), .width(32), .disabled("Z"), .enable("false")) multiplexer_15 (
    .in0(multiplexer_14_out), .in1({32{1'b0}}), .out(multiplexer_15_out), .sel(BGEZ));
  Shifter #(.width(32), .shift("ll")) shifter_1 (.in(multiplexer_12_out), .\dist (5'b00010), .out(shifter_1_out));
  Register #(.width(2), .trigger("rising"), .Select("low")) register_1 (
    .D(priority_encoder_1_out), .en(\中断请求 ), .Q(register_1_q), .clk(CLK));  // open: clr
  not not_1 (not_1_out, mips_alu_1_equal);
  and and_2 (and_2_out, beq, mips_alu_1_equal);
  MIPS_ALU mips_alu_1 (
    .X(PC_JR), .Y(multiplexer_15_out), .AluOP(\单周期硬布线控制器_1_alu_op ), .Equal(mips_alu_1_equal),
    .Result({mips_alu_1_result[31:19], mips_alu_1_result_2, mips_alu_1_result[1:0]}), .shamt(shamt));  // open: Result_2
  Adder #(.width(32)) adder_2 (
    .a(shifter_1_out), .b({adder_1_out_2, adder_1_out}), .out(adder_2_out));  // open: cin, cout
  Demultiplexer #(.select(2), .width(1), .tristate("false"), .disabled("Z"), .enable("false")) demultiplexer_1 (
    .out0(RST1), .out1(RST2), .out2(RST3), .in(JMP), .sel(register_1_q));  // open: out3
  or or_8 (or_8_out, and_3_out, and_2_out, and_4_out);
  and and_3 (and_3_out, bne, not_1_out);
  and and_4 (and_4_out, or_9_out, BGEZ);
  or or_9 (or_9_out, mips_alu_1_equal, ~mips_alu_1_result[0]);  // OR_Gate
  // Probe on multiplexer_17_out
  Button button_1 (.out(RESET));
  // Probe on mips_alu_1_result_2
  or or_10 (or_10_out, JMP, IE);
  D_Flip_Flop #(.trigger("rising"), .Pre_Clr_Positions("ABOVE_BELOW"), .NegatePresetClear("false"), .enable("true"), .NewFFLayout("true")) d_ff_1 (
    .clk(CLK), .D(\中断请求 ), .Qn(IE), .en(or_10_out));  // open: Q, preset, reset
  RAM #(.addrWidth(17), .dataWidth(32), .bus("combined"), .Select("low")) ram_1 (
    .addr(mips_alu_1_result_2), .data(ram_1_data));  // open: sel, clk, ld, clr
  D_Flip_Flop #(.trigger("high"), .Pre_Clr_Positions("LEGACY"), .NegatePresetClear("false"), .enable("true"), .NewFFLayout("false")) d_ff_2 (.Q(d_ff_2_q));  // open: clk, D, Qn, preset, en, reset
  // Probe on 13'hbb
  Multiplexer #(.select(1), .width(32), .disabled("Z"), .enable("false")) multiplexer_16 (
    .in0({mips_alu_1_result[31:19], mips_alu_1_result_2, mips_alu_1_result[1:0]}), .in1(ram_1_data),
    .out(multiplexer_16_out), .sel(\单周期硬布线控制器_1_memtoreg ));
  Shifter #(.width(32), .shift("ll")) shifter_2 (.in(multiplexer_16_out), .\dist (5'b10000), .out(shifter_2_out));
  Comparator #(.width(13), .mode("twosComplement")) comparator_5 (
    .a(CNT_num), .b(13'hbb), .eq(comparator_5_eq), .lt(comparator_5_lt));  // open: gt
  Clock #(.highDuration(1), .lowDuration(1)) clock_2 (.out(clock_2_out));
  and and_5 (and_5_out, \中断请求 , IE);
  Shifter #(.width(32), .shift("ar")) shifter_3 (.in(shifter_2_out), .\dist (5'b10000), .out(shifter_3_out));
  Shifter #(.width(32), .shift("ar")) shifter_4 (.in(multiplexer_16_out), .\dist (5'b10000), .out(shifter_4_out));
  nand nand_1 (nand_1_out, d_ff_2_q, comparator_5_eq);
  Counter #(.width(13), .max('h1fff), .ongoal("stay"), .trigger("rising"), .behavior("old")) counter_2 (
    .count(comparator_5_lt), .Q(CNT_num), .clk(clock_2_out));  // open: load, D, carry, clr, preset
  Register #(.width(32), .trigger("rising"), .Select("low")) register_2 (
    .D(NextPC), .en(and_5_out), .Q(EPCAddress), .clk(CLK));  // open: clr
  Counter #(.width(7), .max('h7f), .ongoal("wrap"), .trigger("rising"), .behavior("new")) counter_3 (
    .count(show), .Q(x), .carry(counter_3_carry), .clk(CLK), .clr(or_12_out));  // open: load, D, preset, down
  // Probe on MDin
  // Mips_Probe mips_probe_2: pin names not known; wires that end beside it: IR
  Multiplexer #(.select(2), .width(32), .disabled("Z"), .enable("false")) multiplexer_17 (
    .in0(multiplexer_16_out), .in1(shifter_3_out), .in2(multiplexer_16_out), .in3(shifter_4_out),
    .out(multiplexer_17_out), .sel({mips_alu_1_result[1], LH}));
  // Probe on x
  // Probe on PC_JR
  assign CLK = nand_1_out ? clock_2_out : 1'bz;  // Controlled_Buffer controlled_buffer_1
  Pull_Resistor #(.pull(1)) pull_resistor_4 (.node(CLK));
  // Probe on y
  and and_6 (and_6_out, counter_3_carry, show);
  Counter #(.width(7), .max('h7f), .ongoal("wrap"), .trigger("rising"), .behavior("new")) counter_4 (
    .count(and_6_out), .Q(y), .clk(CLK), .clr(or_12_out));  // open: load, D, carry, preset, down
  or or_11 (or_11_out, or_12_out, RESET);
  Multiplier #(.width(17)) multiplier_1 (.a(17'h80), .b({{10{1'b0}}, y}), .out(multiplier_1_out));  // open: cin, cout
  Multiplier #(.width(17)) multiplier_2 (.a(17'h3fff), .b(PC_JR[16:0]), .out(multiplier_2_out));  // open: cin, cout
  Adder #(.width(17)) adder_3 (.a(multiplier_1_out), .b({{10{1'b0}}, x}), .out(adder_3_out));  // open: cin, cout
  Comparator #(.width(32), .mode("twosComplement")) comparator_6 (
    .a(PC_JR), .b(32'h32), .eq(comparator_6_eq));  // open: gt, lt
  or or_12 (or_12_out, \左 , \右 );
  Adder #(.width(17)) adder_4 (.a(multiplier_2_out), .b(adder_3_out), .out(adder_4_out));  // open: cin, cout
  // Probe on adder_4_out
  Register #(.width(32), .trigger("rising"), .Select("low")) register_3 (
    .D(MDin), .en(show), .Q(LedData), .clk(CLK), .clr(RESET));
  and and_7 (show, ~comparator_6_eq, Syscall);  // AND_Gate
  and and_8 (and_8_out, comparator_6_eq, Syscall);
  // LCD_Video lcd_video_1: pin names not known; wires that end beside it: or_11_out, CLK, show, x, y, lcd_video_1_p6
  or or_13 (Halt, show, and_8_out);
  or or_14 (or_14_out, W1, W2);
  ROM #(.addrWidth(17), .dataWidth(32), .Select("low")) rom_2 (.addr(adder_4_out), .data({rom_2_data, lcd_video_1_p6}));
  Button button_2 (.out(\左 ));
  Button button_3 (.out(\右 ));

  // Other names for the same wires on the sheet: A0[31:0] = MDin; V0[31:0] = PC_JR

  // Notes on the sheet:
  //   中断源
  //   中断等待指示
  //   总复位信号应将除ROM以外所有存储组件全部清零
  //   单级中断测试信号模拟器
  //   数码管输出
  //   数码管输出应该用寄存器锁存，否则显示数据只能一闪而过
  //   指令存储器
  //   branch
  //   指令字
  //   contents of rom_1 (hex, n*v repeats v):
  //   20100000 20110080 1189c0 20120000 20130001 121020 c 20020032 c 2118022 2539022 8000c05 2118020
  //   2539020 8000c05
  //   OP
  //   Func
  //   rs
  //   rt
  //   rd
  //   $ra
  //   JMP
  //   JR
  //   OP
  //   Func
  //   Syscall
  //   Beq
  //   Bne
  //   MemToReg
  //   MemWrite
  //   AluOP
  //   AluSrcB
  //   RegWrite
  //   JAL
  //   RegDst
  //   LUI
  //   LH
  //   BGEZ
  //   为方便自动评测，需要输出PC，IR，寄存器堆写如数据RDin
  //   RAM写使能MemWrite、RAM写入数据MDin等信号
  //   用这个时钟源需要去掉电路中的其他时钟源
  //   控制位
  //   暂停节拍，不能为0
  //   戳工具置1进入计数暂停模式，ctrl+k时钟自动运行到对应节拍暂停
  //   ctrl+k关闭时钟连续运行，将控制位置零，进入单步调试模式调试
  //   可计数暂停的时钟源
  //   contents of rom_2 (hex, n*v repeats v):
  //   925*7fff 4631 5b18 56f7 737b 677b 675a 6b7a 6f7b 6f7b 739c 739d 739c 739d 77be 7bff 112*7fff 0 4631
  //   6bdd 679d 5f38 677c 6fbb 637a 6fbd 577c 575b 672f 62e8 734c 734e 5ec9 56aa 62ed 4ef0 5339 3ed6 635a
  //   5718 6318 6739 6b7a 6f7b 6f7b 739c 77bd 96*7fff 7bde 0 0 422f 73bc 679a 6b9b 5b5b 6f9b 5b7b 475b
  //   473a 575b 4685 324f 7b8e 736c 6f6b 5358 5f9e 5f9e 6fbd 433a 4b39 46f9 7ffd 7fde 6f9c 331a 3f3b 4e66
  //   66cf 4e2d 2d28 5e27 670f 6eea 422b 5ad2 62ce 62f1 6310 677b 6b7b 6759 6715 6b5a 6fbd 79*7fff 739c 0
  //   0 0 3a0b 679c 6b7b 73bc 677d 6352 570a 6b72 639c 77dd 679a 6b71 6f4b 6b08 5713 5b7d 5b7b 5b7b 5b7d
  //   3eb4 3e95 2675 3ed6 5b5a 5f7b 3b19 5b9c 4318 6357 5af3 6ad2 562a 62ab 7f6f 6f4d 630e 5ec8 51e6 5663
  //   639b 7bff 7ff8 7aea 6a64 4da2 4980 51a4 59e5 526b 564c 55c7 5e6d 666d 66d1 62b0 5eb3 62b4 6718 6f7a
  //   739c 739c 73bf 77df 60*7fff 6739 4*0 422d 5b32 5f14 77b9 6773 470f 6350 5f76 5f9c 73be 4f7d 6750
  //   56ea 52ea 6356 73be 535b 371b 6fbc 52d5 4671 3e96 1213 3ab7 3b19 5739 679b 5f5c 6333 398d 5250 6734
  //   7b95 66ef 6eee 4aae 5acc 4629 6643 4712 679a 7fd6 6f0e 62ed 6acc 5e66 6648 5625 6e27 5e49 51a5 66aa
  //   5e25 66cf 72ac 7753 65e2 69e1 7282 7283 76c8 72c5 6660 5648 526f 5e8b 5ea9 62aa 668c 66cf 66d0 6ad1
  //   6f35 6f35 737a 48*7fff 3def 4*0 464f 6b4f 52c8 5e6e 666f 4af9 5b9d 679d 6fbd 5b7c 5b30 672d 52ed
  //   3f3b 575c 4719 679c 639c 677a 6359 4ef5 637b 4af7 5739 5758 3f19 3af9 677a 5e90 524f 4e90 6ef0 5af5
  //   2672 7732 56af 4a8e 6339 6acc 5202 6283 6f0b 6f56 7352 6eea 732e 6eea 6a87 6a26 5de6 6249 7242 7f2b
  //   6eed 6e64 72ed 6a69 6a49 76ca 76e7 66cf 6262 7752 72e6 7710 7331 7706 6241 6642 6203 6687 5dc2 6626
  //   7223 6f15 48*7fff 4210 0 0 2884 0 4651 6335 65a7 4d65 4187 622b 67be 7bfe 6bdf 572f 5310 634e 4f15
  //   5b3a 473b 639c 7fbc 77de 5ad0 56d2 21f1 3eb5 2252 4af7 4b18 36f9 5716 4ad6 6ad4 4ef4 62f4 72b0 4e70
  //   46d5 637b 4738 66ef 7f53 7f72 51c3 52c5 6b74 6ac8 6f52 7393 6f09 668c 6f33 774f 730f 6641 65c4 7ae7
  //   776f 772e 7332 6e45 6a45 6e88 7b28 66cd 730e 6ee7 6aa4 6aec 6eee 7b70 6ec6 6ec5 6a41 732d 6244 6a68
  //   6ecd 6b16 48*7fff 4210 0 3885 516b 0 3ded 66d0 5a04 6289 45a9 3944 3eaf 18a6 2127 2d68 2147 2147
  //   35ce 216c 2dce 5270 3a31 3a72 2e0f 25cf 2ab5 6758 3f3a 371a 477b 5758 4b38 32b6 6b78 6b58 7736 76f2
  //   39ee 2a31 5316 5758 5ab0 7eeb 7f54 4a27 4315 56c8 5a46 630e 5333 56ce 468c 5e43 7309 6e88 6a65 6e8a
  //   7b4b 772e 7310 770e 6e44 6a67 6e87 72eb 6b31 7728 6ee7 6ee4 72ea 7398 670a 6f6f 6b0c 6ae9 6f2e 6f0b
  //   6645 6a67 6f57 48*7fff 4210 0 4d29 48a5 0 3e2f 6b34 428a 59a7 6a8c 5f2c 42a6 402 210a 292b 4*1cc6
  //   2529 2d8c 254a 318c 1d08 2529 318c c63 1ce6 18e7 6ef5 5718 2a96 679a 6f99 62f4 735a 5e8f 258a 4a4e
  //   564d 464c 5648 5e25 528d 6737 4f38 3ed4 6352 4664 574a 3e49 52f2 7b0b 7f07 6283 6a64 72cb 7f50 7b0a
  //   772f 7acc 6e69 72ab 6668 72ab 6f0e 6ee8 6a66 6ae7 6b51 6b2f 6b2a 6f93 7351 6f0a 7371 6f4f 6a8a 6686
  //   6b57 48*7fff 4210 0 4d4a 514a 0 4a50 364b 6311 622c 5a6d 5f9c 7396 6f96 5b0b 3649 4ef4 5b19 4eb6
  //   4a94 3486 38a7 3065 30a7 3086 30a7 30c8 2065 2ce8 1864 5e51 4671 19ef 5358 5314 62f3 6337 4e50 524f
  //   260e 522d 56d6 6711 4a8d 3eb5 5711 1d05 35ae 1ce8 1d09 2928 1ce6 2949 35a9 3d85 3543 3922 3921 4a4e
  //   4da4 55e7 4dc7 4d62 4e28 5a6b 5e47 6ecb 6ee8 772e 7728 776f 6f92 6b8f 6fb4 734a 7350 7372 6f4c 6acd
  //   6eab 62f5 48*7fff 4210 0 4ce7 3084 0 3ded 6b76 7377 6290 5b13 5290 5b11 6332 52cf 4648 5f7b 5f79
  //   6fbe 4b9d 616e 7f5c 6dd1 7b5b 7af8 7676 7b19 6469 64aa 6d2e 654e 650c 64eb 6089 6273 6336 6f59 5692
  //   41ee 2a52 5b7a 5f5a 4a6d 56cf 5a8f 5eef 256b 4e74 2d6b 4210 5295 4a53 4653 4e95 5ad8 52b6 4232 4e95
  //   4632 296c 18e8 56b6 35cf 254b 296c 2d8d 252a 318c 2d49 2d49 294a 2d69 3188 2525 2d87 734a 7393 6f4d
  //   6687 6e89 5ef6 48*7fff 4210 0 2442 0 0 4650 5f74 5f35 6797 5eaf 630e 6b57 6353 6774 4eee 4ed7 5b7d
  //   6bbd 6bfe 6275 5d4d 69ae 590c 552c 65d0 65d1 5c69 6089 60ca 5cca 650d 650c 608a 5e73 6337 6a71 498c
  //   562c 664e 5716 4ab2 52f0 5b15 4a8f 4eac 5311 4acf 468e 3e2b 39e6 41e7 3523 2d03 3184 3522 2d47 3147
  //   2948 2d68 2d6a 2d6c 14a5 1ce7 35ad 35ad 318c 3def 5294 4631 5294 4a52 6319 4231 35ac 774a 6f2d 734f
  //   66c9 6f11 66f2 48*7fff 4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
endmodule

module \单周期MIPS  (
  output RegWrite,
  output MemWrite,
  output [31:0] PC,
  output [31:0] IR,
  output [31:0] RDin,
  output [31:0] MDin,
  output [31:0] LedData
);

  wire and_1_out, and_2_out, and_3_out, and_4_out, beq, BGEZ, bne, CLK, clock_2_out, comparator_1_eq,
       comparator_1_lt, comparator_2_eq, d_ff_1_q, Go, Halt, IRA, IRB, IRC, JAL, lcd_video_1_p3,
       lcd_video_1_p5, LH, LUI, mips_alu_1_equal, nand_1_out, not_1_out, or_1_out, or_2_out, or_3_out,
       or_4_out, or_5_out, RESET, SignedExt, Syscall, W1, W2, W3, \单周期硬布线控制器_1_alu_src , \单周期硬布线控制器_1_jmp ,
       \单周期硬布线控制器_1_jr , \单周期硬布线控制器_1_memtoreg , \单周期硬布线控制器_1_regdst ;
  wire [3:0] adder_1_out_2, \单周期硬布线控制器_1_alu_op ;
  wire [4:0] mips_probe_1_p3, multiplexer_6_out, multiplexer_7_out, multiplexer_8_out, shamt;
  wire [12:0] CNT_num;
  wire [15:0] \总周期数 ;
  wire [27:0] adder_1_out;
  wire [31:0] adder_2_out, bit_extender_1_out, bit_extender_2_out, mips_alu_1_result, multiplexer_1_out,
       multiplexer_2_out, multiplexer_3_out, multiplexer_10_out, multiplexer_11_out, multiplexer_12_out,
       multiplexer_13_out, multiplexer_14_out, PC_JR, rom_2_data, shifter_1_out, shifter_2_out,
       shifter_3_out, shifter_4_out;

  Clock #(.highDuration(1), .lowDuration(1)) clock_1 ();  // open: out
  Button _1 (.out(IRA));
  Button _2 (.out(IRB));
  Button _3 (.out(IRC));
  Button \u_继续运行  (.out(Go));
  LED #(.active("true")) led_1 (.in(W1));
  LED #(.active("true")) led_2 (.in(W2));
  LED #(.active("true")) led_3 (.in(W3));
  Multiplexer #(.select(1), .width(32), .disabled("Z"), .enable("false")) multiplexer_1 (
    .in0({adder_1_out_2, adder_1_out}), .in1(adder_2_out), .out(multiplexer_1_out), .sel(or_4_out));
  Hex_Digit_Display hex_digit_display_1 (.value(LedData[31:28]));  // open: dp
  or or_1 (or_1_out, JAL, \单周期硬布线控制器_1_jmp );
  Multiplexer #(.select(1), .width(32), .disabled("Z"), .enable("false")) multiplexer_2 (
    .in0(multiplexer_1_out), .in1({adder_1_out_2, IR[25:0], 2'b00}), .out(multiplexer_2_out), .sel(or_1_out));
  Hex_Digit_Display hex_digit_display_2 (.value(LedData[27:24]));  // open: dp
  Hex_Digit_Display hex_digit_display_3 (.value(LedData[23:20]));  // open: dp
  Multiplexer #(.select(1), .width(32), .disabled("Z"), .enable("false")) multiplexer_3 (
    .in0(multiplexer_2_out), .in1(PC_JR), .out(multiplexer_3_out), .sel(\单周期硬布线控制器_1_jr ));
  or or_2 (or_2_out, ~Halt, Go);  // OR_Gate
  Hex_Digit_Display hex_digit_display_4 (.value(LedData[19:16]));  // open: dp
  Hex_Digit_Display hex_digit_display_5 (.value(LedData[15:12]));  // open: dp
  Counter #(.width(16), .max('hffff), .ongoal("wrap"), .trigger("rising"), .behavior("new")) counter_1 (
    .count(or_2_out), .Q(\总周期数 ), .clk(CLK), .clr(RESET));  // open: load, D, carry, preset, down
  Register #(.width(32), .trigger("rising"), .Select("low")) u_PC (
    .D(multiplexer_3_out), .en(or_2_out), .Q(PC), .clk(CLK));  // open: clr
  Hex_Digit_Display hex_digit_display_6 (.value(LedData[11:8]));  // open: dp
  Hex_Digit_Display hex_digit_display_7 (.value(LedData[7:4]));  // open: dp
  // Probe on \总周期数 
  Adder #(.width(32)) adder_1 (.a(PC), .b(32'h4), .out({adder_1_out_2, adder_1_out}));  // open: cin, cout
  Hex_Digit_Display hex_digit_display_8 (.value(LedData[3:0]));  // open: dp
  Multiplexer #(.select(1), .width(5), .disabled("Z"), .enable("false")) multiplexer_4 (
    .in0(IR[10:6]), .in1(5'b10000), .out(shamt), .sel(LUI));
  // Mips_Probe mips_probe_1: pin names not known; wires that end beside it: IR, Syscall, mips_probe_1_p3
  ROM #(.addrWidth(10), .dataWidth(32), .Select("high")) rom_1 (.addr(PC[11:2]), .data(IR));
  D_Flip_Flop #(.trigger("high"), .Pre_Clr_Positions("LEGACY"), .NegatePresetClear("false"), .enable("true"), .NewFFLayout("false")) d_ff_1 (.Q(d_ff_1_q));  // open: clk, D, Qn, preset, en, reset
  // Probe on 13'h58
  Clock #(.highDuration(1), .lowDuration(1)) clock_2 (.out(clock_2_out));
  \单周期硬布线控制器  \u_单周期硬布线控制器_1  (
    .Func(IR[5:0]), .OP(IR[31:26]), .ALU_OP(\单周期硬布线控制器_1_alu_op ), .MemToReg(\单周期硬布线控制器_1_memtoreg ),
    .MemWrite(MemWrite), .ALU_SRC(\单周期硬布线控制器_1_alu_src ), .RegWrite(RegWrite), .SysCALL(Syscall),
    .SignedExt(SignedExt), .RegDst(\单周期硬布线控制器_1_regdst ), .JR(\单周期硬布线控制器_1_jr ), .JMP(\单周期硬布线控制器_1_jmp ),
    .Beq(beq), .JAL(JAL), .Bne(bne), .LUI(LUI), .LH(LH), .BGEZ(BGEZ));  // open: rs, rt, ERET, INTO, INTC
  Multiplexer #(.select(1), .width(5), .disabled("Z"), .enable("false")) multiplexer_5 (
    .in0(IR[25:21]), .in1(5'b00010), .out(mips_probe_1_p3), .sel(Syscall));
  Multiplexer #(.select(1), .width(5), .disabled("Z"), .enable("false")) multiplexer_6 (
    .in0(IR[20:16]), .in1(5'b00100), .out(multiplexer_6_out), .sel(Syscall));
  Multiplexer #(.select(1), .width(5), .disabled("Z"), .enable("false")) multiplexer_7 (
    .in0(IR[20:16]), .in1(IR[15:11]), .out(multiplexer_7_out), .sel(\单周期硬布线控制器_1_regdst ));
  Multiplexer #(.select(1), .width(5), .disabled("Z"), .enable("false")) multiplexer_8 (
    .in0(multiplexer_7_out), .in1({5{1'b1}}), .out(multiplexer_8_out), .sel(JAL));
  Comparator #(.width(13), .mode("twosComplement")) comparator_1 (
    .a(CNT_num), .b(13'h58), .eq(comparator_1_eq), .lt(comparator_1_lt));  // open: gt
  assign bit_extender_1_out = {{16{1'b0}}, IR[15:0]};  // Bit_Extender bit_extender_1
  assign bit_extender_2_out = {{16{IR[15]}}, IR[15:0]};  // Bit_Extender bit_extender_2
  Multiplexer #(.select(1), .width(32), .disabled("Z"), .enable("false")) multiplexer_9 (
    .in0(multiplexer_14_out), .in1({adder_1_out_2, adder_1_out}), .out(RDin), .sel(JAL));
  nand nand_1 (nand_1_out, d_ff_1_q, comparator_1_eq);
  Counter #(.width(13), .max('h1fff), .ongoal("stay"), .trigger("rising"), .behavior("old")) counter_2 (
    .count(comparator_1_lt), .Q(CNT_num), .clk(clock_2_out));  // open: load, D, carry, clr, preset
  MIPS_Regifile mips_regifile_1 (
    .Din(RDin), .Clk(CLK), .R1(PC_JR), .R2(MDin), .WE(RegWrite), .W_num(multiplexer_8_out),
    .R1_num(mips_probe_1_p3), .R2_num(multiplexer_6_out));
  Multiplexer #(.select(1), .width(32), .disabled("Z"), .enable("false")) multiplexer_10 (
    .in0(bit_extender_1_out), .in1(bit_extender_2_out), .out(multiplexer_10_out), .sel(or_3_out));
  or or_3 (or_3_out, beq, SignedExt, bne, BGEZ);
  assign CLK = nand_1_out ? clock_2_out : 1'bz;  // Controlled_Buffer controlled_buffer_1
  Pull_Resistor #(.pull(1)) pull_resistor_1 (.node(CLK));
  Multiplexer #(.select(1), .width(32), .disabled("Z"), .enable("false")) multiplexer_11 (
    .in0(MDin), .in1(multiplexer_10_out), .out(multiplexer_11_out), .sel(\单周期硬布线控制器_1_alu_src ));
  Multiplexer #(.select(1), .width(32), .disabled("Z"), .enable("false")) multiplexer_12 (
    .in0(multiplexer_11_out), .in1({32{1'b0}}), .out(multiplexer_12_out), .sel(BGEZ));
  Shifter #(.width(32), .shift("ll")) shifter_1 (.in(multiplexer_10_out), .\dist (5'b00010), .out(shifter_1_out));
  not not_1 (not_1_out, mips_alu_1_equal);
  and and_1 (and_1_out, beq, mips_alu_1_equal);
  MIPS_ALU mips_alu_1 (
    .X(PC_JR), .Y(multiplexer_12_out), .AluOP(\单周期硬布线控制器_1_alu_op ), .Equal(mips_alu_1_equal),
    .Result(mips_alu_1_result), .shamt(shamt));  // open: Result_2
  Adder #(.width(32)) adder_2 (
    .a(shifter_1_out), .b({adder_1_out_2, adder_1_out}), .out(adder_2_out));  // open: cin, cout
  or or_4 (or_4_out, and_2_out, and_1_out, and_3_out);
  and and_2 (and_2_out, bne, not_1_out);
  and and_3 (and_3_out, or_5_out, BGEZ);
  or or_5 (or_5_out, mips_alu_1_equal, ~mips_alu_1_result[0]);  // OR_Gate
  Button button_1 (.out(RESET));
  ROM #(.addrWidth(14), .dataWidth(32), .Select("high")) rom_2 (.data(rom_2_data));  // open: addr
  Multiplexer #(.select(1), .width(32), .disabled("Z"), .enable("false")) multiplexer_13 (
    .in0(mips_alu_1_result), .in1(rom_2_data), .out(multiplexer_13_out), .sel(\单周期硬布线控制器_1_memtoreg ));
  Shifter #(.width(32), .shift("ll")) shifter_2 (.in(multiplexer_13_out), .\dist (5'b10000), .out(shifter_2_out));
  Shifter #(.width(32), .shift("ar")) shifter_3 (.in(shifter_2_out), .\dist (5'b10000), .out(shifter_3_out));
  Shifter #(.width(32), .shift("ar")) shifter_4 (.in(multiplexer_13_out), .\dist (5'b10000), .out(shifter_4_out));
  Comparator #(.width(32), .mode("twosComplement")) comparator_2 (
    .a(PC_JR), .b(32'ha), .eq(comparator_2_eq));  // open: gt, lt
  Multiplexer #(.select(2), .width(32), .disabled("Z"), .enable("false")) multiplexer_14 (
    .in0(multiplexer_13_out), .in1(shifter_3_out), .in2(multiplexer_13_out), .in3(shifter_4_out),
    .out(multiplexer_14_out), .sel({mips_alu_1_result[1], LH}));
  and and_4 (and_4_out, ~comparator_2_eq, Syscall);  // AND_Gate
  and and_5 (Halt, comparator_2_eq, Syscall);
  Register #(.width(32), .trigger("rising"), .Select("low")) register_1 (
    .D(MDin), .en(and_4_out), .Q(LedData), .clk(CLK), .clr(RESET));
  // LCD_Video lcd_video_1: pin names not known; wires that end beside it: RESET, CLK, lcd_video_1_p3, lcd_video_1_p3, lcd_video_1_p5, lcd_video_1_p5, MDin[15:0]

  // Other names for the same wires on the sheet: A0[31:0] = MDin; V0[31:0] = PC_JR

  // Notes on the sheet:
  //   中断源
  //   中断等待指示
  //   总复位信号应将除ROM以外所有存储组件全部清零
  //   数码管输出
  //   数码管输出应该用寄存器锁存，否则显示数据只能一闪而过
  //   指令存储器
  //   branch
  //   OP
  //   rs
  //   指令字
  //   contents of rom_1 (hex, n*v repeats v):
  //   20110001 8000c05 20110001 20120002 20130003 8000c09 20110001 20120002 20130003 8000c0d 20110001
  //   20120002 20130003 8000c11 20110001 20120002 20130003 c000cfb 20100001 20110001 118fc0 112020
  //   20020022 c 118882 12200001 8000c15 112020 20020022 c 20110001 118880 112020 20020022 c 12200001
  //   8000c1f 20110001 118fc0 112020 20020022 c 1188c3 112020 20020022 c 118903 112020 20020022 c 118903
  //   112020 20020022 c 118903 112020 20020022 c 118903 112020 20020022 c 118903 112020 20020022 c 118903
  //   112020 20020022 c 118903 112020 20020022 c 20100001 109fc0 139fc3 8021 2012000c 24160003 26100001
  //   3210000f 20080008 20090001 139900 2709825 132020 20020022 c 1094022 1500fff9 22100001 2018000f
  //   2188024 108700 20080008 20090001 139902 2709825 132021 20020022 c 1094022 1500fff9 108702 2c9b022
  //   12c00001 8000c50 4020 1084027 84400 3508ffff 82021 20020022 c 2010ffff 20110000 ae300000 22100001
  //   22310004 ae300000 22100001 22310004 ae300000 22100001 22310004 ae300000 22100001 22310004 ae300000
  //   22100001 22310004 ae300000 22100001 22310004 ae300000 22100001 22310004 ae300000 22100001 22310004
  //   ae300000 22100001 22310004 ae300000 22100001 22310004 ae300000 22100001 22310004 ae300000 22100001
  //   22310004 ae300000 22100001 22310004 ae300000 22100001 22310004 ae300000 22100001 22310004 ae300000
  //   22100001 22310004 22100001 8020 2011003c 8e130000 8e340000 274402a 11000002 ae330000 ae140000
  //   2231fffc 1611fff8 102020 20020022 c 22100004 2011003c 1611fff2 2002000a c 200b0008 3c11fedc 3631ffff
  //   112020 20020022 c 3c11ba98 112020 c 3c117654 112020 c 3c113210 112020 c 216bffff 1560fff0 2002000a c
  //   2008ffff 20117777 112020 20020022 c 200b0010 3a31ffff 112020 20020022 c 216bffff 1560fffa 2002000a c
  //   20090000 200b0010 34118483 20120404 118c00 129400 36318281 22520404 ad310000 2328820 21290004
  //   216bffff 1560fffb 200b0020 20090000 85310000 112020 20020022 c 21290002 216bffff 1560fff9 2002000a c
  //   2011000f 112020 20020022 c 2231ffff 621fffb 2002000a c 2002000a c 20100000 22100001 102020 20020022
  //   c 22100002 102020 20020022 c 22100003 102020 20020022 c 22100004 102020 20020022 c 22100005 102020
  //   20020022 c 22100006 102020 20020022 c 22100007 102020 20020022 c 22100008 102020 20020022 20020022 c
  //   3e00008
  //   rt
  //   rd
  //   控制位
  //   暂停节拍，不能为0
  //   Func
  //   $ra
  //   戳工具置1进入计数暂停模式，ctrl+k时钟自动运行到对应节拍暂停
  //   ctrl+k关闭时钟连续运行，将控制位置零，进入单步调试模式调试
  //   用这个时钟源需要去掉电路中的其他时钟源
  //   Beq
  //   JMP
  //   JR
  //   Bne
  //   OP
  //   JAL
  //   Func
  //   LUI
  //   LH
  //   BGEZ
  //   Syscall
  //   MemToReg
  //   MemWrite
  //   AluOP
  //   AluSrcB
  //   RegWrite
  //   RegDst
  //   可计数暂停的时钟源
  //   为方便自动评测，需要输出PC，IR，寄存器堆写如数据RDin
  //   RAM写使能MemWrite、RAM写入数据MDin等信号
  //   contents of rom_2 (hex, n*v repeats v):
  //   925*ff7f 3146 185b f756 7b73 7b67 5a67 7a6b 7b6f 7b6f 9c73 9d73 9c73 9d73 be77 ff7b 112*ff7f 0 3146
  //   dd6b 9d67 385f 7c67 bb6f 7a63 bd6f 7c57 5b57 2f67 e862 4c73 4e73 c95e aa56 ed62 f04e 3953 d63e 5a63
  //   1857 1863 3967 7a6b 7b6f 7b6f 9c73 bd77 96*ff7f de7b 0 0 2f42 bc73 9a67 9b6b 5b5b 9b6f 7b5b 5b47
  //   3a47 5b57 8546 4f32 8e7b 6c73 6b6f 5853 9e5f 9e5f bd6f 3a43 394b f946 fd7f de7f 9c6f 1a33 3b3f 664e
  //   cf66 2d4e 282d 275e f67 ea6e 2b42 d25a ce62 f162 1063 7b67 7b6b 5967 1567 5a6b bd6f 79*ff7f 9c73 0 0
  //   0 b3a 9c67 7b6b bc73 7d67 5263 a57 726b 9c63 dd77 9a67 716b 4b6f 86b 1357 7d5b 7b5b 7b5b 7d5b b43e
  //   953e 7526 d63e 5a5b 7b5f 193b 9c5b 1843 5763 f35a d26a 2a56 ab62 6f7f 4d6f e63 c85e e651 6356 9b63
  //   ff7b f87f ea7a 646a a24d 8049 a451 e559 6b52 4c56 c755 6d5e 6d66 d166 b062 b35e b462 1867 7a6f 9c73
  //   9c73 bf73 df77 60*ff7f 3967 4*0 2d42 325b 145f b977 7367 f47 5063 765f 9c5f be73 7d4f 5067 ea56 ea52
  //   5663 be73 5b53 1b37 bc6f d552 7146 963e 1312 b73a 193b 3957 9b67 5c5f 3363 8d39 5052 3467 957b ef66
  //   ee6e ae4a cc5a 2946 4366 1247 9a67 d67f e6f ed62 cc6a 665e 4866 2556 276e 495e a551 aa66 255e cf66
  //   ac72 5377 e265 e169 8272 8372 c876 c572 6066 4856 6f52 8b5e a95e aa62 8c66 cf66 d066 d16a 356f 356f
  //   7a73 48*ff7f ef3d 4*0 4f46 4f6b c852 6e5e 6f66 f94a 9d5b 9d67 bd6f 7c5b 305b 2d67 ed52 3b3f 5c57
  //   1947 9c67 9c63 7a67 5963 f54e 7b63 f74a 3957 5857 193f f93a 7a67 905e 4f52 904e f06e f55a 7226 3277
  //   af56 8e4a 3963 cc6a 252 8362 b6f 566f 5273 ea6e 2e73 ea6e 876a 266a e65d 4962 4272 2b7f ed6e 646e
  //   ed72 696a 496a ca76 e776 cf66 6262 5277 e672 1077 3173 677 4162 4266 362 8766 c25d 2666 2372 156f
  //   48*ff7f 1042 0 0 8428 0 5146 3563 a765 654d 8741 2b62 be67 fe7b df6b 2f57 1053 4e63 154f 3a5b 3b47
  //   9c63 bc7f de77 d05a d256 f121 b53e 5222 f74a 184b f936 1657 d64a d46a f44e f462 b072 704e d546 7b63
  //   3847 ef66 537f 727f c351 c552 746b c86a 526f 9373 96f 8c66 336f 4f77 f73 4166 c465 e77a 6f77 2e77
  //   3273 456e 456a 886e 287b cd66 e73 e76e a46a ec6a ee6e 707b c66e c56e 416a 2d73 4462 686a cd6e 166b
  //   48*ff7f 1042 0 8538 6b51 0 ed3d d066 45a 8962 a945 4439 af3e a618 2721 682d 4721 4721 ce35 6c21 ce2d
  //   7052 313a 723a f2e cf25 b52a 5867 3a3f 1a37 7b47 5857 384b b632 786b 586b 3677 f276 ee39 312a 1653
  //   5857 b05a eb7e 547f 274a 1543 c856 465a e63 3353 ce56 8c46 435e 973 886e 656a 8a6e 4b7b 2e77 1073
  //   e77 446e 676a 876e eb72 316b 2877 e76e e46e ea72 9873 a67 6f6f c6b e96a 2e6f b6f 4566 676a 576f
  //   48*ff7f 1042 0 294d a548 0 2f3e 346b 8a42 a759 8c6a 2c5f a642 204 a21 2b29 4*c61c 2925 8c2d 4a25
  //   8c31 81d 2925 8c31 630c e61c e718 f56e 1857 962a 9a67 996f f462 5a73 8f5e 8a25 4e4a 4d56 4c46 4856
  //   255e 8d52 3767 384f d43e 5263 6446 4a57 493e f252 b7b 77f 8362 646a cb72 507f a7b 2f77 cc7a 696e
  //   ab72 6866 ab72 e6f e86e 666a e76a 516b 2f6b 2a6b 936f 5173 a6f 7173 4f6f 8a6a 8666 576b 48*ff7f 1042
  //   0 4a4d 4a51 0 504a 4b36 1163 2c62 6d5a 9c5f 9673 966f b5b 4936 f44e 195b b64e 944a 8634 a738 6530
  //   a730 8630 a730 c830 6520 e82c 6418 515e 7146 ef19 5853 1453 f362 3763 504e 4f52 e26 2d52 d656 1167
  //   8d4a b53e 1157 51d ae35 e81c 91d 2829 e61c 4929 a935 853d 4335 2239 2139 4e4a a44d e755 c74d 624d
  //   284e 6b5a 475e cb6e e86e 2e77 2877 6f77 926f 8f6b b46f 4a73 5073 7273 4c6f cd6a ab6e f562 48*ff7f
  //   1042 0 e74c 8430 0 ed3d 766b 7773 9062 135b 9052 115b 3263 cf52 4846 7b5f 795f be6f 9d4b 6e61 5c7f
  //   d16d 5b7b f87a 7676 197b 6964 aa64 2e6d 4e65 c65 eb64 8960 7362 3663 596f 9256 ee41 522a 7a5b 5a5f
  //   6d4a cf56 8f5a ef5e 6b25 744e 6b2d 1042 9552 534a 5346 954e d85a b652 3242 954e 3246 6c29 e818 b656
  //   cf35 4b25 6c29 8d2d 2a25 8c31 492d 492d 4a29 692d 8831 2525 872d 4a73 9373 4d6f 8766 896e f65e
  //   48*ff7f 1042 0 4224 0 0 5046 745f 355f 9767 af5e e63 576b 5363 7467 ee4e d74e 7d5b bd6b fe6b 7562
  //   4d5d ae69 c59 2c55 d065 d165 695c 8960 ca60 ca5c d65 c65 8a60 735e 3763 716a 8c49 2c56 4e66 1657
  //   b24a f052 155b 8f4a ac4e 1153 cf4a 8e46 2b3e e639 e741 2335 32d 8431 2235 472d 4731 4829 682d 6a2d
  //   6c2d a514 e71c ad35 ad35 8c31 ef3d 9452 3146 9452 524a 1963 3142 ac35 4a77 2d6f 4f73 c966 116f f266
  //   48*ff7f 1042 0 0 821 0 4e42 525f 535f 535f 8b3a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
endmodule

// 单周期硬布线控制器
module \单周期硬布线控制器  (
  input  [5:0] OP,
  input  [5:0] Func,
  output [3:0] ALU_OP,
  output MemToReg,
  output MemWrite,
  output ALU_SRC,
  output RegWrite,
  output SysCALL,
  output SignedExt,
  output RegDst,
  output Beq,
  output Bne,
  output JR,
  output JMP,
  output JAL,
  output LUI,
  output LH,
  output BGEZ,
  output rs,
  output rt,
  output ERET,
  output INTO,
  output INTC
);

  \运算控制器自动生成  \u_运算控制器自动生成_1  (
    .OP0(OP[0]), .OP1(OP[1]), .OP2(OP[2]), .OP3(OP[3]), .OP4(OP[4]), .OP5(OP[5]), .F0(Func[0]), .F1(Func[1]),
    .F2(Func[2]), .F3(Func[3]), .F4(Func[4]), .F5(Func[5]), .S0(ALU_OP[0]), .S1(ALU_OP[1]), .S2(ALU_OP[2]),
    .S3(ALU_OP[3]));
  \控制信号自动生成  \u_控制信号自动生成_1  (
    .OP0(OP[0]), .OP1(OP[1]), .OP2(OP[2]), .OP3(OP[3]), .OP4(OP[4]), .OP5(OP[5]), .F0(Func[0]), .F1(Func[1]),
    .F2(Func[2]), .F3(Func[3]), .F4(Func[4]), .F5(Func[5]), .MemToReg(MemToReg), .MemWrite(MemWrite),
    .ALU_SRC(ALU_SRC), .RegWrite(RegWrite), .SysCALL(SysCALL), .SignedExt(SignedExt), .RegDst(RegDst),
    .BEQ(Beq), .BNE(Bne), .JR(JR), .JUMP(JMP), .JAL(JAL), .LUI(LUI), .LH(LH), .BGEZ(BGEZ), .rs(rs), .rt(rt),
    .ERET(ERET), .INTO(INTO), .INTC(INTC));

  // Other names for the same wires on the sheet: OP_CODE[5:0] = OP

  // Notes on the sheet:
  //   运算器控制器，根据指令生成运算器功能选择信号
  //   控制信号生成，产生数据通路需要的其他控制信号
endmodule

// 运算器控制器
module \运算控制器自动生成  (
  input  OP0,
  input  OP1,
  input  OP2,
  input  OP3,
  input  OP4,
  input  OP5,
  input  F0,
  input  F1,
  input  F2,
  input  F3,
  input  F4,
  input  F5,
  output S0,
  output S1,
  output S2,
  output S3
);

  wire and_1_out, and_2_out, and_3_out, and_4_out, and_5_out, and_6_out, and_7_out, and_8_out, and_9_out,
       and_10_out, and_11_out, and_12_out, and_13_out, and_14_out, and_15_out, and_16_out, and_17_out,
       and_18_out, and_19_out, and_20_out, and_21_out, and_22_out, and_23_out, and_24_out, and_25_out,
       and_26_out, and_27_out, and_28_out, and_29_out, and_30_out, and_31_out, and_32_out, and_33_out,
       and_34_out, and_35_out, and_36_out, and_37_out, and_38_out, and_39_out, and_40_out, and_41_out,
       not_1_out, not_2_out, not_3_out, not_4_out, not_5_out, not_6_out, not_7_out, not_8_out, not_9_out,
       not_10_out, not_11_out, not_12_out, not_13_out, not_14_out, not_15_out, not_16_out, not_17_out,
       not_18_out, not_19_out, not_20_out, not_21_out, not_22_out, not_23_out, not_24_out, not_25_out,
       not_26_out, not_27_out, not_28_out, not_29_out, not_30_out, not_31_out, not_32_out, not_33_out,
       not_34_out, not_35_out, not_36_out, not_37_out, not_38_out, not_39_out, not_40_out, not_41_out,
       not_42_out, not_43_out, not_44_out, not_45_out, not_46_out, not_47_out, not_48_out, not_49_out,
       not_50_out, not_51_out, not_52_out, not_53_out, not_54_out, not_55_out, not_56_out, not_57_out,
       not_58_out, not_59_out, not_60_out, not_61_out, not_62_out, not_63_out, not_64_out, not_65_out,
       not_66_out, not_67_out, not_68_out, not_69_out, not_70_out, not_71_out, not_72_out, not_73_out,
       not_74_out, not_75_out, not_76_out, not_77_out, not_78_out, not_79_out, not_80_out, not_81_out,
       not_82_out, not_83_out, not_84_out, not_85_out, not_86_out, not_87_out, not_88_out, not_89_out,
       not_90_out, not_91_out, not_92_out, not_93_out, not_94_out, not_95_out, not_96_out, not_97_out,
       not_98_out, not_99_out, not_100_out, not_101_out, not_102_out, not_103_out, not_104_out, not_105_out,
       not_106_out, not_107_out, not_108_out, not_109_out, not_110_out, not_111_out, not_112_out,
       not_113_out, not_114_out, not_115_out, not_116_out, not_117_out, not_118_out, not_119_out,
       not_120_out, not_121_out, not_122_out, not_123_out, not_124_out, not_125_out, not_126_out,
       not_127_out, not_128_out, not_129_out, not_130_out, not_131_out, not_132_out, not_133_out,
       not_134_out, not_135_out, not_136_out, not_137_out, not_138_out, not_139_out, not_140_out,
       not_141_out, not_142_out, not_143_out, not_144_out, not_145_out, not_146_out, not_147_out,
       not_148_out, not_149_out, not_150_out, not_151_out, not_152_out, not_153_out, not_154_out,
       not_155_out, not_156_out, not_157_out, not_158_out, not_159_out, not_160_out, not_161_out,
       not_162_out, not_163_out, not_164_out, not_165_out, not_166_out, not_167_out, not_168_out,
       not_169_out, not_170_out, not_171_out, not_172_out, not_173_out, not_174_out, not_175_out,
       not_176_out, not_177_out, not_178_out, not_179_out, not_180_out, not_181_out, not_182_out,
       not_183_out, not_184_out, not_185_out, not_186_out, not_187_out, not_188_out, not_189_out,
       not_190_out, not_191_out, not_192_out, not_193_out, not_194_out, not_195_out, not_196_out,
       not_197_out, not_198_out, not_199_out, not_200_out, not_201_out, not_202_out, not_203_out,
       not_204_out, not_205_out, not_206_out, not_207_out, not_208_out, not_209_out, not_210_out,
       not_211_out, not_212_out, not_213_out, not_214_out, not_215_out, not_216_out, not_217_out,
       not_218_out, not_219_out, not_220_out, not_221_out, not_222_out, not_223_out, not_224_out,
       not_225_out, not_226_out, not_227_out, not_228_out, not_229_out, not_230_out, not_231_out,
       not_232_out, not_233_out, not_234_out, not_235_out, not_236_out, not_237_out, not_238_out,
       not_239_out, not_240_out, not_241_out, not_242_out, not_243_out, not_244_out, not_245_out,
       not_246_out, not_247_out, not_248_out, not_249_out, not_250_out, not_251_out, not_252_out,
       not_253_out, not_254_out, not_255_out, not_256_out, not_257_out, not_258_out, not_259_out,
       not_260_out, not_261_out, not_262_out, not_263_out, not_264_out, not_265_out;

  not not_1 (not_1_out, OP5);
  not not_2 (not_2_out, OP4);
  not not_3 (not_3_out, OP3);
  not not_4 (not_4_out, OP2);
  not not_5 (not_5_out, OP1);
  not not_6 (not_6_out, OP0);
  not not_7 (not_7_out, F5);
  not not_8 (not_8_out, F4);
  not not_9 (not_9_out, F3);
  not not_10 (not_10_out, F2);
  not not_11 (not_11_out, OP5);
  not not_12 (not_12_out, OP4);
  not not_13 (not_13_out, OP3);
  not not_14 (not_14_out, OP2);
  not not_15 (not_15_out, OP1);
  not not_16 (not_16_out, OP0);
  not not_17 (not_17_out, F4);
  not not_18 (not_18_out, F3);
  not not_19 (not_19_out, F2);
  not not_20 (not_20_out, F1);
  not not_21 (not_21_out, F0);
  not not_22 (not_22_out, OP5);
  not not_23 (not_23_out, OP4);
  not not_24 (not_24_out, OP3);
  not not_25 (not_25_out, OP2);
  not not_26 (not_26_out, OP1);
  not not_27 (not_27_out, OP0);
  not not_28 (not_28_out, F4);
  not not_29 (not_29_out, F3);
  not not_30 (not_30_out, F2);
  not not_31 (not_31_out, F1);
  not not_32 (not_32_out, OP5);
  not not_33 (not_33_out, OP4);
  not not_34 (not_34_out, OP3);
  not not_35 (not_35_out, OP2);
  not not_36 (not_36_out, OP1);
  not not_37 (not_37_out, OP0);
  not not_38 (not_38_out, F4);
  not not_39 (not_39_out, F3);
  not not_40 (not_40_out, F1);
  not not_41 (not_41_out, F0);
  not not_42 (not_42_out, OP5);
  not not_43 (not_43_out, OP4);
  not not_44 (not_44_out, OP3);
  not not_45 (not_45_out, OP2);
  not not_46 (not_46_out, OP1);
  not not_47 (not_47_out, OP0);
  not not_48 (not_48_out, F4);
  not not_49 (not_49_out, F2);
  not not_50 (not_50_out, F0);
  not not_51 (not_51_out, OP5);
  not not_52 (not_52_out, OP4);
  not not_53 (not_53_out, OP2);
  not not_54 (not_54_out, OP1);
  not not_55 (not_55_out, OP0);
  not not_56 (not_56_out, OP5);
  not not_57 (not_57_out, OP4);
  not not_58 (not_58_out, OP1);
  not not_59 (not_59_out, OP0);
  not not_60 (not_60_out, OP5);
  not not_61 (not_61_out, OP4);
  not not_62 (not_62_out, OP2);
  not not_63 (not_63_out, OP1);
  not not_64 (not_64_out, OP5);
  not not_65 (not_65_out, OP4);
  not not_66 (not_66_out, OP2);
  not not_67 (not_67_out, OP0);
  not not_68 (not_68_out, OP4);
  not not_69 (not_69_out, OP3);
  not not_70 (not_70_out, OP2);
  not not_71 (not_71_out, OP4);
  not not_72 (not_72_out, OP2);
  not not_73 (not_73_out, OP5);
  not not_74 (not_74_out, OP4);
  not not_75 (not_75_out, OP0);
  not not_76 (not_76_out, OP4);
  not not_77 (not_77_out, OP3);
  not not_78 (not_78_out, OP2);
  not not_79 (not_79_out, OP1);
  not not_80 (not_80_out, OP5);
  not not_81 (not_81_out, OP4);
  not not_82 (not_82_out, OP3);
  not not_83 (not_83_out, OP2);
  not not_84 (not_84_out, OP1);
  not not_85 (not_85_out, OP5);
  not not_86 (not_86_out, OP4);
  not not_87 (not_87_out, OP3);
  not not_88 (not_88_out, OP2);
  not not_89 (not_89_out, OP1);
  not not_90 (not_90_out, OP0);
  not not_91 (not_91_out, F5);
  not not_92 (not_92_out, F4);
  not not_93 (not_93_out, F3);
  not not_94 (not_94_out, F2);
  not not_95 (not_95_out, F0);
  not not_96 (not_96_out, OP5);
  not not_97 (not_97_out, OP4);
  not not_98 (not_98_out, OP3);
  not not_99 (not_99_out, OP2);
  not not_100 (not_100_out, OP1);
  not not_101 (not_101_out, OP0);
  not not_102 (not_102_out, F4);
  not not_103 (not_103_out, F3);
  not not_104 (not_104_out, F2);
  not not_105 (not_105_out, F0);
  not not_106 (not_106_out, OP5);
  not not_107 (not_107_out, OP4);
  not not_108 (not_108_out, OP3);
  not not_109 (not_109_out, OP2);
  not not_110 (not_110_out, OP1);
  not not_111 (not_111_out, OP0);
  not not_112 (not_112_out, F4);
  not not_113 (not_113_out, F3);
  not not_114 (not_114_out, F1);
  not not_115 (not_115_out, F0);
  not not_116 (not_116_out, OP5);
  not not_117 (not_117_out, OP4);
  not not_118 (not_118_out, OP3);
  not not_119 (not_119_out, OP2);
  not not_120 (not_120_out, OP1);
  not not_121 (not_121_out, OP0);
  not not_122 (not_122_out, F4);
  not not_123 (not_123_out, F3);
  not not_124 (not_124_out, OP5);
  not not_125 (not_125_out, OP4);
  not not_126 (not_126_out, OP3);
  not not_127 (not_127_out, OP2);
  not not_128 (not_128_out, OP1);
  not not_129 (not_129_out, OP0);
  not not_130 (not_130_out, F4);
  not not_131 (not_131_out, F2);
  not not_132 (not_132_out, F0);
  not not_133 (not_133_out, OP5);
  not not_134 (not_134_out, OP4);
  not not_135 (not_135_out, OP1);
  not not_136 (not_136_out, OP0);
  not not_137 (not_137_out, OP5);
  not not_138 (not_138_out, OP4);
  not not_139 (not_139_out, OP2);
  not not_140 (not_140_out, OP0);
  not not_141 (not_141_out, OP5);
  not not_142 (not_142_out, OP4);
  not not_143 (not_143_out, OP3);
  not not_144 (not_144_out, OP2);
  not not_145 (not_145_out, OP1);
  not not_146 (not_146_out, OP5);
  not not_147 (not_147_out, OP4);
  not not_148 (not_148_out, OP3);
  not not_149 (not_149_out, OP2);
  not not_150 (not_150_out, OP1);
  not not_151 (not_151_out, OP0);
  not not_152 (not_152_out, F4);
  not not_153 (not_153_out, F3);
  not not_154 (not_154_out, F2);
  not not_155 (not_155_out, F1);
  not not_156 (not_156_out, F0);
  not not_157 (not_157_out, OP5);
  not not_158 (not_158_out, OP4);
  not not_159 (not_159_out, OP3);
  not not_160 (not_160_out, OP2);
  not not_161 (not_161_out, OP1);
  not not_162 (not_162_out, OP0);
  not not_163 (not_163_out, F4);
  not not_164 (not_164_out, F3);
  not not_165 (not_165_out, F2);
  not not_166 (not_166_out, F1);
  not not_167 (not_167_out, OP5);
  not not_168 (not_168_out, OP4);
  not not_169 (not_169_out, OP3);
  not not_170 (not_170_out, OP2);
  not not_171 (not_171_out, OP1);
  not not_172 (not_172_out, OP0);
  not not_173 (not_173_out, F4);
  not not_174 (not_174_out, F3);
  not not_175 (not_175_out, F2);
  not not_176 (not_176_out, F0);
  not not_177 (not_177_out, OP5);
  not not_178 (not_178_out, OP4);
  not not_179 (not_179_out, OP3);
  not not_180 (not_180_out, OP2);
  not not_181 (not_181_out, OP1);
  not not_182 (not_182_out, OP0);
  not not_183 (not_183_out, F4);
  not not_184 (not_184_out, F3);
  not not_185 (not_185_out, F1);
  not not_186 (not_186_out, F0);
  not not_187 (not_187_out, OP5);
  not not_188 (not_188_out, OP4);
  not not_189 (not_189_out, OP3);
  not not_190 (not_190_out, OP2);
  not not_191 (not_191_out, OP1);
  not not_192 (not_192_out, OP0);
  not not_193 (not_193_out, F4);
  not not_194 (not_194_out, F2);
  not not_195 (not_195_out, OP5);
  not not_196 (not_196_out, OP4);
  not not_197 (not_197_out, OP2);
  not not_198 (not_198_out, OP1);
  not not_199 (not_199_out, OP0);
  not not_200 (not_200_out, OP5);
  not not_201 (not_201_out, OP4);
  not not_202 (not_202_out, OP1);
  not not_203 (not_203_out, OP0);
  not not_204 (not_204_out, OP5);
  not not_205 (not_205_out, OP4);
  not not_206 (not_206_out, OP2);
  not not_207 (not_207_out, OP1);
  not not_208 (not_208_out, OP4);
  not not_209 (not_209_out, OP3);
  not not_210 (not_210_out, OP2);
  not not_211 (not_211_out, OP4);
  not not_212 (not_212_out, OP2);
  not not_213 (not_213_out, OP4);
  not not_214 (not_214_out, OP3);
  not not_215 (not_215_out, OP2);
  not not_216 (not_216_out, OP1);
  not not_217 (not_217_out, OP5);
  not not_218 (not_218_out, OP4);
  not not_219 (not_219_out, OP3);
  not not_220 (not_220_out, OP2);
  not not_221 (not_221_out, OP1);
  not not_222 (not_222_out, OP0);
  not not_223 (not_223_out, F4);
  not not_224 (not_224_out, F3);
  not not_225 (not_225_out, F1);
  not not_226 (not_226_out, OP5);
  not not_227 (not_227_out, OP4);
  not not_228 (not_228_out, OP3);
  not not_229 (not_229_out, OP2);
  not not_230 (not_230_out, OP1);
  not not_231 (not_231_out, OP0);
  not not_232 (not_232_out, F4);
  not not_233 (not_233_out, F3);
  not not_234 (not_234_out, OP5);
  not not_235 (not_235_out, OP4);
  not not_236 (not_236_out, OP3);
  not not_237 (not_237_out, OP2);
  not not_238 (not_238_out, OP1);
  not not_239 (not_239_out, OP0);
  not not_240 (not_240_out, F4);
  not not_241 (not_241_out, F2);
  not not_242 (not_242_out, F0);
  not not_243 (not_243_out, OP5);
  not not_244 (not_244_out, OP4);
  not not_245 (not_245_out, OP3);
  not not_246 (not_246_out, OP2);
  not not_247 (not_247_out, OP1);
  not not_248 (not_248_out, OP0);
  not not_249 (not_249_out, F4);
  not not_250 (not_250_out, F2);
  not not_251 (not_251_out, OP5);
  not not_252 (not_252_out, OP4);
  not not_253 (not_253_out, OP2);
  not not_254 (not_254_out, OP0);
  not not_255 (not_255_out, OP5);
  not not_256 (not_256_out, OP4);
  not not_257 (not_257_out, OP1);
  not not_258 (not_258_out, OP5);
  not not_259 (not_259_out, OP4);
  not not_260 (not_260_out, OP0);
  not not_261 (not_261_out, OP5);
  not not_262 (not_262_out, OP4);
  not not_263 (not_263_out, OP3);
  not not_264 (not_264_out, OP2);
  not not_265 (not_265_out, OP1);
  and and_1 (and_1_out, not_1_out, not_2_out, not_3_out, not_4_out, not_5_out, not_6_out, not_7_out, not_8_out, not_9_out, not_10_out, F1, F0);
  and and_2 (and_2_out, not_11_out, not_12_out, not_13_out, not_14_out, not_15_out, not_16_out, F5, not_17_out, not_18_out, not_19_out, not_20_out, not_21_out);
  and and_3 (and_3_out, not_22_out, not_23_out, not_24_out, not_25_out, not_26_out, not_27_out, F5, not_28_out, not_29_out, not_30_out, not_31_out, F0);
  and and_4 (and_4_out, not_32_out, not_33_out, not_34_out, not_35_out, not_36_out, not_37_out, F5, not_38_out, not_39_out, F2, not_40_out, not_41_out);
  and and_5 (and_5_out, not_42_out, not_43_out, not_44_out, not_45_out, not_46_out, not_47_out, F5, not_48_out, F3, not_49_out, F1, not_50_out);
  and and_6 (and_6_out, not_51_out, not_52_out, OP3, not_53_out, not_54_out, not_55_out);
  and and_7 (and_7_out, not_56_out, not_57_out, OP3, OP2, not_58_out, not_59_out);
  and and_8 (and_8_out, not_60_out, not_61_out, OP3, not_62_out, not_63_out, OP0);
  and and_9 (and_9_out, not_64_out, not_65_out, OP3, not_66_out, OP1, not_67_out);
  and and_10 (and_10_out, OP5, not_68_out, not_69_out, not_70_out, OP1, OP0);
  and and_11 (and_11_out, OP5, not_71_out, OP3, not_72_out, OP1, OP0);
  and and_12 (and_12_out, not_73_out, not_74_out, OP3, OP2, OP1, not_75_out);
  and and_13 (and_13_out, OP5, not_76_out, not_77_out, not_78_out, not_79_out, OP0);
  and and_14 (and_14_out, not_80_out, not_81_out, not_82_out, not_83_out, not_84_out, OP0);
  and and_15 (and_15_out, not_85_out, not_86_out, not_87_out, not_88_out, not_89_out, not_90_out, not_91_out, not_92_out, not_93_out, not_94_out, F1, not_95_out);
  and and_16 (and_16_out, not_96_out, not_97_out, not_98_out, not_99_out, not_100_out, not_101_out, F5, not_102_out, not_103_out, not_104_out, F1, not_105_out);
  and and_17 (and_17_out, not_106_out, not_107_out, not_108_out, not_109_out, not_110_out, not_111_out, F5, not_112_out, not_113_out, F2, not_114_out, not_115_out);
  and and_18 (and_18_out, not_116_out, not_117_out, not_118_out, not_119_out, not_120_out, not_121_out, F5, not_122_out, not_123_out, F2, F1, F0);
  and and_19 (and_19_out, not_124_out, not_125_out, not_126_out, not_127_out, not_128_out, not_129_out, F5, not_130_out, F3, not_131_out, F1, not_132_out);
  and and_20 (and_20_out, not_133_out, not_134_out, OP3, OP2, not_135_out, not_136_out);
  and and_21 (and_21_out, not_137_out, not_138_out, OP3, not_139_out, OP1, not_140_out);
  and and_22 (and_22_out, not_141_out, not_142_out, not_143_out, not_144_out, not_145_out, OP0);
  and and_23 (and_23_out, not_146_out, not_147_out, not_148_out, not_149_out, not_150_out, not_151_out, F5, not_152_out, not_153_out, not_154_out, not_155_out, not_156_out);
  and and_24 (and_24_out, not_157_out, not_158_out, not_159_out, not_160_out, not_161_out, not_162_out, F5, not_163_out, not_164_out, not_165_out, not_166_out, F0);
  and and_25 (and_25_out, not_167_out, not_168_out, not_169_out, not_170_out, not_171_out, not_172_out, F5, not_173_out, not_174_out, not_175_out, F1, not_176_out);
  and and_26 (and_26_out, not_177_out, not_178_out, not_179_out, not_180_out, not_181_out, not_182_out, F5, not_183_out, not_184_out, F2, not_185_out, not_186_out);
  and and_27 (and_27_out, not_187_out, not_188_out, not_189_out, not_190_out, not_191_out, not_192_out, F5, not_193_out, F3, not_194_out, F1, F0);
  and and_28 (and_28_out, not_195_out, not_196_out, OP3, not_197_out, not_198_out, not_199_out);
  and and_29 (and_29_out, not_200_out, not_201_out, OP3, OP2, not_202_out, not_203_out);
  and and_30 (and_30_out, not_204_out, not_205_out, OP3, not_206_out, not_207_out, OP0);
  and and_31 (and_31_out, OP5, not_208_out, not_209_out, not_210_out, OP1, OP0);
  and and_32 (and_32_out, OP5, not_211_out, OP3, not_212_out, OP1, OP0);
  and and_33 (and_33_out, OP5, not_213_out, not_214_out, not_215_out, not_216_out, OP0);
  and and_34 (and_34_out, not_217_out, not_218_out, not_219_out, not_220_out, not_221_out, not_222_out, F5, not_223_out, not_224_out, F2, not_225_out, F0);
  and and_35 (and_35_out, not_226_out, not_227_out, not_228_out, not_229_out, not_230_out, not_231_out, F5, not_232_out, not_233_out, F2, F1, F0);
  and and_36 (and_36_out, not_234_out, not_235_out, not_236_out, not_237_out, not_238_out, not_239_out, F5, not_240_out, F3, not_241_out, F1, not_242_out);
  and and_37 (and_37_out, not_243_out, not_244_out, not_245_out, not_246_out, not_247_out, not_248_out, F5, not_249_out, F3, not_250_out, F1, F0);
  and and_38 (and_38_out, not_251_out, not_252_out, OP3, not_253_out, OP1, not_254_out);
  and and_39 (and_39_out, not_255_out, not_256_out, OP3, OP2, not_257_out, OP0);
  and and_40 (and_40_out, not_258_out, not_259_out, OP3, OP2, OP1, not_260_out);
  and and_41 (and_41_out, not_261_out, not_262_out, not_263_out, not_264_out, not_265_out, OP0);
  or or_1 (S1, and_15_out, and_16_out, and_17_out, and_18_out, and_19_out, and_20_out, and_21_out, and_22_out);
  or or_2 (S2, and_23_out, and_24_out, and_25_out, and_26_out, and_27_out, and_28_out, and_29_out, and_30_out, and_31_out, and_32_out, and_33_out);
  or or_3 (S3, and_34_out, and_35_out, and_36_out, and_37_out, and_38_out, and_39_out, and_40_out, and_41_out);
  or or_4 (S0, and_1_out, and_2_out, and_3_out, and_4_out, and_5_out, and_6_out, and_7_out, and_8_out, and_9_out, and_10_out, and_11_out, and_12_out, and_13_out, and_14_out);
endmodule

// 控制信号生成
module \控制信号自动生成  (
  input  OP0,
  input  OP1,
  input  OP2,
  input  OP3,
  input  OP4,
  input  OP5,
  input  F0,
  input  F1,
  input  F2,
  input  F3,
  input  F4,
  input  F5,
  output MemToReg,
  output MemWrite,
  output ALU_SRC,
  output RegWrite,
  output SysCALL,
  output SignedExt,
  output RegDst,
  output BEQ,
  output BNE,
  output JR,
  output JUMP,
  output JAL,
  output LUI,
  output LH,
  output BGEZ,
  output rs,
  output rt,
  output ERET,
  output INTO,
  output INTC
);

  wire and_3_out, and_4_out, and_5_out, and_6_out, and_7_out, and_8_out, and_9_out, and_10_out, and_11_out,
       and_12_out, and_13_out, and_14_out, and_15_out, and_16_out, and_17_out, and_19_out, and_20_out,
       and_21_out, and_22_out, and_23_out, and_24_out, and_25_out, and_26_out, and_27_out, and_31_out,
       and_32_out, and_37_out, and_38_out, and_39_out, and_40_out, and_41_out, and_42_out, and_43_out,
       and_44_out, and_45_out, and_46_out, and_47_out, and_48_out, and_49_out, and_50_out, and_51_out,
       and_52_out, and_53_out, and_54_out, and_55_out, and_56_out, not_1_out, not_2_out, not_3_out,
       not_4_out, not_5_out, not_6_out, not_7_out, not_8_out, not_9_out, not_10_out, not_11_out, not_12_out,
       not_13_out, not_14_out, not_15_out, not_16_out, not_17_out, not_18_out, not_19_out, not_20_out,
       not_21_out, not_22_out, not_23_out, not_24_out, not_25_out, not_26_out, not_27_out, not_28_out,
       not_29_out, not_30_out, not_31_out, not_32_out, not_33_out, not_34_out, not_35_out, not_36_out,
       not_37_out, not_38_out, not_39_out, not_40_out, not_41_out, not_42_out, not_43_out, not_44_out,
       not_45_out, not_46_out, not_47_out, not_48_out, not_49_out, not_50_out, not_51_out, not_52_out,
       not_53_out, not_54_out, not_55_out, not_56_out, not_57_out, not_58_out, not_59_out, not_60_out,
       not_61_out, not_62_out, not_63_out, not_64_out, not_65_out, not_66_out, not_67_out, not_68_out,
       not_69_out, not_70_out, not_71_out, not_72_out, not_73_out, not_74_out, not_75_out, not_76_out,
       not_77_out, not_78_out, not_79_out, not_80_out, not_81_out, not_82_out, not_83_out, not_84_out,
       not_85_out, not_86_out, not_87_out, not_88_out, not_89_out, not_90_out, not_91_out, not_92_out,
       not_93_out, not_94_out, not_95_out, not_96_out, not_97_out, not_98_out, not_99_out, not_100_out,
       not_101_out, not_102_out, not_103_out, not_104_out, not_105_out, not_106_out, not_107_out,
       not_108_out, not_109_out, not_110_out, not_111_out, not_112_out, not_113_out, not_114_out,
       not_115_out, not_116_out, not_117_out, not_118_out, not_119_out, not_120_out, not_121_out,
       not_122_out, not_123_out, not_124_out, not_125_out, not_126_out, not_127_out, not_128_out,
       not_129_out, not_130_out, not_131_out, not_132_out, not_133_out, not_134_out, not_135_out,
       not_136_out, not_137_out, not_138_out, not_139_out, not_140_out, not_141_out, not_142_out,
       not_143_out, not_144_out, not_145_out, not_146_out, not_147_out, not_148_out, not_149_out,
       not_150_out, not_151_out, not_152_out, not_153_out, not_154_out, not_155_out, not_156_out,
       not_157_out, not_158_out, not_159_out, not_160_out, not_161_out, not_162_out, not_163_out,
       not_164_out, not_165_out, not_166_out, not_167_out, not_168_out, not_169_out, not_170_out,
       not_171_out, not_172_out, not_173_out, not_174_out, not_175_out, not_176_out, not_177_out,
       not_178_out, not_179_out, not_180_out, not_181_out, not_182_out, not_183_out, not_184_out,
       not_185_out, not_186_out, not_187_out, not_188_out, not_189_out, not_190_out, not_191_out,
       not_192_out, not_193_out, not_194_out, not_195_out, not_196_out, not_197_out, not_198_out,
       not_199_out, not_200_out, not_201_out, not_202_out, not_203_out, not_204_out, not_205_out,
       not_206_out, not_207_out, not_208_out, not_209_out, not_210_out, not_211_out, not_212_out,
       not_213_out, not_214_out, not_215_out, not_216_out, not_217_out, not_218_out, not_219_out,
       not_220_out, not_221_out, not_222_out, not_223_out, not_224_out, not_225_out, not_226_out,
       not_227_out, not_228_out, not_229_out, not_230_out, not_231_out, not_232_out, not_233_out,
       not_234_out, not_235_out, not_236_out, not_237_out, not_238_out, not_239_out, not_240_out,
       not_241_out, not_242_out, not_243_out, not_244_out, not_245_out, not_246_out, not_247_out,
       not_248_out, not_249_out, not_250_out, not_251_out, not_252_out, not_253_out, not_254_out,
       not_255_out, not_256_out, not_257_out, not_258_out, not_259_out, not_260_out, not_261_out,
       not_262_out, not_263_out, not_264_out, not_265_out, not_266_out, not_267_out, not_268_out,
       not_269_out, not_270_out, not_271_out, not_272_out, not_273_out, not_274_out, not_275_out,
       not_276_out, not_277_out, not_278_out, not_279_out, not_280_out, not_281_out, not_282_out,
       not_283_out, not_284_out, not_285_out, not_286_out, not_287_out, not_288_out, not_289_out,
       not_290_out, not_291_out, not_292_out, not_293_out, not_294_out, not_295_out, not_296_out,
       not_297_out, not_298_out, not_299_out, not_300_out, not_301_out, not_302_out, not_303_out,
       not_304_out, not_305_out, not_306_out, not_307_out, not_308_out, not_309_out, not_310_out,
       not_311_out, not_312_out, not_313_out, not_314_out, not_315_out, not_316_out, not_317_out,
       not_318_out, not_319_out, not_320_out, not_321_out, not_322_out, not_323_out, not_324_out;

  not not_1 (not_1_out, OP2);
  not not_2 (not_2_out, OP3);
  not not_3 (not_3_out, OP4);
  not not_4 (not_4_out, OP2);
  not not_5 (not_5_out, OP4);
  not not_6 (not_6_out, OP0);
  not not_7 (not_7_out, OP4);
  not not_8 (not_8_out, OP5);
  not not_9 (not_9_out, OP1);
  not not_10 (not_10_out, OP4);
  not not_11 (not_11_out, OP5);
  not not_12 (not_12_out, OP4);
  not not_13 (not_13_out, OP5);
  not not_14 (not_14_out, OP2);
  not not_15 (not_15_out, OP3);
  not not_16 (not_16_out, OP4);
  not not_17 (not_17_out, OP2);
  not not_18 (not_18_out, OP4);
  not not_19 (not_19_out, OP0);
  not not_20 (not_20_out, OP1);
  not not_21 (not_21_out, OP2);
  not not_22 (not_22_out, OP4);
  not not_23 (not_23_out, OP5);
  not not_24 (not_24_out, F0);
  not not_25 (not_25_out, F2);
  not not_26 (not_26_out, F3);
  not not_27 (not_27_out, F4);
  not not_28 (not_28_out, OP0);
  not not_29 (not_29_out, OP1);
  not not_30 (not_30_out, OP2);
  not not_31 (not_31_out, OP4);
  not not_32 (not_32_out, OP5);
  not not_33 (not_33_out, F1);
  not not_34 (not_34_out, F3);
  not not_35 (not_35_out, F4);
  not not_36 (not_36_out, OP0);
  not not_37 (not_37_out, OP1);
  not not_38 (not_38_out, OP2);
  not not_39 (not_39_out, OP4);
  not not_40 (not_40_out, OP5);
  not not_41 (not_41_out, F2);
  not not_42 (not_42_out, F3);
  not not_43 (not_43_out, F4);
  not not_44 (not_44_out, F5);
  not not_45 (not_45_out, OP0);
  not not_46 (not_46_out, OP1);
  not not_47 (not_47_out, OP2);
  not not_48 (not_48_out, OP4);
  not not_49 (not_49_out, OP5);
  not not_50 (not_50_out, F2);
  not not_51 (not_51_out, F4);
  not not_52 (not_52_out, OP0);
  not not_53 (not_53_out, OP1);
  not not_54 (not_54_out, OP2);
  not not_55 (not_55_out, OP4);
  not not_56 (not_56_out, OP5);
  not not_57 (not_57_out, F3);
  not not_58 (not_58_out, F4);
  not not_59 (not_59_out, OP0);
  not not_60 (not_60_out, OP4);
  not not_61 (not_61_out, OP5);
  not not_62 (not_62_out, OP1);
  not not_63 (not_63_out, OP4);
  not not_64 (not_64_out, OP5);
  not not_65 (not_65_out, OP4);
  not not_66 (not_66_out, OP5);
  not not_67 (not_67_out, OP2);
  not not_68 (not_68_out, OP3);
  not not_69 (not_69_out, OP4);
  not not_70 (not_70_out, OP2);
  not not_71 (not_71_out, OP3);
  not not_72 (not_72_out, OP4);
  not not_73 (not_73_out, OP0);
  not not_74 (not_74_out, OP1);
  not not_75 (not_75_out, OP2);
  not not_76 (not_76_out, OP3);
  not not_77 (not_77_out, OP4);
  not not_78 (not_78_out, OP5);
  not not_79 (not_79_out, F0);
  not not_80 (not_80_out, F1);
  not not_81 (not_81_out, F4);
  not not_82 (not_82_out, F5);
  not not_83 (not_83_out, OP0);
  not not_84 (not_84_out, OP2);
  not not_85 (not_85_out, OP4);
  not not_86 (not_86_out, OP5);
  not not_87 (not_87_out, OP1);
  not not_88 (not_88_out, OP2);
  not not_89 (not_89_out, OP4);
  not not_90 (not_90_out, OP5);
  not not_91 (not_91_out, OP2);
  not not_92 (not_92_out, OP3);
  not not_93 (not_93_out, OP4);
  not not_94 (not_94_out, OP2);
  not not_95 (not_95_out, OP4);
  not not_96 (not_96_out, OP0);
  not not_97 (not_97_out, OP1);
  not not_98 (not_98_out, OP2);
  not not_99 (not_99_out, OP3);
  not not_100 (not_100_out, OP4);
  not not_101 (not_101_out, OP5);
  not not_102 (not_102_out, F0);
  not not_103 (not_103_out, F2);
  not not_104 (not_104_out, F3);
  not not_105 (not_105_out, F4);
  not not_106 (not_106_out, OP0);
  not not_107 (not_107_out, OP1);
  not not_108 (not_108_out, OP2);
  not not_109 (not_109_out, OP3);
  not not_110 (not_110_out, OP4);
  not not_111 (not_111_out, OP5);
  not not_112 (not_112_out, F1);
  not not_113 (not_113_out, F3);
  not not_114 (not_114_out, F4);
  not not_115 (not_115_out, OP0);
  not not_116 (not_116_out, OP1);
  not not_117 (not_117_out, OP2);
  not not_118 (not_118_out, OP3);
  not not_119 (not_119_out, OP4);
  not not_120 (not_120_out, OP5);
  not not_121 (not_121_out, F2);
  not not_122 (not_122_out, F3);
  not not_123 (not_123_out, F4);
  not not_124 (not_124_out, F5);
  not not_125 (not_125_out, OP0);
  not not_126 (not_126_out, OP1);
  not not_127 (not_127_out, OP2);
  not not_128 (not_128_out, OP3);
  not not_129 (not_129_out, OP4);
  not not_130 (not_130_out, OP5);
  not not_131 (not_131_out, F2);
  not not_132 (not_132_out, F4);
  not not_133 (not_133_out, OP0);
  not not_134 (not_134_out, OP1);
  not not_135 (not_135_out, OP2);
  not not_136 (not_136_out, OP3);
  not not_137 (not_137_out, OP4);
  not not_138 (not_138_out, OP5);
  not not_139 (not_139_out, F3);
  not not_140 (not_140_out, F4);
  not not_141 (not_141_out, OP0);
  not not_142 (not_142_out, OP1);
  not not_143 (not_143_out, OP3);
  not not_144 (not_144_out, OP4);
  not not_145 (not_145_out, OP5);
  not not_146 (not_146_out, OP1);
  not not_147 (not_147_out, OP3);
  not not_148 (not_148_out, OP4);
  not not_149 (not_149_out, OP5);
  not not_150 (not_150_out, OP0);
  not not_151 (not_151_out, OP1);
  not not_152 (not_152_out, OP2);
  not not_153 (not_153_out, OP3);
  not not_154 (not_154_out, OP4);
  not not_155 (not_155_out, OP5);
  not not_156 (not_156_out, F0);
  not not_157 (not_157_out, F1);
  not not_158 (not_158_out, F2);
  not not_159 (not_159_out, F4);
  not not_160 (not_160_out, F5);
  not not_161 (not_161_out, OP0);
  not not_162 (not_162_out, OP2);
  not not_163 (not_163_out, OP3);
  not not_164 (not_164_out, OP4);
  not not_165 (not_165_out, OP5);
  not not_166 (not_166_out, F0);
  not not_167 (not_167_out, F1);
  not not_168 (not_168_out, F2);
  not not_169 (not_169_out, F4);
  not not_170 (not_170_out, F5);
  not not_171 (not_171_out, OP2);
  not not_172 (not_172_out, OP3);
  not not_173 (not_173_out, OP4);
  not not_174 (not_174_out, OP5);
  not not_175 (not_175_out, OP2);
  not not_176 (not_176_out, OP3);
  not not_177 (not_177_out, OP4);
  not not_178 (not_178_out, OP5);
  not not_179 (not_179_out, OP4);
  not not_180 (not_180_out, OP5);
  not not_181 (not_181_out, OP1);
  not not_182 (not_182_out, OP2);
  not not_183 (not_183_out, OP3);
  not not_184 (not_184_out, OP4);
  not not_185 (not_185_out, OP1);
  not not_186 (not_186_out, OP2);
  not not_187 (not_187_out, OP3);
  not not_188 (not_188_out, OP4);
  not not_189 (not_189_out, OP5);
  not not_190 (not_190_out, OP1);
  not not_191 (not_191_out, OP4);
  not not_192 (not_192_out, OP5);
  not not_193 (not_193_out, F0);
  not not_194 (not_194_out, F2);
  not not_195 (not_195_out, F3);
  not not_196 (not_196_out, F4);
  not not_197 (not_197_out, OP1);
  not not_198 (not_198_out, OP4);
  not not_199 (not_199_out, OP5);
  not not_200 (not_200_out, F1);
  not not_201 (not_201_out, F3);
  not not_202 (not_202_out, F4);
  not not_203 (not_203_out, OP1);
  not not_204 (not_204_out, OP4);
  not not_205 (not_205_out, OP5);
  not not_206 (not_206_out, F0);
  not not_207 (not_207_out, F1);
  not not_208 (not_208_out, F4);
  not not_209 (not_209_out, F5);
  not not_210 (not_210_out, OP1);
  not not_211 (not_211_out, OP4);
  not not_212 (not_212_out, OP5);
  not not_213 (not_213_out, F2);
  not not_214 (not_214_out, F4);
  not not_215 (not_215_out, OP1);
  not not_216 (not_216_out, OP4);
  not not_217 (not_217_out, OP5);
  not not_218 (not_218_out, F3);
  not not_219 (not_219_out, F4);
  not not_220 (not_220_out, OP0);
  not not_221 (not_221_out, OP4);
  not not_222 (not_222_out, OP5);
  not not_223 (not_223_out, OP1);
  not not_224 (not_224_out, OP4);
  not not_225 (not_225_out, OP5);
  not not_226 (not_226_out, OP1);
  not not_227 (not_227_out, OP2);
  not not_228 (not_228_out, OP3);
  not not_229 (not_229_out, OP4);
  not not_230 (not_230_out, OP1);
  not not_231 (not_231_out, OP4);
  not not_232 (not_232_out, OP5);
  not not_233 (not_233_out, OP2);
  not not_234 (not_234_out, OP4);
  not not_235 (not_235_out, OP0);
  not not_236 (not_236_out, OP1);
  not not_237 (not_237_out, OP3);
  not not_238 (not_238_out, OP4);
  not not_239 (not_239_out, OP5);
  not not_240 (not_240_out, F0);
  not not_241 (not_241_out, F2);
  not not_242 (not_242_out, F3);
  not not_243 (not_243_out, F4);
  not not_244 (not_244_out, OP0);
  not not_245 (not_245_out, OP1);
  not not_246 (not_246_out, OP3);
  not not_247 (not_247_out, OP4);
  not not_248 (not_248_out, OP5);
  not not_249 (not_249_out, F1);
  not not_250 (not_250_out, F3);
  not not_251 (not_251_out, F4);
  not not_252 (not_252_out, OP0);
  not not_253 (not_253_out, OP1);
  not not_254 (not_254_out, OP3);
  not not_255 (not_255_out, OP4);
  not not_256 (not_256_out, OP5);
  not not_257 (not_257_out, F0);
  not not_258 (not_258_out, F1);
  not not_259 (not_259_out, F4);
  not not_260 (not_260_out, F5);
  not not_261 (not_261_out, OP0);
  not not_262 (not_262_out, OP1);
  not not_263 (not_263_out, OP3);
  not not_264 (not_264_out, OP4);
  not not_265 (not_265_out, OP5);
  not not_266 (not_266_out, F2);
  not not_267 (not_267_out, F3);
  not not_268 (not_268_out, F4);
  not not_269 (not_269_out, F5);
  not not_270 (not_270_out, OP0);
  not not_271 (not_271_out, OP1);
  not not_272 (not_272_out, OP3);
  not not_273 (not_273_out, OP4);
  not not_274 (not_274_out, OP5);
  not not_275 (not_275_out, F2);
  not not_276 (not_276_out, F4);
  not not_277 (not_277_out, OP0);
  not not_278 (not_278_out, OP1);
  not not_279 (not_279_out, OP3);
  not not_280 (not_280_out, OP4);
  not not_281 (not_281_out, OP5);
  not not_282 (not_282_out, F3);
  not not_283 (not_283_out, F4);
  not not_284 (not_284_out, OP1);
  not not_285 (not_285_out, OP3);
  not not_286 (not_286_out, OP4);
  not not_287 (not_287_out, OP5);
  not not_288 (not_288_out, OP2);
  not not_289 (not_289_out, OP3);
  not not_290 (not_290_out, OP4);
  not not_291 (not_291_out, OP2);
  not not_292 (not_292_out, OP4);
  not not_293 (not_293_out, OP4);
  not not_294 (not_294_out, OP5);
  not not_295 (not_295_out, OP0);
  not not_296 (not_296_out, OP1);
  not not_297 (not_297_out, OP2);
  not not_298 (not_298_out, OP3);
  not not_299 (not_299_out, OP5);
  not not_300 (not_300_out, F0);
  not not_301 (not_301_out, F1);
  not not_302 (not_302_out, F2);
  not not_303 (not_303_out, F5);
  not not_304 (not_304_out, OP5);
  not not_305 (not_305_out, OP3);
  not not_306 (not_306_out, OP2);
  not not_307 (not_307_out, OP1);
  not not_308 (not_308_out, OP0);
  not not_309 (not_309_out, F5);
  not not_310 (not_310_out, F4);
  not not_311 (not_311_out, F3);
  not not_312 (not_312_out, F2);
  not not_313 (not_313_out, F1);
  not not_314 (not_314_out, F0);
  not not_315 (not_315_out, OP5);
  not not_316 (not_316_out, OP3);
  not not_317 (not_317_out, OP2);
  not not_318 (not_318_out, OP1);
  not not_319 (not_319_out, OP0);
  not not_320 (not_320_out, F5);
  not not_321 (not_321_out, F4);
  not not_322 (not_322_out, F3);
  not not_323 (not_323_out, F1);
  not not_324 (not_324_out, F0);
  and and_1 (MemToReg, OP0, not_1_out, not_2_out, not_3_out, OP5);
  and and_2 (MemWrite, OP0, OP1, not_4_out, OP3, not_5_out, OP5);
  and and_3 (and_3_out, not_6_out, OP3, not_7_out, not_8_out);
  and and_4 (and_4_out, not_9_out, OP3, not_10_out, not_11_out);
  and and_5 (and_5_out, OP2, OP3, not_12_out, not_13_out);
  and and_6 (and_6_out, OP0, not_14_out, not_15_out, not_16_out, OP5);
  and and_7 (and_7_out, OP0, OP1, not_17_out, not_18_out, OP5);
  and and_8 (and_8_out, not_19_out, not_20_out, not_21_out, not_22_out, not_23_out, not_24_out, not_25_out, not_26_out, not_27_out);
  and and_9 (and_9_out, not_28_out, not_29_out, not_30_out, not_31_out, not_32_out, not_33_out, not_34_out, not_35_out, F5);
  and and_10 (and_10_out, not_36_out, not_37_out, not_38_out, not_39_out, not_40_out, F1, not_41_out, not_42_out, not_43_out, not_44_out);
  and and_11 (and_11_out, not_45_out, not_46_out, not_47_out, not_48_out, not_49_out, F1, not_50_out, F3, not_51_out, F5);
  and and_12 (and_12_out, not_52_out, not_53_out, not_54_out, not_55_out, not_56_out, F0, F2, not_57_out, not_58_out, F5);
  and and_13 (and_13_out, not_59_out, OP3, not_60_out, not_61_out);
  and and_14 (and_14_out, not_62_out, OP3, not_63_out, not_64_out);
  and and_15 (and_15_out, OP2, OP3, not_65_out, not_66_out);
  and and_16 (and_16_out, OP0, not_67_out, not_68_out, not_69_out, OP5);
  and and_17 (and_17_out, OP0, OP1, not_70_out, not_71_out, not_72_out);
  and and_18 (SysCALL, not_73_out, not_74_out, not_75_out, not_76_out, not_77_out, not_78_out, not_79_out, not_80_out, F2, F3, not_81_out, not_82_out);
  and and_19 (and_19_out, not_83_out, not_84_out, OP3, not_85_out, not_86_out);
  and and_20 (and_20_out, not_87_out, not_88_out, OP3, not_89_out, not_90_out);
  and and_21 (and_21_out, OP0, not_91_out, not_92_out, not_93_out, OP5);
  and and_22 (and_22_out, OP0, OP1, not_94_out, not_95_out, OP5);
  and and_23 (and_23_out, not_96_out, not_97_out, not_98_out, not_99_out, not_100_out, not_101_out, not_102_out, not_103_out, not_104_out, not_105_out);
  and and_24 (and_24_out, not_106_out, not_107_out, not_108_out, not_109_out, not_110_out, not_111_out, not_112_out, not_113_out, not_114_out, F5);
  and and_25 (and_25_out, not_115_out, not_116_out, not_117_out, not_118_out, not_119_out, not_120_out, F1, not_121_out, not_122_out, not_123_out, not_124_out);
  and and_26 (and_26_out, not_125_out, not_126_out, not_127_out, not_128_out, not_129_out, not_130_out, F1, not_131_out, F3, not_132_out, F5);
  and and_27 (and_27_out, not_133_out, not_134_out, not_135_out, not_136_out, not_137_out, not_138_out, F0, F2, not_139_out, not_140_out, F5);
  and and_28 (BEQ, not_141_out, not_142_out, OP2, not_143_out, not_144_out, not_145_out);
  and and_29 (BNE, OP0, not_146_out, OP2, not_147_out, not_148_out, not_149_out);
  and and_30 (JR, not_150_out, not_151_out, not_152_out, not_153_out, not_154_out, not_155_out, not_156_out, not_157_out, not_158_out, F3, not_159_out, not_160_out);
  and and_31 (and_31_out, not_161_out, not_162_out, not_163_out, not_164_out, not_165_out, not_166_out, not_167_out, not_168_out, F3, not_169_out, not_170_out);
  and and_32 (and_32_out, OP1, not_171_out, not_172_out, not_173_out, not_174_out);
  and and_33 (JAL, OP0, OP1, not_175_out, not_176_out, not_177_out, not_178_out);
  and and_34 (LUI, OP0, OP1, OP2, OP3, not_179_out, not_180_out);
  and and_35 (LH, OP0, not_181_out, not_182_out, not_183_out, not_184_out, OP5);
  and and_36 (BGEZ, OP0, not_185_out, not_186_out, not_187_out, not_188_out, not_189_out);
  and and_37 (and_37_out, not_190_out, not_191_out, not_192_out, not_193_out, not_194_out, not_195_out, not_196_out, F5);
  and and_38 (and_38_out, not_197_out, not_198_out, not_199_out, not_200_out, not_201_out, not_202_out, F5);
  and and_39 (and_39_out, not_203_out, not_204_out, not_205_out, not_206_out, not_207_out, F3, not_208_out, not_209_out);
  and and_40 (and_40_out, not_210_out, not_211_out, not_212_out, F1, not_213_out, F3, not_214_out, F5);
  and and_41 (and_41_out, not_215_out, not_216_out, not_217_out, F0, F2, not_218_out, not_219_out, F5);
  and and_42 (and_42_out, not_220_out, OP3, not_221_out, not_222_out);
  and and_43 (and_43_out, not_223_out, OP2, not_224_out, not_225_out);
  and and_44 (and_44_out, OP0, not_226_out, not_227_out, not_228_out, not_229_out);
  and and_45 (and_45_out, OP0, not_230_out, not_231_out, not_232_out);
  and and_46 (and_46_out, OP0, OP1, not_233_out, not_234_out, OP5);
  and and_47 (and_47_out, not_235_out, not_236_out, not_237_out, not_238_out, not_239_out, not_240_out, not_241_out, not_242_out, not_243_out);
  and and_48 (and_48_out, not_244_out, not_245_out, not_246_out, not_247_out, not_248_out, not_249_out, not_250_out, not_251_out, F5);
  and and_49 (and_49_out, not_252_out, not_253_out, not_254_out, not_255_out, not_256_out, not_257_out, not_258_out, F2, F3, not_259_out, not_260_out);
  and and_50 (and_50_out, not_261_out, not_262_out, not_263_out, not_264_out, not_265_out, F1, not_266_out, not_267_out, not_268_out, not_269_out);
  and and_51 (and_51_out, not_270_out, not_271_out, not_272_out, not_273_out, not_274_out, F1, not_275_out, F3, not_276_out, F5);
  and and_52 (and_52_out, not_277_out, not_278_out, not_279_out, not_280_out, not_281_out, F0, F2, not_282_out, not_283_out, F5);
  and and_53 (and_53_out, not_284_out, OP2, not_285_out, not_286_out, not_287_out);
  and and_54 (and_54_out, OP0, not_288_out, not_289_out, not_290_out, OP5);
  and and_55 (and_55_out, OP0, OP1, not_291_out, not_292_out, OP5);
  and and_56 (and_56_out, OP0, OP1, OP2, OP3, not_293_out, not_294_out);
  and and_57 (ERET, not_295_out, not_296_out, not_297_out, not_298_out, OP4, not_299_out, not_300_out, not_301_out, not_302_out, F3, F4, not_303_out);
  and and_58 (INTO, not_304_out, OP4, not_305_out, not_306_out, not_307_out, not_308_out, not_309_out, not_310_out, not_311_out, not_312_out, not_313_out, not_314_out);
  and and_59 (INTC, not_315_out, OP4, not_316_out, not_317_out, not_318_out, not_319_out, not_320_out, not_321_out, not_322_out, F2, not_323_out, not_324_out);
  or or_1 (ALU_SRC, and_3_out, and_4_out, and_5_out, and_6_out, and_7_out);
  or or_2 (RegWrite, and_8_out, and_9_out, and_10_out, and_11_out, and_12_out, and_13_out, and_14_out, and_15_out, and_16_out, and_17_out);
  or or_3 (SignedExt, and_19_out, and_20_out, and_21_out, and_22_out);
  or or_4 (RegDst, and_23_out, and_24_out, and_25_out, and_26_out, and_27_out);
  or or_5 (JUMP, and_31_out, and_32_out);
  or or_6 (rs, and_37_out, and_38_out, and_39_out, and_40_out, and_41_out, and_42_out, and_43_out, and_44_out, and_45_out, and_46_out);
  or or_7 (rt, and_47_out, and_48_out, and_49_out, and_50_out, and_51_out, and_52_out, and_53_out, and_54_out, and_55_out, and_56_out);
endmodule

// ALU
module MIPS_ALU (
  input  [4:0] shamt,
  input  [31:0] X,
  input  [31:0] Y,
  input  [3:0] AluOP,
  output Equal,
  output [31:0] Result,
  output [31:0] Result_2
);

  wire [0:0] comparator_1_lt, comparator_2_lt;
  wire [31:0] adder_1_out, AND_out, divider_1_out, divider_1_rem, multiplier_1_cout, multiplier_1_out,
       NOR_out, OR_out, shifter_1_out, shifter_2_out, shifter_3_out, subtractor_1_out, XOR_out;

  assign AND_out = X & Y;  // AND_Gate AND, 32 bits wide
  assign OR_out = X | Y;  // OR_Gate OR, 32 bits wide
  Shifter #(.width(32), .shift("ll")) shifter_1 (.in(Y), .\dist (shamt), .out(shifter_1_out));
  Shifter #(.width(32), .shift("ar")) shifter_2 (.in(Y), .\dist (shamt), .out(shifter_2_out));
  Shifter #(.width(32), .shift("lr")) shifter_3 (.in(Y), .\dist (shamt), .out(shifter_3_out));
  Multiplier #(.width(32)) multiplier_1 (.a(X), .b(Y), .out(multiplier_1_out), .cout(multiplier_1_cout));  // open: cin
  Divider #(.width(32)) divider_1 (.a(X), .b(Y), .out(divider_1_out), .rem(divider_1_rem));  // open: upper
  Adder #(.width(32)) adder_1 (.a(X), .b(Y), .out(adder_1_out));  // open: cin, cout
  Subtractor #(.width(32)) subtractor_1 (.a(X), .b(Y), .out(subtractor_1_out));  // open: bin, bout
  assign XOR_out = X ^ Y;  // XOR_Gate XOR, 32 bits wide
  assign NOR_out = ~(X | Y);  // NOR_Gate NOR, 32 bits wide
  Comparator #(.width(32), .mode("twosComplement")) comparator_1 (
    .a(X), .b(Y), .eq(Equal), .lt(comparator_1_lt[0]));  // open: gt
  Comparator #(.width(32), .mode("unsigned")) comparator_2 (.a(X), .b(Y), .lt(comparator_2_lt[0]));  // open: gt, eq
  Multiplexer #(.select(4), .width(32), .disabled("Z"), .enable("false")) multiplexer_1 (
    .in0(shifter_1_out), .in1(shifter_2_out), .in2(shifter_3_out), .in3(multiplier_1_out),
    .in4(divider_1_out), .in5(adder_1_out), .in6(subtractor_1_out), .in7(AND_out), .in8(OR_out),
    .in9(XOR_out), .in10(NOR_out), .in11({{31{1'b0}}, comparator_1_lt[0]}),
    .in12({{31{1'b0}}, comparator_2_lt[0]}), .in13({32{1'b0}}), .in14({32{1'b0}}), .in15({32{1'b0}}),
    .out(Result), .sel(AluOP));
  Multiplexer #(.select(4), .width(32), .disabled("Z"), .enable("false")) multiplexer_2 (
    .in0({32{1'b0}}), .in1({32{1'b0}}), .in2({32{1'b0}}), .in3(multiplier_1_cout), .in4(divider_1_rem),
    .in5({32{1'b0}}), .in6({32{1'b0}}), .in7({32{1'b0}}), .in8({32{1'b0}}), .in9({32{1'b0}}),
    .in10({32{1'b0}}), .in11({32{1'b0}}), .in12({32{1'b0}}), .in13({32{1'b0}}), .in14({32{1'b0}}),
    .in15({32{1'b0}}), .out(Result_2), .sel(AluOP));

  // Other names for the same wires on the sheet: Result2[31:0] = Result_2; S[3:0] = AluOP

  // Notes on the sheet:
  //   不要改变此引脚区域内容，也不要改变ALU封装形式
  //   输入引脚
  //   输出引脚
endmodule

module MIPS_Regifile (
  input  [31:0] Din,
  input  Clk,
  input  WE,
  input  [4:0] R1_num,
  input  [4:0] W_num,
  input  [4:0] R2_num,
  output [31:0] R1,
  output [31:0] R2
);

  // RegisterFile registerfile_1: pin names not known; wires that end beside it: Din, Clk, WE, W_num, R1_num, R2_num, R1, R2
endmodule

module \理想流水线  (
  output RegWrite,
  output MemWrite,
  output [31:0] IF_PC,
  output [31:0] ID_PC,
  output [31:0] EX_PC,
  output [31:0] M_PC,
  output [31:0] WB_PC,
  output [31:0] RDin,
  output [31:0] MDin,
  output [31:0] LedData
);

  wire and_1_out, and_3_out, and_4_out, and_5_out, beq, BGEZ, bne, CLK, clock_1_out, comparator_1_eq,
       comparator_1_lt, comparator_2_eq, d_ff_1_q, ex_mem_1_jal_2, ex_mem_1_jal_3, ex_mem_1_out_17,
       ex_mem_1_out_19, ex_mem_1_out_20, Go, Halt, id_ex_1_out_31, id_ex_1_out_32, id_ex_1_out_33,
       id_ex_1_out_34, id_ex_1_out_36, id_ex_1_out_37, id_ex_1_out_38, id_ex_1_out_39, id_ex_1_out_40,
       id_ex_1_out_41, IR1, IR2, IR3, JAL, LUI, mem_wb_1_out_17, mem_wb_1_out_20, mips_alu_1_equal,
       nand_1_out, not_1_out, or_1_out, or_2_out, or_3_out, or_4_out, or_5_out, or_6_out, RESET, RST,
       SignedExt, Syscall, W1, W2, W3, \单周期硬布线控制器_1_alu_src , \单周期硬布线控制器_1_jmp , \单周期硬布线控制器_1_jr ,
       \单周期硬布线控制器_1_lh , \单周期硬布线控制器_1_memtoreg , \单周期硬布线控制器_1_memwrite , \单周期硬布线控制器_1_regdst ,
       \单周期硬布线控制器_1_regwrite , \单周期硬布线控制器_1_syscall ;
  wire [0:0] mem_wb_1_out_19;
  wire [3:0] adder_1_out_2, id_ex_1_out_35, \单周期硬布线控制器_1_alu_op ;
  wire [4:0] ex_mem_1_out_26, id_ex_1_out_45, id_ex_1_out_46, mem_wb_1_out_25, multiplexer_4_out,
       multiplexer_5_out, multiplexer_6_out, multiplexer_7_out, multiplexer_8_out;
  wire [12:0] CNT_num;
  wire [15:0] \LoadUse次数 , \总周期数 , \插入气泡数 , \无条件分支数 , \条件分支成功数 ;
  wire [27:0] adder_1_out;
  wire [31:0] A0, adder_2_out, bit_extender_1_out, bit_extender_2_out, EX_IR, ex_mem_1_out_24,
       ex_mem_1_out_27, id_ex_1_out_44, id_ex_1_out_47, id_ex_1_out_48, ID_IR, if_id_1_out_10, IF_IR, MEM_IR,
       mem_wb_1_out_23, mem_wb_1_out_24, mem_wb_1_out_26, mips_alu_1_result, multiplexer_1_out,
       multiplexer_2_out, multiplexer_3_out, multiplexer_9_out, multiplexer_10_out, multiplexer_11_out,
       multiplexer_12_out, PC_JR, ram_1_data, shifter_1_out, shifter_2_out, shifter_3_out, shifter_4_out,
       undriven, V0, WB_IR;

  Button \u_总复位  (.out(RST));
  Button _1 (.out(IR1));
  Button _2 (.out(IR2));
  Button _3 (.out(IR3));
  // Probe on \总周期数 
  // Probe on \总周期数 
  Button \u_继续运行  (.out(Go));
  LED #(.active("true")) led_1 (.in(W1));
  LED #(.active("true")) led_2 (.in(W2));
  LED #(.active("true")) led_3 (.in(W3));
  Hex_Digit_Display hex_digit_display_1 (.value(LedData[31:28]));  // open: dp
  // Probe on IF_PC[19:0]
  // Mips_Probe mips_probe_1: pin names not known; wires that end beside it: IF_IR
  Hex_Digit_Display hex_digit_display_2 (.value(LedData[23:20]));  // open: dp
  Hex_Digit_Display hex_digit_display_3 (.value(LedData[27:24]));  // open: dp
  // Probe on ID_PC[19:0]
  // Mips_Probe mips_probe_2: pin names not known; wires that end beside it: ID_IR
  Hex_Digit_Display hex_digit_display_4 (.value(LedData[19:16]));  // open: dp
  Hex_Digit_Display hex_digit_display_5 (.value(LedData[15:12]));  // open: dp
  Hex_Digit_Display hex_digit_display_6 (.value(LedData[11:8]));  // open: dp
  Hex_Digit_Display hex_digit_display_7 (.value(LedData[7:4]));  // open: dp
  // Probe on EX_PC[19:0]
  // Mips_Probe mips_probe_3: pin names not known; wires that end beside it: EX_IR
  Hex_Digit_Display hex_digit_display_8 (.value(LedData[3:0]));  // open: dp
  // Probe on \总周期数 
  // Probe on M_PC[19:0]
  // Mips_Probe mips_probe_4: pin names not known; wires that end beside it: MEM_IR
  or or_1 (or_1_out, JAL, \单周期硬布线控制器_1_jmp );
  Multiplexer #(.select(1), .width(32), .disabled("Z"), .enable("false")) multiplexer_1 (
    .in0({adder_1_out_2, adder_1_out}), .in1(adder_2_out), .out(multiplexer_1_out), .sel(or_5_out));
  Multiplexer #(.select(1), .width(32), .disabled("Z"), .enable("false")) multiplexer_2 (
    .in0(multiplexer_1_out), .in1({adder_1_out_2, ID_IR[25:0], 2'b00}), .out(multiplexer_2_out),
    .sel(or_1_out));
  // Probe on \总周期数 
  // Probe on \无条件分支数 
  // Probe on \条件分支成功数 
  // Probe on \插入气泡数 
  // Probe on \LoadUse次数 
  Multiplexer #(.select(1), .width(32), .disabled("Z"), .enable("false")) multiplexer_3 (
    .in0(multiplexer_2_out), .in1(PC_JR), .out(multiplexer_3_out), .sel(\单周期硬布线控制器_1_jr ));
  or or_2 (or_2_out, ~Halt, Go);  // OR_Gate
  // Probe on IF_PC[11:0]
  // Probe on WB_PC[19:0]
  // Mips_Probe mips_probe_5: pin names not known; wires that end beside it: WB_IR
  Counter #(.width(16), .max('hffff), .ongoal("wrap"), .trigger("rising"), .behavior("new")) counter_1 (
    .count(or_2_out), .Q(\总周期数 ), .clk(CLK), .clr(RST));  // open: load, D, carry, preset, down
  Register #(.width(32), .trigger("rising"), .Select("low")) PC (
    .D(multiplexer_3_out), .en(or_2_out), .Q(IF_PC), .clk(CLK));  // open: clr
  // Probe on EX_PC[11:0]
  // Probe on ID_PC[11:0]
  // Probe on M_PC[11:0]
  D_Flip_Flop #(.trigger("high"), .Pre_Clr_Positions("LEGACY"), .NegatePresetClear("false"), .enable("true"), .NewFFLayout("false")) d_ff_1 (.Q(d_ff_1_q));  // open: clk, D, Qn, preset, en, reset
  // Probe on 13'h11
  Adder #(.width(32)) adder_1 (.a(IF_PC), .b(32'h4), .out({adder_1_out_2, adder_1_out}));  // open: cin, cout
  // Probe on WB_PC[11:0]
  Comparator #(.width(13), .mode("twosComplement")) comparator_1 (
    .a(CNT_num), .b(13'h11), .eq(comparator_1_eq), .lt(comparator_1_lt));  // open: gt
  Clock #(.highDuration(1), .lowDuration(1)) clock_1 (.out(clock_1_out));
  ROM #(.addrWidth(10), .dataWidth(32), .Select("high")) rom_1 (.addr(IF_PC[11:2]), .data(IF_IR));
  nand nand_1 (nand_1_out, d_ff_1_q, comparator_1_eq);
  Counter #(.width(13), .max('h1fff), .ongoal("stay"), .trigger("rising"), .behavior("old")) counter_2 (
    .count(comparator_1_lt), .Q(CNT_num), .clk(clock_1_out));  // open: load, D, carry, clr, preset
  or or_3 (or_3_out, or_5_out, \单周期硬布线控制器_1_jmp , \单周期硬布线控制器_1_jr , JAL);
  // Mips_Probe mips_probe_6: pin names not known; wires that end beside it: ID_IR
  IF_ID if_id_1 (
    .Instr(IF_IR), .PC_4({adder_1_out_2, adder_1_out}), .out_9(ID_IR), .out_10(if_id_1_out_10), .EN(1'b1),
    .CLK(CLK), .RST(or_3_out), .PC(IF_PC), .out_11(ID_PC));  // open: PredictJump, out_8
  assign CLK = nand_1_out ? clock_1_out : 1'bz;  // Controlled_Buffer controlled_buffer_1
  Pull_Resistor #(.pull(1)) pull_resistor_1 (.node(CLK));
  Multiplexer #(.select(1), .width(5), .disabled("Z"), .enable("false")) multiplexer_4 (
    .in0(ID_IR[20:16]), .in1(ID_IR[15:11]), .out(multiplexer_4_out), .sel(\单周期硬布线控制器_1_regdst ));
  Multiplexer #(.select(1), .width(5), .disabled("Z"), .enable("false")) multiplexer_5 (
    .in0(ID_IR[10:6]), .in1(5'b10000), .out(multiplexer_5_out), .sel(LUI));
  \单周期硬布线控制器  \u_单周期硬布线控制器_1  (
    .Func(ID_IR[5:0]), .OP(ID_IR[31:26]), .ALU_OP(\单周期硬布线控制器_1_alu_op ), .MemToReg(\单周期硬布线控制器_1_memtoreg ),
    .MemWrite(\单周期硬布线控制器_1_memwrite ), .ALU_SRC(\单周期硬布线控制器_1_alu_src ), .RegWrite(\单周期硬布线控制器_1_regwrite ),
    .SysCALL(\单周期硬布线控制器_1_syscall ), .SignedExt(SignedExt), .RegDst(\单周期硬布线控制器_1_regdst ),
    .JR(\单周期硬布线控制器_1_jr ), .JMP(\单周期硬布线控制器_1_jmp ), .Beq(beq), .JAL(JAL), .Bne(bne), .LUI(LUI),
    .LH(\单周期硬布线控制器_1_lh ), .BGEZ(BGEZ));  // open: rs, rt, ERET, INTO, INTC
  Multiplexer #(.select(1), .width(5), .disabled("Z"), .enable("false")) multiplexer_6 (
    .in0(ID_IR[25:21]), .in1(5'b00010), .out(multiplexer_6_out), .sel(\单周期硬布线控制器_1_syscall ));
  Multiplexer #(.select(1), .width(5), .disabled("Z"), .enable("false")) multiplexer_7 (
    .in0(ID_IR[20:16]), .in1(5'b00100), .out(multiplexer_7_out), .sel(\单周期硬布线控制器_1_syscall ));
  Multiplexer #(.select(1), .width(5), .disabled("Z"), .enable("false")) multiplexer_8 (
    .in0(multiplexer_4_out), .in1({5{1'b1}}), .out(multiplexer_8_out), .sel(JAL));
  assign bit_extender_1_out = {{16{1'b0}}, ID_IR[15:0]};  // Bit_Extender bit_extender_1
  assign bit_extender_2_out = {{16{ID_IR[15]}}, ID_IR[15:0]};  // Bit_Extender bit_extender_2
  MIPS_Regifile mips_regifile_1 (
    .Din(RDin), .Clk(CLK), .R1(V0), .R2(A0), .WE(RegWrite), .W_num(mem_wb_1_out_25),
    .R1_num(multiplexer_6_out), .R2_num(multiplexer_7_out));
  Multiplexer #(.select(1), .width(32), .disabled("Z"), .enable("false")) multiplexer_9 (
    .in0(bit_extender_1_out), .in1(bit_extender_2_out), .out(multiplexer_9_out), .sel(or_4_out));
  or or_4 (or_4_out, beq, SignedExt, bne, BGEZ);
  Comparator #(.width(32), .mode("twosComplement")) comparator_2 (
    .a(V0), .b(32'h32), .eq(comparator_2_eq));  // open: gt, lt
  ID_EX id_ex_1 (
    .BEQ(beq), .BNE(bne), .MemToReg(\单周期硬布线控制器_1_memtoreg ), .MemWrite(\单周期硬布线控制器_1_memwrite ),
    .AluOP(\单周期硬布线控制器_1_alu_op ), .AluSrc(\单周期硬布线控制器_1_alu_src ), .RegWrite(\单周期硬布线控制器_1_regwrite ),
    .JAL(JAL), .LH(\单周期硬布线控制器_1_lh ), .BGEZ(BGEZ), .RS(V0), .RT(A0), .shamt(multiplexer_5_out),
    .WriteReg_num(multiplexer_8_out), .Imm(multiplexer_9_out), .PC_4(if_id_1_out_10),
    .out_31(id_ex_1_out_31), .out_32(id_ex_1_out_32), .out_33(id_ex_1_out_33), .out_34(id_ex_1_out_34),
    .out_35(id_ex_1_out_35), .out_36(id_ex_1_out_36), .out_37(id_ex_1_out_37), .out_38(id_ex_1_out_38),
    .out_39(id_ex_1_out_39), .out_40(id_ex_1_out_40), .out_43(PC_JR), .out_44(id_ex_1_out_44),
    .out_45(id_ex_1_out_45), .out_46(id_ex_1_out_46), .out_47(id_ex_1_out_47), .out_48(id_ex_1_out_48),
    .EN(1'b1), .CLK(CLK), .RST(or_5_out), .PC(ID_PC), .out_49(EX_PC), .Syscall(\单周期硬布线控制器_1_syscall ),
    .out_41(id_ex_1_out_41), .Instr(ID_IR), .out_42(EX_IR));  // open: JUMP, out_30, JR, out_29, RsForward, out_50, RtForward, out_51, PredictJump, out_28
  Register #(.width(32), .trigger("rising"), .Select("low")) register_1 (
    .D(A0), .en(and_1_out), .Q(LedData), .clk(CLK), .clr(RESET));
  and and_1 (and_1_out, ~comparator_2_eq, Syscall);  // AND_Gate
  and and_2 (Halt, comparator_2_eq, Syscall);
  Multiplexer #(.select(1), .width(32), .disabled("Z"), .enable("false")) multiplexer_10 (
    .in0(id_ex_1_out_44), .in1(id_ex_1_out_47), .out(multiplexer_10_out), .sel(id_ex_1_out_36));
  Shifter #(.width(32), .shift("ll")) shifter_1 (.in(id_ex_1_out_47), .\dist (5'b00010), .out(shifter_1_out));
  Multiplexer #(.select(1), .width(32), .disabled("Z"), .enable("false")) multiplexer_11 (
    .in0(multiplexer_10_out), .in1({32{1'b0}}), .out(multiplexer_11_out), .sel(id_ex_1_out_40));
  Adder #(.width(32)) adder_2 (.a(shifter_1_out), .b(id_ex_1_out_48), .out(adder_2_out));  // open: cin, cout
  and and_3 (and_3_out, id_ex_1_out_32, not_1_out);
  not not_1 (not_1_out, mips_alu_1_equal);
  and and_4 (and_4_out, id_ex_1_out_31, mips_alu_1_equal);
  MIPS_ALU mips_alu_1 (
    .X(PC_JR), .Y(multiplexer_11_out), .AluOP(id_ex_1_out_35), .Equal(mips_alu_1_equal),
    .Result(mips_alu_1_result), .shamt(id_ex_1_out_45));  // open: Result_2
  or or_5 (or_5_out, and_3_out, and_4_out, and_5_out);
  and and_5 (and_5_out, or_6_out, id_ex_1_out_40);
  or or_6 (or_6_out, mips_alu_1_equal, ~mips_alu_1_result[0]);  // OR_Gate
  EX_MEM ex_mem_1 (
    .MemtoReg(id_ex_1_out_33), .MemWrite(id_ex_1_out_34), .RegWrite(id_ex_1_out_37), .LH(id_ex_1_out_39),
    .Result(mips_alu_1_result), .WriteData(id_ex_1_out_44), .WriteReg_num(id_ex_1_out_46),
    .out_17(ex_mem_1_out_17), .out_18(MemWrite), .out_19(ex_mem_1_out_19), .out_20(ex_mem_1_out_20),
    .out_24(ex_mem_1_out_24), .out_25(MDin), .out_26(ex_mem_1_out_26), .EN(1'b1), .RST(RST), .CLK(CLK),
    .JAL(id_ex_1_out_38), .JAL_2(ex_mem_1_jal_2), .PC_4(id_ex_1_out_48), .out_27(ex_mem_1_out_27),
    .PC(EX_PC), .out_28(M_PC), .Syscall(id_ex_1_out_41), .JAL_3(ex_mem_1_jal_3), .Instr(EX_IR),
    .out_23(MEM_IR));  // open: V0, out_29
  RAM #(.addrWidth(10), .dataWidth(32), .bus("separate"), .Select("high")) ram_1 (
    .addr(ex_mem_1_out_24[11:2]), .din(MDin), .data(ram_1_data), .str(MemWrite), .clk(CLK), .clr(RESET));  // open: sel, ld
  MEM_WB mem_wb_1 (
    .MemtoReg(ex_mem_1_out_17), .RegWrite(ex_mem_1_out_19), .LH(ex_mem_1_out_20),
    .AluResult(ex_mem_1_out_24), .RD(ram_1_data), .WriteReg_num(ex_mem_1_out_26), .out_17(mem_wb_1_out_17),
    .out_18(RegWrite), .out_19(mem_wb_1_out_19[0]), .out_23(mem_wb_1_out_23), .out_24(mem_wb_1_out_24),
    .out_25(mem_wb_1_out_25), .EN(1'b1), .RST(RST), .CLK(CLK), .PC_4(ex_mem_1_out_27),
    .out_26(mem_wb_1_out_26), .JAL(ex_mem_1_jal_2), .out_20(mem_wb_1_out_20), .PC(M_PC), .out_27(WB_PC),
    .Syscall(ex_mem_1_jal_3), .out_21(Syscall), .Instr(MEM_IR), .out_22(WB_IR));  // open: A0, out_28, V0, out_29
  Multiplexer #(.select(1), .width(32), .disabled("Z"), .enable("false")) multiplexer_12 (
    .in0(mem_wb_1_out_23), .in1(mem_wb_1_out_24), .out(multiplexer_12_out), .sel(mem_wb_1_out_17));
  Shifter #(.width(32), .shift("ll")) shifter_2 (.in(multiplexer_12_out), .\dist (5'b10000), .out(shifter_2_out));
  Shifter #(.width(32), .shift("ar")) shifter_3 (.in(multiplexer_12_out), .\dist (5'b10000), .out(shifter_3_out));
  Shifter #(.width(32), .shift("ar")) shifter_4 (.in(shifter_2_out), .\dist (5'b10000), .out(shifter_4_out));
  Multiplexer #(.select(2), .width(32), .disabled("Z"), .enable("false")) multiplexer_13 (
    .in0(multiplexer_12_out), .in1(shifter_4_out), .in2(multiplexer_12_out), .in3(shifter_3_out),
    .sel({mem_wb_1_out_23[1], mem_wb_1_out_19[0]}));  // open: out
  Multiplexer #(.select(1), .width(32), .disabled("Z"), .enable("false")) multiplexer_14 (
    .in0(undriven), .in1(mem_wb_1_out_26), .out(RDin), .sel(mem_wb_1_out_20));

  // Other names for the same wires on the sheet: IR[31:0] = ID_IR; MEM_PC[31:0] = M_PC

  // Notes on the sheet:
  //   中断源
  //   时空图监测，可删除
  //   中断等待指示
  //   数码管输出
  //   控制位
  //   branch
  //   流水调试日志用
  //   暂停节拍，不能为0
  //   指令存储器
  //   戳工具置1进入计数暂停模式，ctrl+k时钟自动运行到对应节拍暂停
  //   ctrl+k关闭时钟连续运行，将控制位置零，进入单步调试模式调试
  //   用这个时钟源需要去掉电路中的其他时钟源
  //   contents of rom_1 (hex, n*v repeats v):
  //   20100000 20110000 20120000 20130000 36100000 36310001 36520002 36730003 ae100000 ae110004 ae120008
  //   ae13000c 2002000a 20110000 20120000 20130000 c
  //   or_3 drives only 0 and floats otherwise
  //   指令字
  //   可计数暂停的时钟源
  //   OP
  //   Func
  //   rs
  //   rt
  //   rd
  //   JMP
  //   JR
  //   OP
  //   Func
  //   Syscall
  //   $ra
  //   Beq
  //   Bne
  //   MemToReg
  //   MemWrite
  //   AluOP
  //   AluSrcB
  //   RegWrite
  //   JAL
  //   RegDst
  //   LUI
  //   LH
  //   BGEZ
  //   为方便自动评测，需要输出流水线各段保存的PC值，注意是PC不是PC+4，另外ID段寄存器写入信息，Mem段内存写入信息也要输出
  //   PC+4
  //   WriteBackData
  //   WriteReg#
  //   MemToReg
  //   MemWrite
  //   RegWrite
  //   JAL
  //   LH
  //   WriteData
  //   WriteReg#
  //   PC+4
  //   PC+4
  //   WriteBackData
endmodule
module \气泡流水线  (
  output RegWrite,
  output MemWrite,
  output [31:0] IF_PC,
  output [31:0] ID_PC,
  output [31:0] EX_PC,
  output [31:0] M_PC,
  output [31:0] WB_PC,
  output [31:0] RDin,
  output [31:0] MDin,
  output [31:0] LedData
);

  wire and_1_out, and_2_out, and_3_out, and_4_out, and_5_out, and_6_out, and_7_out, and_8_out, and_9_out,
       and_10_out, and_11_out, and_12_out, and_13_out, and_14_out, B_EX, beq, BGEZ, bne, CLK, clock_1_out,
       comparator_1_eq, comparator_1_lt, comparator_2_eq, d_ff_1_q, DataHazzard, ex_mem_1_jal_2,
       ex_mem_1_jal_3, ex_mem_1_out_17, ex_mem_1_out_19, ex_mem_1_out_20, GG, Go, Halt, id_ex_1_out_31,
       id_ex_1_out_32, id_ex_1_out_33, id_ex_1_out_34, id_ex_1_out_36, id_ex_1_out_37, id_ex_1_out_39,
       id_ex_1_out_40, id_ex_1_out_41, IR1, IR2, IR3, JAL, JAL_EX, JMP_EX, JR_EX, \J型 , LUI, mem_wb_1_out_17,
       mem_wb_1_out_20, mips_alu_1_equal, nand_1_out, not_1_out, not_2_out, not_3_out, not_4_out, or_3_out,
       or_6_out, or_7_out, or_8_out, or_9_out, or_10_out, or_12_out, PC_EN, RESET, RST, RsUsed, RtUsed,
       SignedExt, Syscall, W1, W2, W3, \冲突检测电路_1_id_ex_rst , \冲突检测电路_1_if_id_en , \单周期硬布线控制器_1_alu_src ,
       \单周期硬布线控制器_1_jmp , \单周期硬布线控制器_1_jr , \单周期硬布线控制器_1_lh , \单周期硬布线控制器_1_memtoreg , \单周期硬布线控制器_1_memwrite ,
       \单周期硬布线控制器_1_regdst , \单周期硬布线控制器_1_regwrite , \单周期硬布线控制器_1_syscall , \无条件 , \气泡 ;
  wire [0:0] mem_wb_1_out_19;
  wire [3:0] adder_1_out_2, id_ex_1_out_35, \单周期硬布线控制器_1_alu_op ;
  wire [4:0] ex_mem_1_out_26, id_ex_1_out_45, id_ex_1_out_46, mem_wb_1_out_25, multiplexer_4_out,
       multiplexer_5_out, multiplexer_8_out, R1_num, R2_num;
  wire [12:0] CNT_num;
  wire [15:0] \LoadUse次数 , \总周期数 , \插入气泡数 , \无条件分支数 , \条件分支成功数 ;
  wire [27:0] adder_1_out;
  wire [31:0] A0, adder_2_out, bit_extender_1_out, bit_extender_2_out, EX_IR, ex_mem_1_out_24,
       ex_mem_1_out_27, ex_mem_1_out_29, id_ex_1_out_44, id_ex_1_out_47, id_ex_1_out_48, ID_IR,
       if_id_1_out_10, IF_IR, MEM_IR, mem_wb_1_out_23, mem_wb_1_out_24, mem_wb_1_out_26, mips_alu_1_result,
       mips_regifile_1_r1, mips_regifile_1_r2, multiplexer_1_out, multiplexer_2_out, multiplexer_3_out,
       multiplexer_9_out, multiplexer_10_out, multiplexer_11_out, multiplexer_12_out, multiplexer_13_out,
       PC_JR, ram_1_data, shifter_1_out, shifter_2_out, shifter_3_out, shifter_4_out, V0, WB_IR;

  Button \u_总复位  (.out(RST));
  Button _1 (.out(IR1));
  Button _2 (.out(IR2));
  Button _3 (.out(IR3));
  // Probe on \总周期数 
  // Probe on \总周期数 
  Button \u_继续运行  (.out(Go));
  LED #(.active("true")) led_1 (.in(W1));
  LED #(.active("true")) led_2 (.in(W2));
  LED #(.active("true")) led_3 (.in(W3));
  Hex_Digit_Display hex_digit_display_1 (.value(LedData[31:28]));  // open: dp
  // Probe on IF_PC[19:0]
  // Mips_Probe mips_probe_1: pin names not known; wires that end beside it: IF_IR
  and and_1 (and_1_out, CLK, not_1_out);
  Hex_Digit_Display hex_digit_display_2 (.value(LedData[23:20]));  // open: dp
  Hex_Digit_Display hex_digit_display_3 (.value(LedData[27:24]));  // open: dp
  // Probe on ID_PC[19:0]
  // Mips_Probe mips_probe_2: pin names not known; wires that end beside it: ID_IR
  Counter #(.width(16), .max('hffff), .ongoal("wrap"), .trigger("falling"), .behavior("old")) counter_1 (
    .count(\无条件 ), .Q(\无条件分支数 ), .clk(and_1_out));  // open: load, D, carry, clr, preset
  not not_1 (not_1_out, Halt);
  Hex_Digit_Display hex_digit_display_4 (.value(LedData[15:12]));  // open: dp
  Hex_Digit_Display hex_digit_display_5 (.value(LedData[19:16]));  // open: dp
  and and_2 (and_2_out, CLK, not_2_out);
  Hex_Digit_Display hex_digit_display_6 (.value(LedData[11:8]));  // open: dp
  Hex_Digit_Display hex_digit_display_7 (.value(LedData[7:4]));  // open: dp
  // Probe on EX_PC[19:0]
  // Mips_Probe mips_probe_3: pin names not known; wires that end beside it: EX_IR
  Counter #(.width(16), .max('hffff), .ongoal("wrap"), .trigger("rising"), .behavior("old")) counter_2 (
    .count(B_EX), .Q(\条件分支成功数 ), .clk(and_2_out));  // open: load, D, carry, clr, preset
  not not_2 (not_2_out, Halt);
  Hex_Digit_Display hex_digit_display_8 (.value(LedData[3:0]));  // open: dp
  \冲突检测电路  \u_冲突检测电路_1  (
    .WriteReg__EX(id_ex_1_out_46), .WriteReg__MEM(ex_mem_1_out_26), .RsUsed(RsUsed), .RtUsed(RtUsed),
    .RegWrite_EX(id_ex_1_out_37), .RegWrite_MEM(ex_mem_1_out_19), .Branch(B_EX), .PC_EN(PC_EN),
    .IF_ID_EN(\冲突检测电路_1_if_id_en ), .ID_EX_RST(\冲突检测电路_1_id_ex_rst ), .R1_num(R1_num), .R2_num(R2_num),
    .DataHazzaed(DataHazzard));  // open: IF_ID_RST
  // Probe on \总周期数 
  // Probe on M_PC[19:0]
  // Mips_Probe mips_probe_4: pin names not known; wires that end beside it: MEM_IR
  or or_1 (\气泡 , B_EX, \无条件 );
  or or_2 (\J型 , JAL_EX, JMP_EX);
  Multiplexer #(.select(1), .width(32), .disabled("Z"), .enable("false")) multiplexer_1 (
    .in0({adder_1_out_2, adder_1_out}), .in1(adder_2_out), .out(multiplexer_1_out), .sel(B_EX));
  Multiplexer #(.select(1), .width(32), .disabled("Z"), .enable("false")) multiplexer_2 (
    .in0(multiplexer_1_out), .in1({adder_1_out_2, EX_IR[25:0], 2'b00}), .out(multiplexer_2_out), .sel(\J型 ));
  // Probe on \总周期数 
  // Probe on \无条件分支数 
  // Probe on \条件分支成功数 
  // Probe on \插入气泡数 
  // Probe on \LoadUse次数 
  Multiplexer #(.select(1), .width(32), .disabled("Z"), .enable("false")) multiplexer_3 (
    .in0(multiplexer_2_out), .in1(PC_JR), .out(multiplexer_3_out), .sel(JR_EX));
  or or_3 (or_3_out, \J型 , and_3_out);
  and and_3 (and_3_out, PC_EN, GG);
  // Probe on IF_PC[11:0]
  // Probe on WB_PC[19:0]
  // Mips_Probe mips_probe_5: pin names not known; wires that end beside it: WB_IR
  or or_4 (\无条件 , JMP_EX, JAL_EX, JR_EX);
  Register #(.width(32), .trigger("rising"), .Select("low")) PC (
    .D(multiplexer_3_out), .en(or_3_out), .Q(IF_PC), .clk(CLK));  // open: clr
  or or_5 (GG, ~Halt, Go);  // OR_Gate
  // Probe on ID_PC[11:0]
  // Probe on EX_PC[11:0]
  // Probe on M_PC[11:0]
  D_Flip_Flop #(.trigger("high"), .Pre_Clr_Positions("LEGACY"), .NegatePresetClear("false"), .enable("true"), .NewFFLayout("false")) d_ff_1 (.Q(d_ff_1_q));  // open: clk, D, Qn, preset, en, reset
  // Probe on 13'h1130
  Adder #(.width(32)) adder_1 (.a(IF_PC), .b(32'h4), .out({adder_1_out_2, adder_1_out}));  // open: cin, cout
  Counter #(.width(16), .max('hffff), .ongoal("wrap"), .trigger("rising"), .behavior("new")) counter_3 (
    .count(GG), .Q(\总周期数 ), .clk(CLK), .clr(RESET));  // open: load, D, carry, preset, down
  // Probe on WB_PC[11:0]
  Comparator #(.width(13), .mode("twosComplement")) comparator_1 (
    .a(CNT_num), .b(13'h1130), .eq(comparator_1_eq), .lt(comparator_1_lt));  // open: gt
  Clock #(.highDuration(1), .lowDuration(1)) clock_1 (.out(clock_1_out));
  and and_4 (and_4_out, DataHazzard, ~\气泡 );  // AND_Gate
  or or_6 (or_6_out, \冲突检测电路_1_if_id_en , or_10_out);
  and and_5 (and_5_out, GG, or_6_out);
  ROM #(.addrWidth(10), .dataWidth(32), .Select("high")) rom_1 (.addr(IF_PC[11:2]), .data(IF_IR));
  nand nand_1 (nand_1_out, d_ff_1_q, comparator_1_eq);
  Counter #(.width(13), .max('h1fff), .ongoal("stay"), .trigger("rising"), .behavior("old")) counter_4 (
    .count(comparator_1_lt), .Q(CNT_num), .clk(clock_1_out));  // open: load, D, carry, clr, preset
  and and_6 (and_6_out, CLK, not_3_out);
  // Mips_Probe mips_probe_6: pin names not known; wires that end beside it: ID_IR
  IF_ID if_id_1 (
    .Instr(IF_IR), .PC_4({adder_1_out_2, adder_1_out}), .out_9(ID_IR), .out_10(if_id_1_out_10),
    .EN(and_5_out), .CLK(CLK), .RST(or_10_out), .PC(IF_PC), .out_11(ID_PC));  // open: PredictJump, out_8
  assign CLK = nand_1_out ? clock_1_out : 1'bz;  // Controlled_Buffer controlled_buffer_1
  Counter #(.width(16), .max('hffff), .ongoal("wrap"), .trigger("rising"), .behavior("old")) counter_5 (
    .count(and_4_out), .Q(\插入气泡数 ), .clk(and_6_out));  // open: load, D, carry, clr, preset
  not not_3 (not_3_out, Halt);
  Pull_Resistor #(.pull(1)) pull_resistor_1 (.node(CLK));
  Multiplexer #(.select(1), .width(5), .disabled("Z"), .enable("false")) multiplexer_4 (
    .in0(ID_IR[20:16]), .in1(ID_IR[15:11]), .out(multiplexer_4_out), .sel(\单周期硬布线控制器_1_regdst ));
  Multiplexer #(.select(1), .width(5), .disabled("Z"), .enable("false")) multiplexer_5 (
    .in0(ID_IR[10:6]), .in1(5'b10000), .out(multiplexer_5_out), .sel(LUI));
  \单周期硬布线控制器  \u_单周期硬布线控制器_1  (
    .Func(ID_IR[5:0]), .OP(ID_IR[31:26]), .ALU_OP(\单周期硬布线控制器_1_alu_op ), .MemToReg(\单周期硬布线控制器_1_memtoreg ),
    .MemWrite(\单周期硬布线控制器_1_memwrite ), .ALU_SRC(\单周期硬布线控制器_1_alu_src ), .RegWrite(\单周期硬布线控制器_1_regwrite ),
    .SysCALL(\单周期硬布线控制器_1_syscall ), .SignedExt(SignedExt), .RegDst(\单周期硬布线控制器_1_regdst ),
    .JR(\单周期硬布线控制器_1_jr ), .JMP(\单周期硬布线控制器_1_jmp ), .Beq(beq), .JAL(JAL), .Bne(bne), .LUI(LUI),
    .LH(\单周期硬布线控制器_1_lh ), .BGEZ(BGEZ), .rs(RsUsed), .rt(RtUsed));  // open: ERET, INTO, INTC
  Multiplexer #(.select(1), .width(5), .disabled("Z"), .enable("false")) multiplexer_6 (
    .in0(ID_IR[25:21]), .in1(5'b00010), .out(R1_num), .sel(\单周期硬布线控制器_1_syscall ));
  Multiplexer #(.select(1), .width(5), .disabled("Z"), .enable("false")) multiplexer_7 (
    .in0(ID_IR[20:16]), .in1(5'b00100), .out(R2_num), .sel(\单周期硬布线控制器_1_syscall ));
  Multiplexer #(.select(1), .width(5), .disabled("Z"), .enable("false")) multiplexer_8 (
    .in0(multiplexer_4_out), .in1({5{1'b1}}), .out(multiplexer_8_out), .sel(JAL));
  assign bit_extender_1_out = {{16{1'b0}}, ID_IR[15:0]};  // Bit_Extender bit_extender_1
  assign bit_extender_2_out = {{16{ID_IR[15]}}, ID_IR[15:0]};  // Bit_Extender bit_extender_2
  MIPS_Regifile mips_regifile_1 (
    .Din(RDin), .Clk(CLK), .R1(mips_regifile_1_r1), .R2(mips_regifile_1_r2), .WE(RegWrite),
    .W_num(mem_wb_1_out_25), .R1_num(R1_num), .R2_num(R2_num));
  Multiplexer #(.select(1), .width(32), .disabled("Z"), .enable("false")) multiplexer_9 (
    .in0(bit_extender_1_out), .in1(bit_extender_2_out), .out(multiplexer_9_out), .sel(or_7_out));
  or or_7 (or_7_out, beq, SignedExt, bne, BGEZ);
  Comparator #(.width(32), .mode("twosComplement")) comparator_2 (
    .a(V0), .b(32'ha), .eq(comparator_2_eq));  // open: gt, lt
  and and_7 (and_7_out, GG, 1'b1);
  or or_8 (or_8_out, \冲突检测电路_1_id_ex_rst , or_10_out);
  ID_EX id_ex_1 (
    .BEQ(beq), .BNE(bne), .MemToReg(\单周期硬布线控制器_1_memtoreg ), .MemWrite(\单周期硬布线控制器_1_memwrite ),
    .AluOP(\单周期硬布线控制器_1_alu_op ), .AluSrc(\单周期硬布线控制器_1_alu_src ), .RegWrite(\单周期硬布线控制器_1_regwrite ),
    .JAL(JAL), .LH(\单周期硬布线控制器_1_lh ), .BGEZ(BGEZ), .RS(mips_regifile_1_r1), .RT(mips_regifile_1_r2),
    .shamt(multiplexer_5_out), .WriteReg_num(multiplexer_8_out), .Imm(multiplexer_9_out),
    .PC_4(if_id_1_out_10), .out_31(id_ex_1_out_31), .out_32(id_ex_1_out_32), .out_33(id_ex_1_out_33),
    .out_34(id_ex_1_out_34), .out_35(id_ex_1_out_35), .out_36(id_ex_1_out_36), .out_37(id_ex_1_out_37),
    .out_38(JAL_EX), .out_39(id_ex_1_out_39), .out_40(id_ex_1_out_40), .out_43(PC_JR),
    .out_44(id_ex_1_out_44), .out_45(id_ex_1_out_45), .out_46(id_ex_1_out_46), .out_47(id_ex_1_out_47),
    .out_48(id_ex_1_out_48), .EN(and_7_out), .CLK(CLK), .RST(or_8_out), .PC(ID_PC), .out_49(EX_PC),
    .Syscall(\单周期硬布线控制器_1_syscall ), .out_41(id_ex_1_out_41), .JUMP(\单周期硬布线控制器_1_jmp ), .out_30(JMP_EX),
    .JR(\单周期硬布线控制器_1_jr ), .out_29(JR_EX), .Instr(ID_IR), .out_42(EX_IR));  // open: RsForward, out_50, RtForward, out_51, PredictJump, out_28
  Register #(.width(32), .trigger("rising"), .Select("low")) register_1 (
    .D(A0), .en(and_8_out), .Q(LedData), .clk(CLK), .clr(RST));
  and and_8 (and_8_out, ~comparator_2_eq, Syscall);  // AND_Gate
  and and_9 (and_9_out, comparator_2_eq, Syscall);
  Register #(.width(1), .trigger("rising"), .Select("low")) register_2 (
    .D(and_9_out), .en(or_9_out), .Q(Halt), .clk(CLK), .clr(RST));
  or or_9 (or_9_out, ~Halt, Go);  // OR_Gate
  Multiplexer #(.select(1), .width(32), .disabled("Z"), .enable("false")) multiplexer_10 (
    .in0(id_ex_1_out_44), .in1(id_ex_1_out_47), .out(multiplexer_10_out), .sel(id_ex_1_out_36));
  Shifter #(.width(32), .shift("ll")) shifter_1 (.in(id_ex_1_out_47), .\dist (5'b00010), .out(shifter_1_out));
  Multiplexer #(.select(1), .width(32), .disabled("Z"), .enable("false")) multiplexer_11 (
    .in0(multiplexer_10_out), .in1({32{1'b0}}), .out(multiplexer_11_out), .sel(id_ex_1_out_40));
  Adder #(.width(32)) adder_2 (.a(shifter_1_out), .b(id_ex_1_out_48), .out(adder_2_out));  // open: cin, cout
  or or_10 (or_10_out, JR_EX, JMP_EX, JAL_EX, B_EX);
  and and_10 (and_10_out, id_ex_1_out_32, not_4_out);
  not not_4 (not_4_out, mips_alu_1_equal);
  and and_11 (and_11_out, id_ex_1_out_31, mips_alu_1_equal);
  MIPS_ALU mips_alu_1 (
    .X(PC_JR), .Y(multiplexer_11_out), .AluOP(id_ex_1_out_35), .Equal(mips_alu_1_equal),
    .Result(mips_alu_1_result), .shamt(id_ex_1_out_45));  // open: Result_2
  or or_11 (B_EX, and_10_out, and_11_out, and_12_out);
  and and_12 (and_12_out, or_12_out, id_ex_1_out_40);
  or or_12 (or_12_out, mips_alu_1_equal, ~mips_alu_1_result[0]);  // OR_Gate
  and and_13 (and_13_out, GG, 1'b1);
  EX_MEM ex_mem_1 (
    .MemtoReg(id_ex_1_out_33), .MemWrite(id_ex_1_out_34), .RegWrite(id_ex_1_out_37), .LH(id_ex_1_out_39),
    .Result(mips_alu_1_result), .WriteData(id_ex_1_out_44), .WriteReg_num(id_ex_1_out_46),
    .out_17(ex_mem_1_out_17), .out_18(MemWrite), .out_19(ex_mem_1_out_19), .out_20(ex_mem_1_out_20),
    .out_24(ex_mem_1_out_24), .out_25(MDin), .out_26(ex_mem_1_out_26), .EN(and_13_out), .RST(RST), .CLK(CLK),
    .JAL(JAL_EX), .JAL_2(ex_mem_1_jal_2), .PC_4(id_ex_1_out_48), .out_27(ex_mem_1_out_27), .PC(EX_PC),
    .out_28(M_PC), .Syscall(id_ex_1_out_41), .JAL_3(ex_mem_1_jal_3), .Instr(EX_IR), .out_23(MEM_IR),
    .V0(PC_JR), .out_29(ex_mem_1_out_29));
  RAM #(.addrWidth(10), .dataWidth(32), .bus("separate"), .Select("high")) ram_1 (
    .addr(ex_mem_1_out_24[11:2]), .din(MDin), .data(ram_1_data), .str(MemWrite), .clk(CLK), .clr(RST));  // open: sel, ld
  and and_14 (and_14_out, GG, 1'b1);
  MEM_WB mem_wb_1 (
    .MemtoReg(ex_mem_1_out_17), .RegWrite(ex_mem_1_out_19), .LH(ex_mem_1_out_20),
    .AluResult(ex_mem_1_out_24), .RD(ram_1_data), .WriteReg_num(ex_mem_1_out_26), .out_17(mem_wb_1_out_17),
    .out_18(RegWrite), .out_19(mem_wb_1_out_19[0]), .out_23(mem_wb_1_out_23), .out_24(mem_wb_1_out_24),
    .out_25(mem_wb_1_out_25), .EN(and_14_out), .RST(RST), .CLK(CLK), .PC_4(ex_mem_1_out_27),
    .out_26(mem_wb_1_out_26), .JAL(ex_mem_1_jal_2), .out_20(mem_wb_1_out_20), .PC(M_PC), .out_27(WB_PC),
    .Syscall(ex_mem_1_jal_3), .out_21(Syscall), .Instr(MEM_IR), .out_22(WB_IR), .A0(MDin), .out_28(A0),
    .V0(ex_mem_1_out_29), .out_29(V0));
  Multiplexer #(.select(1), .width(32), .disabled("Z"), .enable("false")) multiplexer_12 (
    .in0(mem_wb_1_out_23), .in1(mem_wb_1_out_24), .out(multiplexer_12_out), .sel(mem_wb_1_out_17));
  Shifter #(.width(32), .shift("ll")) shifter_2 (.in(multiplexer_12_out), .\dist (5'b10000), .out(shifter_2_out));
  Shifter #(.width(32), .shift("ar")) shifter_3 (.in(multiplexer_12_out), .\dist (5'b10000), .out(shifter_3_out));
  Shifter #(.width(32), .shift("ar")) shifter_4 (.in(shifter_2_out), .\dist (5'b10000), .out(shifter_4_out));
  Multiplexer #(.select(2), .width(32), .disabled("Z"), .enable("false")) multiplexer_13 (
    .in0(multiplexer_12_out), .in1(shifter_4_out), .in2(multiplexer_12_out), .in3(shifter_3_out),
    .out(multiplexer_13_out), .sel({mem_wb_1_out_23[1], mem_wb_1_out_19[0]}));
  Multiplexer #(.select(1), .width(32), .disabled("Z"), .enable("false")) multiplexer_14 (
    .in0(multiplexer_13_out), .in1(mem_wb_1_out_26), .out(RDin), .sel(mem_wb_1_out_20));

  // Other names for the same wires on the sheet: IR[31:0] = ID_IR; MEM_PC[31:0] = M_PC

  // Notes on the sheet:
  //   中断源
  //   时空图监测，可删除
  //   中断等待指示
  //   数码管输出
  //   控制位
  //   branch
  //   流水调试日志用
  //   暂停节拍，不能为0
  //   指令存储器
  //   戳工具置1进入计数暂停模式，ctrl+k时钟自动运行到对应节拍暂停
  //   ctrl+k关闭时钟连续运行，将控制位置零，进入单步调试模式调试
  //   IF/ID.EN
  //   contents of rom_1 (hex, n*v repeats v):
  //   20110001 8000c05 20110001 20120002 20130003 8000c09 20110001 20120002 20130003 8000c0d 20110001
  //   20120002 20130003 8000c11 20110001 20120002 20130003 c000cf9 20100001 20110001 118fc0 112020
  //   20020022 c 118882 12200001 8000c15 112020 20020022 c 20110001 118880 112020 20020022 c 12200001
  //   8000c1f 20110001 118fc0 112020 20020022 c 1188c3 112020 20020022 c 118903 112020 20020022 c 118903
  //   112020 20020022 c 118903 112020 20020022 c 118903 112020 20020022 c 118903 112020 20020022 c 118903
  //   112020 20020022 c 118903 112020 20020022 c 20100001 109fc0 139fc3 8021 2012000c 24160003 26100001
  //   3210000f 20080008 20090001 139900 2709825 132020 20020022 c 1094022 1500fff9 22100001 2018000f
  //   2188024 108700 20080008 20090001 139902 2709825 132021 20020022 c 1094022 1500fff9 108702 2c9b022
  //   12c00001 8000c50 4020 1084027 84400 3508ffff 82021 20020022 c 2010ffff 20110000 ae300000 22100001
  //   22310004 ae300000 22100001 22310004 ae300000 22100001 22310004 ae300000 22100001 22310004 ae300000
  //   22100001 22310004 ae300000 22100001 22310004 ae300000 22100001 22310004 ae300000 22100001 22310004
  //   ae300000 22100001 22310004 ae300000 22100001 22310004 ae300000 22100001 22310004 ae300000 22100001
  //   22310004 ae300000 22100001 22310004 ae300000 22100001 22310004 ae300000 22100001 22310004 ae300000
  //   22100001 22310004 22100001 8020 2011003c 8e130000 8e340000 274402a 11000002 ae330000 ae140000
  //   2231fffc 1611fff8 102020 20020022 c 22100004 2011003c 1611fff2 2002000a c 200b0008 3c11fedc 3631ffff
  //   112020 20020022 c 3c11ba98 112020 c 3c117654 112020 c 3c113210 112020 c 216bffff 1560fff0 2002000a c
  //   2008ffff 20117777 112020 20020022 c 200b0010 3a31ffff 112020 20020022 c 216bffff 1560fffa 2002000a c
  //   20090000 200b0010 34118483 20120404 118c00 129400 36318281 22520404 ad310000 2328820 21290004
  //   216bffff 1560fffb 200b0020 20090000 85310000 112020 20020022 c 21290002 216bffff 1560fff9 2002000a c
  //   2011000f 112020 20020022 c 2231ffff 621fffb 2002000a c 20100000 22100001 102020 20020022 c 22100002
  //   102020 20020022 c 22100003 102020 20020022 c 22100004 102020 20020022 c 22100005 102020 20020022 c
  //   22100006 102020 20020022 c 22100007 102020 20020022 c 22100008 102020 20020022 20020022 c 3e00008
  //   IF/ID/RST
  //   指令字
  //   可计数暂停的时钟源
  //   Instr
  //   OP
  //   Func
  //   rs
  //   rt
  //   rd
  //   JMP
  //   JR
  //   OP
  //   Func
  //   Syscall
  //   $ra
  //   Beq
  //   Bne
  //   MemToReg
  //   MemWrite
  //   AluOP
  //   AluSrcB
  //   RegWrite
  //   JAL
  //   RegDst
  //   LUI
  //   LH
  //   BGEZ
  //   为方便自动评测，需要输出流水线各段保存的PC值，注意是PC不是PC+4，另外ID段寄存器写入信息，Mem段内存写入信息也要输出
  //   PC+4
  //   WriteReg#
  //   ID/EX.RST
  //   RegWrite
  //   branch
  //   WriteBackData
  //   WriteReg#
  //   MemToReg
  //   MemWrite
  //   RegWrite
  //   JAL
  //   LH
  //   WriteData
  //   WriteReg#
  //   PC+4
  //   PC+4
  //   WriteBackData
endmodule

module \重定向流水线  (
  output RegWrite,
  output MemWrite,
  output [31:0] IF_PC,
  output [31:0] ID_PC,
  output [31:0] EX_PC,
  output [31:0] M_PC,
  output [31:0] WB_PC,
  output [31:0] RDin,
  output [31:0] MDin,
  output [31:0] LedData
);

  wire and_1_out, and_2_out, and_3_out, and_4_out, and_5_out, and_6_out, and_7_out, and_8_out, and_9_out,
       and_10_out, and_11_out, and_12_out, and_13_out, and_14_out, and_15_out, B_EX, beq, BGEZ, bne, CLK,
       clock_1_out, comparator_1_eq, comparator_1_lt, comparator_2_eq, d_ff_1_q, ex_mem_1_jal_2,
       ex_mem_1_jal_3, ex_mem_1_out_17, ex_mem_1_out_19, ex_mem_1_out_20, GG, Go, Halt, id_ex_1_out_31,
       id_ex_1_out_32, id_ex_1_out_33, id_ex_1_out_34, id_ex_1_out_36, id_ex_1_out_37, id_ex_1_out_39,
       id_ex_1_out_40, id_ex_1_out_41, IR1, IR2, IR3, JAL, JAL_EX, JMP_EX, JR_EX, \J型 , loaduse, LUI,
       mem_wb_1_out_17, mem_wb_1_out_20, mips_alu_1_equal, nand_1_out, not_1_out, not_2_out, not_3_out,
       not_4_out, not_5_out, or_3_out, or_6_out, or_7_out, or_8_out, or_9_out, or_10_out, or_12_out, PC_EN,
       RST, RsUsed, RtUsed, SignedExt, Syscall, W1, W2, W3, \单周期硬布线控制器_1_alu_src , \单周期硬布线控制器_1_jmp ,
       \单周期硬布线控制器_1_jr , \单周期硬布线控制器_1_lh , \单周期硬布线控制器_1_memtoreg , \单周期硬布线控制器_1_memwrite ,
       \单周期硬布线控制器_1_regdst , \单周期硬布线控制器_1_regwrite , \单周期硬布线控制器_1_syscall , \无条件 , \气泡 ,
       \重定向检测电路_1_id_ex_rst , \重定向检测电路_1_if_id_en ;
  wire [0:0] mem_wb_1_out_19;
  wire [1:0] id_ex_1_out_50, id_ex_1_out_51, RsForward, RtForward;
  wire [3:0] id_ex_1_out_35, \单周期硬布线控制器_1_alu_op ;
  wire [4:0] ex_mem_1_out_26, id_ex_1_out_45, id_ex_1_out_46, mem_wb_1_out_25, multiplexer_4_out,
       multiplexer_5_out, multiplexer_8_out, R1_num, R2_num;
  wire [12:0] CNT_num;
  wire [15:0] \LoadUse次数 , \总周期数 , \插入气泡数 , \无条件分支数 , \条件分支成功数 ;
  wire [31:0] A0, adder_1_out, adder_2_out, bit_extender_1_out, bit_extender_2_out, EX_IR, ex_mem_1_out_24,
       ex_mem_1_out_27, ex_mem_1_out_29, id_ex_1_out_43, id_ex_1_out_44, id_ex_1_out_47, id_ex_1_out_48,
       ID_IR, if_id_1_out_10, IF_IR, MEM_IR, mem_wb_1_out_23, mem_wb_1_out_24, mem_wb_1_out_26,
       mips_alu_1_result, mips_regifile_1_r1, mips_regifile_1_r2, multiplexer_1_out, multiplexer_2_out,
       multiplexer_3_out, multiplexer_9_out, multiplexer_11_out, multiplexer_12_out, multiplexer_13_out,
       multiplexer_14_out, multiplexer_15_out, PC_JR, ram_1_data, shifter_1_out, shifter_2_out,
       shifter_3_out, shifter_4_out, V0, WB_IR;

  Button \u_总复位  (.out(RST));
  Button _1 (.out(IR1));
  Button _2 (.out(IR2));
  Button _3 (.out(IR3));
  // Probe on \总周期数 
  // Probe on \总周期数 
  Button \u_继续运行  (.out(Go));
  LED #(.active("true")) led_1 (.in(W1));
  LED #(.active("true")) led_2 (.in(W2));
  LED #(.active("true")) led_3 (.in(W3));
  Hex_Digit_Display hex_digit_display_1 (.value(LedData[31:28]));  // open: dp
  // Probe on IF_PC[19:0]
  // Mips_Probe mips_probe_1: pin names not known; wires that end beside it: IF_IR
  and and_1 (and_1_out, CLK, not_1_out);
  Hex_Digit_Display hex_digit_display_2 (.value(LedData[27:24]));  // open: dp
  Hex_Digit_Display hex_digit_display_3 (.value(LedData[23:20]));  // open: dp
  // Probe on ID_PC[19:0]
  // Mips_Probe mips_probe_2: pin names not known; wires that end beside it: ID_IR
  Counter #(.width(16), .max('hffff), .ongoal("wrap"), .trigger("falling"), .behavior("old")) counter_1 (
    .count(\无条件 ), .Q(\无条件分支数 ), .clk(and_1_out));  // open: load, D, carry, clr, preset
  not not_1 (not_1_out, Halt);
  Hex_Digit_Display hex_digit_display_4 (.value(LedData[19:16]));  // open: dp
  Hex_Digit_Display hex_digit_display_5 (.value(LedData[15:12]));  // open: dp
  and and_2 (and_2_out, CLK, not_2_out);
  Hex_Digit_Display hex_digit_display_6 (.value(LedData[7:4]));  // open: dp
  Hex_Digit_Display hex_digit_display_7 (.value(LedData[11:8]));  // open: dp
  // Probe on EX_PC[19:0]
  // Mips_Probe mips_probe_3: pin names not known; wires that end beside it: EX_IR
  Counter #(.width(16), .max('hffff), .ongoal("wrap"), .trigger("rising"), .behavior("old")) counter_2 (
    .count(B_EX), .Q(\条件分支成功数 ), .clk(and_2_out));  // open: load, D, carry, clr, preset
  not not_2 (not_2_out, Halt);
  Hex_Digit_Display hex_digit_display_8 (.value(LedData[3:0]));  // open: dp
  // Probe on \总周期数 
  // Probe on M_PC[19:0]
  // Mips_Probe mips_probe_4: pin names not known; wires that end beside it: MEM_IR
  or or_1 (\气泡 , B_EX, \无条件 );
  \重定向检测电路  \u_重定向检测电路_1  (
    .R1_num(R1_num), .R2_num(R2_num), .WriteReg__EX(id_ex_1_out_46), .WriteReg__MEM(ex_mem_1_out_26),
    .RsUsed(RsUsed), .RtUsed(RtUsed), .RegWrite_EX(id_ex_1_out_37), .RegWrite_MEM(ex_mem_1_out_19),
    .EX_MemToReg(id_ex_1_out_33), .Branch(B_EX), .RsForward(RsForward), .RtForward(RtForward), .PC_EN(PC_EN),
    .IF_ID_EN(\重定向检测电路_1_if_id_en ), .ID_EX_RST(\重定向检测电路_1_id_ex_rst ), .LoadUse(loaduse));  // open: IF_ID_RST
  or or_2 (\J型 , JAL_EX, JMP_EX);
  Multiplexer #(.select(1), .width(32), .disabled("Z"), .enable("false")) multiplexer_1 (
    .in0(adder_1_out), .in1(adder_2_out), .out(multiplexer_1_out), .sel(B_EX));
  Multiplexer #(.select(1), .width(32), .disabled("Z"), .enable("false")) multiplexer_2 (
    .in0(multiplexer_1_out), .in1({EX_PC[31:28], EX_IR[25:0], 2'b00}), .out(multiplexer_2_out), .sel(\J型 ));
  // Probe on \总周期数 
  // Probe on \无条件分支数 
  // Probe on \条件分支成功数 
  // Probe on \插入气泡数 
  // Probe on \LoadUse次数 
  Multiplexer #(.select(1), .width(32), .disabled("Z"), .enable("false")) multiplexer_3 (
    .in0(multiplexer_2_out), .in1(PC_JR), .out(multiplexer_3_out), .sel(JR_EX));
  or or_3 (or_3_out, \J型 , and_3_out);
  and and_3 (and_3_out, PC_EN, GG);
  // Probe on IF_PC[11:0]
  // Probe on WB_PC[19:0]
  // Mips_Probe mips_probe_5: pin names not known; wires that end beside it: WB_IR
  or or_4 (\无条件 , JMP_EX, JAL_EX, JR_EX);
  Register #(.width(32), .trigger("rising"), .Select("low")) PC (
    .D(multiplexer_3_out), .en(or_3_out), .Q(IF_PC), .clk(CLK));  // open: clr
  or or_5 (GG, ~Halt, Go);  // OR_Gate
  // Probe on ID_PC[11:0]
  // Probe on EX_PC[11:0]
  // Probe on M_PC[11:0]
  D_Flip_Flop #(.trigger("high"), .Pre_Clr_Positions("LEGACY"), .NegatePresetClear("false"), .enable("true"), .NewFFLayout("false")) d_ff_1 (.Q(d_ff_1_q));  // open: clk, D, Qn, preset, en, reset
  // Probe on 13'h1b
  Adder #(.width(32)) adder_1 (.a(IF_PC), .b(32'h4), .out(adder_1_out));  // open: cin, cout
  Counter #(.width(16), .max('hffff), .ongoal("wrap"), .trigger("rising"), .behavior("new")) counter_3 (
    .count(GG), .Q(\总周期数 ), .clk(CLK), .clr(RST));  // open: load, D, carry, preset, down
  // Probe on WB_PC[11:0]
  Comparator #(.width(13), .mode("twosComplement")) comparator_1 (
    .a(CNT_num), .b(13'h1b), .eq(comparator_1_eq), .lt(comparator_1_lt));  // open: gt
  Clock #(.highDuration(1), .lowDuration(1)) clock_1 (.out(clock_1_out));
  Counter #(.width(16), .max('hffff), .ongoal("wrap"), .trigger("rising"), .behavior("old")) counter_4 (
    .count(loaduse), .Q(\LoadUse次数 ), .clk(and_4_out));  // open: load, D, carry, clr, preset
  and and_4 (and_4_out, CLK, not_3_out);
  not not_3 (not_3_out, Halt);
  or or_6 (or_6_out, \重定向检测电路_1_if_id_en , or_10_out);
  and and_5 (and_5_out, GG, or_6_out);
  ROM #(.addrWidth(10), .dataWidth(32), .Select("high")) rom_1 (.addr(IF_PC[11:2]), .data(IF_IR));
  nand nand_1 (nand_1_out, d_ff_1_q, comparator_1_eq);
  Counter #(.width(13), .max('h1fff), .ongoal("stay"), .trigger("rising"), .behavior("old")) counter_5 (
    .count(comparator_1_lt), .Q(CNT_num), .clk(clock_1_out));  // open: load, D, carry, clr, preset
  // Mips_Probe mips_probe_6: pin names not known; wires that end beside it: ID_IR
  IF_ID if_id_1 (
    .Instr(IF_IR), .PC_4(adder_1_out), .out_9(ID_IR), .out_10(if_id_1_out_10), .EN(and_5_out), .CLK(CLK),
    .RST(or_10_out), .PC(IF_PC), .out_11(ID_PC));  // open: PredictJump, out_8
  assign CLK = nand_1_out ? clock_1_out : 1'bz;  // Controlled_Buffer controlled_buffer_1
  Pull_Resistor #(.pull(1)) pull_resistor_1 (.node(CLK));
  and and_6 (and_6_out, \气泡 , ~loaduse);  // AND_Gate
  Multiplexer #(.select(1), .width(5), .disabled("Z"), .enable("false")) multiplexer_4 (
    .in0(ID_IR[20:16]), .in1(ID_IR[15:11]), .out(multiplexer_4_out), .sel(\单周期硬布线控制器_1_regdst ));
  Multiplexer #(.select(1), .width(5), .disabled("Z"), .enable("false")) multiplexer_5 (
    .in0(ID_IR[10:6]), .in1(5'b10000), .out(multiplexer_5_out), .sel(LUI));
  Counter #(.width(16), .max('hffff), .ongoal("wrap"), .trigger("rising"), .behavior("old")) counter_6 (
    .count(and_6_out), .Q(\插入气泡数 ), .clk(and_7_out));  // open: load, D, carry, clr, preset
  and and_7 (and_7_out, CLK, not_4_out);
  not not_4 (not_4_out, Halt);
  \单周期硬布线控制器  \u_单周期硬布线控制器_1  (
    .Func(ID_IR[5:0]), .OP(ID_IR[31:26]), .ALU_OP(\单周期硬布线控制器_1_alu_op ), .MemToReg(\单周期硬布线控制器_1_memtoreg ),
    .MemWrite(\单周期硬布线控制器_1_memwrite ), .ALU_SRC(\单周期硬布线控制器_1_alu_src ), .RegWrite(\单周期硬布线控制器_1_regwrite ),
    .SysCALL(\单周期硬布线控制器_1_syscall ), .SignedExt(SignedExt), .RegDst(\单周期硬布线控制器_1_regdst ),
    .JR(\单周期硬布线控制器_1_jr ), .JMP(\单周期硬布线控制器_1_jmp ), .Beq(beq), .JAL(JAL), .Bne(bne), .LUI(LUI),
    .LH(\单周期硬布线控制器_1_lh ), .BGEZ(BGEZ), .rs(RsUsed), .rt(RtUsed));  // open: ERET, INTO, INTC
  Multiplexer #(.select(1), .width(5), .disabled("Z"), .enable("false")) multiplexer_6 (
    .in0(ID_IR[25:21]), .in1(5'b00010), .out(R1_num), .sel(\单周期硬布线控制器_1_syscall ));
  Multiplexer #(.select(1), .width(5), .disabled("Z"), .enable("false")) multiplexer_7 (
    .in0(ID_IR[20:16]), .in1(5'b00100), .out(R2_num), .sel(\单周期硬布线控制器_1_syscall ));
  Multiplexer #(.select(1), .width(5), .disabled("Z"), .enable("false")) multiplexer_8 (
    .in0(multiplexer_4_out), .in1({5{1'b1}}), .out(multiplexer_8_out), .sel(JAL));
  assign bit_extender_1_out = {{16{1'b0}}, ID_IR[15:0]};  // Bit_Extender bit_extender_1
  assign bit_extender_2_out = {{16{ID_IR[15]}}, ID_IR[15:0]};  // Bit_Extender bit_extender_2
  MIPS_Regifile mips_regifile_1 (
    .Din(RDin), .Clk(CLK), .R1(mips_regifile_1_r1), .R2(mips_regifile_1_r2), .WE(RegWrite),
    .W_num(mem_wb_1_out_25), .R1_num(R1_num), .R2_num(R2_num));
  Multiplexer #(.select(1), .width(32), .disabled("Z"), .enable("false")) multiplexer_9 (
    .in0(bit_extender_1_out), .in1(bit_extender_2_out), .out(multiplexer_9_out), .sel(or_7_out));
  or or_7 (or_7_out, beq, SignedExt, bne, BGEZ);
  Comparator #(.width(32), .mode("twosComplement")) comparator_2 (
    .a(V0), .b(32'ha), .eq(comparator_2_eq));  // open: gt, lt
  or or_8 (or_8_out, \重定向检测电路_1_id_ex_rst , or_10_out);
  and and_8 (and_8_out, GG, 1'b1);
  ID_EX id_ex_1 (
    .BEQ(beq), .BNE(bne), .MemToReg(\单周期硬布线控制器_1_memtoreg ), .MemWrite(\单周期硬布线控制器_1_memwrite ),
    .AluOP(\单周期硬布线控制器_1_alu_op ), .AluSrc(\单周期硬布线控制器_1_alu_src ), .RegWrite(\单周期硬布线控制器_1_regwrite ),
    .JAL(JAL), .LH(\单周期硬布线控制器_1_lh ), .BGEZ(BGEZ), .RS(mips_regifile_1_r1), .RT(mips_regifile_1_r2),
    .shamt(multiplexer_5_out), .WriteReg_num(multiplexer_8_out), .Imm(multiplexer_9_out),
    .PC_4(if_id_1_out_10), .out_31(id_ex_1_out_31), .out_32(id_ex_1_out_32), .out_33(id_ex_1_out_33),
    .out_34(id_ex_1_out_34), .out_35(id_ex_1_out_35), .out_36(id_ex_1_out_36), .out_37(id_ex_1_out_37),
    .out_38(JAL_EX), .out_39(id_ex_1_out_39), .out_40(id_ex_1_out_40), .out_43(id_ex_1_out_43),
    .out_44(id_ex_1_out_44), .out_45(id_ex_1_out_45), .out_46(id_ex_1_out_46), .out_47(id_ex_1_out_47),
    .out_48(id_ex_1_out_48), .EN(and_8_out), .CLK(CLK), .RST(or_8_out), .PC(ID_PC), .out_49(EX_PC),
    .Syscall(\单周期硬布线控制器_1_syscall ), .out_41(id_ex_1_out_41), .JUMP(\单周期硬布线控制器_1_jmp ), .out_30(JMP_EX),
    .JR(\单周期硬布线控制器_1_jr ), .out_29(JR_EX), .Instr(ID_IR), .out_42(EX_IR), .RsForward(RsForward),
    .out_50(id_ex_1_out_50), .RtForward(RtForward), .out_51(id_ex_1_out_51));  // open: PredictJump, out_28
  Register #(.width(32), .trigger("rising"), .Select("low")) register_1 (
    .D(A0), .en(and_9_out), .Q(LedData), .clk(CLK), .clr(RST));
  and and_9 (and_9_out, ~comparator_2_eq, Syscall);  // AND_Gate
  Register #(.width(1), .trigger("rising"), .Select("low")) register_2 (
    .D(and_10_out), .en(or_9_out), .Q(Halt), .clk(CLK), .clr(RST));
  and and_10 (and_10_out, comparator_2_eq, Syscall);
  or or_9 (or_9_out, ~Halt, Go);  // OR_Gate
  Multiplexer #(.select(2), .width(32), .disabled("Z"), .enable("false")) multiplexer_10 (
    .in0(id_ex_1_out_43), .in1(RDin), .in2(ex_mem_1_out_24), .out(PC_JR), .sel(id_ex_1_out_50));  // open: in3
  Multiplexer #(.select(2), .width(32), .disabled("Z"), .enable("false")) multiplexer_11 (
    .in0(id_ex_1_out_44), .in1(RDin), .in2(ex_mem_1_out_24), .out(multiplexer_11_out), .sel(id_ex_1_out_51));  // open: in3
  Multiplexer #(.select(1), .width(32), .disabled("Z"), .enable("false")) multiplexer_12 (
    .in0(multiplexer_11_out), .in1(id_ex_1_out_47), .out(multiplexer_12_out), .sel(id_ex_1_out_36));
  Shifter #(.width(32), .shift("ll")) shifter_1 (.in(id_ex_1_out_47), .\dist (5'b00010), .out(shifter_1_out));
  Multiplexer #(.select(1), .width(32), .disabled("Z"), .enable("false")) multiplexer_13 (
    .in0(multiplexer_12_out), .in1({32{1'b0}}), .out(multiplexer_13_out), .sel(id_ex_1_out_40));
  Adder #(.width(32)) adder_2 (.a(shifter_1_out), .b(id_ex_1_out_48), .out(adder_2_out));  // open: cin, cout
  or or_10 (or_10_out, JR_EX, JMP_EX, JAL_EX, B_EX);
  and and_11 (and_11_out, id_ex_1_out_32, not_5_out);
  not not_5 (not_5_out, mips_alu_1_equal);
  and and_12 (and_12_out, id_ex_1_out_31, mips_alu_1_equal);
  MIPS_ALU mips_alu_1 (
    .X(PC_JR), .Y(multiplexer_13_out), .AluOP(id_ex_1_out_35), .Equal(mips_alu_1_equal),
    .Result(mips_alu_1_result), .shamt(id_ex_1_out_45));  // open: Result_2
  or or_11 (B_EX, and_11_out, and_12_out, and_13_out);
  and and_13 (and_13_out, or_12_out, id_ex_1_out_40);
  or or_12 (or_12_out, mips_alu_1_equal, ~mips_alu_1_result[0]);  // OR_Gate
  and and_14 (and_14_out, GG, 1'b1);
  EX_MEM ex_mem_1 (
    .MemtoReg(id_ex_1_out_33), .MemWrite(id_ex_1_out_34), .RegWrite(id_ex_1_out_37), .LH(id_ex_1_out_39),
    .Result(mips_alu_1_result), .WriteData(multiplexer_11_out), .WriteReg_num(id_ex_1_out_46),
    .out_17(ex_mem_1_out_17), .out_18(MemWrite), .out_19(ex_mem_1_out_19), .out_20(ex_mem_1_out_20),
    .out_24(ex_mem_1_out_24), .out_25(MDin), .out_26(ex_mem_1_out_26), .EN(and_14_out), .RST(RST), .CLK(CLK),
    .JAL(JAL_EX), .JAL_2(ex_mem_1_jal_2), .PC_4(id_ex_1_out_48), .out_27(ex_mem_1_out_27), .PC(EX_PC),
    .out_28(M_PC), .Syscall(id_ex_1_out_41), .JAL_3(ex_mem_1_jal_3), .Instr(EX_IR), .out_23(MEM_IR),
    .V0(PC_JR), .out_29(ex_mem_1_out_29));
  RAM #(.addrWidth(10), .dataWidth(32), .bus("separate"), .Select("high")) ram_1 (
    .addr(ex_mem_1_out_24[11:2]), .din(MDin), .data(ram_1_data), .str(MemWrite), .clk(CLK), .clr(RST));  // open: sel, ld
  and and_15 (and_15_out, GG, 1'b1);
  MEM_WB mem_wb_1 (
    .MemtoReg(ex_mem_1_out_17), .RegWrite(ex_mem_1_out_19), .LH(ex_mem_1_out_20),
    .AluResult(ex_mem_1_out_24), .RD(ram_1_data), .WriteReg_num(ex_mem_1_out_26), .out_17(mem_wb_1_out_17),
    .out_18(RegWrite), .out_19(mem_wb_1_out_19[0]), .out_23(mem_wb_1_out_23), .out_24(mem_wb_1_out_24),
    .out_25(mem_wb_1_out_25), .EN(and_15_out), .RST(RST), .CLK(CLK), .PC_4(ex_mem_1_out_27),
    .out_26(mem_wb_1_out_26), .JAL(ex_mem_1_jal_2), .out_20(mem_wb_1_out_20), .PC(M_PC), .out_27(WB_PC),
    .Syscall(ex_mem_1_jal_3), .out_21(Syscall), .Instr(MEM_IR), .out_22(WB_IR), .A0(MDin), .out_28(A0),
    .V0(ex_mem_1_out_29), .out_29(V0));
  Multiplexer #(.select(1), .width(32), .disabled("Z"), .enable("false")) multiplexer_14 (
    .in0(mem_wb_1_out_23), .in1(mem_wb_1_out_24), .out(multiplexer_14_out), .sel(mem_wb_1_out_17));
  Shifter #(.width(32), .shift("ll")) shifter_2 (.in(multiplexer_14_out), .\dist (5'b10000), .out(shifter_2_out));
  Shifter #(.width(32), .shift("ar")) shifter_3 (.in(multiplexer_14_out), .\dist (5'b10000), .out(shifter_3_out));
  Shifter #(.width(32), .shift("ar")) shifter_4 (.in(shifter_2_out), .\dist (5'b10000), .out(shifter_4_out));
  Multiplexer #(.select(2), .width(32), .disabled("Z"), .enable("false")) multiplexer_15 (
    .in0(multiplexer_14_out), .in1(shifter_4_out), .in2(multiplexer_14_out), .in3(shifter_3_out),
    .out(multiplexer_15_out), .sel({mem_wb_1_out_23[1], mem_wb_1_out_19[0]}));
  Multiplexer #(.select(1), .width(32), .disabled("Z"), .enable("false")) multiplexer_16 (
    .in0(multiplexer_15_out), .in1(mem_wb_1_out_26), .out(RDin), .sel(mem_wb_1_out_20));

  // Other names for the same wires on the sheet: IR[31:0] = ID_IR; MEM_PC[31:0] = M_PC

  // Notes on the sheet:
  //   中断源
  //   时空图监测，可删除
  //   中断等待指示
  //   数码管输出
  //   控制位
  //   branch
  //   流水调试日志用
  //   暂停节拍，不能为0
  //   指令存储器
  //   戳工具置1进入计数暂停模式，ctrl+k时钟自动运行到对应节拍暂停
  //   ctrl+k关闭时钟连续运行，将控制位置零，进入单步调试模式调试
  //   IF/ID.EN
  //   contents of rom_1 (hex, n*v repeats v):
  //   20110001 8000c05 20110001 20120002 20130003 8000c09 20110001 20120002 20130003 8000c0d 20110001
  //   20120002 20130003 8000c11 20110001 20120002 20130003 c000cf9 20100001 20110001 118fc0 112020
  //   20020022 c 118882 12200001 8000c15 112020 20020022 c 20110001 118880 112020 20020022 c 12200001
  //   8000c1f 20110001 118fc0 112020 20020022 c 1188c3 112020 20020022 c 118903 112020 20020022 c 118903
  //   112020 20020022 c 118903 112020 20020022 c 118903 112020 20020022 c 118903 112020 20020022 c 118903
  //   112020 20020022 c 118903 112020 20020022 c 20100001 109fc0 139fc3 8021 2012000c 24160003 26100001
  //   3210000f 20080008 20090001 139900 2709825 132020 20020022 c 1094022 1500fff9 22100001 2018000f
  //   2188024 108700 20080008 20090001 139902 2709825 132021 20020022 c 1094022 1500fff9 108702 2c9b022
  //   12c00001 8000c50 4020 1084027 84400 3508ffff 82021 20020022 c 2010ffff 20110000 ae300000 22100001
  //   22310004 ae300000 22100001 22310004 ae300000 22100001 22310004 ae300000 22100001 22310004 ae300000
  //   22100001 22310004 ae300000 22100001 22310004 ae300000 22100001 22310004 ae300000 22100001 22310004
  //   ae300000 22100001 22310004 ae300000 22100001 22310004 ae300000 22100001 22310004 ae300000 22100001
  //   22310004 ae300000 22100001 22310004 ae300000 22100001 22310004 ae300000 22100001 22310004 ae300000
  //   22100001 22310004 22100001 8020 2011003c 8e130000 8e340000 274402a 11000002 ae330000 ae140000
  //   2231fffc 1611fff8 102020 20020022 c 22100004 2011003c 1611fff2 2002000a c 200b0008 3c11fedc 3631ffff
  //   112020 20020022 c 3c11ba98 112020 c 3c117654 112020 c 3c113210 112020 c 216bffff 1560fff0 2002000a c
  //   2008ffff 20117777 112020 20020022 c 200b0010 3a31ffff 112020 20020022 c 216bffff 1560fffa 2002000a c
  //   20090000 200b0010 34118483 20120404 118c00 129400 36318281 22520404 ad310000 2328820 21290004
  //   216bffff 1560fffb 200b0020 20090000 85310000 112020 20020022 c 21290002 216bffff 1560fff9 2002000a c
  //   2011000f 112020 20020022 c 2231ffff 621fffb 2002000a c 20100000 22100001 102020 20020022 c 22100002
  //   102020 20020022 c 22100003 102020 20020022 c 22100004 102020 20020022 c 22100005 102020 20020022 c
  //   22100006 102020 20020022 c 22100007 102020 20020022 c 22100008 102020 20020022 20020022 c 3e00008
  //   IF/ID/RST
  //   指令字
  //   可计数暂停的时钟源
  //   Instr
  //   OP
  //   Func
  //   rs
  //   rt
  //   rd
  //   JMP
  //   JR
  //   OP
  //   Func
  //   Syscall
  //   $ra
  //   Beq
  //   Bne
  //   MemToReg
  //   MemWrite
  //   AluOP
  //   AluSrcB
  //   RegWrite
  //   JAL
  //   RegDst
  //   LUI
  //   LH
  //   BGEZ
  //   为方便自动评测，需要输出流水线各段保存的PC值，注意是PC不是PC+4，另外ID段寄存器写入信息，Mem段内存写入信息也要输出
  //   PC+4
  //   ID/EX.RST
  //   WriteReg#
  //   RegWrite
  //   branch
  //   AluResult
  //   WriteBackData
  //   WriteReg#
  //   MemToReg
  //   MemWrite
  //   RegWrite
  //   JAL
  //   LH
  //   WriteData
  //   WriteReg#
  //   PC+4
  //   PC+4
  //   WriteBackData
endmodule

module \单周期MIPS_多级中断  (
  input  IR1,
  input  IR2,
  input  IR3,
  output RegWrite,
  output MemWrite,
  output [31:0] PC,
  output [31:0] IR,
  output [31:0] RDin,
  output [31:0] MDin,
  output [31:0] LedData
);

  wire and_2_out, and_3_out, and_4_out, and_5_out, beq, BGEZ, bne, CLK, clock_1_out, clock_2_out,
       comparator_1_eq, comparator_2_eq, comparator_3_eq, comparator_4_eq, comparator_5_eq, comparator_6_gt,
       comparator_7_eq, comparator_7_lt, comparator_8_eq, d_ff_2_q, ERET, Go, Halt, IE, INT1, INT2, INT3,
       INTC, INTO, INTR, IR1_t, IR2_t, IR3_t, IRA, IRB, IRC, JAL, LH, LUI, mips_alu_1_equal, nand_1_out,
       not_1_out, or_1_out, or_2_out, or_3_out, or_4_out, or_6_out, or_9_out, or_10_out, or_11_out,
       or_12_out, or_13_out, or_14_out, priority_encoder_1_gs, RESET, RST1, RST2, RST3, SignedExt, Syscall,
       W1, W2, W3, \单周期硬布线控制器_1_alu_src , \单周期硬布线控制器_1_jmp , \单周期硬布线控制器_1_jr , \单周期硬布线控制器_1_memtoreg ,
       \单周期硬布线控制器_1_regdst ;
  wire [1:0] INTN, multiplexer_6_out, multiplexer_7_out, multiplexer_10_out, Pri, register_2_q, register_3_q;
  wire [3:0] adder_1_out_2, \单周期硬布线控制器_1_alu_op ;
  wire [4:0] mips_probe_1_p3, multiplexer_11_out, multiplexer_13_out, multiplexer_14_out, shamt;
  wire [12:0] CNT_num;
  wire [15:0] \总周期数 ;
  wire [27:0] adder_1_out;
  wire [31:0] adder_2_out, bit_extender_1_out, bit_extender_2_out, EPC2_q, EPC3_q, EPCAddress, INTAddress,
       mips_alu_1_result, multiplexer_1_out, multiplexer_2_out, multiplexer_4_out, multiplexer_5_out,
       multiplexer_16_out, multiplexer_17_out, multiplexer_18_out, multiplexer_19_out, multiplexer_20_out,
       multiplexer_21_out, multiplexer_22_out, multiplexer_23_out, NextPC, PC_JR, ram_1_data, shifter_1_out,
       shifter_2_out, shifter_3_out, shifter_4_out;

  Clock #(.highDuration(1), .lowDuration(1)) clock_1 (.out(clock_1_out));
  Button _1 (.out(IRA));
  Button _2 (.out(IRB));
  Button _3 (.out(IRC));
  Button \u_继续运行  (.out(Go));
  LED #(.active("true")) led_1 (.in(W1));
  LED #(.active("true")) led_2 (.in(W2));
  LED #(.active("true")) led_3 (.in(W3));
  Hex_Digit_Display hex_digit_display_1 (.value(LedData[31:28]));  // open: dp
  Comparator #(.width(16), .mode("twosComplement")) comparator_1 (
    .a(\总周期数 ), .b(16'h7), .eq(comparator_1_eq));  // open: gt, lt
  Comparator #(.width(16), .mode("twosComplement")) comparator_2 (
    .a(\总周期数 ), .b(16'h241), .eq(comparator_2_eq));  // open: gt, lt
  Hex_Digit_Display hex_digit_display_2 (.value(LedData[23:20]));  // open: dp
  Hex_Digit_Display hex_digit_display_3 (.value(LedData[27:24]));  // open: dp
  Comparator #(.width(16), .mode("twosComplement")) comparator_3 (
    .a(16'h258), .b(\总周期数 ), .eq(comparator_3_eq));  // open: gt, lt
  or or_1 (or_1_out, comparator_3_eq, comparator_4_eq);
  Comparator #(.width(16), .mode("twosComplement")) comparator_4 (
    .a(\总周期数 ), .b(16'h1), .eq(comparator_4_eq));  // open: gt, lt
  Comparator #(.width(16), .mode("twosComplement")) comparator_5 (
    .a(\总周期数 ), .b(16'h4), .eq(comparator_5_eq));  // open: gt, lt
  or or_2 (or_2_out, comparator_1_eq, comparator_2_eq);
  Hex_Digit_Display hex_digit_display_4 (.value(LedData[19:16]));  // open: dp
  Hex_Digit_Display hex_digit_display_5 (.value(LedData[15:12]));  // open: dp
  Pull_Resistor #(.pull(0)) pull_resistor_1 (.node(IRA));
  assign IRA = or_1_out ? ~CLK : 1'bz;  // Controlled_Inverter controlled_inverter_1
  Pull_Resistor #(.pull(0)) pull_resistor_2 (.node(IRB));
  assign IRB = comparator_5_eq ? ~CLK : 1'bz;  // Controlled_Inverter controlled_inverter_2
  Pull_Resistor #(.pull(0)) pull_resistor_3 (.node(IRC));
  assign IRC = or_2_out ? ~CLK : 1'bz;  // Controlled_Inverter controlled_inverter_3
  \中断按键参考电路  \u_中断按键参考电路_1  (.\与中断屏蔽位与 (INT1), .\同步清零信号 (RST1), .CLK(CLK), .INT(IRA), .\中断等待指示灯 (W1));
  \中断按键参考电路  \u_中断按键参考电路_2  (.\与中断屏蔽位与 (INT2), .\同步清零信号 (RST2), .CLK(CLK), .INT(IRB), .\中断等待指示灯 (W2));
  \中断按键参考电路  \u_中断按键参考电路_3  (.\与中断屏蔽位与 (INT3), .\同步清零信号 (RST3), .CLK(CLK), .INT(IRC), .\中断等待指示灯 (W3));
  or or_3 (or_3_out, JAL, \单周期硬布线控制器_1_jmp );
  Multiplexer #(.select(1), .width(32), .disabled("Z"), .enable("false")) multiplexer_1 (
    .in0({adder_1_out_2, adder_1_out}), .in1(adder_2_out), .out(multiplexer_1_out), .sel(or_12_out));
  Hex_Digit_Display hex_digit_display_6 (.value(LedData[11:8]));  // open: dp
  Hex_Digit_Display hex_digit_display_7 (.value(LedData[7:4]));  // open: dp
  // Probe on \总周期数 
  Multiplexer #(.select(1), .width(32), .disabled("Z"), .enable("false")) multiplexer_2 (
    .in0(multiplexer_1_out), .in1({adder_1_out_2, IR[25:0], 2'b00}), .out(multiplexer_2_out), .sel(or_3_out));
  Multiplexer #(.select(1), .width(32), .disabled("Z"), .enable("false")) multiplexer_3 (
    .in0(multiplexer_2_out), .in1(PC_JR), .out(NextPC), .sel(\单周期硬布线控制器_1_jr ));
  Hex_Digit_Display hex_digit_display_8 (.value(LedData[3:0]));  // open: dp
  Multiplexer #(.select(1), .width(32), .disabled("Z"), .enable("false")) multiplexer_4 (
    .in0(NextPC), .in1(INTAddress), .out(multiplexer_4_out), .sel(INTR));
  // Probe on PC
  Multiplexer #(.select(1), .width(32), .disabled("Z"), .enable("false")) multiplexer_5 (
    .in0(multiplexer_4_out), .in1(EPCAddress), .out(multiplexer_5_out), .sel(ERET));
  or or_4 (or_4_out, ~Halt, Go);  // OR_Gate
  or or_5 (IR1_t, IR1, IRA);
  or or_6 (or_6_out, ERET, INTR);
  Register #(.width(32), .trigger("rising"), .Select("low")) u_PC (
    .D(multiplexer_5_out), .en(or_4_out), .Q(PC), .clk(CLK));  // open: clr
  or or_7 (IR2_t, IR2, IRB);
  Multiplexer #(.select(1), .width(2), .disabled("Z"), .enable("false")) multiplexer_6 (
    .in0(Pri), .in1(register_2_q), .out(multiplexer_6_out), .sel(ERET));
  Register #(.width(2), .trigger("rising"), .Select("low")) register_1 (
    .D(multiplexer_6_out), .en(or_6_out), .Q(INTN), .clk(CLK));  // open: clr
  Priority_Encoder #(.select(2), .disabled("Z")) priority_encoder_1 (
    .in1(INT1), .in2(INT2), .in3(INT3), .out(Pri), .gs(priority_encoder_1_gs));  // open: in0, en_out, en_in
  // Probe on PC
  Counter #(.width(16), .max('hffff), .ongoal("wrap"), .trigger("rising"), .behavior("new")) counter_1 (
    .count(or_4_out), .Q(\总周期数 ), .clk(CLK), .clr(RESET));  // open: load, D, carry, preset, down
  Multiplexer #(.select(1), .width(2), .disabled("Z"), .enable("false")) multiplexer_7 (
    .in0(INTN), .in1(register_3_q), .out(multiplexer_7_out), .sel(ERET));
  Multiplexer #(.select(2), .width(32), .disabled("Z"), .enable("false")) multiplexer_8 (
    .in1(32'h30ac), .in2(32'h3158), .in3(32'h3204), .out(INTAddress), .sel(Pri));  // open: in0
  Adder #(.width(32)) adder_1 (.a(PC), .b(32'h4), .out({adder_1_out_2, adder_1_out}));  // open: cin, cout
  or or_8 (IR3_t, IR3, IRC);
  Register #(.width(2), .trigger("rising"), .Select("low")) register_2 (
    .D(multiplexer_7_out), .en(or_6_out), .Q(register_2_q), .clk(CLK));  // open: clr
  Comparator #(.width(2), .mode("unsigned")) comparator_6 (.a(Pri), .b(INTN), .gt(comparator_6_gt));  // open: eq, lt
  // Mips_Probe mips_probe_1: pin names not known; wires that end beside it: IR, Syscall, mips_probe_1_p3
  ROM #(.addrWidth(10), .dataWidth(32), .Select("high")) rom_1 (.addr(PC[11:2]), .data(IR));
  Multiplexer #(.select(1), .width(5), .disabled("Z"), .enable("false")) multiplexer_9 (
    .in0(IR[10:6]), .in1(5'b10000), .out(shamt), .sel(LUI));
  Multiplexer #(.select(1), .width(2), .disabled("Z"), .enable("false")) multiplexer_10 (
    .in0(register_2_q), .in1(2'b00), .out(multiplexer_10_out), .sel(ERET));
  Pull_Resistor #(.pull(0)) pull_resistor_4 (.node(comparator_6_gt));
  Register #(.width(2), .trigger("rising"), .Select("low")) register_3 (
    .D(multiplexer_10_out), .en(or_6_out), .Q(register_3_q), .clk(CLK));  // open: clr
  and and_1 (INTR, comparator_6_gt, IE, priority_encoder_1_gs);
  Multiplexer #(.select(1), .width(5), .disabled("Z"), .enable("false")) multiplexer_11 (
    .in0(IR[20:16]), .in1(IR[15:11]), .out(multiplexer_11_out), .sel(\单周期硬布线控制器_1_regdst ));
  \单周期硬布线控制器  \u_单周期硬布线控制器_1  (
    .Func(IR[5:0]), .OP(IR[31:26]), .ALU_OP(\单周期硬布线控制器_1_alu_op ), .MemToReg(\单周期硬布线控制器_1_memtoreg ),
    .MemWrite(MemWrite), .ALU_SRC(\单周期硬布线控制器_1_alu_src ), .RegWrite(RegWrite), .SysCALL(Syscall),
    .SignedExt(SignedExt), .RegDst(\单周期硬布线控制器_1_regdst ), .JR(\单周期硬布线控制器_1_jr ), .JMP(\单周期硬布线控制器_1_jmp ),
    .Beq(beq), .JAL(JAL), .Bne(bne), .LUI(LUI), .LH(LH), .BGEZ(BGEZ), .ERET(ERET), .INTO(INTO), .INTC(INTC));  // open: rs, rt
  Multiplexer #(.select(1), .width(5), .disabled("Z"), .enable("false")) multiplexer_12 (
    .in0(IR[25:21]), .in1(5'b00010), .out(mips_probe_1_p3), .sel(Syscall));
  Multiplexer #(.select(1), .width(5), .disabled("Z"), .enable("false")) multiplexer_13 (
    .in0(IR[20:16]), .in1(5'b00100), .out(multiplexer_13_out), .sel(Syscall));
  Multiplexer #(.select(1), .width(5), .disabled("Z"), .enable("false")) multiplexer_14 (
    .in0(multiplexer_11_out), .in1({5{1'b1}}), .out(multiplexer_14_out), .sel(JAL));
  Multiplexer #(.select(1), .width(32), .disabled("Z"), .enable("false")) multiplexer_15 (
    .in0(multiplexer_23_out), .in1({adder_1_out_2, adder_1_out}), .out(RDin), .sel(JAL));
  Demultiplexer #(.select(2), .width(1), .tristate("false"), .disabled("Z"), .enable("false")) demultiplexer_1 (
    .out1(RST1), .out2(RST2), .out3(RST3), .in(ERET), .sel(INTN));  // open: out0
  MIPS_Regifile mips_regifile_1 (
    .Din(RDin), .Clk(CLK), .R1(PC_JR), .R2(MDin), .WE(RegWrite), .W_num(multiplexer_14_out),
    .R1_num(mips_probe_1_p3), .R2_num(multiplexer_13_out));
  assign bit_extender_1_out = {{16{1'b0}}, IR[15:0]};  // Bit_Extender bit_extender_1
  assign bit_extender_2_out = {{16{IR[15]}}, IR[15:0]};  // Bit_Extender bit_extender_2
  or or_9 (or_9_out, beq, SignedExt, bne, BGEZ);
  or or_10 (or_10_out, INTR, INTC);
  Multiplexer #(.select(1), .width(32), .disabled("Z"), .enable("false")) multiplexer_16 (
    .in0(bit_extender_1_out), .in1(bit_extender_2_out), .out(multiplexer_16_out), .sel(or_9_out));
  or or_11 (or_11_out, ERET, INTO, IE);
  D_Flip_Flop #(.trigger("rising"), .Pre_Clr_Positions("ABOVE_BELOW"), .NegatePresetClear("false"), .enable("true"), .NewFFLayout("true")) d_ff_1 (
    .clk(CLK), .D(or_10_out), .Qn(IE), .en(or_11_out));  // open: Q, preset, reset
  Multiplexer #(.select(1), .width(32), .disabled("Z"), .enable("false")) multiplexer_17 (
    .in0(MDin), .in1(multiplexer_16_out), .out(multiplexer_17_out), .sel(\单周期硬布线控制器_1_alu_src ));
  Multiplexer #(.select(1), .width(32), .disabled("Z"), .enable("false")) multiplexer_18 (
    .in0(multiplexer_17_out), .in1({32{1'b0}}), .out(multiplexer_18_out), .sel(BGEZ));
  Shifter #(.width(32), .shift("ll")) shifter_1 (.in(multiplexer_16_out), .\dist (5'b00010), .out(shifter_1_out));
  Button button_1 (.out(RESET));
  MIPS_ALU mips_alu_1 (
    .X(PC_JR), .Y(multiplexer_18_out), .AluOP(\单周期硬布线控制器_1_alu_op ), .Equal(mips_alu_1_equal),
    .Result(mips_alu_1_result), .shamt(shamt));  // open: Result_2
  Adder #(.width(32)) adder_2 (
    .a(shifter_1_out), .b({adder_1_out_2, adder_1_out}), .out(adder_2_out));  // open: cin, cout
  or or_12 (or_12_out, and_2_out, and_3_out, and_4_out);
  and and_2 (and_2_out, bne, not_1_out);
  not not_1 (not_1_out, mips_alu_1_equal);
  and and_3 (and_3_out, beq, mips_alu_1_equal);
  and and_4 (and_4_out, or_13_out, BGEZ);
  or or_13 (or_13_out, mips_alu_1_equal, ~mips_alu_1_result[0]);  // OR_Gate
  Multiplexer #(.select(1), .width(32), .disabled("Z"), .enable("false")) multiplexer_19 (
    .in0(NextPC), .in1(EPC2_q), .out(multiplexer_19_out), .sel(ERET));
  D_Flip_Flop #(.trigger("high"), .Pre_Clr_Positions("LEGACY"), .NegatePresetClear("false"), .enable("true"), .NewFFLayout("false")) d_ff_2 (.Q(d_ff_2_q));  // open: clk, D, Qn, preset, en, reset
  // Probe on 13'hcc
  Register #(.width(32), .trigger("rising"), .Select("low")) EPC1 (
    .D(multiplexer_19_out), .en(or_14_out), .Q(EPCAddress), .clk(CLK));  // open: clr
  or or_14 (or_14_out, ERET, INTR);
  Comparator #(.width(13), .mode("twosComplement")) comparator_7 (
    .a(CNT_num), .b(13'hcc), .eq(comparator_7_eq), .lt(comparator_7_lt));  // open: gt
  Clock #(.highDuration(1), .lowDuration(1)) clock_2 (.out(clock_2_out));
  Multiplexer #(.select(1), .width(32), .disabled("Z"), .enable("false")) multiplexer_20 (
    .in0(EPCAddress), .in1(EPC3_q), .out(multiplexer_20_out), .sel(ERET));
  RAM #(.addrWidth(10), .dataWidth(32), .bus("separate"), .Select("high")) ram_1 (
    .addr(mips_alu_1_result[11:2]), .din(MDin), .data(ram_1_data), .str(MemWrite), .clk(CLK), .clr(RESET));  // open: sel, ld
  nand nand_1 (nand_1_out, d_ff_2_q, comparator_7_eq);
  Counter #(.width(13), .max('h1fff), .ongoal("stay"), .trigger("rising"), .behavior("old")) counter_2 (
    .count(comparator_7_lt), .Q(CNT_num), .clk(clock_2_out));  // open: load, D, carry, clr, preset
  Multiplexer #(.select(1), .width(32), .disabled("Z"), .enable("false")) multiplexer_21 (
    .in0(mips_alu_1_result), .in1(ram_1_data), .out(multiplexer_21_out), .sel(\单周期硬布线控制器_1_memtoreg ));
  Register #(.width(32), .trigger("rising"), .Select("low")) EPC2 (
    .D(multiplexer_20_out), .en(or_14_out), .Q(EPC2_q), .clk(CLK));  // open: clr
  Shifter #(.width(32), .shift("ll")) shifter_2 (.in(multiplexer_21_out), .\dist (5'b10000), .out(shifter_2_out));
  Shifter #(.width(32), .shift("ar")) shifter_3 (.in(multiplexer_21_out), .\dist (5'b10000), .out(shifter_3_out));
  assign CLK = nand_1_out ? clock_2_out : 1'bz;  // Controlled_Buffer controlled_buffer_1
  Pull_Resistor #(.pull(1)) pull_resistor_5 (.node(CLK));
  Register #(.width(32), .trigger("rising"), .Select("low")) EPC3 (
    .D(multiplexer_22_out), .en(or_14_out), .Q(EPC3_q), .clk(CLK));  // open: clr
  Multiplexer #(.select(1), .width(32), .disabled("Z"), .enable("false")) multiplexer_22 (
    .in0(EPC2_q), .out(multiplexer_22_out), .sel(ERET));  // open: in1
  Shifter #(.width(32), .shift("ar")) shifter_4 (.in(shifter_2_out), .\dist (5'b10000), .out(shifter_4_out));
  Multiplexer #(.select(2), .width(32), .disabled("Z"), .enable("false")) multiplexer_23 (
    .in0(multiplexer_21_out), .in1(shifter_4_out), .in2(multiplexer_21_out), .in3(shifter_3_out),
    .out(multiplexer_23_out), .sel({mips_alu_1_result[1], LH}));
  Comparator #(.width(32), .mode("twosComplement")) comparator_8 (
    .a(PC_JR), .b(32'h32), .eq(comparator_8_eq));  // open: gt, lt
  and and_5 (and_5_out, ~comparator_8_eq, Syscall);  // AND_Gate
  and and_6 (Halt, comparator_8_eq, Syscall);
  Register #(.width(32), .trigger("rising"), .Select("low")) register_4 (
    .D(MDin), .en(and_5_out), .Q(LedData), .clk(CLK), .clr(RESET));

  // Other names for the same wires on the sheet: A0[31:0] = MDin; V0[31:0] = PC_JR

  // Notes on the sheet:
  //   中断源
  //   中断等待指示
  //   总复位信号应将除ROM以外所有存储组件全部清零
  //   多级中断测试信号模拟器
  //   中断生成
  //   数码管输出
  //   数码管输出应该用寄存器锁存，否则显示数据只能一闪而过
  //   中断号堆栈
  //   指令存储器
  //   branch
  //   指令字
  //   contents of rom_1 (hex, n*v repeats v):
  //   201d07d0 20100001 109fc0 139fc3 8021 2012000c 24160008 26100001 3210000f 20080008 20090001 139900
  //   2709825 132020 20020022 c 1094022 1500fff9 22100001 2018000f 2188024 108700 20080008 20090001 139902
  //   2709825 132021 20020022 c 1094022 1500fff9 108702 2c9b022 12c00001 8000c07 4020 1084027 84400
  //   3508ffff 82021 20020022 c 8000c01 afa20000 23bd0004 afa40000 23bd0004 afb00000 23bd0004 afb30000
  //   23bd0004 afb40000 23bd0004 afb50000 23bd0004 afb60000 23bd0004 40000000 20160001 20140003 20150001
  //   168020 108100 2149825 132020 20020022 c 1600fffa 295a022 1680fff7 40800000 23bdfffc 8fb60000
  //   23bdfffc 8fb50000 23bdfffc 8fb40000 23bdfffc 8fb30000 23bdfffc 8fb00000 23bdfffc 8fa40000 23bdfffc
  //   8fa20000 42000018 afa20000 23bd0004 afa40000 23bd0004 afb00000 23bd0004 afb30000 23bd0004 afb40000
  //   23bd0004 afb50000 23bd0004 afb60000 23bd0004 40000000 20160002 20140003 20150001 168020 108100
  //   2149825 132020 20020022 c 1600fffa 295a022 1680fff7 40800000 23bdfffc 8fb60000 23bdfffc 8fb50000
  //   23bdfffc 8fb40000 23bdfffc 8fb30000 23bdfffc 8fb00000 23bdfffc 8fa40000 23bdfffc 8fa20000 42000018
  //   afa20000 23bd0004 afa40000 23bd0004 afb00000 23bd0004 afb30000 23bd0004 afb40000 23bd0004 afb50000
  //   23bd0004 afb60000 23bd0004 40000000 20160003 20140003 20150001 168020 108100 2149825 132020 2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
  //   OP
  //   Func
  //   rs
  //   rt
  //   rd
  //   JMP
  //   JR
  //   OP
  //   Func
  //   Syscall
  //   $ra
  //   为方便自动评测，需要输出PC，IR，寄存器堆写如数据RDin
  //   Beq
  //   Bne
  //   MemToReg
  //   MemWrite
  //   AluOP
  //   AluSrcB
  //   RegWrite
  //   JAL
  //   RegDst
  //   LUI
  //   LH
  //   BGEZ
  //   RAM写使能MemWrite、RAM写入数据MDin等信号
  //   用这个时钟源需要去掉电路中的其他时钟源
  //   控制位
  //   暂停节拍，不能为0
  //   戳工具置1进入计数暂停模式，ctrl+k时钟自动运行到对应节拍暂停
  //   ctrl+k关闭时钟连续运行，将控制位置零，进入单步调试模式调试
  //   EPC堆栈
  //   可计数暂停的时钟源
endmodule

module \重定向流水线_单级中断  (
  input  IR1,
  input  IR2,
  input  IR3,
  output RegWrite,
  output MemWrite,
  output [31:0] IF_PC,
  output [31:0] ID_PC,
  output [31:0] EX_PC,
  output [31:0] M_PC,
  output [31:0] WB_PC,
  output [31:0] RDin,
  output [31:0] MDin,
  output [31:0] LedData
);

  wire and_1_out, and_2_out, and_3_out, and_4_out, and_5_out, and_6_out, and_7_out, and_9_out, and_10_out,
       and_11_out, and_12_out, and_13_out, and_14_out, and_15_out, and_16_out, and_17_out, B_EX, beq, BGEZ,
       bne, CLK, clock_1_out, comparator_1_eq, comparator_2_eq, comparator_3_eq, comparator_4_eq,
       comparator_5_eq, comparator_5_lt, comparator_6_eq, d_ff_1_q, ERET, ex_mem_1_jal_2, ex_mem_1_jal_3,
       ex_mem_1_out_17, ex_mem_1_out_19, ex_mem_1_out_20, GG, Go, Halt, id_ex_1_out_31, id_ex_1_out_32,
       id_ex_1_out_33, id_ex_1_out_34, id_ex_1_out_36, id_ex_1_out_37, id_ex_1_out_39, id_ex_1_out_40,
       id_ex_1_out_41, IE, INT1, INT2, INT3, IR1_t, IR2_t, IR3_t, IRA, IRB, IRC, JAL, JAL_EX, JMP_EX, JR_EX,
       \J型 , loaduse, LUI, mem_wb_1_out_17, mem_wb_1_out_20, mips_alu_1_equal, nand_1_out, not_1_out,
       not_2_out, not_3_out, not_4_out, not_5_out, or_3_out, or_4_out, or_7_out, or_8_out, or_9_out,
       or_10_out, or_11_out, or_13_out, or_14_out, or_17_out, PC_EN, priority_encoder_1_gs,
       pull_resistor_1_node, pull_resistor_2_node, pull_resistor_3_node, RST, RST1, RST2, RST3, RsUsed,
       RtUsed, SignedExt, Syscall, W1, W2, W3, \中断请求 , \单周期硬布线控制器_1_alu_src , \单周期硬布线控制器_1_jmp ,
       \单周期硬布线控制器_1_jr , \单周期硬布线控制器_1_lh , \单周期硬布线控制器_1_memtoreg , \单周期硬布线控制器_1_memwrite ,
       \单周期硬布线控制器_1_regdst , \单周期硬布线控制器_1_regwrite , \单周期硬布线控制器_1_syscall , \无条件 , \气泡 ,
       \重定向检测电路_1_id_ex_rst , \重定向检测电路_1_if_id_en ;
  wire [0:0] mem_wb_1_out_19;
  wire [1:0] id_ex_1_out_50, id_ex_1_out_51, priority_encoder_1_out, register_1_q, RsForward, RtForward;
  wire [3:0] id_ex_1_out_35, \单周期硬布线控制器_1_alu_op ;
  wire [4:0] ex_mem_1_out_26, id_ex_1_out_45, id_ex_1_out_46, mem_wb_1_out_25, multiplexer_6_out,
       multiplexer_7_out, multiplexer_10_out, R1_num, R2_num;
  wire [12:0] CNT_num;
  wire [15:0] \LoadUse次数 , \总周期数 , \插入气泡数 , \无条件分支数 , \条件分支成功数 ;
  wire [31:0] A0, adder_1_out, adder_2_out, bit_extender_1_out, bit_extender_2_out, EPCAddress, EX_IR,
       ex_mem_1_out_24, ex_mem_1_out_27, ex_mem_1_out_29, id_ex_1_out_43, id_ex_1_out_44, id_ex_1_out_47,
       id_ex_1_out_48, ID_IR, if_id_1_out_10, IF_IR, INTAddress, MEM_IR, mem_wb_1_out_23, mem_wb_1_out_24,
       mem_wb_1_out_26, mips_alu_1_result, mips_regifile_1_r1, mips_regifile_1_r2, multiplexer_1_out,
       multiplexer_2_out, multiplexer_4_out, multiplexer_5_out, multiplexer_12_out, multiplexer_14_out,
       multiplexer_15_out, multiplexer_16_out, multiplexer_17_out, multiplexer_18_out, NextPC, PC_JR,
       ram_1_data, shifter_1_out, shifter_2_out, shifter_3_out, shifter_4_out, V0, WB_IR;

  Button \u_总复位  (.out(RST));
  Button _1 (.out(IRA));
  Button _2 (.out(IRB));
  Button _3 (.out(IRC));
  // Probe on \总周期数 
  // Probe on \总周期数 
  Button \u_继续运行  (.out(Go));
  LED #(.active("true")) led_1 (.in(W1));
  LED #(.active("true")) led_2 (.in(W2));
  LED #(.active("true")) led_3 (.in(W3));
  Hex_Digit_Display hex_digit_display_1 (.value(LedData[31:28]));  // open: dp
  // Probe on IF_PC[19:0]
  // Mips_Probe mips_probe_1: pin names not known; wires that end beside it: IF_IR
  and and_1 (and_1_out, CLK, not_1_out);
  Hex_Digit_Display hex_digit_display_2 (.value(LedData[23:20]));  // open: dp
  Hex_Digit_Display hex_digit_display_3 (.value(LedData[27:24]));  // open: dp
  // Probe on ID_PC[19:0]
  // Mips_Probe mips_probe_2: pin names not known; wires that end beside it: ID_IR
  Counter #(.width(16), .max('hffff), .ongoal("wrap"), .trigger("falling"), .behavior("old")) counter_1 (
    .count(\无条件 ), .Q(\无条件分支数 ), .clk(and_1_out));  // open: load, D, carry, clr, preset
  not not_1 (not_1_out, Halt);
  Hex_Digit_Display hex_digit_display_4 (.value(LedData[19:16]));  // open: dp
  Hex_Digit_Display hex_digit_display_5 (.value(LedData[15:12]));  // open: dp
  and and_2 (and_2_out, CLK, not_2_out);
  Hex_Digit_Display hex_digit_display_6 (.value(LedData[7:4]));  // open: dp
  Hex_Digit_Display hex_digit_display_7 (.value(LedData[11:8]));  // open: dp
  // Probe on EX_PC[19:0]
  // Mips_Probe mips_probe_3: pin names not known; wires that end beside it: EX_IR
  Counter #(.width(16), .max('hffff), .ongoal("wrap"), .trigger("rising"), .behavior("old")) counter_2 (
    .count(B_EX), .Q(\条件分支成功数 ), .clk(and_2_out));  // open: load, D, carry, clr, preset
  not not_2 (not_2_out, Halt);
  or or_1 (\J型 , JAL_EX, JMP_EX);
  Multiplexer #(.select(1), .width(32), .disabled("Z"), .enable("false")) multiplexer_1 (
    .in0(adder_1_out), .in1(adder_2_out), .out(multiplexer_1_out), .sel(B_EX));
  Multiplexer #(.select(1), .width(32), .disabled("Z"), .enable("false")) multiplexer_2 (
    .in0(multiplexer_1_out), .in1({adder_1_out[31:28], EX_IR[25:0], 2'b00}), .out(multiplexer_2_out),
    .sel(\J型 ));
  Hex_Digit_Display hex_digit_display_8 (.value(LedData[3:0]));  // open: dp
  Multiplexer #(.select(1), .width(32), .disabled("Z"), .enable("false")) multiplexer_3 (
    .in0(multiplexer_2_out), .in1(PC_JR), .out(NextPC), .sel(JR_EX));
  Comparator #(.width(16), .mode("twosComplement")) comparator_1 (
    .a(16'h23b), .b(\总周期数 ), .eq(comparator_1_eq));  // open: gt, lt
  Comparator #(.width(16), .mode("twosComplement")) comparator_2 (
    .a(\总周期数 ), .b(16'h1), .eq(comparator_2_eq));  // open: gt, lt
  Comparator #(.width(16), .mode("twosComplement")) comparator_3 (
    .a(\总周期数 ), .b(16'h4), .eq(comparator_3_eq));  // open: gt, lt
  Comparator #(.width(16), .mode("twosComplement")) comparator_4 (
    .a(\总周期数 ), .b(16'h7), .eq(comparator_4_eq));  // open: gt, lt
  // Probe on \总周期数 
  // Probe on M_PC[19:0]
  // Mips_Probe mips_probe_4: pin names not known; wires that end beside it: MEM_IR
  or or_2 (\气泡 , B_EX, \无条件 );
  \重定向检测电路  \u_重定向检测电路_1  (
    .R1_num(R1_num), .R2_num(R2_num), .WriteReg__EX(id_ex_1_out_46), .WriteReg__MEM(ex_mem_1_out_26),
    .RsUsed(RsUsed), .RtUsed(RtUsed), .RegWrite_EX(id_ex_1_out_37), .RegWrite_MEM(ex_mem_1_out_19),
    .EX_MemToReg(id_ex_1_out_33), .Branch(B_EX), .RsForward(RsForward), .RtForward(RtForward), .PC_EN(PC_EN),
    .IF_ID_EN(\重定向检测电路_1_if_id_en ), .ID_EX_RST(\重定向检测电路_1_id_ex_rst ), .LoadUse(loaduse));  // open: IF_ID_RST
  Multiplexer #(.select(1), .width(32), .disabled("Z"), .enable("false")) multiplexer_4 (
    .in0(NextPC), .in1(INTAddress), .out(multiplexer_4_out), .sel(\中断请求 ));
  or or_3 (or_3_out, comparator_1_eq, comparator_2_eq);
  Pull_Resistor #(.pull(0)) pull_resistor_1 (.node(pull_resistor_1_node));
  assign pull_resistor_1_node = or_3_out ? ~CLK : 1'bz;  // Controlled_Inverter controlled_inverter_1
  Pull_Resistor #(.pull(0)) pull_resistor_2 (.node(pull_resistor_2_node));
  assign pull_resistor_2_node = comparator_3_eq ? ~CLK : 1'bz;  // Controlled_Inverter controlled_inverter_2
  Pull_Resistor #(.pull(0)) pull_resistor_3 (.node(pull_resistor_3_node));
  assign pull_resistor_3_node = comparator_4_eq ? ~CLK : 1'bz;  // Controlled_Inverter controlled_inverter_3
  // Probe on \总周期数 
  // Probe on \无条件分支数 
  // Probe on \条件分支成功数 
  // Probe on \插入气泡数 
  // Probe on \LoadUse次数 
  Multiplexer #(.select(1), .width(32), .disabled("Z"), .enable("false")) multiplexer_5 (
    .in0(multiplexer_4_out), .in1(EPCAddress), .out(multiplexer_5_out), .sel(ERET));
  or or_4 (or_4_out, \J型 , and_3_out);
  and and_3 (and_3_out, PC_EN, GG);
  // Probe on IF_PC[11:0]
  // Probe on WB_PC[19:0]
  // Mips_Probe mips_probe_5: pin names not known; wires that end beside it: WB_IR
  or or_5 (\无条件 , JMP_EX, JAL_EX, JR_EX);
  Register #(.width(32), .trigger("rising"), .Select("low")) PC (
    .D(multiplexer_5_out), .en(or_4_out), .Q(IF_PC), .clk(CLK));  // open: clr
  or or_6 (GG, ~Halt, Go);  // OR_Gate
  // Probe on ID_PC[11:0]
  // Probe on EX_PC[11:0]
  // Probe on M_PC[11:0]
  D_Flip_Flop #(.trigger("high"), .Pre_Clr_Positions("LEGACY"), .NegatePresetClear("false"), .enable("true"), .NewFFLayout("false")) d_ff_1 (.Q(d_ff_1_q));  // open: clk, D, Qn, preset, en, reset
  // Probe on 13'h165
  Adder #(.width(32)) adder_1 (.a(IF_PC), .b(32'h4), .out(adder_1_out));  // open: cin, cout
  Counter #(.width(16), .max('hffff), .ongoal("wrap"), .trigger("rising"), .behavior("new")) counter_3 (
    .count(GG), .Q(\总周期数 ), .clk(CLK), .clr(RST));  // open: load, D, carry, preset, down
  // Probe on WB_PC[11:0]
  Comparator #(.width(13), .mode("twosComplement")) comparator_5 (
    .a(CNT_num), .b(13'h165), .eq(comparator_5_eq), .lt(comparator_5_lt));  // open: gt
  Clock #(.highDuration(1), .lowDuration(1)) clock_1 (.out(clock_1_out));
  Counter #(.width(16), .max('hffff), .ongoal("wrap"), .trigger("rising"), .behavior("old")) counter_4 (
    .count(loaduse), .Q(\LoadUse次数 ), .clk(and_4_out));  // open: load, D, carry, clr, preset
  and and_4 (and_4_out, CLK, not_3_out);
  not not_3 (not_3_out, Halt);
  or or_7 (or_7_out, \重定向检测电路_1_if_id_en , or_14_out);
  and and_5 (and_5_out, GG, or_7_out);
  ROM #(.addrWidth(10), .dataWidth(32), .Select("high")) rom_1 (.addr(IF_PC[11:2]), .data(IF_IR));
  \中断按键参考电路  \u_中断按键参考电路_1  (.\与中断屏蔽位与 (INT1), .\同步清零信号 (RST1), .CLK(CLK), .INT(IRA), .\中断等待指示灯 (W1));
  \中断按键参考电路  \u_中断按键参考电路_2  (.\与中断屏蔽位与 (INT2), .\同步清零信号 (RST2), .CLK(CLK), .INT(IRB), .\中断等待指示灯 (W2));
  \中断按键参考电路  \u_中断按键参考电路_3  (.\与中断屏蔽位与 (INT3), .\同步清零信号 (RST3), .CLK(CLK), .INT(IRC), .\中断等待指示灯 (W3));
  nand nand_1 (nand_1_out, d_ff_1_q, comparator_5_eq);
  Counter #(.width(13), .max('h1fff), .ongoal("stay"), .trigger("rising"), .behavior("old")) counter_5 (
    .count(comparator_5_lt), .Q(CNT_num), .clk(clock_1_out));  // open: load, D, carry, clr, preset
  or or_8 (or_8_out, or_14_out, ERET);
  // Mips_Probe mips_probe_6: pin names not known; wires that end beside it: ID_IR
  IF_ID if_id_1 (
    .Instr(IF_IR), .PC_4(adder_1_out), .out_9(ID_IR), .out_10(if_id_1_out_10), .EN(and_5_out), .CLK(CLK),
    .RST(or_8_out), .PC(IF_PC), .out_11(ID_PC));  // open: PredictJump, out_8
  assign CLK = nand_1_out ? clock_1_out : 1'bz;  // Controlled_Buffer controlled_buffer_1
  Pull_Resistor #(.pull(1)) pull_resistor_4 (.node(CLK));
  and and_6 (and_6_out, \气泡 , ~loaduse);  // AND_Gate
  Multiplexer #(.select(1), .width(5), .disabled("Z"), .enable("false")) multiplexer_6 (
    .in0(ID_IR[20:16]), .in1(ID_IR[15:11]), .out(multiplexer_6_out), .sel(\单周期硬布线控制器_1_regdst ));
  Multiplexer #(.select(1), .width(5), .disabled("Z"), .enable("false")) multiplexer_7 (
    .in0(ID_IR[10:6]), .in1(5'b10000), .out(multiplexer_7_out), .sel(LUI));
  Counter #(.width(16), .max('hffff), .ongoal("wrap"), .trigger("rising"), .behavior("old")) counter_6 (
    .count(and_6_out), .Q(\插入气泡数 ), .clk(and_7_out));  // open: load, D, carry, clr, preset
  and and_7 (and_7_out, CLK, not_4_out);
  not not_4 (not_4_out, Halt);
  \单周期硬布线控制器  \u_单周期硬布线控制器_1  (
    .Func(ID_IR[5:0]), .OP(ID_IR[31:26]), .ALU_OP(\单周期硬布线控制器_1_alu_op ), .MemToReg(\单周期硬布线控制器_1_memtoreg ),
    .MemWrite(\单周期硬布线控制器_1_memwrite ), .ALU_SRC(\单周期硬布线控制器_1_alu_src ), .RegWrite(\单周期硬布线控制器_1_regwrite ),
    .SysCALL(\单周期硬布线控制器_1_syscall ), .SignedExt(SignedExt), .RegDst(\单周期硬布线控制器_1_regdst ),
    .JR(\单周期硬布线控制器_1_jr ), .JMP(\单周期硬布线控制器_1_jmp ), .Beq(beq), .JAL(JAL), .Bne(bne), .LUI(LUI),
    .LH(\单周期硬布线控制器_1_lh ), .BGEZ(BGEZ), .rs(RsUsed), .rt(RtUsed), .ERET(ERET));  // open: INTO, INTC
  Multiplexer #(.select(1), .width(5), .disabled("Z"), .enable("false")) multiplexer_8 (
    .in0(ID_IR[25:21]), .in1(5'b00010), .out(R1_num), .sel(\单周期硬布线控制器_1_syscall ));
  Multiplexer #(.select(1), .width(5), .disabled("Z"), .enable("false")) multiplexer_9 (
    .in0(ID_IR[20:16]), .in1(5'b00100), .out(R2_num), .sel(\单周期硬布线控制器_1_syscall ));
  Multiplexer #(.select(1), .width(5), .disabled("Z"), .enable("false")) multiplexer_10 (
    .in0(multiplexer_6_out), .in1({5{1'b1}}), .out(multiplexer_10_out), .sel(JAL));
  Priority_Encoder #(.select(2), .disabled("Z")) priority_encoder_1 (
    .in1(INT1), .in2(INT2), .in3(INT3), .out(priority_encoder_1_out), .gs(priority_encoder_1_gs));  // open: in0, en_out, en_in
  assign bit_extender_1_out = {{16{1'b0}}, ID_IR[15:0]};  // Bit_Extender bit_extender_1
  assign bit_extender_2_out = {{16{ID_IR[15]}}, ID_IR[15:0]};  // Bit_Extender bit_extender_2
  Multiplexer #(.select(2), .width(32), .disabled("Z"), .enable("false")) multiplexer_11 (
    .in1(32'h30ac), .in2(32'h3150), .in3(32'h31f4), .out(INTAddress), .sel(priority_encoder_1_out));  // open: in0
  and and_8 (\中断请求 , priority_encoder_1_gs, IE);
  MIPS_Regifile mips_regifile_1 (
    .Din(RDin), .Clk(CLK), .R1(mips_regifile_1_r1), .R2(mips_regifile_1_r2), .WE(RegWrite),
    .W_num(mem_wb_1_out_25), .R1_num(R1_num), .R2_num(R2_num));
  Multiplexer #(.select(1), .width(32), .disabled("Z"), .enable("false")) multiplexer_12 (
    .in0(bit_extender_1_out), .in1(bit_extender_2_out), .out(multiplexer_12_out), .sel(or_9_out));
  or or_9 (or_9_out, beq, SignedExt, bne, BGEZ);
  Comparator #(.width(32), .mode("twosComplement")) comparator_6 (
    .a(V0), .b(32'ha), .eq(comparator_6_eq));  // open: gt, lt
  or or_10 (or_10_out, \重定向检测电路_1_id_ex_rst , or_14_out);
  and and_9 (and_9_out, GG, 1'b1);
  ID_EX id_ex_1 (
    .BEQ(beq), .BNE(bne), .MemToReg(\单周期硬布线控制器_1_memtoreg ), .MemWrite(\单周期硬布线控制器_1_memwrite ),
    .AluOP(\单周期硬布线控制器_1_alu_op ), .AluSrc(\单周期硬布线控制器_1_alu_src ), .RegWrite(\单周期硬布线控制器_1_regwrite ),
    .JAL(JAL), .LH(\单周期硬布线控制器_1_lh ), .BGEZ(BGEZ), .RS(mips_regifile_1_r1), .RT(mips_regifile_1_r2),
    .shamt(multiplexer_7_out), .WriteReg_num(multiplexer_10_out), .Imm(multiplexer_12_out),
    .PC_4(if_id_1_out_10), .out_31(id_ex_1_out_31), .out_32(id_ex_1_out_32), .out_33(id_ex_1_out_33),
    .out_34(id_ex_1_out_34), .out_35(id_ex_1_out_35), .out_36(id_ex_1_out_36), .out_37(id_ex_1_out_37),
    .out_38(JAL_EX), .out_39(id_ex_1_out_39), .out_40(id_ex_1_out_40), .out_43(id_ex_1_out_43),
    .out_44(id_ex_1_out_44), .out_45(id_ex_1_out_45), .out_46(id_ex_1_out_46), .out_47(id_ex_1_out_47),
    .out_48(id_ex_1_out_48), .EN(and_9_out), .CLK(CLK), .RST(or_10_out), .PC(ID_PC), .out_49(EX_PC),
    .Syscall(\单周期硬布线控制器_1_syscall ), .out_41(id_ex_1_out_41), .JUMP(\单周期硬布线控制器_1_jmp ), .out_30(JMP_EX),
    .JR(\单周期硬布线控制器_1_jr ), .out_29(JR_EX), .Instr(ID_IR), .out_42(EX_IR), .RsForward(RsForward),
    .out_50(id_ex_1_out_50), .RtForward(RtForward), .out_51(id_ex_1_out_51));  // open: PredictJump, out_28
  Register #(.width(2), .trigger("rising"), .Select("low")) register_1 (
    .D(priority_encoder_1_out), .en(\中断请求 ), .Q(register_1_q), .clk(CLK));  // open: clr
  Register #(.width(32), .trigger("rising"), .Select("low")) register_2 (
    .D(A0), .en(and_10_out), .Q(LedData), .clk(CLK), .clr(RST));
  and and_10 (and_10_out, ~comparator_6_eq, Syscall);  // AND_Gate
  Register #(.width(1), .trigger("rising"), .Select("low")) register_3 (
    .D(and_11_out), .en(or_11_out), .Q(Halt), .clk(CLK), .clr(RST));
  and and_11 (and_11_out, comparator_6_eq, Syscall);
  or or_11 (or_11_out, ~Halt, Go);  // OR_Gate
  Demultiplexer #(.select(2), .width(1), .tristate("false"), .disabled("Z"), .enable("false")) demultiplexer_1 (
    .out1(RST1), .out2(RST2), .out3(RST3), .in(ERET), .sel(register_1_q));  // open: out0
  Multiplexer #(.select(2), .width(32), .disabled("Z"), .enable("false")) multiplexer_13 (
    .in0(id_ex_1_out_43), .in1(RDin), .in2(ex_mem_1_out_24), .out(PC_JR), .sel(id_ex_1_out_50));  // open: in3
  Multiplexer #(.select(2), .width(32), .disabled("Z"), .enable("false")) multiplexer_14 (
    .in0(id_ex_1_out_44), .in1(RDin), .in2(ex_mem_1_out_24), .out(multiplexer_14_out), .sel(id_ex_1_out_51));  // open: in3
  Multiplexer #(.select(1), .width(32), .disabled("Z"), .enable("false")) multiplexer_15 (
    .in0(multiplexer_14_out), .in1(id_ex_1_out_47), .out(multiplexer_15_out), .sel(id_ex_1_out_36));
  Shifter #(.width(32), .shift("ll")) shifter_1 (.in(id_ex_1_out_47), .\dist (5'b00010), .out(shifter_1_out));
  or or_12 (IR1_t, IR1, IRA);
  Multiplexer #(.select(1), .width(32), .disabled("Z"), .enable("false")) multiplexer_16 (
    .in0(multiplexer_15_out), .in1({32{1'b0}}), .out(multiplexer_16_out), .sel(id_ex_1_out_40));
  Adder #(.width(32)) adder_2 (.a(shifter_1_out), .b(id_ex_1_out_48), .out(adder_2_out));  // open: cin, cout
  or or_13 (or_13_out, ERET, IE);
  or or_14 (or_14_out, JR_EX, JMP_EX, JAL_EX, B_EX);
  and and_12 (and_12_out, id_ex_1_out_32, not_5_out);
  not not_5 (not_5_out, mips_alu_1_equal);
  and and_13 (and_13_out, id_ex_1_out_31, mips_alu_1_equal);
  MIPS_ALU mips_alu_1 (
    .X(PC_JR), .Y(multiplexer_16_out), .AluOP(id_ex_1_out_35), .Equal(mips_alu_1_equal),
    .Result(mips_alu_1_result), .shamt(id_ex_1_out_45));  // open: Result_2
  D_Flip_Flop #(.trigger("rising"), .Pre_Clr_Positions("ABOVE_BELOW"), .NegatePresetClear("false"), .enable("true"), .NewFFLayout("true")) d_ff_2 (
    .clk(CLK), .D(\中断请求 ), .Qn(IE), .en(or_13_out));  // open: Q, preset, reset
  or or_15 (IR2_t, IR2, IRB);
  or or_16 (B_EX, and_12_out, and_13_out, and_14_out);
  and and_14 (and_14_out, or_17_out, id_ex_1_out_40);
  or or_17 (or_17_out, mips_alu_1_equal, ~mips_alu_1_result[0]);  // OR_Gate
  and and_15 (and_15_out, GG, 1'b1);
  and and_16 (and_16_out, \中断请求 , IE);
  or or_18 (IR3_t, IR3, IRC);
  EX_MEM ex_mem_1 (
    .MemtoReg(id_ex_1_out_33), .MemWrite(id_ex_1_out_34), .RegWrite(id_ex_1_out_37), .LH(id_ex_1_out_39),
    .Result(mips_alu_1_result), .WriteData(multiplexer_14_out), .WriteReg_num(id_ex_1_out_46),
    .out_17(ex_mem_1_out_17), .out_18(MemWrite), .out_19(ex_mem_1_out_19), .out_20(ex_mem_1_out_20),
    .out_24(ex_mem_1_out_24), .out_25(MDin), .out_26(ex_mem_1_out_26), .EN(and_15_out), .RST(RST), .CLK(CLK),
    .JAL(JAL_EX), .JAL_2(ex_mem_1_jal_2), .PC_4(id_ex_1_out_48), .out_27(ex_mem_1_out_27), .PC(EX_PC),
    .out_28(M_PC), .Syscall(id_ex_1_out_41), .JAL_3(ex_mem_1_jal_3), .Instr(EX_IR), .out_23(MEM_IR),
    .V0(PC_JR), .out_29(ex_mem_1_out_29));
  Register #(.width(32), .trigger("rising"), .Select("low")) register_4 (
    .D(NextPC), .en(and_16_out), .Q(EPCAddress), .clk(CLK));  // open: clr
  RAM #(.addrWidth(10), .dataWidth(32), .bus("separate"), .Select("high")) ram_1 (
    .addr(ex_mem_1_out_24[11:2]), .din(MDin), .data(ram_1_data), .str(MemWrite), .clk(CLK), .clr(RST));  // open: sel, ld
  and and_17 (and_17_out, GG, 1'b1);
  MEM_WB mem_wb_1 (
    .MemtoReg(ex_mem_1_out_17), .RegWrite(ex_mem_1_out_19), .LH(ex_mem_1_out_20),
    .AluResult(ex_mem_1_out_24), .RD(ram_1_data), .WriteReg_num(ex_mem_1_out_26), .out_17(mem_wb_1_out_17),
    .out_18(RegWrite), .out_19(mem_wb_1_out_19[0]), .out_23(mem_wb_1_out_23), .out_24(mem_wb_1_out_24),
    .out_25(mem_wb_1_out_25), .EN(and_17_out), .RST(RST), .CLK(CLK), .PC_4(ex_mem_1_out_27),
    .out_26(mem_wb_1_out_26), .JAL(ex_mem_1_jal_2), .out_20(mem_wb_1_out_20), .PC(M_PC), .out_27(WB_PC),
    .Syscall(ex_mem_1_jal_3), .out_21(Syscall), .Instr(MEM_IR), .out_22(WB_IR), .A0(MDin), .out_28(A0),
    .V0(ex_mem_1_out_29), .out_29(V0));
  Multiplexer #(.select(1), .width(32), .disabled("Z"), .enable("false")) multiplexer_17 (
    .in0(mem_wb_1_out_23), .in1(mem_wb_1_out_24), .out(multiplexer_17_out), .sel(mem_wb_1_out_17));
  Shifter #(.width(32), .shift("ll")) shifter_2 (.in(multiplexer_17_out), .\dist (5'b10000), .out(shifter_2_out));
  Shifter #(.width(32), .shift("ar")) shifter_3 (.in(multiplexer_17_out), .\dist (5'b10000), .out(shifter_3_out));
  Shifter #(.width(32), .shift("ar")) shifter_4 (.in(shifter_2_out), .\dist (5'b10000), .out(shifter_4_out));
  Multiplexer #(.select(2), .width(32), .disabled("Z"), .enable("false")) multiplexer_18 (
    .in0(multiplexer_17_out), .in1(shifter_4_out), .in2(multiplexer_17_out), .in3(shifter_3_out),
    .out(multiplexer_18_out), .sel({mem_wb_1_out_23[1], mem_wb_1_out_19[0]}));
  Multiplexer #(.select(1), .width(32), .disabled("Z"), .enable("false")) multiplexer_19 (
    .in0(multiplexer_18_out), .in1(mem_wb_1_out_26), .out(RDin), .sel(mem_wb_1_out_20));

  // Other names for the same wires on the sheet: IR[31:0] = ID_IR; MEM_PC[31:0] = M_PC

  // Notes on the sheet:
  //   中断源
  //   时空图监测，可删除
  //   中断等待指示
  //   数码管输出
  //   单级中断测试信号模拟器
  //   控制位
  //   branch
  //   流水调试日志用
  //   暂停节拍，不能为0
  //   指令存储器
  //   戳工具置1进入计数暂停模式，ctrl+k时钟自动运行到对应节拍暂停
  //   ctrl+k关闭时钟连续运行，将控制位置零，进入单步调试模式调试
  //   IF/ID.EN
  //   contents of rom_1 (hex, n*v repeats v):
  //   201d07d0 20100001 109fc0 139fc3 8021 2012000c 24160008 26100001 3210000f 20080008 20090001 139900
  //   2709825 132020 20020022 c 1094022 1500fff9 22100001 2018000f 2188024 108700 20080008 20090001 139902
  //   2709825 132021 20020022 c 1094022 1500fff9 108702 2c9b022 12c00001 8000c07 4020 1084027 84400
  //   3508fff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
  //   IF/ID/RST
  //   指令字
  //   可计数暂停的时钟源
  //   Instr
  //   OP
  //   Func
  //   rs
  //   rt
  //   rd
  //   JMP
  //   JR
  //   OP
  //   Func
  //   Syscall
  //   $ra
  //   Beq
  //   Bne
  //   MemToReg
  //   MemWrite
  //   AluOP
  //   AluSrcB
  //   RegWrite
  //   JAL
  //   RegDst
  //   LUI
  //   LH
  //   BGEZ
  //   为方便自动评测，需要输出流水线各段保存的PC值，注意是PC不是PC+4，另外ID段寄存器写入信息，Mem段内存写入信息也要输出
  //   PC+4
  //   WriteReg#
  //   ID/EX.RST
  //   RegWrite
  //   branch
  //   AluResult
  //   WriteBackData
  //   WriteReg#
  //   MemToReg
  //   MemWrite
  //   RegWrite
  //   JAL
  //   LH
  //   WriteData
  //   WriteReg#
  //   PC+4
  //   PC+4
  //   WriteBackData
endmodule

module \重定向流水线_动态分支预测  (
  output RegWrite,
  output MemWrite,
  output [31:0] IF_PC,
  output [31:0] ID_PC,
  output [31:0] EX_PC,
  output [31:0] M_PC,
  output [31:0] WB_PC,
  output [31:0] RDin,
  output [31:0] MDin,
  output [31:0] LedData
);

  wire and_1_out, and_2_out, and_3_out, and_4_out, and_5_out, and_6_out, and_7_out, and_8_out, and_9_out,
       and_10_out, and_11_out, and_12_out, and_13_out, and_14_out, and_15_out, B_EX, beq, Beq_EX, BGEZ,
       BGEZ_EX, bne, Bne_EX, CLK, clock_1_out, comparator_1_eq, comparator_1_lt, comparator_2_eq, d_ff_1_q,
       EX_Branch, EX_BranchTaken, ex_mem_1_jal_2, ex_mem_1_jal_3, ex_mem_1_out_17, ex_mem_1_out_19,
       ex_mem_1_out_20, GG, Go, Halt, id_ex_1_out_28, id_ex_1_out_33, id_ex_1_out_34, id_ex_1_out_36,
       id_ex_1_out_37, id_ex_1_out_39, id_ex_1_out_41, if_id_1_out_8, IR1, IR2, IR3, J, JAL, JAL_EX, JMP_EX,
       JR_EX, loaduse, LUI, mem_wb_1_out_17, mem_wb_1_out_20, mips_alu_1_equal, nand_1_out, not_1_out,
       not_2_out, not_3_out, not_4_out, not_5_out, or_7_out, or_8_out, or_9_out, or_10_out, or_12_out, PC_EN,
       PredictJump, RST, RsUsed, RtUsed, SignedExt, Syscall, W1, W2, W3, xor_1_out, \单周期硬布线控制器_1_alu_src ,
       \单周期硬布线控制器_1_jmp , \单周期硬布线控制器_1_jr , \单周期硬布线控制器_1_lh , \单周期硬布线控制器_1_memtoreg , \单周期硬布线控制器_1_memwrite ,
       \单周期硬布线控制器_1_regdst , \单周期硬布线控制器_1_regwrite , \单周期硬布线控制器_1_syscall , \无条件 , \气泡 ,
       \重定向检测电路_1_id_ex_rst , \重定向检测电路_1_if_id_en ;
  wire [0:0] mem_wb_1_out_19;
  wire [1:0] id_ex_1_out_50, id_ex_1_out_51, RsForward, RtForward;
  wire [3:0] id_ex_1_out_35, \单周期硬布线控制器_1_alu_op ;
  wire [4:0] ex_mem_1_out_26, id_ex_1_out_45, id_ex_1_out_46, mem_wb_1_out_25, multiplexer_6_out,
       multiplexer_7_out, multiplexer_10_out, R1_num, R2_num;
  wire [12:0] CNT_num;
  wire [15:0] \LoadUse次数 , \总周期数 , \插入气泡数 , \无条件分支数 , \条件分支成功数 ;
  wire [31:0] A0, adder_1_out, adder_2_out, adder_3_out, bit_extender_1_out, bit_extender_2_out,
       btb_1_jumpaddr, EX_IR, ex_mem_1_out_24, ex_mem_1_out_27, ex_mem_1_out_29, id_ex_1_out_43,
       id_ex_1_out_44, id_ex_1_out_47, id_ex_1_out_48, ID_IR, if_id_1_out_10, IF_IR, MEM_IR, mem_wb_1_out_23,
       mem_wb_1_out_24, mem_wb_1_out_26, mips_alu_1_result, mips_regifile_1_r1, mips_regifile_1_r2,
       multiplexer_1_out, multiplexer_2_out, multiplexer_3_out, multiplexer_4_out, multiplexer_5_out,
       multiplexer_11_out, multiplexer_13_out, multiplexer_14_out, multiplexer_15_out, multiplexer_16_out,
       multiplexer_17_out, PC_JR, ram_1_data, shifter_1_out, shifter_2_out, shifter_3_out, shifter_4_out, V0,
       WB_IR;

  Button \u_总复位  (.out(RST));
  Button _1 (.out(IR1));
  Button _2 (.out(IR2));
  Button _3 (.out(IR3));
  // Probe on \总周期数 
  // Probe on \总周期数 
  Button \u_继续运行  (.out(Go));
  LED #(.active("true")) led_1 (.in(W1));
  LED #(.active("true")) led_2 (.in(W2));
  LED #(.active("true")) led_3 (.in(W3));
  Multiplexer #(.select(1), .width(32), .disabled("Z"), .enable("false")) multiplexer_1 (
    .in0(multiplexer_2_out), .in1(PC_JR), .out(multiplexer_1_out), .sel(JR_EX));
  Hex_Digit_Display hex_digit_display_1 (.value(LedData[31:28]));  // open: dp
  // Probe on IF_PC[19:0]
  // Mips_Probe mips_probe_1: pin names not known; wires that end beside it: IF_IR
  and and_1 (and_1_out, CLK, not_1_out);
  Multiplexer #(.select(1), .width(32), .disabled("Z"), .enable("false")) multiplexer_2 (
    .in0(multiplexer_4_out), .in1({EX_PC[31:28], EX_IR[25:0], 2'b00}), .out(multiplexer_2_out), .sel(J));
  Hex_Digit_Display hex_digit_display_2 (.value(LedData[23:20]));  // open: dp
  Hex_Digit_Display hex_digit_display_3 (.value(LedData[27:24]));  // open: dp
  // Probe on ID_PC[19:0]
  // Mips_Probe mips_probe_2: pin names not known; wires that end beside it: ID_IR
  Counter #(.width(16), .max('hffff), .ongoal("wrap"), .trigger("falling"), .behavior("old")) counter_1 (
    .count(\无条件 ), .Q(\无条件分支数 ), .clk(and_1_out));  // open: load, D, carry, clr, preset
  not not_1 (not_1_out, Halt);
  Hex_Digit_Display hex_digit_display_4 (.value(LedData[19:16]));  // open: dp
  Hex_Digit_Display hex_digit_display_5 (.value(LedData[15:12]));  // open: dp
  and and_2 (and_2_out, CLK, not_2_out);
  Multiplexer #(.select(1), .width(32), .disabled("Z"), .enable("false")) multiplexer_3 (
    .in0(multiplexer_5_out), .in1(multiplexer_1_out), .out(multiplexer_3_out), .sel(xor_1_out));
  Multiplexer #(.select(1), .width(32), .disabled("Z"), .enable("false")) multiplexer_4 (
    .in0(adder_1_out), .in1(adder_3_out), .out(multiplexer_4_out), .sel(B_EX));
  Adder #(.width(32)) adder_1 (.a(32'h4), .b(EX_PC), .out(adder_1_out));  // open: cin, cout
  Hex_Digit_Display hex_digit_display_6 (.value(LedData[11:8]));  // open: dp
  Hex_Digit_Display hex_digit_display_7 (.value(LedData[7:4]));  // open: dp
  // Probe on EX_PC[19:0]
  // Mips_Probe mips_probe_3: pin names not known; wires that end beside it: EX_IR
  Counter #(.width(16), .max('hffff), .ongoal("wrap"), .trigger("rising"), .behavior("old")) counter_2 (
    .count(B_EX), .Q(\条件分支成功数 ), .clk(and_2_out));  // open: load, D, carry, clr, preset
  not not_2 (not_2_out, Halt);
  or or_1 (EX_Branch, Beq_EX, Bne_EX, BGEZ_EX, JAL_EX, JMP_EX);
  or or_2 (J, JMP_EX, JAL_EX);
  or or_3 (EX_BranchTaken, B_EX, JAL_EX, JMP_EX);
  Hex_Digit_Display hex_digit_display_8 (.value(LedData[3:0]));  // open: dp
  BTB btb_1 (
    .PC(IF_PC), .EX_PC(EX_PC), .EX_PredictErr(EX_BranchTaken), .CLK(CLK), .EX_Branch(EX_Branch),
    .EX_BranchAddr(multiplexer_1_out), .JumpAddr(btb_1_jumpaddr), .PredictJump(PredictJump));
  Multiplexer #(.select(1), .width(32), .disabled("Z"), .enable("false")) multiplexer_5 (
    .in0(adder_2_out), .in1(btb_1_jumpaddr), .out(multiplexer_5_out), .sel(PredictJump));
  // Probe on \总周期数 
  // Probe on M_PC[19:0]
  // Mips_Probe mips_probe_4: pin names not known; wires that end beside it: MEM_IR
  or or_4 (\气泡 , B_EX, \无条件 );
  \重定向检测电路  \u_重定向检测电路_1  (
    .R1_num(R1_num), .R2_num(R2_num), .WriteReg__EX(id_ex_1_out_46), .WriteReg__MEM(ex_mem_1_out_26),
    .RsUsed(RsUsed), .RtUsed(RtUsed), .RegWrite_EX(id_ex_1_out_37), .RegWrite_MEM(ex_mem_1_out_19),
    .EX_MemToReg(id_ex_1_out_33), .Branch(xor_1_out), .RsForward(RsForward), .RtForward(RtForward),
    .PC_EN(PC_EN), .IF_ID_EN(\重定向检测电路_1_if_id_en ), .ID_EX_RST(\重定向检测电路_1_id_ex_rst ), .LoadUse(loaduse));  // open: IF_ID_RST
  // Probe on \总周期数 
  // Probe on \无条件分支数 
  // Probe on \条件分支成功数 
  // Probe on \插入气泡数 
  // Probe on \LoadUse次数 
  and and_3 (and_3_out, PC_EN, GG);
  // Probe on IF_PC[11:0]
  // Probe on WB_PC[19:0]
  // Mips_Probe mips_probe_5: pin names not known; wires that end beside it: WB_IR
  or or_5 (\无条件 , JMP_EX, JAL_EX, JR_EX);
  Register #(.width(32), .trigger("rising"), .Select("low")) PC (
    .D(multiplexer_3_out), .en(and_3_out), .Q(IF_PC), .clk(CLK));  // open: clr
  or or_6 (GG, ~Halt, Go);  // OR_Gate
  // Probe on EX_PC[11:0]
  // Probe on ID_PC[11:0]
  Counter #(.width(16), .max('hffff), .ongoal("wrap"), .trigger("rising"), .behavior("new")) counter_3 (
    .count(GG), .Q(\总周期数 ), .clk(CLK), .clr(RST));  // open: load, D, carry, preset, down
  // Probe on M_PC[11:0]
  D_Flip_Flop #(.trigger("high"), .Pre_Clr_Positions("LEGACY"), .NegatePresetClear("false"), .enable("true"), .NewFFLayout("false")) d_ff_1 (.Q(d_ff_1_q));  // open: clk, D, Qn, preset, en, reset
  // Probe on 13'h1b3
  Adder #(.width(32)) adder_2 (.a(IF_PC), .b(32'h4), .out(adder_2_out));  // open: cin, cout
  // Probe on WB_PC[11:0]
  Comparator #(.width(13), .mode("twosComplement")) comparator_1 (
    .a(CNT_num), .b(13'h1b3), .eq(comparator_1_eq), .lt(comparator_1_lt));  // open: gt
  Clock #(.highDuration(1), .lowDuration(1)) clock_1 (.out(clock_1_out));
  Counter #(.width(16), .max('hffff), .ongoal("wrap"), .trigger("rising"), .behavior("old")) counter_4 (
    .count(loaduse), .Q(\LoadUse次数 ), .clk(and_4_out));  // open: load, D, carry, clr, preset
  and and_4 (and_4_out, CLK, not_3_out);
  not not_3 (not_3_out, Halt);
  or or_7 (or_7_out, \重定向检测电路_1_if_id_en , or_10_out);
  and and_5 (and_5_out, GG, or_7_out);
  ROM #(.addrWidth(10), .dataWidth(32), .Select("high")) rom_1 (.addr(IF_PC[11:2]), .data(IF_IR));
  nand nand_1 (nand_1_out, d_ff_1_q, comparator_1_eq);
  Counter #(.width(13), .max('h1fff), .ongoal("stay"), .trigger("rising"), .behavior("old")) counter_5 (
    .count(comparator_1_lt), .Q(CNT_num), .clk(clock_1_out));  // open: load, D, carry, clr, preset
  // Mips_Probe mips_probe_6: pin names not known; wires that end beside it: ID_IR
  IF_ID if_id_1 (
    .Instr(IF_IR), .PC_4(adder_2_out), .out_9(ID_IR), .out_10(if_id_1_out_10), .EN(and_5_out), .CLK(CLK),
    .RST(xor_1_out), .PC(IF_PC), .out_11(ID_PC), .PredictJump(PredictJump), .out_8(if_id_1_out_8));
  assign CLK = nand_1_out ? clock_1_out : 1'bz;  // Controlled_Buffer controlled_buffer_1
  Pull_Resistor #(.pull(1)) pull_resistor_1 (.node(CLK));
  and and_6 (and_6_out, \气泡 , ~loaduse);  // AND_Gate
  Multiplexer #(.select(1), .width(5), .disabled("Z"), .enable("false")) multiplexer_6 (
    .in0(ID_IR[20:16]), .in1(ID_IR[15:11]), .out(multiplexer_6_out), .sel(\单周期硬布线控制器_1_regdst ));
  Multiplexer #(.select(1), .width(5), .disabled("Z"), .enable("false")) multiplexer_7 (
    .in0(ID_IR[10:6]), .in1(5'b10000), .out(multiplexer_7_out), .sel(LUI));
  Counter #(.width(16), .max('hffff), .ongoal("wrap"), .trigger("rising"), .behavior("old")) counter_6 (
    .count(and_6_out), .Q(\插入气泡数 ), .clk(and_7_out));  // open: load, D, carry, clr, preset
  and and_7 (and_7_out, CLK, not_4_out);
  not not_4 (not_4_out, Halt);
  \单周期硬布线控制器  \u_单周期硬布线控制器_1  (
    .Func(ID_IR[5:0]), .OP(ID_IR[31:26]), .ALU_OP(\单周期硬布线控制器_1_alu_op ), .MemToReg(\单周期硬布线控制器_1_memtoreg ),
    .MemWrite(\单周期硬布线控制器_1_memwrite ), .ALU_SRC(\单周期硬布线控制器_1_alu_src ), .RegWrite(\单周期硬布线控制器_1_regwrite ),
    .SysCALL(\单周期硬布线控制器_1_syscall ), .SignedExt(SignedExt), .RegDst(\单周期硬布线控制器_1_regdst ),
    .JR(\单周期硬布线控制器_1_jr ), .JMP(\单周期硬布线控制器_1_jmp ), .Beq(beq), .JAL(JAL), .Bne(bne), .LUI(LUI),
    .LH(\单周期硬布线控制器_1_lh ), .BGEZ(BGEZ), .rs(RsUsed), .rt(RtUsed));  // open: ERET, INTO, INTC
  Multiplexer #(.select(1), .width(5), .disabled("Z"), .enable("false")) multiplexer_8 (
    .in0(ID_IR[25:21]), .in1(5'b00010), .out(R1_num), .sel(\单周期硬布线控制器_1_syscall ));
  Multiplexer #(.select(1), .width(5), .disabled("Z"), .enable("false")) multiplexer_9 (
    .in0(ID_IR[20:16]), .in1(5'b00100), .out(R2_num), .sel(\单周期硬布线控制器_1_syscall ));
  Multiplexer #(.select(1), .width(5), .disabled("Z"), .enable("false")) multiplexer_10 (
    .in0(multiplexer_6_out), .in1({5{1'b1}}), .out(multiplexer_10_out), .sel(JAL));
  assign bit_extender_1_out = {{16{1'b0}}, ID_IR[15:0]};  // Bit_Extender bit_extender_1
  assign bit_extender_2_out = {{16{ID_IR[15]}}, ID_IR[15:0]};  // Bit_Extender bit_extender_2
  MIPS_Regifile mips_regifile_1 (
    .Din(RDin), .Clk(CLK), .R1(mips_regifile_1_r1), .R2(mips_regifile_1_r2), .WE(RegWrite),
    .W_num(mem_wb_1_out_25), .R1_num(R1_num), .R2_num(R2_num));
  Multiplexer #(.select(1), .width(32), .disabled("Z"), .enable("false")) multiplexer_11 (
    .in0(bit_extender_1_out), .in1(bit_extender_2_out), .out(multiplexer_11_out), .sel(or_8_out));
  or or_8 (or_8_out, beq, SignedExt, bne, BGEZ);
  Comparator #(.width(32), .mode("twosComplement")) comparator_2 (
    .a(V0), .b(32'ha), .eq(comparator_2_eq));  // open: gt, lt
  and and_8 (and_8_out, GG, 1'b1);
  ID_EX id_ex_1 (
    .BEQ(beq), .BNE(bne), .MemToReg(\单周期硬布线控制器_1_memtoreg ), .MemWrite(\单周期硬布线控制器_1_memwrite ),
    .AluOP(\单周期硬布线控制器_1_alu_op ), .AluSrc(\单周期硬布线控制器_1_alu_src ), .RegWrite(\单周期硬布线控制器_1_regwrite ),
    .JAL(JAL), .LH(\单周期硬布线控制器_1_lh ), .BGEZ(BGEZ), .RS(mips_regifile_1_r1), .RT(mips_regifile_1_r2),
    .shamt(multiplexer_7_out), .WriteReg_num(multiplexer_10_out), .Imm(multiplexer_11_out),
    .PC_4(if_id_1_out_10), .out_31(Beq_EX), .out_32(Bne_EX), .out_33(id_ex_1_out_33),
    .out_34(id_ex_1_out_34), .out_35(id_ex_1_out_35), .out_36(id_ex_1_out_36), .out_37(id_ex_1_out_37),
    .out_38(JAL_EX), .out_39(id_ex_1_out_39), .out_40(BGEZ_EX), .out_43(id_ex_1_out_43),
    .out_44(id_ex_1_out_44), .out_45(id_ex_1_out_45), .out_46(id_ex_1_out_46), .out_47(id_ex_1_out_47),
    .out_48(id_ex_1_out_48), .EN(and_8_out), .CLK(CLK), .RST(\重定向检测电路_1_id_ex_rst ), .PC(ID_PC),
    .out_49(EX_PC), .Syscall(\单周期硬布线控制器_1_syscall ), .out_41(id_ex_1_out_41), .JUMP(\单周期硬布线控制器_1_jmp ),
    .out_30(JMP_EX), .JR(\单周期硬布线控制器_1_jr ), .out_29(JR_EX), .Instr(ID_IR), .out_42(EX_IR),
    .RsForward(RsForward), .out_50(id_ex_1_out_50), .RtForward(RtForward), .out_51(id_ex_1_out_51),
    .PredictJump(if_id_1_out_8), .out_28(id_ex_1_out_28));
  Register #(.width(32), .trigger("rising"), .Select("low")) register_1 (
    .D(A0), .en(and_9_out), .Q(LedData), .clk(CLK), .clr(RST));
  and and_9 (and_9_out, ~comparator_2_eq, Syscall);  // AND_Gate
  Register #(.width(1), .trigger("rising"), .Select("low")) register_2 (
    .D(and_10_out), .en(or_9_out), .Q(Halt), .clk(CLK), .clr(RST));
  and and_10 (and_10_out, comparator_2_eq, Syscall);
  or or_9 (or_9_out, ~Halt, Go);  // OR_Gate
  Multiplexer #(.select(2), .width(32), .disabled("Z"), .enable("false")) multiplexer_12 (
    .in0(id_ex_1_out_43), .in1(RDin), .in2(ex_mem_1_out_24), .out(PC_JR), .sel(id_ex_1_out_50));  // open: in3
  Multiplexer #(.select(2), .width(32), .disabled("Z"), .enable("false")) multiplexer_13 (
    .in0(id_ex_1_out_44), .in1(RDin), .in2(ex_mem_1_out_24), .out(multiplexer_13_out), .sel(id_ex_1_out_51));  // open: in3
  xor xor_1 (xor_1_out, or_10_out, id_ex_1_out_28);
  Multiplexer #(.select(1), .width(32), .disabled("Z"), .enable("false")) multiplexer_14 (
    .in0(multiplexer_13_out), .in1(id_ex_1_out_47), .out(multiplexer_14_out), .sel(id_ex_1_out_36));
  Shifter #(.width(32), .shift("ll")) shifter_1 (.in(id_ex_1_out_47), .\dist (5'b00010), .out(shifter_1_out));
  Multiplexer #(.select(1), .width(32), .disabled("Z"), .enable("false")) multiplexer_15 (
    .in0(multiplexer_14_out), .in1({32{1'b0}}), .out(multiplexer_15_out), .sel(BGEZ_EX));
  Adder #(.width(32)) adder_3 (.a(shifter_1_out), .b(id_ex_1_out_48), .out(adder_3_out));  // open: cin, cout
  or or_10 (or_10_out, JR_EX, JMP_EX, JAL_EX, B_EX);
  and and_11 (and_11_out, Bne_EX, not_5_out);
  not not_5 (not_5_out, mips_alu_1_equal);
  and and_12 (and_12_out, Beq_EX, mips_alu_1_equal);
  MIPS_ALU mips_alu_1 (
    .X(PC_JR), .Y(multiplexer_15_out), .AluOP(id_ex_1_out_35), .Equal(mips_alu_1_equal),
    .Result(mips_alu_1_result), .shamt(id_ex_1_out_45));  // open: Result_2
  or or_11 (B_EX, and_11_out, and_12_out, and_13_out);
  and and_13 (and_13_out, or_12_out, BGEZ_EX);
  or or_12 (or_12_out, mips_alu_1_equal, ~mips_alu_1_result[0]);  // OR_Gate
  and and_14 (and_14_out, GG, 1'b1);
  EX_MEM ex_mem_1 (
    .MemtoReg(id_ex_1_out_33), .MemWrite(id_ex_1_out_34), .RegWrite(id_ex_1_out_37), .LH(id_ex_1_out_39),
    .Result(mips_alu_1_result), .WriteData(multiplexer_13_out), .WriteReg_num(id_ex_1_out_46),
    .out_17(ex_mem_1_out_17), .out_18(MemWrite), .out_19(ex_mem_1_out_19), .out_20(ex_mem_1_out_20),
    .out_24(ex_mem_1_out_24), .out_25(MDin), .out_26(ex_mem_1_out_26), .EN(and_14_out), .RST(RST), .CLK(CLK),
    .JAL(JAL_EX), .JAL_2(ex_mem_1_jal_2), .PC_4(id_ex_1_out_48), .out_27(ex_mem_1_out_27), .PC(EX_PC),
    .out_28(M_PC), .Syscall(id_ex_1_out_41), .JAL_3(ex_mem_1_jal_3), .Instr(EX_IR), .out_23(MEM_IR),
    .V0(PC_JR), .out_29(ex_mem_1_out_29));
  RAM #(.addrWidth(10), .dataWidth(32), .bus("separate"), .Select("high")) ram_1 (
    .addr(ex_mem_1_out_24[11:2]), .din(MDin), .data(ram_1_data), .str(MemWrite), .clk(CLK), .clr(RST));  // open: sel, ld
  and and_15 (and_15_out, GG, 1'b1);
  MEM_WB mem_wb_1 (
    .MemtoReg(ex_mem_1_out_17), .RegWrite(ex_mem_1_out_19), .LH(ex_mem_1_out_20),
    .AluResult(ex_mem_1_out_24), .RD(ram_1_data), .WriteReg_num(ex_mem_1_out_26), .out_17(mem_wb_1_out_17),
    .out_18(RegWrite), .out_19(mem_wb_1_out_19[0]), .out_23(mem_wb_1_out_23), .out_24(mem_wb_1_out_24),
    .out_25(mem_wb_1_out_25), .EN(and_15_out), .RST(RST), .CLK(CLK), .PC_4(ex_mem_1_out_27),
    .out_26(mem_wb_1_out_26), .JAL(ex_mem_1_jal_2), .out_20(mem_wb_1_out_20), .PC(M_PC), .out_27(WB_PC),
    .Syscall(ex_mem_1_jal_3), .out_21(Syscall), .Instr(MEM_IR), .out_22(WB_IR), .A0(MDin), .out_28(A0),
    .V0(ex_mem_1_out_29), .out_29(V0));
  Multiplexer #(.select(1), .width(32), .disabled("Z"), .enable("false")) multiplexer_16 (
    .in0(mem_wb_1_out_23), .in1(mem_wb_1_out_24), .out(multiplexer_16_out), .sel(mem_wb_1_out_17));
  Shifter #(.width(32), .shift("ll")) shifter_2 (.in(multiplexer_16_out), .\dist (5'b10000), .out(shifter_2_out));
  Shifter #(.width(32), .shift("ar")) shifter_3 (.in(multiplexer_16_out), .\dist (5'b10000), .out(shifter_3_out));
  Shifter #(.width(32), .shift("ar")) shifter_4 (.in(shifter_2_out), .\dist (5'b10000), .out(shifter_4_out));
  Multiplexer #(.select(2), .width(32), .disabled("Z"), .enable("false")) multiplexer_17 (
    .in0(multiplexer_16_out), .in1(shifter_4_out), .in2(multiplexer_16_out), .in3(shifter_3_out),
    .out(multiplexer_17_out), .sel({mem_wb_1_out_23[1], mem_wb_1_out_19[0]}));
  Multiplexer #(.select(1), .width(32), .disabled("Z"), .enable("false")) multiplexer_18 (
    .in0(multiplexer_17_out), .in1(mem_wb_1_out_26), .out(RDin), .sel(mem_wb_1_out_20));

  // Other names for the same wires on the sheet: JumpAddr[31:2] = {EX_PC[31:28], EX_IR[25:0]}; IR[31:0] = ID_IR;
  //   MEM_PC[31:0] = M_PC

  // Notes on the sheet:
  //   中断源
  //   时空图监测，可删除
  //   中断等待指示
  //   数码管输出
  //   控制位
  //   PredictErr
  //   流水调试日志用
  //   暂停节拍，不能为0
  //   指令存储器
  //   戳工具置1进入计数暂停模式，ctrl+k时钟自动运行到对应节拍暂停
  //   ctrl+k关闭时钟连续运行，将控制位置零，进入单步调试模式调试
  //   IF/ID.EN
  //   contents of rom_1 (hex, n*v repeats v):
  //   20110001 8000c05 20110001 20120002 20130003 8000c09 20110001 20120002 20130003 8000c0d 20110001
  //   20120002 20130003 8000c11 20110001 20120002 20130003 c000cf9 20100001 20110001 118fc0 112020
  //   20020022 c 118882 12200001 8000c15 112020 20020022 c 20110001 118880 112020 20020022 c 12200001
  //   8000c1f 2011000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
  //   IF/ID/RST
  //   指令字
  //   可计数暂停的时钟源
  //   Instr
  //   OP
  //   Func
  //   rs
  //   rt
  //   rd
  //   JMP
  //   JR
  //   OP
  //   Func
  //   Syscall
  //   $ra
  //   Beq
  //   Bne
  //   MemToReg
  //   MemWrite
  //   AluOP
  //   AluSrcB
  //   RegWrite
  //   JAL
  //   RegDst
  //   LUI
  //   LH
  //   BGEZ
  //   为方便自动评测，需要输出流水线各段保存的PC值，注意是PC不是PC+4，另外ID段寄存器写入信息，Mem段内存写入信息也要输出
  //   PC+4
  //   WriteReg#
  //   ID/EX.RST
  //   RegWrite
  //   branch
  //   AluResult
  //   WriteBackData
  //   WriteReg#
  //   MemToReg
  //   MemWrite
  //   RegWrite
  //   JAL
  //   LH
  //   WriteData
  //   WriteReg#
  //   PC+4
  //   PC+4
  //   WriteBackData
endmodule

module \中断按键参考电路  (
  input  CLK,
  input  INT,
  input  \同步清零信号 ,
  output \与中断屏蔽位与 ,
  output \中断等待指示灯 
);

  wire and_1_out, d_ff_1_q, or_2_out;

  or or_1 (\中断等待指示灯 , \与中断屏蔽位与 , d_ff_1_q);
  D_Flip_Flop #(.trigger("rising"), .Pre_Clr_Positions("LEGACY"), .NegatePresetClear("false"), .enable("true"), .NewFFLayout("false")) d_ff_1 (
    .clk(INT), .D(1'b1), .Q(d_ff_1_q), .reset(\与中断屏蔽位与 ));  // open: Qn, preset, en
  or or_2 (or_2_out, d_ff_1_q, \与中断屏蔽位与 );
  Pull_Resistor #(.pull(0)) pull_resistor_1 (.node(\同步清零信号 ));
  and and_1 (and_1_out, or_2_out, ~\同步清零信号 );  // AND_Gate
  D_Flip_Flop #(.trigger("rising"), .Pre_Clr_Positions("LEGACY"), .NegatePresetClear("false"), .enable("true"), .NewFFLayout("false")) IR (
    .clk(CLK), .D(and_1_out), .Q(\与中断屏蔽位与 ));  // open: Qn, preset, en, reset

  // Notes on the sheet:
  //   中断信号采样参考电路
  //   Reset 
endmodule

module \封装正确性测试  (
);

  wire IR1, IR2, IR3, MemW, RegW;
  wire [31:0] EX_PC, ID_PC, IF_PC, IR, LED, MDin, MDinr, MEM_PC, PC, RDin, RDinr, WB_PC;

  \单周期MIPS  \u_单周期mips_1  (.RegWrite(RegW), .MemWrite(MemW), .PC(PC), .IR(IR), .RDin(RDin), .MDin(MDin), .LedData(LED));
  \气泡流水线  \u_气泡流水线_1  (
    .RegWrite(RegW), .MemWrite(MemW), .IF_PC(IF_PC), .ID_PC(ID_PC), .EX_PC(EX_PC), .M_PC(MEM_PC),
    .WB_PC(WB_PC), .RDin(RDinr), .MDin(MDinr), .LedData(LED));
  \单周期MIPS_团队任务  \u_单周期mips_团队任务_1  (
    .IR1(IR1), .IR2(IR2), .IR3(IR3), .RegWrite(RegW), .MemWrite(MemW), .PC(PC), .IR(IR), .RDin(RDin),
    .MDin(MDin), .LedData(LED));
  \理想流水线  \u_理想流水线_1  (
    .RegWrite(RegW), .MemWrite(MemW), .IF_PC(IF_PC), .ID_PC(ID_PC), .EX_PC(EX_PC), .M_PC(MEM_PC),
    .WB_PC(WB_PC), .RDin(RDinr), .MDin(MDinr), .LedData(LED));
  \重定向流水线  \u_重定向流水线_1  (
    .RegWrite(RegW), .MemWrite(MemW), .IF_PC(IF_PC), .ID_PC(ID_PC), .EX_PC(EX_PC), .M_PC(MEM_PC),
    .WB_PC(WB_PC), .RDin(RDinr), .MDin(MDinr), .LedData(LED));
  \单周期MIPS_多级中断  \u_单周期mips_多级中断_1  (
    .IR1(IR1), .IR2(IR2), .IR3(IR3), .RegWrite(RegW), .MemWrite(MemW), .PC(PC), .IR(IR), .RDin(RDin),
    .MDin(MDin), .LedData(LED));

  // Notes on the sheet:
  //   单周期封装测试
  //   气泡流水封装测试
  //   单周期+单级中断封装测试
  //   请检查上面封装有无位宽不匹配，引脚标签是否和连接的标签相对应，否则无法在educoder平台上正确测试
  //   理想流水封装测试
  //   重定向流水封装测试
  //   单周期+多级中断封装测试
endmodule

module aaa (
  input  IR1,
  input  IR2,
  input  IR3
);

  wire IR1_t, IR2_t, IR3_t, IRA, IRB, IRC;

  or or_1 (IR1_t, IR1, IRA);
  or or_2 (IR2_t, IR2, IRB);
  or or_3 (IR3_t, IR3, IRC);
endmodule
module IF_ID (
  input  EN,
  input  PredictJump,
  input  [31:0] Instr,
  input  [31:0] PC_4,
  input  [31:0] PC,
  input  RST,
  input  CLK,
  output out_8,
  output [31:0] out_9,
  output [31:0] out_10,
  output [31:0] out_11
);

  wire multiplexer_1_out;
  wire [31:0] multiplexer_2_out, multiplexer_3_out, multiplexer_4_out;

  Multiplexer #(.select(1), .width(1), .disabled("Z"), .enable("false")) multiplexer_1 (
    .in0(PredictJump), .in1(1'b0), .out(multiplexer_1_out), .sel(RST));
  Multiplexer #(.select(1), .width(32), .disabled("Z"), .enable("false")) multiplexer_2 (
    .in0(Instr), .in1({32{1'b0}}), .out(multiplexer_2_out), .sel(RST));
  Multiplexer #(.select(1), .width(32), .disabled("Z"), .enable("false")) multiplexer_3 (
    .in0(PC_4), .in1({32{1'b0}}), .out(multiplexer_3_out), .sel(RST));
  Multiplexer #(.select(1), .width(32), .disabled("Z"), .enable("false")) multiplexer_4 (
    .in0(PC), .in1({32{1'b0}}), .out(multiplexer_4_out), .sel(RST));
  Register #(.width(1), .trigger("rising"), .Select("low")) u_Instr (
    .D(multiplexer_1_out), .en(EN), .Q(out_8), .clk(CLK));  // open: clr
  Register #(.width(32), .trigger("rising"), .Select("low")) Instr_2 (
    .D(multiplexer_2_out), .en(EN), .Q(out_9), .clk(CLK));  // open: clr
  Register #(.width(32), .trigger("rising"), .Select("low")) u_PC_4 (
    .D(multiplexer_3_out), .en(EN), .Q(out_10), .clk(CLK));  // open: clr
  Register #(.width(32), .trigger("rising"), .Select("low")) u_PC (
    .D(multiplexer_4_out), .en(EN), .Q(out_11), .clk(CLK));  // open: clr
endmodule

module ID_EX (
  input  EN,
  input  PredictJump,
  input  JR,
  input  JUMP,
  input  BEQ,
  input  BNE,
  input  MemToReg,
  input  MemWrite,
  input  [3:0] AluOP,
  input  AluSrc,
  input  RegWrite,
  input  JAL,
  input  LH,
  input  BGEZ,
  input  Syscall,
  input  [31:0] Instr,
  input  [31:0] RS,
  input  [31:0] RT,
  input  [4:0] shamt,
  input  [4:0] WriteReg_num,
  input  [31:0] Imm,
  input  [31:0] PC_4,
  input  [31:0] PC,
  input  [1:0] RsForward,
  input  [1:0] RtForward,
  input  RST,
  input  CLK,
  output out_28,
  output out_29,
  output out_30,
  output out_31,
  output out_32,
  output out_33,
  output out_34,
  output [3:0] out_35,
  output out_36,
  output out_37,
  output out_38,
  output out_39,
  output out_40,
  output out_41,
  output [31:0] out_42,
  output [31:0] out_43,
  output [31:0] out_44,
  output [4:0] out_45,
  output [4:0] out_46,
  output [31:0] out_47,
  output [31:0] out_48,
  output [31:0] out_49,
  output [1:0] out_50,
  output [1:0] out_51
);

  wire multiplexer_1_out, multiplexer_2_out, multiplexer_3_out, multiplexer_4_out, multiplexer_5_out,
       multiplexer_6_out, multiplexer_7_out, multiplexer_9_out, multiplexer_10_out, multiplexer_11_out,
       multiplexer_12_out, multiplexer_13_out, multiplexer_14_out, undriven, undriven_2, undriven_3,
       undriven_4, undriven_5;
  wire [1:0] multiplexer_23_out, multiplexer_24_out;
  wire [3:0] multiplexer_8_out;
  wire [4:0] multiplexer_18_out, multiplexer_19_out;
  wire [31:0] multiplexer_15_out, multiplexer_16_out, multiplexer_17_out, multiplexer_20_out,
       multiplexer_21_out, multiplexer_22_out;

  Multiplexer #(.select(1), .width(1), .disabled("Z"), .enable("false")) multiplexer_1 (
    .in0(PredictJump), .in1(1'b0), .out(multiplexer_1_out), .sel(RST));
  Multiplexer #(.select(1), .width(1), .disabled("Z"), .enable("false")) multiplexer_2 (
    .in0(JR), .in1(1'b0), .out(multiplexer_2_out), .sel(RST));
  Multiplexer #(.select(1), .width(1), .disabled("Z"), .enable("false")) multiplexer_3 (
    .in0(JUMP), .in1(1'b0), .out(multiplexer_3_out), .sel(RST));
  Multiplexer #(.select(1), .width(1), .disabled("Z"), .enable("false")) multiplexer_4 (
    .in0(BEQ), .in1(1'b0), .out(multiplexer_4_out), .sel(RST));
  Multiplexer #(.select(1), .width(1), .disabled("Z"), .enable("false")) multiplexer_5 (
    .in0(BNE), .in1(1'b0), .out(multiplexer_5_out), .sel(RST));
  Multiplexer #(.select(1), .width(1), .disabled("Z"), .enable("false")) multiplexer_6 (
    .in0(MemToReg), .in1(1'b0), .out(multiplexer_6_out), .sel(RST));
  Multiplexer #(.select(1), .width(1), .disabled("Z"), .enable("false")) multiplexer_7 (
    .in0(MemWrite), .in1(1'b0), .out(multiplexer_7_out), .sel(RST));
  Multiplexer #(.select(1), .width(4), .disabled("Z"), .enable("false")) multiplexer_8 (
    .in0(AluOP), .in1(4'b0000), .out(multiplexer_8_out), .sel(RST));
  Multiplexer #(.select(1), .width(1), .disabled("Z"), .enable("false")) multiplexer_9 (
    .in0(AluSrc), .in1(1'b0), .out(multiplexer_9_out), .sel(RST));
  Multiplexer #(.select(1), .width(1), .disabled("Z"), .enable("false")) multiplexer_10 (
    .in0(RegWrite), .in1(1'b0), .out(multiplexer_10_out), .sel(RST));
  Multiplexer #(.select(1), .width(1), .disabled("Z"), .enable("false")) multiplexer_11 (
    .in0(JAL), .in1(1'b0), .out(multiplexer_11_out), .sel(RST));
  Multiplexer #(.select(1), .width(1), .disabled("Z"), .enable("false")) multiplexer_12 (
    .in0(LH), .in1(1'b0), .out(multiplexer_12_out), .sel(RST));
  Multiplexer #(.select(1), .width(1), .disabled("Z"), .enable("false")) multiplexer_13 (
    .in0(BGEZ), .in1(1'b0), .out(multiplexer_13_out), .sel(RST));
  Multiplexer #(.select(1), .width(1), .disabled("Z"), .enable("false")) multiplexer_14 (
    .in0(Syscall), .in1(1'b0), .out(multiplexer_14_out), .sel(RST));
  Multiplexer #(.select(1), .width(32), .disabled("Z"), .enable("false")) multiplexer_15 (
    .in0(Instr), .in1({32{1'b0}}), .out(multiplexer_15_out), .sel(RST));
  Multiplexer #(.select(1), .width(32), .disabled("Z"), .enable("false")) multiplexer_16 (
    .in0(RS), .in1({32{1'b0}}), .out(multiplexer_16_out), .sel(RST));
  Multiplexer #(.select(1), .width(32), .disabled("Z"), .enable("false")) multiplexer_17 (
    .in0(RT), .in1({32{1'b0}}), .out(multiplexer_17_out), .sel(RST));
  Multiplexer #(.select(1), .width(5), .disabled("Z"), .enable("false")) multiplexer_18 (
    .in0(shamt), .in1({5{1'b0}}), .out(multiplexer_18_out), .sel(RST));
  Multiplexer #(.select(1), .width(5), .disabled("Z"), .enable("false")) multiplexer_19 (
    .in0(WriteReg_num), .in1({5{1'b0}}), .out(multiplexer_19_out), .sel(RST));
  Multiplexer #(.select(1), .width(32), .disabled("Z"), .enable("false")) multiplexer_20 (
    .in0(Imm), .in1({32{1'b0}}), .out(multiplexer_20_out), .sel(RST));
  Multiplexer #(.select(1), .width(32), .disabled("Z"), .enable("false")) multiplexer_21 (
    .in0(PC_4), .in1({32{1'b0}}), .out(multiplexer_21_out), .sel(RST));
  Multiplexer #(.select(1), .width(32), .disabled("Z"), .enable("false")) multiplexer_22 (
    .in0(PC), .in1({32{1'b0}}), .out(multiplexer_22_out), .sel(RST));
  Multiplexer #(.select(1), .width(2), .disabled("Z"), .enable("false")) multiplexer_23 (
    .in0(RsForward), .in1(2'b00), .out(multiplexer_23_out), .sel(RST));
  Multiplexer #(.select(1), .width(2), .disabled("Z"), .enable("false")) multiplexer_24 (
    .in0(RtForward), .in1(2'b00), .out(multiplexer_24_out), .sel(RST));
  Register #(.width(1), .trigger("rising"), .Select("low")) register_1 (
    .D(multiplexer_1_out), .en(EN), .Q(out_28), .clk(CLK), .clr(undriven));
  Register #(.width(1), .trigger("rising"), .Select("low")) register_2 (
    .D(multiplexer_2_out), .en(EN), .Q(out_29), .clk(CLK), .clr(undriven_2));
  Register #(.width(1), .trigger("rising"), .Select("low")) register_3 (
    .D(multiplexer_3_out), .en(EN), .Q(out_30), .clk(CLK), .clr(undriven_3));
  Register #(.width(1), .trigger("rising"), .Select("low")) register_4 (
    .D(multiplexer_4_out), .en(EN), .Q(out_31), .clk(CLK), .clr(undriven_4));
  Register #(.width(1), .trigger("rising"), .Select("low")) register_5 (
    .D(multiplexer_5_out), .en(EN), .Q(out_32), .clk(CLK));  // open: clr
  Register #(.width(1), .trigger("rising"), .Select("low")) register_6 (
    .D(multiplexer_6_out), .en(EN), .Q(out_33), .clk(CLK));  // open: clr
  Register #(.width(1), .trigger("rising"), .Select("low")) register_7 (
    .D(multiplexer_7_out), .en(EN), .Q(out_34), .clk(CLK));  // open: clr
  Register #(.width(4), .trigger("rising"), .Select("low")) register_8 (
    .D(multiplexer_8_out), .en(EN), .Q(out_35), .clk(CLK));  // open: clr
  Register #(.width(1), .trigger("rising"), .Select("low")) register_9 (
    .D(multiplexer_9_out), .en(EN), .Q(out_36), .clk(CLK));  // open: clr
  Register #(.width(1), .trigger("rising"), .Select("low")) register_10 (
    .D(multiplexer_10_out), .en(EN), .Q(out_37), .clk(CLK));  // open: clr
  Register #(.width(1), .trigger("rising"), .Select("low")) register_11 (
    .D(multiplexer_11_out), .en(EN), .Q(out_38), .clk(CLK));  // open: clr
  Register #(.width(1), .trigger("rising"), .Select("low")) register_12 (
    .D(multiplexer_12_out), .en(EN), .Q(out_39), .clk(CLK));  // open: clr
  Register #(.width(1), .trigger("rising"), .Select("low")) register_13 (
    .D(multiplexer_13_out), .en(EN), .Q(out_40), .clk(CLK));  // open: clr
  Register #(.width(1), .trigger("rising"), .Select("low")) register_14 (
    .D(multiplexer_14_out), .en(EN), .Q(out_41), .clk(CLK));  // open: clr
  Register #(.width(32), .trigger("rising"), .Select("low")) register_15 (
    .D(multiplexer_15_out), .en(EN), .Q(out_42), .clk(CLK), .clr(undriven_5), .preset(undriven_5));  // open: cs
  Register #(.width(32), .trigger("rising"), .Select("low")) register_16 (
    .D(multiplexer_16_out), .en(EN), .Q(out_43), .clk(CLK));  // open: clr
  Register #(.width(32), .trigger("rising"), .Select("low")) register_17 (
    .D(multiplexer_17_out), .en(EN), .Q(out_44), .clk(CLK));  // open: clr
  Register #(.width(5), .trigger("rising"), .Select("low")) register_18 (
    .D(multiplexer_18_out), .en(EN), .Q(out_45), .clk(CLK));  // open: clr
  Register #(.width(5), .trigger("rising"), .Select("low")) register_19 (
    .D(multiplexer_19_out), .en(EN), .Q(out_46), .clk(CLK));  // open: clr
  Register #(.width(32), .trigger("rising"), .Select("low")) register_20 (
    .D(multiplexer_20_out), .en(EN), .Q(out_47), .clk(CLK));  // open: clr
  Register #(.width(32), .trigger("rising"), .Select("low")) register_21 (
    .D(multiplexer_21_out), .en(EN), .Q(out_48), .clk(CLK));  // open: clr
  Register #(.width(32), .trigger("rising"), .Select("low")) register_22 (
    .D(multiplexer_22_out), .en(EN), .Q(out_49), .clk(CLK));  // open: clr
  Register #(.width(2), .trigger("rising"), .Select("low")) register_23 (
    .D(multiplexer_23_out), .en(EN), .Q(out_50), .clk(CLK));  // open: clr
  Register #(.width(2), .trigger("rising"), .Select("low")) register_24 (
    .D(multiplexer_24_out), .en(EN), .Q(out_51), .clk(CLK));  // open: clr
endmodule

module EX_MEM (
  input  EN,
  input  RST,
  input  MemtoReg,
  input  MemWrite,
  input  RegWrite,
  input  LH,
  input  JAL,
  input  Syscall,
  input  [31:0] Instr,
  input  [31:0] Result,
  input  [31:0] WriteData,
  input  [4:0] WriteReg_num,
  input  [31:0] PC_4,
  input  [31:0] PC,
  input  [31:0] V0,
  input  CLK,
  output out_17,
  output out_18,
  output out_19,
  output out_20,
  output JAL_2,
  output JAL_3,
  output [31:0] out_23,
  output [31:0] out_24,
  output [31:0] out_25,
  output [4:0] out_26,
  output [31:0] out_27,
  output [31:0] out_28,
  output [31:0] out_29
);

  Register #(.width(1), .trigger("rising"), .Select("low")) register_1 (
    .D(MemtoReg), .en(EN), .Q(out_17), .clk(CLK), .clr(RST));
  Register #(.width(1), .trigger("rising"), .Select("low")) register_2 (
    .D(MemWrite), .en(EN), .Q(out_18), .clk(CLK), .clr(RST));
  Register #(.width(1), .trigger("rising"), .Select("low")) register_3 (
    .D(RegWrite), .en(EN), .Q(out_19), .clk(CLK), .clr(RST));
  Register #(.width(1), .trigger("rising"), .Select("low")) register_4 (
    .D(LH), .en(EN), .Q(out_20), .clk(CLK), .clr(RST));
  Register #(.width(1), .trigger("rising"), .Select("low")) register_5 (
    .D(JAL), .en(EN), .Q(JAL_2), .clk(CLK), .clr(RST));
  Register #(.width(1), .trigger("rising"), .Select("low")) register_6 (
    .D(Syscall), .en(EN), .Q(JAL_3), .clk(CLK), .clr(RST));
  Register #(.width(32), .trigger("rising"), .Select("low")) register_7 (
    .D(Instr), .en(EN), .Q(out_23), .clk(CLK), .clr(RST));
  Register #(.width(32), .trigger("rising"), .Select("low")) register_8 (
    .D(Result), .en(EN), .Q(out_24), .clk(CLK), .clr(RST));
  Register #(.width(32), .trigger("rising"), .Select("low")) register_9 (
    .D(WriteData), .en(EN), .Q(out_25), .clk(CLK), .clr(RST));
  Register #(.width(5), .trigger("rising"), .Select("low")) register_10 (
    .D(WriteReg_num), .en(EN), .Q(out_26), .clk(CLK), .clr(RST));
  Register #(.width(32), .trigger("rising"), .Select("low")) register_11 (
    .D(PC_4), .en(EN), .Q(out_27), .clk(CLK), .clr(RST));
  Register #(.width(32), .trigger("rising"), .Select("low")) register_12 (
    .D(PC), .en(EN), .Q(out_28), .clk(CLK), .clr(RST));
  Register #(.width(32), .trigger("rising"), .Select("low")) register_13 (
    .D(V0), .en(EN), .Q(out_29), .clk(CLK), .clr(RST));
endmodule

module MEM_WB (
  input  RST,
  input  EN,
  input  MemtoReg,
  input  RegWrite,
  input  LH,
  input  JAL,
  input  Syscall,
  input  [31:0] Instr,
  input  [31:0] AluResult,
  input  [31:0] RD,
  input  [4:0] WriteReg_num,
  input  [31:0] PC_4,
  input  [31:0] PC,
  input  [31:0] A0,
  input  [31:0] V0,
  input  CLK,
  output out_17,
  output out_18,
  output out_19,
  output out_20,
  output out_21,
  output [31:0] out_22,
  output [31:0] out_23,
  output [31:0] out_24,
  output [4:0] out_25,
  output [31:0] out_26,
  output [31:0] out_27,
  output [31:0] out_28,
  output [31:0] out_29
);

  Register #(.width(1), .trigger("rising"), .Select("low")) register_1 (
    .D(MemtoReg), .en(EN), .Q(out_17), .clk(CLK), .clr(RST));
  Register #(.width(1), .trigger("rising"), .Select("low")) register_2 (
    .D(RegWrite), .en(EN), .Q(out_18), .clk(CLK), .clr(RST));
  Register #(.width(1), .trigger("rising"), .Select("low")) register_3 (
    .D(LH), .en(EN), .Q(out_19), .clk(CLK), .clr(RST));
  Register #(.width(1), .trigger("rising"), .Select("low")) register_4 (
    .D(JAL), .Q(out_20), .clk(CLK), .clr(RST));  // open: en
  Register #(.width(1), .trigger("rising"), .Select("low")) register_5 (
    .D(Syscall), .Q(out_21), .clk(CLK), .clr(RST));  // open: en
  Register #(.width(32), .trigger("rising"), .Select("low")) register_6 (
    .D(Instr), .en(EN), .Q(out_22), .clk(CLK), .clr(RST));
  Register #(.width(32), .trigger("rising"), .Select("low")) register_7 (
    .D(AluResult), .en(EN), .Q(out_23), .clk(CLK), .clr(RST));
  Register #(.width(32), .trigger("rising"), .Select("low")) register_8 (
    .D(RD), .en(EN), .Q(out_24), .clk(CLK), .clr(RST));
  Register #(.width(5), .trigger("rising"), .Select("low")) register_9 (
    .D(WriteReg_num), .en(EN), .Q(out_25), .clk(CLK), .clr(RST));
  Register #(.width(32), .trigger("rising"), .Select("low")) register_10 (
    .D(PC_4), .en(EN), .Q(out_26), .clk(CLK), .clr(RST));
  Register #(.width(32), .trigger("rising"), .Select("low")) register_11 (
    .D(PC), .en(EN), .Q(out_27), .clk(CLK), .clr(RST));
  Register #(.width(32), .trigger("rising"), .Select("low")) register_12 (
    .D(A0), .en(EN), .Q(out_28), .clk(CLK), .clr(RST));
  Register #(.width(32), .trigger("rising"), .Select("low")) register_13 (
    .D(V0), .en(EN), .Q(out_29), .clk(CLK), .clr(RST));
endmodule

module \冲突检测电路  (
  input  [4:0] R1_num,
  input  [4:0] R2_num,
  input  [4:0] WriteReg__EX,
  input  [4:0] WriteReg__MEM,
  input  RsUsed,
  input  RtUsed,
  input  RegWrite_EX,
  input  RegWrite_MEM,
  input  Branch,
  output DataHazzaed,
  output PC_EN,
  output IF_ID_EN,
  output IF_ID_RST,
  output ID_EX_RST
);

  wire and_1_out, and_2_out, and_3_out, and_4_out, comparator_1_eq, comparator_2_eq, comparator_3_eq,
       comparator_4_eq, comparator_5_eq, comparator_6_eq, not_1_out, not_2_out;

  Comparator #(.width(5), .mode("twosComplement")) comparator_1 (
    .a(R1_num), .b({5{1'b0}}), .eq(comparator_1_eq));  // open: gt, lt
  Comparator #(.width(5), .mode("twosComplement")) comparator_2 (
    .a(R2_num), .b({5{1'b0}}), .eq(comparator_2_eq));  // open: gt, lt
  Comparator #(.width(5), .mode("twosComplement")) comparator_3 (
    .a(WriteReg__EX), .b(R1_num), .eq(comparator_3_eq));  // open: gt, lt
  Comparator #(.width(5), .mode("twosComplement")) comparator_4 (
    .a(WriteReg__MEM), .b(R1_num), .eq(comparator_4_eq));  // open: gt, lt
  Comparator #(.width(5), .mode("twosComplement")) comparator_5 (
    .a(R2_num), .b(WriteReg__EX), .eq(comparator_5_eq));  // open: gt, lt
  Comparator #(.width(5), .mode("twosComplement")) comparator_6 (
    .a(R2_num), .b(WriteReg__MEM), .eq(comparator_6_eq));  // open: gt, lt
  not not_1 (not_1_out, comparator_1_eq);
  not not_2 (not_2_out, comparator_2_eq);
  not not_3 (IF_ID_EN, DataHazzaed);
  or or_1 (ID_EX_RST, Branch, DataHazzaed);
  and and_1 (and_1_out, not_1_out, RsUsed, RegWrite_EX, comparator_3_eq);
  and and_2 (and_2_out, RegWrite_EX, not_2_out, RtUsed, comparator_5_eq);
  and and_3 (and_3_out, RsUsed, not_1_out, RegWrite_MEM, comparator_4_eq);
  and and_4 (and_4_out, RtUsed, not_2_out, RegWrite_MEM, comparator_6_eq);
  or or_2 (DataHazzaed, and_1_out, and_2_out, and_3_out, and_4_out);

  assign IF_ID_RST = Branch;
  assign PC_EN = IF_ID_EN;

  // Other names for the same wires on the sheet: DataHazzard = DataHazzaed
endmodule

module \重定向检测电路  (
  input  [4:0] R1_num,
  input  [4:0] R2_num,
  input  [4:0] WriteReg__EX,
  input  [4:0] WriteReg__MEM,
  input  RsUsed,
  input  RtUsed,
  input  RegWrite_EX,
  input  RegWrite_MEM,
  input  EX_MemToReg,
  input  Branch,
  output LoadUse,
  output [1:0] RsForward,
  output [1:0] RtForward,
  output PC_EN,
  output IF_ID_EN,
  output IF_ID_RST,
  output ID_EX_RST
);

  wire and_1_out, and_2_out, comparator_1_eq, comparator_2_eq, comparator_3_eq, comparator_4_eq,
       comparator_5_eq, comparator_6_eq, not_1_out, not_2_out;
  wire [1:0] and_3_out, and_5_out;

  Comparator #(.width(5), .mode("twosComplement")) comparator_1 (
    .a(R1_num), .b({5{1'b0}}), .eq(comparator_1_eq));  // open: gt, lt
  Comparator #(.width(5), .mode("twosComplement")) comparator_2 (
    .a(R2_num), .b({5{1'b0}}), .eq(comparator_2_eq));  // open: gt, lt
  Comparator #(.width(5), .mode("twosComplement")) comparator_3 (
    .a(WriteReg__EX), .b(R1_num), .eq(comparator_3_eq));  // open: gt, lt
  Comparator #(.width(5), .mode("twosComplement")) comparator_4 (
    .a(WriteReg__MEM), .b(R1_num), .eq(comparator_4_eq));  // open: gt, lt
  Comparator #(.width(5), .mode("twosComplement")) comparator_5 (
    .a(R2_num), .b(WriteReg__EX), .eq(comparator_5_eq));  // open: gt, lt
  Comparator #(.width(5), .mode("twosComplement")) comparator_6 (
    .a(R2_num), .b(WriteReg__MEM), .eq(comparator_6_eq));  // open: gt, lt
  not not_1 (not_1_out, comparator_1_eq);
  not not_2 (not_2_out, comparator_2_eq);
  not not_3 (IF_ID_EN, LoadUse);
  or or_1 (ID_EX_RST, Branch, LoadUse);
  and and_1 (and_1_out, not_1_out, comparator_3_eq, RsUsed, EX_MemToReg);
  and and_2 (and_2_out, not_2_out, comparator_5_eq, EX_MemToReg, RtUsed);
  and and_3 (and_3_out[0], not_1_out, comparator_3_eq, RsUsed, RegWrite_EX);
  and and_4 (and_3_out[1], not_1_out, comparator_4_eq, RsUsed, RegWrite_MEM);
  and and_5 (and_5_out[0], not_2_out, comparator_5_eq, RegWrite_EX, RtUsed);
  and and_6 (and_5_out[1], not_2_out, RegWrite_MEM, comparator_6_eq, RtUsed);
  or or_2 (LoadUse, and_1_out, and_2_out);
  Multiplexer #(.select(2), .width(2), .disabled("Z"), .enable("false")) multiplexer_1 (
    .in0(2'b00), .in1(2'b10), .in2(2'b01), .in3(2'b10), .out(RsForward), .sel(and_3_out));
  Multiplexer #(.select(2), .width(2), .disabled("Z"), .enable("false")) multiplexer_2 (
    .in0(2'b00), .in1(2'b10), .in2(2'b01), .in3(2'b10), .out(RtForward), .sel(and_5_out));

  assign IF_ID_RST = Branch;
  assign PC_EN = IF_ID_EN;
endmodule

module BTB (
  input  [31:0] PC,
  input  [31:0] EX_PC,
  input  EX_PredictErr,
  input  CLK,
  input  EX_Branch,
  input  [31:0] EX_BranchAddr,
  output [31:0] JumpAddr,
  output PredictJump
);

  wire and_1_out, and_2_out, and_3_out, and_4_out, and_5_out, and_6_out, and_7_out, and_8_out,
       comparator_1_eq, comparator_2_eq, comparator_3_eq, comparator_4_eq, comparator_5_eq, comparator_6_eq,
       comparator_7_eq, comparator_8_eq, comparator_9_eq, comparator_10_eq, comparator_11_eq,
       comparator_12_eq, comparator_13_eq, comparator_14_eq, comparator_15_eq, comparator_16_eq, d_ff_1_q,
       d_ff_2_q, d_ff_3_q, d_ff_4_q, d_ff_5_q, d_ff_6_q, d_ff_7_q, d_ff_8_q, decoder_1_out0, decoder_1_out1,
       decoder_1_out2, decoder_1_out3, decoder_1_out4, decoder_1_out5, decoder_1_out6, decoder_1_out7,
       decoder_2_out0, decoder_2_out1, decoder_2_out2, decoder_2_out3, decoder_2_out4, decoder_2_out5,
       decoder_2_out6, decoder_2_out7, empty, EX_Hit, EX_Miss, H0, H1, H2, H3, H4, H5, H6, H7, Hit, L0, L1,
       L2, L3, L4, L5, L6, L7, Miss, not_1_out, not_2_out, not_3_out, not_4_out, not_5_out, not_6_out,
       not_7_out, not_8_out, not_9_out, not_10_out, not_11_out, not_12_out, not_13_out, not_14_out,
       not_15_out, not_16_out, not_17_out, not_19_out, or_1_out, or_2_out, or_3_out, or_4_out, or_5_out,
       or_6_out, or_7_out, or_8_out, or_9_out, or_10_out, or_11_out, or_12_out, or_13_out, or_14_out,
       or_15_out, or_16_out, or_18_out, or_19_out, or_20_out, or_21_out, or_22_out, or_23_out, or_24_out,
       or_25_out, or_26_out, V0, V1, V2, V3, V4, V5, V6, V7, W0, W1, W2, W3, W4, W5, W6, W7;
  wire [1:0] adder_1_out, adder_2_out, adder_3_out, adder_4_out, adder_5_out, adder_6_out, adder_7_out,
       adder_8_out, controlled_buffer_9_out, controlled_buffer_11_out, controlled_buffer_13_out,
       controlled_buffer_15_out, controlled_buffer_17_out, controlled_buffer_19_out,
       controlled_buffer_21_out, controlled_buffer_23_out, multiplexer_1_out, multiplexer_2_out,
       multiplexer_3_out, multiplexer_4_out, multiplexer_5_out, multiplexer_6_out, multiplexer_7_out,
       multiplexer_8_out, multiplexer_9_out, multiplexer_10_out, multiplexer_11_out, multiplexer_12_out,
       multiplexer_13_out, multiplexer_14_out, multiplexer_15_out, multiplexer_16_out, multiplexer_17_out,
       multiplexer_18_out, multiplexer_19_out, multiplexer_20_out, multiplexer_21_out, multiplexer_22_out,
       multiplexer_23_out, multiplexer_24_out, multiplexer_25_out, multiplexer_26_out, multiplexer_27_out,
       multiplexer_28_out, multiplexer_29_out, multiplexer_30_out, multiplexer_31_out, multiplexer_32_out,
       multiplexer_33_out, multiplexer_34_out, multiplexer_35_out, multiplexer_36_out, multiplexer_37_out,
       multiplexer_38_out, multiplexer_39_out, multiplexer_40_out, \分支预测历史位_2_q , \分支预测历史位_3_q ,
       \分支预测历史位_4_q , \分支预测历史位_5_q , \分支预测历史位_6_q , \分支预测历史位_7_q , \分支预测历史位_8_q , \分支预测历史位_q ;
  wire [2:0] priority_encoder_1_out, \二路归并比较_1_max_num , \二路归并比较_2_max_num , \二路归并比较_3_max_num ,
       \二路归并比较_4_max_num , \二路归并比较_5_max_num , \二路归并比较_6_max_num , \二路归并比较_7_max_num ;
  wire [15:0] C0, C1, C2, C3, C4, C5, C6, C7, \二路归并比较_1_max , \二路归并比较_2_max , \二路归并比较_3_max , \二路归并比较_4_max ,
       \二路归并比较_5_max , \二路归并比较_6_max ;
  wire [31:0] tag0, tag1, tag2, tag3, tag4, tag5, tag6, tag7, \分支目标地址_2_q , \分支目标地址_3_q , \分支目标地址_4_q ,
       \分支目标地址_5_q , \分支目标地址_6_q , \分支目标地址_7_q , \分支目标地址_8_q , \分支目标地址_q ;

  Register #(.width(1), .trigger("rising"), .Select("low")) Valid (.D(W0), .en(W0), .Q(V0), .clk(CLK));  // open: clr
  Register #(.width(1), .trigger("rising"), .Select("low")) Valid_2 (.D(W1), .en(W1), .Q(V1), .clk(CLK));  // open: clr
  Register #(.width(1), .trigger("rising"), .Select("low")) Valid_3 (.D(W2), .en(W2), .Q(V2), .clk(CLK));  // open: clr
  Register #(.width(1), .trigger("rising"), .Select("low")) Valid_4 (.D(W3), .en(W3), .Q(V3), .clk(CLK));  // open: clr
  Register #(.width(1), .trigger("rising"), .Select("low")) Valid_5 (.D(W4), .en(W4), .Q(V4), .clk(CLK));  // open: clr
  Register #(.width(1), .trigger("rising"), .Select("low")) Valid_6 (.D(W5), .en(W5), .Q(V5), .clk(CLK));  // open: clr
  Register #(.width(1), .trigger("rising"), .Select("low")) Valid_7 (.D(W6), .en(W6), .Q(V6), .clk(CLK));  // open: clr
  Register #(.width(1), .trigger("rising"), .Select("low")) Valid_8 (.D(W7), .en(W7), .Q(V7), .clk(CLK));  // open: clr
  Register #(.width(32), .trigger("rising"), .Select("low")) \u_分支指令地址  (
    .D(EX_PC), .en(W0), .Q(tag0), .clk(CLK));  // open: clr
  Register #(.width(32), .trigger("rising"), .Select("low")) \u_分支指令地址_2  (
    .D(EX_PC), .en(W1), .Q(tag1), .clk(CLK));  // open: clr
  Register #(.width(32), .trigger("rising"), .Select("low")) \u_分支指令地址_3  (
    .D(EX_PC), .en(W2), .Q(tag2), .clk(CLK));  // open: clr
  Register #(.width(32), .trigger("rising"), .Select("low")) \u_分支指令地址_4  (
    .D(EX_PC), .en(W3), .Q(tag3), .clk(CLK));  // open: clr
  Register #(.width(32), .trigger("rising"), .Select("low")) \u_分支指令地址_5  (
    .D(EX_PC), .en(W4), .Q(tag4), .clk(CLK));  // open: clr
  Register #(.width(32), .trigger("rising"), .Select("low")) \u_分支指令地址_6  (
    .D(EX_PC), .en(W5), .Q(tag5), .clk(CLK));  // open: clr
  Register #(.width(32), .trigger("rising"), .Select("low")) \u_分支指令地址_7  (
    .D(EX_PC), .en(W6), .Q(tag6), .clk(CLK));  // open: clr
  Register #(.width(32), .trigger("rising"), .Select("low")) \u_分支指令地址_8  (
    .D(EX_PC), .en(W7), .Q(tag7), .clk(CLK));  // open: clr
  Pull_Resistor #(.pull(0)) pull_resistor_1 (.node(PredictJump));
  Register #(.width(32), .trigger("rising"), .Select("low")) \u_分支目标地址  (
    .D(EX_BranchAddr), .en(W0), .Q(\分支目标地址_q ), .clk(CLK));  // open: clr
  Register #(.width(32), .trigger("rising"), .Select("low")) \u_分支目标地址_2  (
    .D(EX_BranchAddr), .en(W1), .Q(\分支目标地址_2_q ), .clk(CLK));  // open: clr
  assign JumpAddr = L1 ? \分支目标地址_2_q  : 32'bz;  // Controlled_Buffer controlled_buffer_1
  Register #(.width(32), .trigger("rising"), .Select("low")) \u_分支目标地址_3  (
    .D(EX_BranchAddr), .en(W2), .Q(\分支目标地址_3_q ), .clk(CLK));  // open: clr
  Register #(.width(32), .trigger("rising"), .Select("low")) \u_分支目标地址_4  (
    .D(EX_BranchAddr), .en(W3), .Q(\分支目标地址_4_q ), .clk(CLK));  // open: clr
  assign JumpAddr = L3 ? \分支目标地址_4_q  : 32'bz;  // Controlled_Buffer controlled_buffer_2
  Register #(.width(32), .trigger("rising"), .Select("low")) \u_分支目标地址_5  (
    .D(EX_BranchAddr), .en(W4), .Q(\分支目标地址_5_q ), .clk(CLK));  // open: clr
  assign JumpAddr = L4 ? \分支目标地址_5_q  : 32'bz;  // Controlled_Buffer controlled_buffer_3
  Register #(.width(32), .trigger("rising"), .Select("low")) \u_分支目标地址_6  (
    .D(EX_BranchAddr), .en(W5), .Q(\分支目标地址_6_q ), .clk(CLK));  // open: clr
  assign JumpAddr = L5 ? \分支目标地址_6_q  : 32'bz;  // Controlled_Buffer controlled_buffer_4
  Register #(.width(32), .trigger("rising"), .Select("low")) \u_分支目标地址_7  (
    .D(EX_BranchAddr), .en(W6), .Q(\分支目标地址_7_q ), .clk(CLK));  // open: clr
  assign JumpAddr = L6 ? \分支目标地址_7_q  : 32'bz;  // Controlled_Buffer controlled_buffer_5
  Register #(.width(32), .trigger("rising"), .Select("low")) \u_分支目标地址_8  (
    .D(EX_BranchAddr), .en(W7), .Q(\分支目标地址_8_q ), .clk(CLK));  // open: clr
  assign JumpAddr = L7 ? \分支目标地址_8_q  : 32'bz;  // Controlled_Buffer controlled_buffer_6
  assign JumpAddr = L0 ? \分支目标地址_q  : 32'bz;  // Controlled_Buffer controlled_buffer_7
  or or_1 (or_1_out, or_9_out, W0);
  or or_2 (or_2_out, or_10_out, W1);
  assign JumpAddr = L2 ? \分支目标地址_3_q  : 32'bz;  // Controlled_Buffer controlled_buffer_8
  or or_3 (or_3_out, or_15_out, W2);
  or or_4 (or_4_out, or_11_out, W3);
  or or_5 (or_5_out, or_16_out, W4);
  or or_6 (or_6_out, or_12_out, W5);
  or or_7 (or_7_out, or_13_out, W6);
  or or_8 (or_8_out, or_14_out, W7);
  Counter #(.width(16), .max('hffff), .ongoal("wrap"), .trigger("rising"), .behavior("new")) \u_置换标记  (
    .Q(C4), .clk(CLK), .clr(d_ff_1_q));  // open: load, D, count, carry, preset, down
  D_Flip_Flop #(.trigger("rising"), .Pre_Clr_Positions("ABOVE_BELOW"), .NegatePresetClear("false"), .enable("false"), .NewFFLayout("true")) d_ff_1 (
    .clk(CLK), .D(or_5_out), .Q(d_ff_1_q));  // open: Qn, preset, reset
  Counter #(.width(16), .max('hffff), .ongoal("wrap"), .trigger("rising"), .behavior("new")) \u_置换标记_2  (
    .Q(C5), .clk(CLK), .clr(d_ff_2_q));  // open: load, D, count, carry, preset, down
  D_Flip_Flop #(.trigger("rising"), .Pre_Clr_Positions("ABOVE_BELOW"), .NegatePresetClear("false"), .enable("false"), .NewFFLayout("true")) d_ff_2 (
    .clk(CLK), .D(or_6_out), .Q(d_ff_2_q));  // open: Qn, preset, reset
  Counter #(.width(16), .max('hffff), .ongoal("wrap"), .trigger("rising"), .behavior("new")) \u_置换标记_3  (
    .Q(C6), .clk(CLK), .clr(d_ff_3_q));  // open: load, D, count, carry, preset, down
  D_Flip_Flop #(.trigger("rising"), .Pre_Clr_Positions("ABOVE_BELOW"), .NegatePresetClear("false"), .enable("false"), .NewFFLayout("true")) d_ff_3 (
    .clk(CLK), .D(or_7_out), .Q(d_ff_3_q));  // open: Qn, preset, reset
  Counter #(.width(16), .max('hffff), .ongoal("wrap"), .trigger("rising"), .behavior("new")) \u_置换标记_4  (
    .Q(C7), .clk(CLK), .clr(d_ff_4_q), .down(1'b0));  // open: load, D, count, carry, preset
  D_Flip_Flop #(.trigger("rising"), .Pre_Clr_Positions("ABOVE_BELOW"), .NegatePresetClear("false"), .enable("false"), .NewFFLayout("true")) d_ff_4 (
    .clk(CLK), .D(or_8_out), .Q(d_ff_4_q));  // open: Qn, preset, reset
  Counter #(.width(16), .max('hffff), .ongoal("wrap"), .trigger("rising"), .behavior("new")) \u_置换标记_5  (
    .Q(C0), .clk(CLK), .clr(d_ff_5_q));  // open: load, D, count, carry, preset, down
  D_Flip_Flop #(.trigger("rising"), .Pre_Clr_Positions("ABOVE_BELOW"), .NegatePresetClear("false"), .enable("false"), .NewFFLayout("true")) d_ff_5 (
    .clk(CLK), .D(or_1_out), .Q(d_ff_5_q));  // open: Qn, preset, reset
  Counter #(.width(16), .max('hffff), .ongoal("wrap"), .trigger("rising"), .behavior("new")) \u_置换标记_6  (
    .Q(C1), .clk(CLK), .clr(d_ff_6_q));  // open: load, D, count, carry, preset, down
  D_Flip_Flop #(.trigger("rising"), .Pre_Clr_Positions("ABOVE_BELOW"), .NegatePresetClear("false"), .enable("false"), .NewFFLayout("true")) d_ff_6 (
    .clk(CLK), .D(or_2_out), .Q(d_ff_6_q));  // open: Qn, preset, reset
  Counter #(.width(16), .max('hffff), .ongoal("wrap"), .trigger("rising"), .behavior("new")) \u_置换标记_7  (
    .Q(C2), .clk(CLK), .clr(d_ff_7_q));  // open: load, D, count, carry, preset, down
  D_Flip_Flop #(.trigger("rising"), .Pre_Clr_Positions("ABOVE_BELOW"), .NegatePresetClear("false"), .enable("false"), .NewFFLayout("true")) d_ff_7 (
    .clk(CLK), .D(or_3_out), .Q(d_ff_7_q));  // open: Qn, preset, reset
  Counter #(.width(16), .max('hffff), .ongoal("wrap"), .trigger("rising"), .behavior("new")) \u_置换标记_8  (
    .Q(C3), .clk(CLK), .clr(d_ff_8_q));  // open: load, D, count, carry, preset, down
  D_Flip_Flop #(.trigger("rising"), .Pre_Clr_Positions("ABOVE_BELOW"), .NegatePresetClear("false"), .enable("false"), .NewFFLayout("true")) d_ff_8 (
    .clk(CLK), .D(or_4_out), .Q(d_ff_8_q));  // open: Qn, preset, reset
  Multiplexer #(.select(1), .width(2), .disabled("Z"), .enable("false")) multiplexer_1 (
    .in0(2'b00), .in1(2'b01), .out(multiplexer_1_out), .sel(EX_PredictErr));
  Multiplexer #(.select(1), .width(2), .disabled("Z"), .enable("false")) multiplexer_2 (
    .in0(2'b11), .in1(2'b01), .out(multiplexer_2_out), .sel(EX_PredictErr));
  Multiplexer #(.select(1), .width(2), .disabled("Z"), .enable("false")) multiplexer_3 (
    .in0(2'b01), .in1(2'b00), .out(multiplexer_3_out), .sel(EX_PredictErr));
  Multiplexer #(.select(1), .width(2), .disabled("Z"), .enable("false")) multiplexer_4 (
    .in0(2'b01), .in1(2'b11), .out(multiplexer_4_out), .sel(EX_PredictErr));
  Multiplexer #(.select(1), .width(2), .disabled("Z"), .enable("false")) multiplexer_5 (
    .in0(2'b00), .in1(2'b01), .out(multiplexer_5_out), .sel(EX_PredictErr));
  Multiplexer #(.select(1), .width(2), .disabled("Z"), .enable("false")) multiplexer_6 (
    .in0(2'b11), .in1(2'b01), .out(multiplexer_6_out), .sel(EX_PredictErr));
  Multiplexer #(.select(1), .width(2), .disabled("Z"), .enable("false")) multiplexer_7 (
    .in0(2'b01), .in1(2'b00), .out(multiplexer_7_out), .sel(EX_PredictErr));
  Multiplexer #(.select(1), .width(2), .disabled("Z"), .enable("false")) multiplexer_8 (
    .in0(2'b01), .in1(2'b11), .out(multiplexer_8_out), .sel(EX_PredictErr));
  Multiplexer #(.select(1), .width(2), .disabled("Z"), .enable("false")) multiplexer_9 (
    .in0(2'b00), .in1(2'b01), .out(multiplexer_9_out), .sel(EX_PredictErr));
  Multiplexer #(.select(1), .width(2), .disabled("Z"), .enable("false")) multiplexer_10 (
    .in0(2'b11), .in1(2'b01), .out(multiplexer_10_out), .sel(EX_PredictErr));
  Multiplexer #(.select(1), .width(2), .disabled("Z"), .enable("false")) multiplexer_11 (
    .in0(2'b01), .in1(2'b00), .out(multiplexer_11_out), .sel(EX_PredictErr));
  Multiplexer #(.select(1), .width(2), .disabled("Z"), .enable("false")) multiplexer_12 (
    .in0(2'b01), .in1(2'b11), .out(multiplexer_12_out), .sel(EX_PredictErr));
  Multiplexer #(.select(1), .width(2), .disabled("Z"), .enable("false")) multiplexer_13 (
    .in0(2'b00), .in1(2'b01), .out(multiplexer_13_out), .sel(EX_PredictErr));
  Multiplexer #(.select(1), .width(2), .disabled("Z"), .enable("false")) multiplexer_14 (
    .in0(2'b11), .in1(2'b01), .out(multiplexer_14_out), .sel(EX_PredictErr));
  Multiplexer #(.select(1), .width(2), .disabled("Z"), .enable("false")) multiplexer_15 (
    .in0(2'b01), .in1(2'b00), .out(multiplexer_15_out), .sel(EX_PredictErr));
  Multiplexer #(.select(1), .width(2), .disabled("Z"), .enable("false")) multiplexer_16 (
    .in0(2'b01), .in1(2'b11), .out(multiplexer_16_out), .sel(EX_PredictErr));
  Multiplexer #(.select(1), .width(2), .disabled("Z"), .enable("false")) multiplexer_17 (
    .in0(2'b00), .in1(2'b01), .out(multiplexer_17_out), .sel(EX_PredictErr));
  Multiplexer #(.select(1), .width(2), .disabled("Z"), .enable("false")) multiplexer_18 (
    .in0(2'b11), .in1(2'b01), .out(multiplexer_18_out), .sel(EX_PredictErr));
  Multiplexer #(.select(1), .width(2), .disabled("Z"), .enable("false")) multiplexer_19 (
    .in0(2'b01), .in1(2'b00), .out(multiplexer_19_out), .sel(EX_PredictErr));
  Multiplexer #(.select(1), .width(2), .disabled("Z"), .enable("false")) multiplexer_20 (
    .in0(2'b01), .in1(2'b11), .out(multiplexer_20_out), .sel(EX_PredictErr));
  Multiplexer #(.select(1), .width(2), .disabled("Z"), .enable("false")) multiplexer_21 (
    .in0(2'b00), .in1(2'b01), .out(multiplexer_21_out), .sel(EX_PredictErr));
  Multiplexer #(.select(1), .width(2), .disabled("Z"), .enable("false")) multiplexer_22 (
    .in0(2'b11), .in1(2'b01), .out(multiplexer_22_out), .sel(EX_PredictErr));
  Multiplexer #(.select(1), .width(2), .disabled("Z"), .enable("false")) multiplexer_23 (
    .in0(2'b01), .in1(2'b00), .out(multiplexer_23_out), .sel(EX_PredictErr));
  Multiplexer #(.select(1), .width(2), .disabled("Z"), .enable("false")) multiplexer_24 (
    .in0(2'b01), .in1(2'b11), .out(multiplexer_24_out), .sel(EX_PredictErr));
  Multiplexer #(.select(1), .width(2), .disabled("Z"), .enable("false")) multiplexer_25 (
    .in0(2'b00), .in1(2'b01), .out(multiplexer_25_out), .sel(EX_PredictErr));
  Multiplexer #(.select(1), .width(2), .disabled("Z"), .enable("false")) multiplexer_26 (
    .in0(2'b11), .in1(2'b01), .out(multiplexer_26_out), .sel(EX_PredictErr));
  Multiplexer #(.select(1), .width(2), .disabled("Z"), .enable("false")) multiplexer_27 (
    .in0(2'b01), .in1(2'b00), .out(multiplexer_27_out), .sel(EX_PredictErr));
  Multiplexer #(.select(1), .width(2), .disabled("Z"), .enable("false")) multiplexer_28 (
    .in0(2'b01), .in1(2'b11), .out(multiplexer_28_out), .sel(EX_PredictErr));
  Multiplexer #(.select(1), .width(2), .disabled("Z"), .enable("false")) multiplexer_29 (
    .in0(2'b00), .in1(2'b01), .out(multiplexer_29_out), .sel(EX_PredictErr));
  Multiplexer #(.select(1), .width(2), .disabled("Z"), .enable("false")) multiplexer_30 (
    .in0(2'b11), .in1(2'b01), .out(multiplexer_30_out), .sel(EX_PredictErr));
  Multiplexer #(.select(1), .width(2), .disabled("Z"), .enable("false")) multiplexer_31 (
    .in0(2'b01), .in1(2'b00), .out(multiplexer_31_out), .sel(EX_PredictErr));
  Multiplexer #(.select(1), .width(2), .disabled("Z"), .enable("false")) multiplexer_32 (
    .in0(2'b01), .in1(2'b11), .out(multiplexer_32_out), .sel(EX_PredictErr));
  Multiplexer #(.select(2), .width(2), .disabled("Z"), .enable("false")) multiplexer_33 (
    .in0(multiplexer_17_out), .in1(multiplexer_18_out), .in2(multiplexer_19_out), .in3(multiplexer_20_out),
    .out(multiplexer_33_out), .sel(\分支预测历史位_q ));
  Multiplexer #(.select(2), .width(2), .disabled("Z"), .enable("false")) multiplexer_34 (
    .in0(multiplexer_21_out), .in1(multiplexer_22_out), .in2(multiplexer_23_out), .in3(multiplexer_24_out),
    .out(multiplexer_34_out), .sel(\分支预测历史位_8_q ));
  Multiplexer #(.select(2), .width(2), .disabled("Z"), .enable("false")) multiplexer_35 (
    .in0(multiplexer_1_out), .in1(multiplexer_2_out), .in2(multiplexer_3_out), .in3(multiplexer_4_out),
    .out(multiplexer_35_out), .sel(\分支预测历史位_2_q ));
  Multiplexer #(.select(2), .width(2), .disabled("Z"), .enable("false")) multiplexer_36 (
    .in0(multiplexer_25_out), .in1(multiplexer_26_out), .in2(multiplexer_27_out), .in3(multiplexer_28_out),
    .out(multiplexer_36_out), .sel(\分支预测历史位_3_q ));
  Multiplexer #(.select(2), .width(2), .disabled("Z"), .enable("false")) multiplexer_37 (
    .in0(multiplexer_29_out), .in1(multiplexer_30_out), .in2(multiplexer_31_out), .in3(multiplexer_32_out),
    .out(multiplexer_37_out), .sel(\分支预测历史位_4_q ));
  Multiplexer #(.select(2), .width(2), .disabled("Z"), .enable("false")) multiplexer_38 (
    .in0(multiplexer_5_out), .in1(multiplexer_6_out), .in2(multiplexer_7_out), .in3(multiplexer_8_out),
    .out(multiplexer_38_out), .sel(\分支预测历史位_5_q ));
  Multiplexer #(.select(2), .width(2), .disabled("Z"), .enable("false")) multiplexer_39 (
    .in0(multiplexer_9_out), .in1(multiplexer_10_out), .in2(multiplexer_11_out), .in3(multiplexer_12_out),
    .out(multiplexer_39_out), .sel(\分支预测历史位_6_q ));
  Multiplexer #(.select(2), .width(2), .disabled("Z"), .enable("false")) multiplexer_40 (
    .in0(multiplexer_13_out), .in1(multiplexer_14_out), .in2(multiplexer_15_out), .in3(multiplexer_16_out),
    .out(multiplexer_40_out), .sel(\分支预测历史位_7_q ));
  not not_1 (not_1_out, W7);
  Adder #(.width(2)) adder_1 (.a(\分支预测历史位_q ), .b(multiplexer_33_out), .out(adder_1_out));  // open: cin, cout
  assign controlled_buffer_9_out = W0 ? 2'b10 : 2'bz;  // Controlled_Buffer controlled_buffer_9
  not not_2 (not_2_out, W0);
  Adder #(.width(2)) adder_2 (.a(\分支预测历史位_8_q ), .b(multiplexer_34_out), .out(adder_2_out));  // open: cin, cout
  assign controlled_buffer_9_out = not_2_out ? adder_2_out : 2'bz;  // Controlled_Buffer controlled_buffer_10
  or or_9 (or_9_out, W0, and_1_out);
  and and_1 (and_1_out, EX_Hit, H0);
  assign controlled_buffer_11_out = W1 ? 2'b10 : 2'bz;  // Controlled_Buffer controlled_buffer_11
  not not_3 (not_3_out, W1);
  assign controlled_buffer_11_out = not_3_out ? adder_3_out : 2'bz;  // Controlled_Buffer controlled_buffer_12
  Adder #(.width(2)) adder_3 (.a(\分支预测历史位_2_q ), .b(multiplexer_35_out), .out(adder_3_out));  // open: cin, cout
  or or_10 (or_10_out, W1, and_2_out);
  and and_2 (and_2_out, EX_Hit, H1);
  assign controlled_buffer_13_out = W2 ? 2'b10 : 2'bz;  // Controlled_Buffer controlled_buffer_13
  not not_4 (not_4_out, W2);
  assign controlled_buffer_13_out = not_4_out ? adder_4_out : 2'bz;  // Controlled_Buffer controlled_buffer_14
  Adder #(.width(2)) adder_4 (.a(\分支预测历史位_3_q ), .b(multiplexer_36_out), .out(adder_4_out));  // open: cin, cout
  and and_3 (and_3_out, EX_Hit, H2);
  assign controlled_buffer_15_out = W3 ? 2'b10 : 2'bz;  // Controlled_Buffer controlled_buffer_15
  not not_5 (not_5_out, W3);
  Adder #(.width(2)) adder_5 (.a(\分支预测历史位_4_q ), .b(multiplexer_37_out), .out(adder_5_out));  // open: cin, cout
  assign controlled_buffer_15_out = not_5_out ? adder_5_out : 2'bz;  // Controlled_Buffer controlled_buffer_16
  or or_11 (or_11_out, W3, and_4_out);
  and and_4 (and_4_out, EX_Hit, H3);
  assign controlled_buffer_17_out = W4 ? 2'b10 : 2'bz;  // Controlled_Buffer controlled_buffer_17
  not not_6 (not_6_out, W4);
  assign controlled_buffer_17_out = not_6_out ? adder_6_out : 2'bz;  // Controlled_Buffer controlled_buffer_18
  Adder #(.width(2)) adder_6 (.a(\分支预测历史位_5_q ), .b(multiplexer_38_out), .out(adder_6_out));  // open: cin, cout
  and and_5 (and_5_out, EX_Hit, H4);
  assign controlled_buffer_19_out = W5 ? 2'b10 : 2'bz;  // Controlled_Buffer controlled_buffer_19
  not not_7 (not_7_out, W5);
  assign controlled_buffer_19_out = not_7_out ? adder_7_out : 2'bz;  // Controlled_Buffer controlled_buffer_20
  Adder #(.width(2)) adder_7 (.a(\分支预测历史位_6_q ), .b(multiplexer_39_out), .out(adder_7_out));  // open: cin, cout
  or or_12 (or_12_out, W5, and_6_out);
  and and_6 (and_6_out, EX_Hit, H5);
  assign controlled_buffer_21_out = W6 ? 2'b10 : 2'bz;  // Controlled_Buffer controlled_buffer_21
  not not_8 (not_8_out, W6);
  Adder #(.width(2)) adder_8 (.a(\分支预测历史位_7_q ), .b(multiplexer_40_out), .out(adder_8_out));  // open: cin, cout
  assign controlled_buffer_21_out = not_8_out ? adder_8_out : 2'bz;  // Controlled_Buffer controlled_buffer_22
  or or_13 (or_13_out, W6, and_7_out);
  and and_7 (and_7_out, EX_Hit, H6);
  assign controlled_buffer_23_out = W7 ? 2'b10 : 2'bz;  // Controlled_Buffer controlled_buffer_23
  Register #(.width(2), .trigger("rising"), .Select("low")) \u_分支预测历史位  (
    .D(controlled_buffer_23_out), .en(or_14_out), .Q(\分支预测历史位_q ), .clk(CLK));  // open: clr
  assign controlled_buffer_23_out = not_1_out ? adder_1_out : 2'bz;  // Controlled_Buffer controlled_buffer_24
  or or_14 (or_14_out, W7, and_8_out);
  and and_8 (and_8_out, EX_Hit, H7);
  Register #(.width(2), .trigger("rising"), .Select("low")) \u_分支预测历史位_2  (
    .D(controlled_buffer_11_out), .en(or_10_out), .Q(\分支预测历史位_2_q ), .clk(CLK));  // open: clr
  Register #(.width(2), .trigger("rising"), .Select("low")) \u_分支预测历史位_3  (
    .D(controlled_buffer_13_out), .en(or_15_out), .Q(\分支预测历史位_3_q ), .clk(CLK));  // open: clr
  or or_15 (or_15_out, W2, and_3_out);
  Register #(.width(2), .trigger("rising"), .Select("low")) \u_分支预测历史位_4  (
    .D(controlled_buffer_15_out), .en(or_11_out), .Q(\分支预测历史位_4_q ), .clk(CLK));  // open: clr
  Register #(.width(2), .trigger("rising"), .Select("low")) \u_分支预测历史位_5  (
    .D(controlled_buffer_17_out), .en(or_16_out), .Q(\分支预测历史位_5_q ), .clk(CLK));  // open: clr
  or or_16 (or_16_out, W4, and_5_out);
  Register #(.width(2), .trigger("rising"), .Select("low")) \u_分支预测历史位_6  (
    .D(controlled_buffer_19_out), .en(or_12_out), .Q(\分支预测历史位_6_q ), .clk(CLK));  // open: clr
  Register #(.width(2), .trigger("rising"), .Select("low")) \u_分支预测历史位_7  (
    .D(controlled_buffer_21_out), .en(or_13_out), .Q(\分支预测历史位_7_q ), .clk(CLK));  // open: clr
  Register #(.width(2), .trigger("rising"), .Select("low")) \u_分支预测历史位_8  (
    .D(controlled_buffer_9_out), .en(or_9_out), .Q(\分支预测历史位_8_q ), .clk(CLK));  // open: clr
  assign PredictJump = L1 ? \分支预测历史位_2_q [1] : 1'bz;  // Controlled_Buffer controlled_buffer_25
  assign PredictJump = L3 ? \分支预测历史位_4_q [1] : 1'bz;  // Controlled_Buffer controlled_buffer_26
  assign PredictJump = L5 ? \分支预测历史位_6_q [1] : 1'bz;  // Controlled_Buffer controlled_buffer_27
  assign PredictJump = L6 ? \分支预测历史位_7_q [1] : 1'bz;  // Controlled_Buffer controlled_buffer_28
  assign PredictJump = L7 ? \分支预测历史位_q [1] : 1'bz;  // Controlled_Buffer controlled_buffer_29
  assign PredictJump = L0 ? \分支预测历史位_8_q [1] : 1'bz;  // Controlled_Buffer controlled_buffer_30
  assign PredictJump = L2 ? \分支预测历史位_3_q [1] : 1'bz;  // Controlled_Buffer controlled_buffer_31
  assign PredictJump = L4 ? \分支预测历史位_5_q [1] : 1'bz;  // Controlled_Buffer controlled_buffer_32
  Comparator #(.width(32), .mode("twosComplement")) comparator_1 (
    .a(PC), .b(tag0), .eq(comparator_1_eq));  // open: gt, lt
  Comparator #(.width(32), .mode("twosComplement")) comparator_2 (
    .a(PC), .b(tag1), .eq(comparator_2_eq));  // open: gt, lt
  Comparator #(.width(32), .mode("twosComplement")) comparator_3 (
    .a(PC), .b(tag2), .eq(comparator_3_eq));  // open: gt, lt
  Comparator #(.width(32), .mode("twosComplement")) comparator_4 (
    .a(PC), .b(tag3), .eq(comparator_4_eq));  // open: gt, lt
  Comparator #(.width(32), .mode("twosComplement")) comparator_5 (
    .a(PC), .b(tag4), .eq(comparator_5_eq));  // open: gt, lt
  Comparator #(.width(32), .mode("twosComplement")) comparator_6 (
    .a(PC), .b(tag5), .eq(comparator_6_eq));  // open: gt, lt
  Comparator #(.width(32), .mode("twosComplement")) comparator_7 (
    .a(PC), .b(tag6), .eq(comparator_7_eq));  // open: gt, lt
  Comparator #(.width(32), .mode("twosComplement")) comparator_8 (
    .a(PC), .b(tag7), .eq(comparator_8_eq));  // open: gt, lt
  and and_9 (L0, comparator_1_eq, V0);
  and and_10 (L1, comparator_2_eq, V1);
  and and_11 (L2, comparator_3_eq, V2);
  and and_12 (L3, comparator_4_eq, V3);
  and and_13 (L4, comparator_5_eq, V4);
  and and_14 (L5, comparator_6_eq, V5);
  and and_15 (L6, comparator_7_eq, V6);
  and and_16 (L7, comparator_8_eq, V7);
  not not_9 (not_9_out, V0);
  not not_10 (not_10_out, V1);
  not not_11 (not_11_out, V2);
  not not_12 (not_12_out, V3);
  not not_13 (not_13_out, V4);
  not not_14 (not_14_out, V5);
  not not_15 (not_15_out, V6);
  not not_16 (not_16_out, V7);
  \二路归并比较  \u_二路归并比较_1  (
    .Y(C0), .X(C1), .Y_num(3'b000), .X_num(3'b001), .MAX(\二路归并比较_1_max ), .MAX_num(\二路归并比较_1_max_num ));
  \二路归并比较  \u_二路归并比较_2  (
    .Y(C2), .X(C3), .Y_num(3'b010), .X_num(3'b011), .MAX(\二路归并比较_2_max ), .MAX_num(\二路归并比较_2_max_num ));
  \二路归并比较  \u_二路归并比较_3  (
    .Y(C4), .X(C5), .Y_num(3'b100), .X_num(3'b101), .MAX(\二路归并比较_3_max ), .MAX_num(\二路归并比较_3_max_num ));
  \二路归并比较  \u_二路归并比较_4  (
    .Y(C6), .X(C7), .Y_num(3'b110), .X_num(3'b111), .MAX(\二路归并比较_4_max ), .MAX_num(\二路归并比较_4_max_num ));
  Priority_Encoder #(.select(3), .disabled("Z")) priority_encoder_1 (
    .in0(not_9_out), .in1(not_10_out), .in2(not_11_out), .in3(not_12_out), .in4(not_13_out),
    .in5(not_14_out), .in6(not_15_out), .in7(not_16_out), .out(priority_encoder_1_out), .gs(empty),
    .en_in(1'b1));  // open: en_out
  \二路归并比较  \u_二路归并比较_5  (
    .Y(\二路归并比较_1_max ), .X(\二路归并比较_2_max ), .Y_num(\二路归并比较_1_max_num ), .X_num(\二路归并比较_2_max_num ),
    .MAX(\二路归并比较_5_max ), .MAX_num(\二路归并比较_5_max_num ));
  \二路归并比较  \u_二路归并比较_6  (
    .Y(\二路归并比较_3_max ), .X(\二路归并比较_4_max ), .Y_num(\二路归并比较_3_max_num ), .X_num(\二路归并比较_4_max_num ),
    .MAX(\二路归并比较_6_max ), .MAX_num(\二路归并比较_6_max_num ));
  or or_17 (Hit, L0, L1, L2, L3, L4, L5, L6, L7);
  Decoder #(.select(3), .tristate("false"), .disabled(0), .enable("true")) decoder_1 (
    .out0(decoder_1_out0), .out1(decoder_1_out1), .out2(decoder_1_out2), .out3(decoder_1_out3),
    .out4(decoder_1_out4), .out5(decoder_1_out5), .out6(decoder_1_out6), .out7(decoder_1_out7),
    .sel(priority_encoder_1_out), .en(empty));
  not not_17 (not_17_out, empty);
  Decoder #(.select(3), .tristate("false"), .disabled(0), .enable("true")) decoder_2 (
    .out0(decoder_2_out0), .out1(decoder_2_out1), .out2(decoder_2_out2), .out3(decoder_2_out3),
    .out4(decoder_2_out4), .out5(decoder_2_out5), .out6(decoder_2_out6), .out7(decoder_2_out7),
    .sel(\二路归并比较_7_max_num ), .en(not_17_out));
  \二路归并比较  \u_二路归并比较_7  (
    .Y(\二路归并比较_5_max ), .X(\二路归并比较_6_max ), .Y_num(\二路归并比较_5_max_num ), .X_num(\二路归并比较_6_max_num ),
    .MAX_num(\二路归并比较_7_max_num ));  // open: MAX
  not not_18 (Miss, Hit);
  or or_18 (or_18_out, decoder_1_out0, decoder_2_out0);
  or or_19 (or_19_out, decoder_1_out1, decoder_2_out1);
  or or_20 (or_20_out, decoder_1_out2, decoder_2_out2);
  or or_21 (or_21_out, decoder_1_out3, decoder_2_out3);
  or or_22 (or_22_out, decoder_1_out4, decoder_2_out4);
  or or_23 (or_23_out, decoder_1_out5, decoder_2_out5);
  or or_24 (or_24_out, decoder_1_out6, decoder_2_out6);
  or or_25 (or_25_out, decoder_1_out7, decoder_2_out7);
  Comparator #(.width(32), .mode("twosComplement")) comparator_9 (
    .a(EX_PC), .b(tag0), .eq(comparator_9_eq));  // open: gt, lt
  Comparator #(.width(32), .mode("twosComplement")) comparator_10 (
    .a(EX_PC), .b(tag1), .eq(comparator_10_eq));  // open: gt, lt
  Comparator #(.width(32), .mode("twosComplement")) comparator_11 (
    .a(EX_PC), .b(tag2), .eq(comparator_11_eq));  // open: gt, lt
  Comparator #(.width(32), .mode("twosComplement")) comparator_12 (
    .a(EX_PC), .b(tag3), .eq(comparator_12_eq));  // open: gt, lt
  Comparator #(.width(32), .mode("twosComplement")) comparator_13 (
    .a(EX_PC), .b(tag4), .eq(comparator_13_eq));  // open: gt, lt
  Comparator #(.width(32), .mode("twosComplement")) comparator_14 (
    .a(EX_PC), .b(tag5), .eq(comparator_14_eq));  // open: gt, lt
  Comparator #(.width(32), .mode("twosComplement")) comparator_15 (
    .a(EX_PC), .b(tag6), .eq(comparator_15_eq));  // open: gt, lt
  Comparator #(.width(32), .mode("twosComplement")) comparator_16 (
    .a(EX_PC), .b(tag7), .eq(comparator_16_eq));  // open: gt, lt
  and and_17 (W0, EX_Miss, or_18_out);
  and and_18 (W1, EX_Miss, or_19_out);
  and and_19 (W2, EX_Miss, or_20_out);
  and and_20 (W3, EX_Miss, or_21_out);
  and and_21 (W4, EX_Miss, or_22_out);
  and and_22 (W5, EX_Miss, or_23_out);
  and and_23 (W6, EX_Miss, or_24_out);
  and and_24 (W7, EX_Miss, or_25_out);
  and and_25 (H0, comparator_9_eq, V0);
  and and_26 (H1, comparator_10_eq, V1);
  and and_27 (H2, comparator_11_eq, V2);
  and and_28 (H3, comparator_12_eq, V3);
  and and_29 (H4, comparator_13_eq, V4);
  and and_30 (H5, comparator_14_eq, V5);
  and and_31 (H6, comparator_15_eq, V6);
  and and_32 (H7, comparator_16_eq, V7);
  or or_26 (or_26_out, H0, H1, H2, H3, H4, H5, H6, H7);
  and and_33 (EX_Hit, EX_Branch, or_26_out);
  not not_19 (not_19_out, EX_Hit);
  and and_34 (EX_Miss, not_19_out, EX_Branch, EX_PredictErr);

  // Other names for the same wires on the sheet: EX_BranchTaken = EX_PredictErr
endmodule

// MAX2
module \二路归并比较  (
  input  [15:0] Y,
  input  [15:0] X,
  input  [2:0] Y_num,
  input  [2:0] X_num,
  output [15:0] MAX,
  output [2:0] MAX_num
);

  wire comparator_1_eq, comparator_1_gt, or_1_out;

  Multiplexer #(.select(1), .width(16), .disabled("Z"), .enable("true")) multiplexer_1 (
    .in0(Y), .in1(X), .out(MAX), .sel(or_1_out), .en(1'b1));
  Comparator #(.width(16), .mode("unsigned")) comparator_1 (
    .a(X), .b(Y), .gt(comparator_1_gt), .eq(comparator_1_eq));  // open: lt
  or or_1 (or_1_out, comparator_1_gt, comparator_1_eq);
  Multiplexer #(.select(1), .width(3), .disabled("Z"), .enable("false")) multiplexer_2 (
    .in0(Y_num), .in1(X_num), .out(MAX_num), .sel(or_1_out));

  // Notes on the sheet:
  //   输出两个输入中的较大值，并输出较大值的2位编号
endmodule
