// Logisim project 张睿_CSIE1902_U201912633_RiscvOnBusCpu-2.circ as structural Verilog: 15 circuits, main circuit ◇指令译码器
module \单总线CPU_微程序  (
  output [21:0] \控制总线 
);

  wire and_1_out, CLK, comparator_1_eq, comparator_2_eq, equal, not_1_out, risc_v_alu_1_equal, RST;
  wire [4:0] registerfile_1_p6, \微地址_状态 ;
  wire [11:0] Clks, \指令数 ;
  wire [31:0] AR_q, bit_extender_1_out, bit_extender_2_out, bit_extender_3_out, controlled_buffer_1_out,
       controlled_buffer_3_out, DR_q, IR, PC_q, ram_1_data, registerfile_1_p7, risc_v_alu_1_result,
       shifter_1_out, subtractor_1_out, X_q, Z_q, \内总线 ;

  // Probe on Clks
  Register #(.width(32), .trigger("rising"), .Select("low")) AR (
    .D(\内总线 ), .en(\控制总线 [12]), .Q(AR_q), .clk(CLK));  // open: clr
  // Probe on controlled_buffer_3_out
  // RiscV_Probe riscv_probe_1: pin names not known; wires that end beside it: IR
  Register #(.width(32), .trigger("rising"), .Select("low")) X (
    .D(\内总线 ), .en(\控制总线 [9]), .Q(X_q), .clk(CLK));  // open: clr
  // Probe on \指令数 
  RAM #(.addrWidth(10), .dataWidth(32), .bus("separate"), .Select("high")) ram_1 (
    .addr(AR_q[11:2]), .din(controlled_buffer_3_out), .data(ram_1_data), .str(\控制总线 [0]), .clk(CLK),
    .ld(\控制总线 [1]));  // open: sel, clr
  RISC_V_ALU risc_v_alu_1 (
    .X(X_q), .Y(\内总线 ), .Equal(risc_v_alu_1_equal), .Result(risc_v_alu_1_result), .ADD(\控制总线 [4]),
    .ADD4(\控制总线 [3]), .SLT(\控制总线 [2]));  // open: SUB
  assign controlled_buffer_1_out = \控制总线 [10] ? \内总线  : 32'bz;  // Controlled_Buffer controlled_buffer_1
  assign controlled_buffer_1_out = \控制总线 [11] ? ram_1_data : 32'bz;  // Controlled_Buffer controlled_buffer_2
  assign controlled_buffer_3_out = \控制总线 [14] ? DR_q : 32'bz;  // Controlled_Buffer controlled_buffer_3
  // Probe on \内总线 
  Register #(.width(32), .trigger("rising"), .Select("low")) PC (
    .D(\内总线 ), .en(\控制总线 [13]), .Q(PC_q), .clk(CLK), .clr(RST));
  Register #(.width(32), .trigger("rising"), .Select("low")) DR (
    .D(controlled_buffer_1_out), .Q(DR_q), .clk(CLK));  // open: en, clr
  Register #(.width(1), .trigger("rising"), .Select("low")) PSW (
    .D(risc_v_alu_1_equal), .en(\控制总线 [6]), .Q(equal), .clk(CLK));  // open: clr
  Register #(.width(32), .trigger("rising"), .Select("low")) Z (
    .D(risc_v_alu_1_result), .Q(Z_q), .clk(CLK));  // open: en, clr
  assign \内总线  = \控制总线 [21] ? PC_q : 32'bz;  // Controlled_Buffer controlled_buffer_4
  assign \内总线  = \控制总线 [20] ? DR_q : 32'bz;  // Controlled_Buffer controlled_buffer_5
  assign \内总线  = \控制总线 [19] ? Z_q : 32'bz;  // Controlled_Buffer controlled_buffer_6
  Register #(.width(32), .trigger("rising"), .Select("low")) u_IR (
    .D(\内总线 ), .en(\控制总线 [7]), .Q(IR), .clk(CLK));  // open: clr
  \硬布线控制器  \u_硬布线控制器_1  (.CLK(CLK), .EQUAL(equal), .statu(\微地址_状态 ), .\控制总线 (\控制总线 ), .\指令字 (IR));
  Comparator #(.width(32), .mode("twosComplement")) comparator_1 (
    .a(IR), .b(32'h63), .eq(comparator_1_eq));  // open: gt, lt
  Clock #(.highDuration(1), .lowDuration(1)) clock_1 (.out(CLK));
  // Probe on \微地址_状态 
  // RegisterFile registerfile_1: pin names not known; wires that end beside it: \内总线 , CLK, \控制总线 [8], IR, IR[11:7], registerfile_1_p6, registerfile_1_p7
  not not_1 (not_1_out, comparator_1_eq);
  Counter #(.width(12), .max('hfff), .ongoal("wrap"), .trigger("rising"), .behavior("new")) counter_1 (
    .count(not_1_out), .Q(Clks), .clk(CLK));  // open: load, D, carry, clr, preset, down
  assign bit_extender_1_out = {{20{IR[31]}}, {IR[31], IR[7], IR[30:25], IR[11:8]}};  // Bit_Extender bit_extender_1
  assign \内总线  = \控制总线 [18] ? registerfile_1_p7 : 32'bz;  // Controlled_Buffer controlled_buffer_7
  Multiplexer #(.select(1), .width(5), .disabled("Z"), .enable("false")) multiplexer_1 (
    .in0(IR[19:15]), .in1(IR[24:20]), .out(registerfile_1_p6), .sel(\控制总线 [5]));
  assign bit_extender_2_out = {{20{IR[31]}}, {IR[31:25], IR[11:7]}};  // Bit_Extender bit_extender_2
  assign bit_extender_3_out = {{20{IR[31]}}, IR[31:20]};  // Bit_Extender bit_extender_3
  Shifter #(.width(32), .shift("ll")) shifter_1 (.in(bit_extender_1_out), .\dist (5'b00001), .out(shifter_1_out));
  Subtractor #(.width(32)) subtractor_1 (.a(shifter_1_out), .b(32'h4), .out(subtractor_1_out));  // open: bin, bout
  and and_1 (and_1_out, not_1_out, comparator_2_eq);
  Comparator #(.width(5), .mode("twosComplement")) comparator_2 (
    .a(5'b00011), .b(\微地址_状态 ), .eq(comparator_2_eq));  // open: gt, lt
  assign \内总线  = \控制总线 [17] ? bit_extender_3_out : 32'bz;  // Controlled_Buffer controlled_buffer_8
  assign \内总线  = \控制总线 [15] ? subtractor_1_out : 32'bz;  // Controlled_Buffer controlled_buffer_9
  Counter #(.width(12), .max('hfff), .ongoal("wrap"), .trigger("rising"), .behavior("old")) counter_2 (
    .count(and_1_out), .Q(\指令数 ), .clk(CLK));  // open: load, D, carry, clr, preset
  assign \内总线  = \控制总线 [16] ? bit_extender_2_out : 32'bz;  // Controlled_Buffer controlled_buffer_10

  // Other names for the same wires on the sheet: rd[4:0] = IR[11:7]; rs1[4:0] = IR[19:15]; rs2[4:0] = IR[24:20];
  //   Write = \控制总线 [0]; READ = \控制总线 [1]; Slt = \控制总线 [2]; Add4 = \控制总线 [3]; Add = \控制总线 [4]; rs1_2 = \控制总线 [5];
  //   PSWin = \控制总线 [6]; IRin = \控制总线 [7]; Rin = \控制总线 [8]; Xin = \控制总线 [9]; DRin = \控制总线 [10]; DREin = \控制总线 [11];
  //   ARin = \控制总线 [12]; PCin = \控制总线 [13]; DREout = \控制总线 [14]; IR_B_out = \控制总线 [15]; IR_S_out = \控制总线 [16];
  //   IR_I_out = \控制总线 [17]; Rout = \控制总线 [18]; Zout = \控制总线 [19]; DRout = \控制总线 [20]; PCout = \控制总线 [21]

  // Notes on the sheet:
  //   单总线 RISC-V 现代时序
  //   RAM
  //   外总线
  //   内总线
  //   B_imm12
endmodule

// Decoder
module \指令译码器  (
  input  [31:0] IR,
  output LW,
  output SW,
  output BEQ,
  output ADDI,
  output SLT,
  output OtherInstr
);

  Comparator #(.width(8), .mode("twosComplement")) comparator_1 (
    .a({IR[14:12], IR[6:2]}), .b(8'h40), .eq(LW));  // open: gt, lt
  Comparator #(.width(8), .mode("twosComplement")) comparator_2 (
    .a({IR[14:12], IR[6:2]}), .b(8'h48), .eq(SW));  // open: gt, lt
  Comparator #(.width(8), .mode("twosComplement")) comparator_3 (
    .a({IR[14:12], IR[6:2]}), .b(8'h18), .eq(BEQ));  // open: gt, lt
  Comparator #(.width(8), .mode("twosComplement")) comparator_4 (
    .a({IR[14:12], IR[6:2]}), .b(8'h4), .eq(ADDI));  // open: gt, lt
  Comparator #(.width(15), .mode("twosComplement")) comparator_5 (
    .a({IR[31:25], IR[14:12], IR[6:2]}), .b(15'h4c), .eq(SLT));  // open: gt, lt
  nor nor_1 (OtherInstr, BEQ, SW, LW, ADDI, SLT);

  // Other names for the same wires on the sheet: OP[4:0] = IR[6:2]; OP_Funct3[7:0] = {IR[14:12], IR[6:2]};
  //   FUNCT3[2:0] = IR[14:12]; FUNCT7[6:0] = IR[31:25]
endmodule

module \微程序控制器  (
  input  EQUAL,
  input  [31:0] \指令字 ,
  input  CLK,
  output [4:0] mAddr,
  output [21:0] \控制总线 
);

  wire ADDI, BEQ, LW, Other, P0, P1, P2, SLT, SW;
  wire [1:0] \条件判别测试逻辑_1_s0 ;
  wire [4:0] adder_1_out, multiplexer_1_out, rom_1_data, \微程序入口查找逻辑_1_s0 ;

  \微程序入口查找逻辑  \u_微程序入口查找逻辑_1  (
    .LW(LW), .SW(SW), .BEQ(BEQ), .SLT(SLT), .ADDI(ADDI), .S4(\微程序入口查找逻辑_1_s0 [4]), .S3(\微程序入口查找逻辑_1_s0 [3]),
    .S2(\微程序入口查找逻辑_1_s0 [2]), .S1(\微程序入口查找逻辑_1_s0 [1]), .S0(\微程序入口查找逻辑_1_s0 [0]));
  // Probe on \微程序入口查找逻辑_1_s0 
  Adder #(.width(5)) adder_1 (.a(mAddr), .b(5'b00001), .out(adder_1_out));  // open: cin, cout
  \条件判别测试逻辑  \u_条件判别测试逻辑_1  (.P0(P0), .P1(P1), .equal(EQUAL), .S1(\条件判别测试逻辑_1_s0 [1]), .S0(\条件判别测试逻辑_1_s0 [0]));
  Multiplexer #(.select(2), .width(5), .disabled("Z"), .enable("false")) multiplexer_1 (
    .in0(rom_1_data), .in1(\微程序入口查找逻辑_1_s0 ), .in2(adder_1_out), .out(multiplexer_1_out),
    .sel(\条件判别测试逻辑_1_s0 ));  // open: in3
  Register #(.width(5), .trigger("falling"), .Select("low")) register_1 (
    .D(multiplexer_1_out), .Q(mAddr), .clk(CLK));  // open: en, clr
  // Probe on mAddr
  \指令译码器  \u_指令译码器_1  (.IR(\指令字 ), .LW(LW), .SW(SW), .BEQ(BEQ), .ADDI(ADDI), .SLT(SLT), .OtherInstr(Other));
  ROM #(.addrWidth(5), .dataWidth(30), .Select("high")) rom_1 (.addr(mAddr), .data({\控制总线 , P0, P1, P2, rom_1_data}));

  // Notes on the sheet:
  //   不要改变此引脚区域内容，也不要改变封装形式
  //   地址转移逻辑
  //   入口地址
  //   beq分支
  //   下址字段
  //   输入输出引脚
  //   μAR
  //   时钟是上跳沿还是下跳沿有效？
  //   微程序控制器（下址字段法）
  //   微地址
  //   控制存储器
  //   指令译码器
  //   contents of rom_1 (hex, n*v repeats v):
  //   20120001 802 8280203 10008080 4020005 2001006 8100007 80208 10010000 402000a 100100b 810000c 404200d
  //   400100 402000f 4006040 20020011 801012 8200000 4020014 4002415 8010000 4020017 2001018 8010000
  //   控制字段
  //   指令译码信号
  //   微指令
  //   指令译码逻辑ID
  //   判断逻辑
endmodule

module \微程序入口查找逻辑  (
  input  LW,
  input  SW,
  input  BEQ,
  input  SLT,
  input  ADDI,
  output S4,
  output S3,
  output S2,
  output S1,
  output S0
);

  or or_1 (S4, SLT, ADDI);
  or or_2 (S3, SW, BEQ);
  or or_3 (S2, LW, BEQ, ADDI);
  or or_4 (S1, BEQ, SLT, ADDI);
  or or_5 (S0, SW, SLT);
endmodule

module \条件判别测试逻辑  (
  input  P0,
  input  P1,
  input  equal,
  output S1,
  output S0
);

  wire and_1_out, and_2_out, and_3_out, and_4_out, and_5_out, not_1_out, not_2_out, not_3_out, not_4_out,
       not_5_out;

  not not_1 (not_1_out, P0);
  not not_2 (not_2_out, P1);
  not not_3 (not_3_out, equal);
  not not_4 (not_4_out, P1);
  not not_5 (not_5_out, equal);
  and and_1 (and_1_out, P0, P1, equal);
  and and_2 (and_2_out, not_1_out, P1, equal);
  and and_3 (and_3_out, P0, not_2_out, not_3_out);
  and and_4 (and_4_out, P0, not_4_out, equal);
  and and_5 (and_5_out, P0, P1, not_5_out);
  or or_1 (S1, and_1_out, and_2_out);
  or or_2 (S0, and_3_out, and_4_out, and_5_out);
endmodule

module \硬布线控制器  (
  input  EQUAL,
  input  [31:0] \指令字 ,
  input  CLK,
  output [4:0] statu,
  output [21:0] \控制总线 
);

  wire ADDI, BEQ, LW, Other, SLT, SW;
  wire [4:0] \硬布线状态机_1_n0 ;
  wire [7:0] rom_1_data;

  \硬布线状态机  \u_硬布线状态机_1  (
    .S4(statu[4]), .S3(statu[3]), .S2(statu[2]), .S1(statu[1]), .S0(statu[0]), .LW(LW), .SW(SW), .BEQ(BEQ),
    .SLT(SLT), .ADDI(ADDI), .EQUAL(EQUAL), .N4(\硬布线状态机_1_n0 [4]), .N3(\硬布线状态机_1_n0 [3]),
    .N2(\硬布线状态机_1_n0 [2]), .N1(\硬布线状态机_1_n0 [1]), .N0(\硬布线状态机_1_n0 [0]));
  // Probe on \硬布线状态机_1_n0 
  Register #(.width(5), .trigger("falling"), .Select("low")) register_1 (
    .D(\硬布线状态机_1_n0 ), .Q(statu), .clk(CLK));  // open: en, clr
  \指令译码器  \u_指令译码器_1  (.IR(\指令字 ), .LW(LW), .SW(SW), .BEQ(BEQ), .ADDI(ADDI), .SLT(SLT), .OtherInstr(Other));
  ROM #(.addrWidth(5), .dataWidth(30), .Select("high")) rom_1 (.addr(statu), .data({\控制总线 , rom_1_data}));

  // Other names for the same wires on the sheet: status[4:0] = statu; Write = \控制总线 [0]; READ = \控制总线 [1];
  //   Slt_t = \控制总线 [2]; Add4 = \控制总线 [3]; Add = \控制总线 [4]; rs1_2 = \控制总线 [5]; PSWin = \控制总线 [6]; IRin = \控制总线 [7];
  //   Rin = \控制总线 [8]; Xin = \控制总线 [9]; DRin = \控制总线 [10]; DREin = \控制总线 [11]; ARin = \控制总线 [12]; PCin = \控制总线 [13];
  //   DREout = \控制总线 [14]; IR_B_out = \控制总线 [15]; IR_S_out = \控制总线 [16]; IR_I_out = \控制总线 [17]; Rout = \控制总线 [18];
  //   Zout = \控制总线 [19]; DRout = \控制总线 [20]; PCout = \控制总线 [21]

  // Notes on the sheet:
  //   不要改变此引脚区域内容，也不要改变封装形式
  //   输入输出引脚
  //   时钟是上跳沿还是下跳沿有效？
  //   状态寄存器
  //   指令译码器
  //   控制存储器
  //   contents of rom_1 (hex, n*v repeats v):
  //   20120001 802 8280203 10008080 4020005 2001006 8100007 80208 10010000 402000a 100100b 810000c 404200d
  //   400100 402000f 4006040 20020011 801012 8200000 4020014 4002415 8010000 4020017 2001018 8010000
  //   指令译码信号
  //   控制字段
  //   微指令
  //   指令译码逻辑ID
endmodule

// 硬布线状态机
module \硬布线状态机  (
  input  S4,
  input  S3,
  input  S2,
  input  S1,
  input  S0,
  input  LW,
  input  SW,
  input  BEQ,
  input  SLT,
  input  ADDI,
  input  EQUAL,
  output N4,
  output N3,
  output N2,
  output N1,
  output N0
);

  wire and_1_out, and_2_out, and_3_out, and_4_out, and_5_out, and_6_out, and_7_out, and_8_out, and_9_out,
       and_10_out, and_11_out, and_12_out, and_13_out, and_14_out, and_15_out, and_16_out, and_17_out,
       and_18_out, and_19_out, and_20_out, and_21_out, and_22_out, and_23_out, and_24_out, and_25_out,
       and_26_out, and_27_out, and_28_out, and_29_out, and_30_out, and_31_out, and_32_out, and_33_out,
       and_34_out, and_35_out, and_36_out, and_37_out, and_38_out, and_39_out, and_40_out, and_41_out,
       and_42_out, and_43_out, and_44_out, and_45_out, and_46_out, and_47_out, and_48_out, and_49_out,
       and_50_out, and_51_out, and_52_out, and_53_out, and_54_out, not_1_out, not_2_out, not_3_out,
       not_4_out, not_5_out, not_6_out, not_7_out, not_8_out, not_9_out, not_10_out, not_11_out, not_12_out,
       not_13_out, not_14_out, not_15_out, not_16_out, not_17_out, not_18_out, not_19_out, not_20_out,
       not_21_out, not_22_out, not_23_out, not_24_out, not_25_out, not_26_out, not_27_out, not_28_out,
       not_29_out, not_30_out, not_31_out, not_32_out, not_33_out, not_34_out, not_35_out, not_36_out,
       not_37_out, not_38_out, not_39_out, not_40_out, not_41_out, not_42_out, not_43_out, not_44_out,
       not_45_out, not_46_out, not_47_out, not_48_out, not_49_out, not_50_out, not_51_out, not_52_out,
       not_53_out, not_54_out, not_55_out, not_56_out, not_57_out, not_58_out, not_59_out, not_60_out,
       not_61_out, not_62_out, not_63_out, not_64_out, not_65_out, not_66_out, not_67_out, not_68_out,
       not_69_out, not_70_out, not_71_out, not_72_out, not_73_out, not_74_out, not_75_out, not_76_out,
       not_77_out, not_78_out, not_79_out, not_80_out, not_81_out, not_82_out, not_83_out, not_84_out,
       not_85_out, not_86_out, not_87_out, not_88_out, not_89_out, not_90_out, not_91_out, not_92_out,
       not_93_out, not_94_out, not_95_out, not_96_out, not_97_out, not_98_out, not_99_out, not_100_out,
       not_101_out, not_102_out, not_103_out, not_104_out, not_105_out, not_106_out, not_107_out,
       not_108_out, not_109_out, not_110_out, not_111_out, not_112_out, not_113_out, not_114_out,
       not_115_out, not_116_out, not_117_out, not_118_out, not_119_out, not_120_out, not_121_out,
       not_122_out, not_123_out, not_124_out, not_125_out, not_126_out, not_127_out, not_128_out,
       not_129_out, not_130_out, not_131_out, not_132_out, not_133_out, not_134_out, not_135_out,
       not_136_out, not_137_out, not_138_out, not_139_out, not_140_out, not_141_out, not_142_out,
       not_143_out, not_144_out, not_145_out, not_146_out, not_147_out, not_148_out, not_149_out,
       not_150_out, not_151_out, not_152_out;

  not not_1 (not_1_out, S4);
  not not_2 (not_2_out, S3);
  not not_3 (not_3_out, S2);
  not not_4 (not_4_out, S1);
  not not_5 (not_5_out, S0);
  not not_6 (not_6_out, S3);
  not not_7 (not_7_out, S2);
  not not_8 (not_8_out, S1);
  not not_9 (not_9_out, S4);
  not not_10 (not_10_out, S3);
  not not_11 (not_11_out, S2);
  not not_12 (not_12_out, S3);
  not not_13 (not_13_out, S2);
  not not_14 (not_14_out, S3);
  not not_15 (not_15_out, S1);
  not not_16 (not_16_out, S0);
  not not_17 (not_17_out, S4);
  not not_18 (not_18_out, S3);
  not not_19 (not_19_out, S2);
  not not_20 (not_20_out, S3);
  not not_21 (not_21_out, S0);
  not not_22 (not_22_out, S3);
  not not_23 (not_23_out, S4);
  not not_24 (not_24_out, S3);
  not not_25 (not_25_out, S4);
  not not_26 (not_26_out, S3);
  not not_27 (not_27_out, S2);
  not not_28 (not_28_out, S4);
  not not_29 (not_29_out, S2);
  not not_30 (not_30_out, S1);
  not not_31 (not_31_out, S4);
  not not_32 (not_32_out, S2);
  not not_33 (not_33_out, S0);
  not not_34 (not_34_out, S4);
  not not_35 (not_35_out, S2);
  not not_36 (not_36_out, S4);
  not not_37 (not_37_out, S1);
  not not_38 (not_38_out, S0);
  not not_39 (not_39_out, S4);
  not not_40 (not_40_out, S3);
  not not_41 (not_41_out, S2);
  not not_42 (not_42_out, S4);
  not not_43 (not_43_out, S0);
  not not_44 (not_44_out, S3);
  not not_45 (not_45_out, S4);
  not not_46 (not_46_out, S3);
  not not_47 (not_47_out, S2);
  not not_48 (not_48_out, S4);
  not not_49 (not_49_out, S3);
  not not_50 (not_50_out, S1);
  not not_51 (not_51_out, S0);
  not not_52 (not_52_out, S4);
  not not_53 (not_53_out, S3);
  not not_54 (not_54_out, S1);
  not not_55 (not_55_out, S4);
  not not_56 (not_56_out, S3);
  not not_57 (not_57_out, S0);
  not not_58 (not_58_out, S4);
  not not_59 (not_59_out, S2);
  not not_60 (not_60_out, S4);
  not not_61 (not_61_out, S1);
  not not_62 (not_62_out, S0);
  not not_63 (not_63_out, S4);
  not not_64 (not_64_out, S3);
  not not_65 (not_65_out, S2);
  not not_66 (not_66_out, S4);
  not not_67 (not_67_out, S0);
  not not_68 (not_68_out, S3);
  not not_69 (not_69_out, S2);
  not not_70 (not_70_out, S3);
  not not_71 (not_71_out, S1);
  not not_72 (not_72_out, S0);
  not not_73 (not_73_out, S4);
  not not_74 (not_74_out, S3);
  not not_75 (not_75_out, S2);
  not not_76 (not_76_out, S3);
  not not_77 (not_77_out, S0);
  not not_78 (not_78_out, S4);
  not not_79 (not_79_out, S3);
  not not_80 (not_80_out, S2);
  not not_81 (not_81_out, S1);
  not not_82 (not_82_out, S4);
  not not_83 (not_83_out, S3);
  not not_84 (not_84_out, S2);
  not not_85 (not_85_out, S0);
  not not_86 (not_86_out, S4);
  not not_87 (not_87_out, S3);
  not not_88 (not_88_out, S1);
  not not_89 (not_89_out, S4);
  not not_90 (not_90_out, S3);
  not not_91 (not_91_out, S0);
  not not_92 (not_92_out, S4);
  not not_93 (not_93_out, S2);
  not not_94 (not_94_out, S1);
  not not_95 (not_95_out, S4);
  not not_96 (not_96_out, S2);
  not not_97 (not_97_out, S0);
  not not_98 (not_98_out, S4);
  not not_99 (not_99_out, S3);
  not not_100 (not_100_out, S2);
  not not_101 (not_101_out, S4);
  not not_102 (not_102_out, S0);
  not not_103 (not_103_out, S3);
  not not_104 (not_104_out, S2);
  not not_105 (not_105_out, S1);
  not not_106 (not_106_out, S4);
  not not_107 (not_107_out, S3);
  not not_108 (not_108_out, S2);
  not not_109 (not_109_out, S4);
  not not_110 (not_110_out, S3);
  not not_111 (not_111_out, S2);
  not not_112 (not_112_out, S3);
  not not_113 (not_113_out, S0);
  not not_114 (not_114_out, S4);
  not not_115 (not_115_out, S3);
  not not_116 (not_116_out, S2);
  not not_117 (not_117_out, S1);
  not not_118 (not_118_out, S0);
  not not_119 (not_119_out, S4);
  not not_120 (not_120_out, S3);
  not not_121 (not_121_out, S2);
  not not_122 (not_122_out, S0);
  not not_123 (not_123_out, S4);
  not not_124 (not_124_out, S3);
  not not_125 (not_125_out, S1);
  not not_126 (not_126_out, S0);
  not not_127 (not_127_out, S4);
  not not_128 (not_128_out, S3);
  not not_129 (not_129_out, S0);
  not not_130 (not_130_out, S4);
  not not_131 (not_131_out, S3);
  not not_132 (not_132_out, S2);
  not not_133 (not_133_out, S4);
  not not_134 (not_134_out, S2);
  not not_135 (not_135_out, S0);
  not not_136 (not_136_out, S4);
  not not_137 (not_137_out, S1);
  not not_138 (not_138_out, S0);
  not not_139 (not_139_out, S4);
  not not_140 (not_140_out, S0);
  not not_141 (not_141_out, S3);
  not not_142 (not_142_out, S2);
  not not_143 (not_143_out, S1);
  not not_144 (not_144_out, S0);
  not not_145 (not_145_out, S4);
  not not_146 (not_146_out, S3);
  not not_147 (not_147_out, S2);
  not not_148 (not_148_out, S3);
  not not_149 (not_149_out, S1);
  not not_150 (not_150_out, S0);
  not not_151 (not_151_out, S3);
  not not_152 (not_152_out, S0);
  and and_1 (and_1_out, not_1_out, S3, S2, S1, S0, EQUAL);
  and and_2 (and_2_out, S4, not_2_out, not_3_out, not_4_out, not_5_out);
  and and_3 (and_3_out, S4, not_6_out, not_7_out, not_8_out, S0);
  and and_4 (and_4_out, not_9_out, not_10_out, not_11_out, S1, S0, SLT);
  and and_5 (and_5_out, S4, not_12_out, not_13_out, S1, S0);
  and and_6 (and_6_out, S4, not_14_out, S2, not_15_out, not_16_out);
  and and_7 (and_7_out, not_17_out, not_18_out, not_19_out, S1, S0, ADDI);
  and and_8 (and_8_out, S4, not_20_out, S2, S1, not_21_out);
  and and_9 (and_9_out, S4, not_22_out, S2, S1, S0);
  and and_10 (and_10_out, not_23_out, not_24_out, S2, S1, S0);
  and and_11 (and_11_out, not_25_out, not_26_out, not_27_out, S1, S0, SW);
  and and_12 (and_12_out, not_28_out, S3, not_29_out, not_30_out, S0);
  and and_13 (and_13_out, not_31_out, S3, not_32_out, S1, not_33_out);
  and and_14 (and_14_out, not_34_out, S3, not_35_out, S1, S0);
  and and_15 (and_15_out, not_36_out, S3, S2, not_37_out, not_38_out);
  and and_16 (and_16_out, not_39_out, not_40_out, not_41_out, S1, S0, BEQ);
  and and_17 (and_17_out, not_42_out, S3, S2, S1, not_43_out);
  and and_18 (and_18_out, S4, not_44_out, S2, S1, S0);
  and and_19 (and_19_out, not_45_out, not_46_out, not_47_out, S1, S0, LW);
  and and_20 (and_20_out, not_48_out, not_49_out, S2, not_50_out, not_51_out);
  and and_21 (and_21_out, not_52_out, not_53_out, S2, not_54_out, S0);
  and and_22 (and_22_out, not_55_out, not_56_out, S2, S1, not_57_out);
  and and_23 (and_23_out, not_58_out, S3, not_59_out, S1, S0);
  and and_24 (and_24_out, not_60_out, S3, S2, not_61_out, not_62_out);
  and and_25 (and_25_out, not_63_out, not_64_out, not_65_out, S1, S0, BEQ);
  and and_26 (and_26_out, not_66_out, S3, S2, S1, not_67_out);
  and and_27 (and_27_out, S4, not_68_out, not_69_out, S1, S0);
  and and_28 (and_28_out, S4, not_70_out, S2, not_71_out, not_72_out);
  and and_29 (and_29_out, not_73_out, not_74_out, not_75_out, S1, S0, ADDI);
  and and_30 (and_30_out, S4, not_76_out, S2, S1, not_77_out);
  and and_31 (and_31_out, not_78_out, not_79_out, not_80_out, not_81_out, S0);
  and and_32 (and_32_out, not_82_out, not_83_out, not_84_out, S1, not_85_out);
  and and_33 (and_33_out, not_86_out, not_87_out, S2, not_88_out, S0);
  and and_34 (and_34_out, not_89_out, not_90_out, S2, S1, not_91_out);
  and and_35 (and_35_out, not_92_out, S3, not_93_out, not_94_out, S0);
  and and_36 (and_36_out, not_95_out, S3, not_96_out, S1, not_97_out);
  and and_37 (and_37_out, not_98_out, not_99_out, not_100_out, S1, S0, BEQ);
  and and_38 (and_38_out, not_101_out, S3, S2, S1, not_102_out);
  and and_39 (and_39_out, S4, not_103_out, not_104_out, not_105_out, S0);
  and and_40 (and_40_out, not_106_out, not_107_out, not_108_out, S1, S0, SLT);
  and and_41 (and_41_out, not_109_out, not_110_out, not_111_out, S1, S0, ADDI);
  and and_42 (and_42_out, S4, not_112_out, S2, S1, not_113_out);
  and and_43 (and_43_out, not_114_out, not_115_out, not_116_out, not_117_out, not_118_out);
  and and_44 (and_44_out, not_119_out, not_120_out, not_121_out, S1, not_122_out);
  and and_45 (and_45_out, not_123_out, not_124_out, S2, not_125_out, not_126_out);
  and and_46 (and_46_out, not_127_out, not_128_out, S2, S1, not_129_out);
  and and_47 (and_47_out, not_130_out, not_131_out, not_132_out, S1, S0, SW);
  and and_48 (and_48_out, not_133_out, S3, not_134_out, S1, not_135_out);
  and and_49 (and_49_out, not_136_out, S3, S2, not_137_out, not_138_out);
  and and_50 (and_50_out, not_139_out, S3, S2, S1, not_140_out);
  and and_51 (and_51_out, S4, not_141_out, not_142_out, not_143_out, not_144_out);
  and and_52 (and_52_out, not_145_out, not_146_out, not_147_out, S1, S0, SLT);
  and and_53 (and_53_out, S4, not_148_out, S2, not_149_out, not_150_out);
  and and_54 (and_54_out, S4, not_151_out, S2, S1, not_152_out);
  or or_1 (N4, and_1_out, and_2_out, and_3_out, and_4_out, and_5_out, and_6_out, and_7_out, and_8_out, and_9_out);
  or or_2 (N3, and_10_out, and_11_out, and_12_out, and_13_out, and_14_out, and_15_out, and_16_out, and_17_out, and_18_out);
  or or_3 (N2, and_19_out, and_20_out, and_21_out, and_22_out, and_23_out, and_24_out, and_25_out, and_26_out, and_27_out, and_28_out, and_29_out, and_30_out);
  or or_4 (N1, and_31_out, and_32_out, and_33_out, and_34_out, and_35_out, and_36_out, and_37_out, and_38_out, and_39_out, and_40_out, and_41_out, and_42_out);
  or or_5 (N0, and_43_out, and_44_out, and_45_out, and_46_out, and_47_out, and_48_out, and_49_out, and_50_out, and_51_out, and_52_out, and_53_out, and_54_out);
endmodule

module \单总线CPU_中断_微程序  (
  input  [1:0] EduInt,
  output [21:0] \控制总线 ,
  output [4:0] \EDU中断信号 
);

  wire _1_out, _2_out, and_1_out, CLK, comparator_1_eq, comparator_2_eq, d_ff_1_qn, equal, not_1_out,
       risc_v_alu_1_equal, RST, \中断控制器_1_intr , \中断控制器_1_ir1w , \中断控制器_1_ir2w , \中断请求 ;
  wire [1:0] \中断控制器_1_intno ;
  wire [4:0] registerfile_1_p6, \微地址_状态 ;
  wire [9:0] AR_q_2;
  wire [11:0] Clks, \指令数 ;
  wire [31:0] AR_q, bit_extender_1_out, bit_extender_2_out, bit_extender_3_out, controlled_buffer_1_out,
       controlled_buffer_3_out, DR_q, IR, mEPC_q, multiplexer_2_out, PC_q, ram_1_data, registerfile_1_p7,
       risc_v_alu_1_result, shifter_1_out, subtractor_1_out, X_q, Z_q, \内总线 ;

  // Probe on Clks
  Register #(.width(32), .trigger("rising"), .Select("low")) AR (
    .D(\内总线 ), .en(\控制总线 [12]), .Q({AR_q[31:12], AR_q_2, AR_q[1:0]}), .clk(CLK));  // open: clr
  // Probe on controlled_buffer_3_out
  Register #(.width(32), .trigger("rising"), .Select("low")) X (
    .D(\内总线 ), .en(\控制总线 [9]), .Q(X_q), .clk(CLK));  // open: clr
  // RiscV_Probe riscv_probe_1: pin names not known; wires that end beside it: IR
  // Probe on \指令数 
  RAM #(.addrWidth(10), .dataWidth(32), .bus("separate"), .Select("high")) ram_1 (
    .addr(AR_q_2), .din(controlled_buffer_3_out), .data(ram_1_data), .str(\控制总线 [0]), .clk(CLK),
    .ld(\控制总线 [1]));  // open: sel, clr
  RISC_V_ALU risc_v_alu_1 (
    .X(X_q), .Y(\内总线 ), .Equal(risc_v_alu_1_equal), .Result(risc_v_alu_1_result), .ADD(\控制总线 [4]),
    .ADD4(\控制总线 [3]), .SLT(\控制总线 [2]));  // open: SUB
  assign controlled_buffer_1_out = \控制总线 [10] ? \内总线  : 32'bz;  // Controlled_Buffer controlled_buffer_1
  assign controlled_buffer_1_out = \控制总线 [11] ? ram_1_data : 32'bz;  // Controlled_Buffer controlled_buffer_2
  assign controlled_buffer_3_out = \控制总线 [14] ? DR_q : 32'bz;  // Controlled_Buffer controlled_buffer_3
  // Probe on \内总线 
  Register #(.width(32), .trigger("rising"), .Select("low")) PC (
    .D(\内总线 ), .en(\控制总线 [13]), .Q(PC_q), .clk(CLK), .clr(RST));
  Register #(.width(32), .trigger("rising"), .Select("low")) DR (
    .D(controlled_buffer_1_out), .Q(DR_q), .clk(CLK));  // open: en, clr
  Register #(.width(1), .trigger("rising"), .Select("low")) PSW (
    .D(risc_v_alu_1_equal), .en(\控制总线 [6]), .Q(equal), .clk(CLK));  // open: clr
  Register #(.width(32), .trigger("rising"), .Select("low")) Z (
    .D(risc_v_alu_1_result), .Q(Z_q), .clk(CLK));  // open: en, clr
  assign \内总线  = \控制总线 [21] ? PC_q : 32'bz;  // Controlled_Buffer controlled_buffer_4
  assign \内总线  = \控制总线 [20] ? DR_q : 32'bz;  // Controlled_Buffer controlled_buffer_5
  assign \内总线  = \控制总线 [19] ? Z_q : 32'bz;  // Controlled_Buffer controlled_buffer_6
  Register #(.width(32), .trigger("rising"), .Select("low")) u_IR (
    .D(\内总线 ), .en(\控制总线 [7]), .Q(IR), .clk(CLK));  // open: clr
  \微程序控制器_中断  \u_微程序控制器_中断_1  (
    .EQUAL(equal), .\指令字 (IR), .IntR(\中断请求 ), .CLK(CLK), .mAddr(\微地址_状态 ), .\控制总线 (\控制总线 ),
    .\中断控制信号 (\EDU中断信号 ));
  // Probe on \微地址_状态 
  Comparator #(.width(32), .mode("twosComplement")) comparator_1 (
    .a(IR), .b(32'h63), .eq(comparator_1_eq));  // open: gt, lt
  Clock #(.highDuration(1), .lowDuration(1)) clock_1 (.out(CLK));
  assign bit_extender_1_out = {{20{IR[31]}}, {IR[31], IR[7], IR[30:25], IR[11:8]}};  // Bit_Extender bit_extender_1
  // RegisterFile registerfile_1: pin names not known; wires that end beside it: \内总线 , CLK, \控制总线 [8], IR, IR[11:7], registerfile_1_p6, registerfile_1_p7
  Multiplexer #(.select(1), .width(5), .disabled("Z"), .enable("false")) multiplexer_1 (
    .in0(IR[19:15]), .in1(IR[24:20]), .out(registerfile_1_p6), .sel(\控制总线 [5]));
  not not_1 (not_1_out, comparator_1_eq);
  Counter #(.width(12), .max('hfff), .ongoal("wrap"), .trigger("rising"), .behavior("new")) counter_1 (
    .count(not_1_out), .Q(Clks), .clk(CLK));  // open: load, D, carry, clr, preset, down
  assign bit_extender_2_out = {{20{IR[31]}}, IR[31:20]};  // Bit_Extender bit_extender_2
  Shifter #(.width(32), .shift("ll")) shifter_1 (.in(bit_extender_1_out), .\dist (5'b00001), .out(shifter_1_out));
  assign \内总线  = \控制总线 [18] ? registerfile_1_p7 : 32'bz;  // Controlled_Buffer controlled_buffer_7
  Comparator #(.width(5), .mode("twosComplement")) comparator_2 (
    .a(5'b00011), .b(\微地址_状态 ), .eq(comparator_2_eq));  // open: gt, lt
  assign bit_extender_3_out = {{20{IR[31]}}, {IR[31:25], IR[11:7]}};  // Bit_Extender bit_extender_3
  Subtractor #(.width(32)) subtractor_1 (.a(shifter_1_out), .b(32'h4), .out(subtractor_1_out));  // open: bin, bout
  assign \内总线  = \控制总线 [15] ? subtractor_1_out : 32'bz;  // Controlled_Buffer controlled_buffer_8
  Counter #(.width(12), .max('hfff), .ongoal("wrap"), .trigger("rising"), .behavior("old")) counter_2 (
    .count(and_1_out), .Q(\指令数 ), .clk(CLK));  // open: load, D, carry, clr, preset
  and and_1 (and_1_out, not_1_out, comparator_2_eq);
  assign \内总线  = \控制总线 [17] ? bit_extender_2_out : 32'bz;  // Controlled_Buffer controlled_buffer_9
  assign \内总线  = \控制总线 [16] ? bit_extender_3_out : 32'bz;  // Controlled_Buffer controlled_buffer_10
  Button _1 (.out(_1_out));
  Button _2 (.out(_2_out));
  D_Flip_Flop #(.trigger("rising"), .Pre_Clr_Positions("LEGACY"), .NegatePresetClear("false"), .enable("true"), .NewFFLayout("false")) d_ff_1 (
    .clk(CLK), .Qn(d_ff_1_qn), .preset(\EDU中断信号 [0]), .reset(\EDU中断信号 [1]));  // open: D, Q, en
  LED #(.active("true")) _1_2 (.in(\中断控制器_1_ir1w ));
  LED #(.active("true")) _2_2 (.in(\中断控制器_1_ir2w ));
  \中断控制器  \u_中断控制器_1  (
    .CLK(CLK), .Key1(_1_out), .Key2(_2_out), .Clr(\EDU中断信号 [1]), .IR1W(\中断控制器_1_ir1w ),
    .IR2W(\中断控制器_1_ir2w ), .IntNo(\中断控制器_1_intno ), .IntR(\中断控制器_1_intr ), .EDU_TEST(EduInt));  // open: IR3W, Key3
  Register #(.width(32), .trigger("rising"), .Select("low")) mEPC (
    .D(\内总线 ), .en(\EDU中断信号 [3]), .Q(mEPC_q), .clk(CLK));  // open: clr
  assign \内总线  = \EDU中断信号 [4] ? mEPC_q : 32'bz;  // Controlled_Buffer controlled_buffer_11
  and and_2 (\中断请求 , d_ff_1_qn, \中断控制器_1_intr );
  Multiplexer #(.select(2), .width(32), .disabled("Z"), .enable("false")) multiplexer_2 (
    .in1(32'ha4), .in2(32'hec), .out(multiplexer_2_out), .sel(\中断控制器_1_intno ));  // open: in0, in3
  assign \内总线  = \EDU中断信号 [2] ? multiplexer_2_out : 32'bz;  // Controlled_Buffer controlled_buffer_12

  // Other names for the same wires on the sheet: rd[4:0] = IR[11:7]; rs1[4:0] = IR[19:15]; rs2[4:0] = IR[24:20];
  //   中断控制信号[4:0] = \EDU中断信号 ; 关中断 = \EDU中断信号 [0]; 开中断 = \EDU中断信号 [1]; Addrout = \EDU中断信号 [2]; mEPCin = \EDU中断信号 [3];
  //   mEPCout = \EDU中断信号 [4]; Write = \控制总线 [0]; READ = \控制总线 [1]; Slt = \控制总线 [2]; Add4 = \控制总线 [3]; Add = \控制总线 [4];
  //   rs1_2 = \控制总线 [5]; PSWin = \控制总线 [6]; IRin = \控制总线 [7]; Rin = \控制总线 [8]; Xin = \控制总线 [9]; DRin = \控制总线 [10];
  //   DREin = \控制总线 [11]; ARin = \控制总线 [12]; PCin = \控制总线 [13]; DREout = \控制总线 [14]; IR_B_out = \控制总线 [15];
  //   IR_S_out = \控制总线 [16]; IR_I_out = \控制总线 [17]; Rout = \控制总线 [18]; Zout = \控制总线 [19]; DRout = \控制总线 [20];
  //   PCout = \控制总线 [21]

  // Notes on the sheet:
  //   单总线 RISC-V 现代时序+中断
  //   RAM
  //   外总线
  //   内总线
  //   B_imm12
  //   中断使能寄存器
  //   中断信号
  //   执行ERET时开中断，同时清除中断源
  //   中断逻辑
endmodule

module \微程序控制器_中断  (
  input  EQUAL,
  input  [31:0] \指令字 ,
  input  IntR,
  input  CLK,
  output [4:0] mAddr,
  output [21:0] \控制总线 ,
  output [4:0] \中断控制信号 
);

  wire ADDI, BEQ, ERET, LW, P0, P1, P2, SLT, SW;
  wire [2:0] \条件判别测试逻辑_中断_1_s0 ;
  wire [4:0] adder_1_out, multiplexer_1_out, \微程序入口查找逻辑_中断_1_s0 ;

  \微程序入口查找逻辑_中断  \u_微程序入口查找逻辑_中断_1  (
    .LW(LW), .SW(SW), .BEQ(BEQ), .SLT(SLT), .ADDI(ADDI), .ERET(ERET), .S4(\微程序入口查找逻辑_中断_1_s0 [4]),
    .S3(\微程序入口查找逻辑_中断_1_s0 [3]), .S2(\微程序入口查找逻辑_中断_1_s0 [2]), .S1(\微程序入口查找逻辑_中断_1_s0 [1]),
    .S0(\微程序入口查找逻辑_中断_1_s0 [0]));
  // Probe on \微程序入口查找逻辑_中断_1_s0 
  \条件判别测试逻辑_中断  \u_条件判别测试逻辑_中断_1  (
    .P0(P0), .P1(P1), .P2(P2), .equal(EQUAL), .IntR(IntR), .S2(\条件判别测试逻辑_中断_1_s0 [2]),
    .S1(\条件判别测试逻辑_中断_1_s0 [1]), .S0(\条件判别测试逻辑_中断_1_s0 [0]));
  Multiplexer #(.select(3), .width(5), .disabled("Z"), .enable("false")) multiplexer_1 (
    .in0(adder_1_out), .in1(\微程序入口查找逻辑_中断_1_s0 ), .in2(adder_1_out), .in3(5'b11010), .in4({5{1'b0}}),
    .out(multiplexer_1_out), .sel(\条件判别测试逻辑_中断_1_s0 ));  // open: in5, in6, in7
  // Probe on multiplexer_1_out
  Register #(.width(5), .trigger("falling"), .Select("low")) register_1 (
    .D(multiplexer_1_out), .Q(mAddr), .clk(CLK));  // open: en, clr
  Adder #(.width(5)) adder_1 (.a(5'b00001), .b(mAddr), .out(adder_1_out));  // open: cin, cout
  \指令译码器  \u_指令译码器_1  (.IR(\指令字 ), .LW(LW), .SW(SW), .BEQ(BEQ), .ADDI(ADDI), .SLT(SLT), .OtherInstr(ERET));
  ROM #(.addrWidth(5), .dataWidth(30), .Select("high")) rom_1 (.addr(mAddr), .data({\控制总线 , \中断控制信号 , P0, P1, P2}));

  // Notes on the sheet:
  //   不要改变此引脚区域内容，也不要改变封装形式
  //   地址转移逻辑
  //   根据指令进行微程序地址转移
  //   beq分支
  //   中断入口
  //   入口地址
  //   取指微程序入口
  //   顺序地址
  //   判别测试逻辑
  //   μAR
  //   支持中断的微程序控制器（计数器法）
  //   微地址
  //   指令译码器
  //   mAddr++
  //   控制存储器
  //   contents of rom_1 (hex, n*v repeats v):
  //   20120000 800 8280200 10008004 4020000 2001000 8100000 80200 10010001 4020000 1001000 8100000 4042000
  //   400101 4020000 4006003 20020000 801000 8200001 4020000 4002400 8010001 4020000 2001000 8010001
  //   200091 20000048 200021
  //   指令译码信号
  //   控制字段
  //   微指令
  //   指令译码逻辑ID
  //   判断逻辑
endmodule

// 入口查找
module \微程序入口查找逻辑_中断  (
  input  LW,
  input  SW,
  input  BEQ,
  input  SLT,
  input  ADDI,
  input  ERET,
  output S4,
  output S3,
  output S2,
  output S1,
  output S0
);

  or or_1 (S4, SLT, ADDI, ERET);
  or or_2 (S3, SW, BEQ, ERET);
  or or_3 (S2, LW, BEQ, ADDI);
  or or_4 (S1, BEQ, SLT, ADDI);
  or or_5 (S0, SW, SLT, ERET);
endmodule

// 判别
module \条件判别测试逻辑_中断  (
  input  P0,
  input  P1,
  input  P2,
  input  equal,
  input  IntR,
  output S2,
  output S1,
  output S0
);

  wire and_1_out, and_2_out, and_3_out, and_4_out, and_5_out, and_6_out, and_7_out, and_8_out, not_1_out,
       not_2_out, not_3_out, not_4_out, not_5_out, not_6_out, not_7_out, not_8_out, not_9_out, not_10_out,
       not_11_out, not_12_out, not_13_out, not_14_out, not_15_out, not_16_out, not_17_out, not_18_out;

  not not_1 (not_1_out, P0);
  not not_2 (not_2_out, P1);
  not not_3 (not_3_out, IntR);
  not not_4 (not_4_out, P0);
  not not_5 (not_5_out, equal);
  not not_6 (not_6_out, IntR);
  not not_7 (not_7_out, P0);
  not not_8 (not_8_out, P2);
  not not_9 (not_9_out, equal);
  not not_10 (not_10_out, P0);
  not not_11 (not_11_out, P1);
  not not_12 (not_12_out, P0);
  not not_13 (not_13_out, equal);
  not not_14 (not_14_out, P0);
  not not_15 (not_15_out, P0);
  not not_16 (not_16_out, P1);
  not not_17 (not_17_out, P0);
  not not_18 (not_18_out, equal);
  and and_1 (and_1_out, not_1_out, not_2_out, P2, not_3_out);
  and and_2 (and_2_out, not_4_out, P1, not_5_out, not_6_out);
  and and_3 (and_3_out, not_7_out, P1, not_8_out, not_9_out, IntR);
  and and_4 (and_4_out, not_10_out, not_11_out, P2, IntR);
  and and_5 (and_5_out, not_12_out, P1, P2, not_13_out, IntR);
  and and_6 (and_6_out, not_14_out, P1, equal);
  and and_7 (and_7_out, not_15_out, not_16_out, P2, IntR);
  and and_8 (and_8_out, not_17_out, P1, P2, not_18_out, IntR);
  or or_1 (S2, and_1_out, and_2_out, and_3_out);
  or or_2 (S1, and_4_out, and_5_out, and_6_out);
  or or_3 (S0, and_7_out, and_8_out, P0);
endmodule

module \硬布线控制器_中断  (
  input  EQUAL,
  input  [31:0] \指令字 ,
  input  IntR,
  input  CLK,
  output [4:0] statu,
  output [21:0] \控制总线 ,
  output [4:0] \中断控制信号 
);

  wire ADDI, BEQ, ERET, LW, SLT, SW;
  wire [2:0] rom_1_data;
  wire [4:0] \硬布线状态机_中断_1_n0 ;

  \硬布线状态机_中断  \u_硬布线状态机_中断_1  (
    .S4(statu[4]), .S3(statu[3]), .S2(statu[2]), .S1(statu[1]), .S0(statu[0]), .LW(LW), .SW(SW), .BEQ(BEQ),
    .SLT(SLT), .ADDI(ADDI), .ERET(ERET), .IR(IntR), .EQUAL(EQUAL), .N4(\硬布线状态机_中断_1_n0 [4]),
    .N3(\硬布线状态机_中断_1_n0 [3]), .N2(\硬布线状态机_中断_1_n0 [2]), .N1(\硬布线状态机_中断_1_n0 [1]), .N0(\硬布线状态机_中断_1_n0 [0]));
  // Probe on \硬布线状态机_中断_1_n0 
  Register #(.width(5), .trigger("falling"), .Select("low")) register_1 (
    .D(\硬布线状态机_中断_1_n0 ), .Q(statu), .clk(CLK));  // open: en, clr
  // Probe on statu
  \指令译码器  \u_指令译码器_1  (.IR(\指令字 ), .LW(LW), .SW(SW), .BEQ(BEQ), .ADDI(ADDI), .SLT(SLT), .OtherInstr(ERET));
  ROM #(.addrWidth(5), .dataWidth(30), .Select("high")) rom_1 (.addr(statu), .data({\控制总线 , \中断控制信号 , rom_1_data}));

  // Other names for the same wires on the sheet: status[4:0] = statu

  // Notes on the sheet:
  //   不要改变此引脚区域内容，也不要改变封装形式
  //   根据指令进行微程序地址转移
  //   μAR
  //   支持中断的硬布线控制器
  //   指令译码器
  //   控制存储器
  //   contents of rom_1 (hex, n*v repeats v):
  //   20120000 800 8280200 10008004 4020000 2001000 8100000 80200 10010001 4020000 1001000 8100000 4042000
  //   400101 4020000 4006003 20020000 801000 8200001 4020000 4002400 8010001 4020000 2001000 8010001
  //   200091 20000048 200021
  //   指令译码信号
  //   控制字段
  //   微指令
  //   指令译码逻辑ID
endmodule

// 带中断硬布线状态机
module \硬布线状态机_中断  (
  input  S4,
  input  S3,
  input  S2,
  input  S1,
  input  S0,
  input  LW,
  input  SW,
  input  BEQ,
  input  SLT,
  input  ADDI,
  input  ERET,
  input  IR,
  input  EQUAL,
  output N4,
  output N3,
  output N2,
  output N1,
  output N0
);

  wire and_1_out, and_2_out, and_3_out, and_4_out, and_5_out, and_6_out, and_7_out, and_8_out, and_9_out,
       and_10_out, and_11_out, and_12_out, and_13_out, and_14_out, and_15_out, and_16_out, and_17_out,
       and_18_out, and_19_out, and_20_out, and_21_out, and_22_out, and_23_out, and_24_out, and_25_out,
       and_26_out, and_27_out, and_28_out, and_29_out, and_30_out, and_31_out, and_32_out, and_33_out,
       and_34_out, and_35_out, and_36_out, and_37_out, and_38_out, and_39_out, and_40_out, and_41_out,
       and_42_out, and_43_out, and_44_out, and_45_out, and_46_out, and_47_out, and_48_out, and_49_out,
       and_50_out, and_51_out, and_52_out, and_53_out, and_54_out, and_55_out, and_56_out, and_57_out,
       and_58_out, and_59_out, and_60_out, and_61_out, and_62_out, and_63_out, and_64_out, and_65_out,
       and_66_out, and_67_out, and_68_out, and_69_out, and_70_out, and_71_out, and_72_out, and_73_out,
       and_74_out, and_75_out, and_76_out, and_77_out, and_78_out, and_79_out, and_80_out, and_81_out,
       and_82_out, and_83_out, and_84_out, and_85_out, and_86_out, and_87_out, and_88_out, and_89_out,
       and_90_out, and_91_out, and_92_out, and_93_out, and_94_out, and_95_out, and_96_out, and_97_out,
       and_98_out, and_99_out, and_100_out, and_101_out, and_102_out, and_103_out, and_104_out, and_105_out,
       and_106_out, and_107_out, and_108_out, and_109_out, and_110_out, and_111_out, and_112_out,
       and_113_out, and_114_out, and_115_out, and_116_out, and_117_out, not_1_out, not_2_out, not_3_out,
       not_4_out, not_5_out, not_6_out, not_7_out, not_8_out, not_9_out, not_10_out, not_11_out, not_12_out,
       not_13_out, not_14_out, not_15_out, not_16_out, not_17_out, not_18_out, not_19_out, not_20_out,
       not_21_out, not_22_out, not_23_out, not_24_out, not_25_out, not_26_out, not_27_out, not_28_out,
       not_29_out, not_30_out, not_31_out, not_32_out, not_33_out, not_34_out, not_35_out, not_36_out,
       not_37_out, not_38_out, not_39_out, not_40_out, not_41_out, not_42_out, not_43_out, not_44_out,
       not_45_out, not_46_out, not_47_out, not_48_out, not_49_out, not_50_out, not_51_out, not_52_out,
       not_53_out, not_54_out, not_55_out, not_56_out, not_57_out, not_58_out, not_59_out, not_60_out,
       not_61_out, not_62_out, not_63_out, not_64_out, not_65_out, not_66_out, not_67_out, not_68_out,
       not_69_out, not_70_out, not_71_out, not_72_out, not_73_out, not_74_out, not_75_out, not_76_out,
       not_77_out, not_78_out, not_79_out, not_80_out, not_81_out, not_82_out, not_83_out, not_84_out,
       not_85_out, not_86_out, not_87_out, not_88_out, not_89_out, not_90_out, not_91_out, not_92_out,
       not_93_out, not_94_out, not_95_out, not_96_out, not_97_out, not_98_out, not_99_out, not_100_out,
       not_101_out, not_102_out, not_103_out, not_104_out, not_105_out, not_106_out, not_107_out,
       not_108_out, not_109_out, not_110_out, not_111_out, not_112_out, not_113_out, not_114_out,
       not_115_out, not_116_out, not_117_out, not_118_out, not_119_out, not_120_out, not_121_out,
       not_122_out, not_123_out, not_124_out, not_125_out, not_126_out, not_127_out, not_128_out,
       not_129_out, not_130_out, not_131_out, not_132_out, not_133_out, not_134_out, not_135_out,
       not_136_out, not_137_out, not_138_out, not_139_out, not_140_out, not_141_out, not_142_out,
       not_143_out, not_144_out, not_145_out, not_146_out, not_147_out, not_148_out, not_149_out,
       not_150_out, not_151_out, not_152_out, not_153_out, not_154_out, not_155_out, not_156_out,
       not_157_out, not_158_out, not_159_out, not_160_out, not_161_out, not_162_out, not_163_out,
       not_164_out, not_165_out, not_166_out, not_167_out, not_168_out, not_169_out, not_170_out,
       not_171_out, not_172_out, not_173_out, not_174_out, not_175_out, not_176_out, not_177_out,
       not_178_out, not_179_out, not_180_out, not_181_out, not_182_out, not_183_out, not_184_out,
       not_185_out, not_186_out, not_187_out, not_188_out, not_189_out, not_190_out, not_191_out,
       not_192_out, not_193_out, not_194_out, not_195_out, not_196_out, not_197_out, not_198_out,
       not_199_out, not_200_out, not_201_out, not_202_out, not_203_out, not_204_out, not_205_out,
       not_206_out, not_207_out, not_208_out, not_209_out, not_210_out, not_211_out, not_212_out,
       not_213_out, not_214_out, not_215_out, not_216_out, not_217_out, not_218_out, not_219_out,
       not_220_out, not_221_out, not_222_out, not_223_out, not_224_out, not_225_out, not_226_out,
       not_227_out, not_228_out, not_229_out, not_230_out, not_231_out, not_232_out, not_233_out,
       not_234_out, not_235_out, not_236_out, not_237_out, not_238_out, not_239_out, not_240_out,
       not_241_out, not_242_out, not_243_out, not_244_out, not_245_out, not_246_out, not_247_out,
       not_248_out, not_249_out, not_250_out, not_251_out, not_252_out, not_253_out, not_254_out,
       not_255_out, not_256_out, not_257_out, not_258_out, not_259_out, not_260_out, not_261_out,
       not_262_out, not_263_out, not_264_out, not_265_out, not_266_out, not_267_out, not_268_out,
       not_269_out, not_270_out, not_271_out, not_272_out, not_273_out, not_274_out, not_275_out,
       not_276_out, not_277_out, not_278_out, not_279_out, not_280_out, not_281_out, not_282_out,
       not_283_out, not_284_out, not_285_out, not_286_out, not_287_out, not_288_out, not_289_out,
       not_290_out, not_291_out, not_292_out, not_293_out, not_294_out, not_295_out, not_296_out,
       not_297_out, not_298_out, not_299_out, not_300_out, not_301_out, not_302_out, not_303_out,
       not_304_out, not_305_out, not_306_out, not_307_out, not_308_out, not_309_out, not_310_out,
       not_311_out, not_312_out, not_313_out, not_314_out, not_315_out, not_316_out, not_317_out,
       not_318_out, not_319_out, not_320_out, not_321_out, not_322_out, not_323_out, not_324_out,
       not_325_out, not_326_out, not_327_out, not_328_out;

  not not_1 (not_1_out, S4);
  not not_2 (not_2_out, S3);
  not not_3 (not_3_out, S2);
  not not_4 (not_4_out, S1);
  not not_5 (not_5_out, S0);
  not not_6 (not_6_out, S3);
  not not_7 (not_7_out, S2);
  not not_8 (not_8_out, S1);
  not not_9 (not_9_out, S4);
  not not_10 (not_10_out, S2);
  not not_11 (not_11_out, S1);
  not not_12 (not_12_out, S0);
  not not_13 (not_13_out, S2);
  not not_14 (not_14_out, S0);
  not not_15 (not_15_out, S4);
  not not_16 (not_16_out, S1);
  not not_17 (not_17_out, S4);
  not not_18 (not_18_out, EQUAL);
  not not_19 (not_19_out, S4);
  not not_20 (not_20_out, S3);
  not not_21 (not_21_out, S2);
  not not_22 (not_22_out, S1);
  not not_23 (not_23_out, S0);
  not not_24 (not_24_out, S3);
  not not_25 (not_25_out, S2);
  not not_26 (not_26_out, S0);
  not not_27 (not_27_out, S4);
  not not_28 (not_28_out, S3);
  not not_29 (not_29_out, S2);
  not not_30 (not_30_out, S3);
  not not_31 (not_31_out, S2);
  not not_32 (not_32_out, S3);
  not not_33 (not_33_out, S1);
  not not_34 (not_34_out, S0);
  not not_35 (not_35_out, S3);
  not not_36 (not_36_out, S1);
  not not_37 (not_37_out, S4);
  not not_38 (not_38_out, S3);
  not not_39 (not_39_out, S2);
  not not_40 (not_40_out, S3);
  not not_41 (not_41_out, S0);
  not not_42 (not_42_out, S3);
  not not_43 (not_43_out, S2);
  not not_44 (not_44_out, S1);
  not not_45 (not_45_out, S0);
  not not_46 (not_46_out, S4);
  not not_47 (not_47_out, S3);
  not not_48 (not_48_out, S2);
  not not_49 (not_49_out, S2);
  not not_50 (not_50_out, S1);
  not not_51 (not_51_out, S4);
  not not_52 (not_52_out, S3);
  not not_53 (not_53_out, S4);
  not not_54 (not_54_out, S3);
  not not_55 (not_55_out, S2);
  not not_56 (not_56_out, S4);
  not not_57 (not_57_out, S2);
  not not_58 (not_58_out, S1);
  not not_59 (not_59_out, S4);
  not not_60 (not_60_out, S2);
  not not_61 (not_61_out, S0);
  not not_62 (not_62_out, S4);
  not not_63 (not_63_out, S2);
  not not_64 (not_64_out, S4);
  not not_65 (not_65_out, S1);
  not not_66 (not_66_out, S0);
  not not_67 (not_67_out, S4);
  not not_68 (not_68_out, S3);
  not not_69 (not_69_out, S2);
  not not_70 (not_70_out, S4);
  not not_71 (not_71_out, S0);
  not not_72 (not_72_out, S4);
  not not_73 (not_73_out, S3);
  not not_74 (not_74_out, S4);
  not not_75 (not_75_out, S2);
  not not_76 (not_76_out, S1);
  not not_77 (not_77_out, S0);
  not not_78 (not_78_out, S2);
  not not_79 (not_79_out, S0);
  not not_80 (not_80_out, S4);
  not not_81 (not_81_out, S3);
  not not_82 (not_82_out, S2);
  not not_83 (not_83_out, S4);
  not not_84 (not_84_out, S2);
  not not_85 (not_85_out, S1);
  not not_86 (not_86_out, S4);
  not not_87 (not_87_out, S2);
  not not_88 (not_88_out, S0);
  not not_89 (not_89_out, S4);
  not not_90 (not_90_out, S2);
  not not_91 (not_91_out, S4);
  not not_92 (not_92_out, S1);
  not not_93 (not_93_out, S0);
  not not_94 (not_94_out, S4);
  not not_95 (not_95_out, S1);
  not not_96 (not_96_out, S4);
  not not_97 (not_97_out, S3);
  not not_98 (not_98_out, S2);
  not not_99 (not_99_out, S4);
  not not_100 (not_100_out, S0);
  not not_101 (not_101_out, S4);
  not not_102 (not_102_out, EQUAL);
  not not_103 (not_103_out, S3);
  not not_104 (not_104_out, S2);
  not not_105 (not_105_out, S0);
  not not_106 (not_106_out, S3);
  not not_107 (not_107_out, S1);
  not not_108 (not_108_out, S3);
  not not_109 (not_109_out, S2);
  not not_110 (not_110_out, S1);
  not not_111 (not_111_out, S0);
  not not_112 (not_112_out, S4);
  not not_113 (not_113_out, S3);
  not not_114 (not_114_out, S2);
  not not_115 (not_115_out, S2);
  not not_116 (not_116_out, S1);
  not not_117 (not_117_out, S4);
  not not_118 (not_118_out, S3);
  not not_119 (not_119_out, S2);
  not not_120 (not_120_out, S4);
  not not_121 (not_121_out, S3);
  not not_122 (not_122_out, S1);
  not not_123 (not_123_out, S0);
  not not_124 (not_124_out, S4);
  not not_125 (not_125_out, S3);
  not not_126 (not_126_out, S1);
  not not_127 (not_127_out, S4);
  not not_128 (not_128_out, S3);
  not not_129 (not_129_out, S0);
  not not_130 (not_130_out, S4);
  not not_131 (not_131_out, S2);
  not not_132 (not_132_out, S4);
  not not_133 (not_133_out, S1);
  not not_134 (not_134_out, S0);
  not not_135 (not_135_out, S4);
  not not_136 (not_136_out, S3);
  not not_137 (not_137_out, S2);
  not not_138 (not_138_out, S4);
  not not_139 (not_139_out, S0);
  not not_140 (not_140_out, S4);
  not not_141 (not_141_out, S3);
  not not_142 (not_142_out, S2);
  not not_143 (not_143_out, S4);
  not not_144 (not_144_out, S3);
  not not_145 (not_145_out, S1);
  not not_146 (not_146_out, S0);
  not not_147 (not_147_out, S4);
  not not_148 (not_148_out, S3);
  not not_149 (not_149_out, S1);
  not not_150 (not_150_out, S4);
  not not_151 (not_151_out, S3);
  not not_152 (not_152_out, S0);
  not not_153 (not_153_out, S4);
  not not_154 (not_154_out, S2);
  not not_155 (not_155_out, S4);
  not not_156 (not_156_out, S1);
  not not_157 (not_157_out, S0);
  not not_158 (not_158_out, S4);
  not not_159 (not_159_out, S3);
  not not_160 (not_160_out, S2);
  not not_161 (not_161_out, S4);
  not not_162 (not_162_out, S0);
  not not_163 (not_163_out, S3);
  not not_164 (not_164_out, S2);
  not not_165 (not_165_out, S3);
  not not_166 (not_166_out, S1);
  not not_167 (not_167_out, S0);
  not not_168 (not_168_out, S4);
  not not_169 (not_169_out, S3);
  not not_170 (not_170_out, S2);
  not not_171 (not_171_out, S3);
  not not_172 (not_172_out, S0);
  not not_173 (not_173_out, S4);
  not not_174 (not_174_out, S3);
  not not_175 (not_175_out, S2);
  not not_176 (not_176_out, S1);
  not not_177 (not_177_out, S4);
  not not_178 (not_178_out, S3);
  not not_179 (not_179_out, S2);
  not not_180 (not_180_out, S0);
  not not_181 (not_181_out, S4);
  not not_182 (not_182_out, S3);
  not not_183 (not_183_out, S1);
  not not_184 (not_184_out, S4);
  not not_185 (not_185_out, S3);
  not not_186 (not_186_out, S0);
  not not_187 (not_187_out, S4);
  not not_188 (not_188_out, S2);
  not not_189 (not_189_out, S1);
  not not_190 (not_190_out, S4);
  not not_191 (not_191_out, S2);
  not not_192 (not_192_out, S0);
  not not_193 (not_193_out, S4);
  not not_194 (not_194_out, S3);
  not not_195 (not_195_out, S2);
  not not_196 (not_196_out, S4);
  not not_197 (not_197_out, S0);
  not not_198 (not_198_out, S3);
  not not_199 (not_199_out, S2);
  not not_200 (not_200_out, S1);
  not not_201 (not_201_out, S4);
  not not_202 (not_202_out, S3);
  not not_203 (not_203_out, S2);
  not not_204 (not_204_out, S1);
  not not_205 (not_205_out, S4);
  not not_206 (not_206_out, S3);
  not not_207 (not_207_out, S2);
  not not_208 (not_208_out, S0);
  not not_209 (not_209_out, S4);
  not not_210 (not_210_out, S3);
  not not_211 (not_211_out, S1);
  not not_212 (not_212_out, S4);
  not not_213 (not_213_out, S3);
  not not_214 (not_214_out, S0);
  not not_215 (not_215_out, S4);
  not not_216 (not_216_out, S2);
  not not_217 (not_217_out, S1);
  not not_218 (not_218_out, S0);
  not not_219 (not_219_out, S2);
  not not_220 (not_220_out, S0);
  not not_221 (not_221_out, S4);
  not not_222 (not_222_out, S2);
  not not_223 (not_223_out, S1);
  not not_224 (not_224_out, S4);
  not not_225 (not_225_out, S2);
  not not_226 (not_226_out, S0);
  not not_227 (not_227_out, S4);
  not not_228 (not_228_out, S1);
  not not_229 (not_229_out, S4);
  not not_230 (not_230_out, S3);
  not not_231 (not_231_out, S2);
  not not_232 (not_232_out, S4);
  not not_233 (not_233_out, S0);
  not not_234 (not_234_out, S4);
  not not_235 (not_235_out, EQUAL);
  not not_236 (not_236_out, S3);
  not not_237 (not_237_out, S2);
  not not_238 (not_238_out, S0);
  not not_239 (not_239_out, S4);
  not not_240 (not_240_out, S3);
  not not_241 (not_241_out, S2);
  not not_242 (not_242_out, S3);
  not not_243 (not_243_out, S1);
  not not_244 (not_244_out, S4);
  not not_245 (not_245_out, S3);
  not not_246 (not_246_out, S2);
  not not_247 (not_247_out, S3);
  not not_248 (not_248_out, S0);
  not not_249 (not_249_out, S2);
  not not_250 (not_250_out, S1);
  not not_251 (not_251_out, S0);
  not not_252 (not_252_out, S2);
  not not_253 (not_253_out, S1);
  not not_254 (not_254_out, S4);
  not not_255 (not_255_out, S3);
  not not_256 (not_256_out, S2);
  not not_257 (not_257_out, S1);
  not not_258 (not_258_out, S0);
  not not_259 (not_259_out, S4);
  not not_260 (not_260_out, S3);
  not not_261 (not_261_out, S2);
  not not_262 (not_262_out, S0);
  not not_263 (not_263_out, S4);
  not not_264 (not_264_out, S3);
  not not_265 (not_265_out, S1);
  not not_266 (not_266_out, S0);
  not not_267 (not_267_out, S4);
  not not_268 (not_268_out, S3);
  not not_269 (not_269_out, S0);
  not not_270 (not_270_out, S4);
  not not_271 (not_271_out, S3);
  not not_272 (not_272_out, S2);
  not not_273 (not_273_out, S4);
  not not_274 (not_274_out, S2);
  not not_275 (not_275_out, S0);
  not not_276 (not_276_out, S4);
  not not_277 (not_277_out, S1);
  not not_278 (not_278_out, S0);
  not not_279 (not_279_out, S4);
  not not_280 (not_280_out, S0);
  not not_281 (not_281_out, S3);
  not not_282 (not_282_out, S2);
  not not_283 (not_283_out, S1);
  not not_284 (not_284_out, S0);
  not not_285 (not_285_out, S4);
  not not_286 (not_286_out, S3);
  not not_287 (not_287_out, S2);
  not not_288 (not_288_out, S1);
  not not_289 (not_289_out, S0);
  not not_290 (not_290_out, S4);
  not not_291 (not_291_out, S3);
  not not_292 (not_292_out, S2);
  not not_293 (not_293_out, S0);
  not not_294 (not_294_out, S4);
  not not_295 (not_295_out, S3);
  not not_296 (not_296_out, S1);
  not not_297 (not_297_out, S0);
  not not_298 (not_298_out, S4);
  not not_299 (not_299_out, S3);
  not not_300 (not_300_out, S0);
  not not_301 (not_301_out, S2);
  not not_302 (not_302_out, S0);
  not not_303 (not_303_out, S4);
  not not_304 (not_304_out, S3);
  not not_305 (not_305_out, S2);
  not not_306 (not_306_out, S4);
  not not_307 (not_307_out, S2);
  not not_308 (not_308_out, S0);
  not not_309 (not_309_out, S4);
  not not_310 (not_310_out, S1);
  not not_311 (not_311_out, S0);
  not not_312 (not_312_out, S4);
  not not_313 (not_313_out, S0);
  not not_314 (not_314_out, S3);
  not not_315 (not_315_out, S2);
  not not_316 (not_316_out, S1);
  not not_317 (not_317_out, S0);
  not not_318 (not_318_out, S4);
  not not_319 (not_319_out, S3);
  not not_320 (not_320_out, S2);
  not not_321 (not_321_out, S3);
  not not_322 (not_322_out, S1);
  not not_323 (not_323_out, S0);
  not not_324 (not_324_out, S3);
  not not_325 (not_325_out, S0);
  not not_326 (not_326_out, S4);
  not not_327 (not_327_out, S3);
  not not_328 (not_328_out, S2);
  and and_1 (and_1_out, not_1_out, S3, S2, S1, S0, EQUAL);
  and and_2 (and_2_out, S4, not_2_out, not_3_out, not_4_out, not_5_out);
  and and_3 (and_3_out, S4, not_6_out, not_7_out, not_8_out, S0);
  and and_4 (and_4_out, not_9_out, S3, not_10_out, not_11_out, not_12_out, IR);
  and and_5 (and_5_out, S4, S3, not_13_out, S1, not_14_out);
  and and_6 (and_6_out, not_15_out, S3, S2, not_16_out, S0, IR);
  and and_7 (and_7_out, not_17_out, S3, S2, S1, S0, IR, not_18_out);
  and and_8 (and_8_out, not_19_out, S3, S2, S1, S0, EQUAL);
  and and_9 (and_9_out, S4, not_20_out, not_21_out, not_22_out, not_23_out);
  and and_10 (and_10_out, S4, not_24_out, not_25_out, S1, not_26_out, IR);
  and and_11 (and_11_out, not_27_out, not_28_out, not_29_out, S1, S0, SLT);
  and and_12 (and_12_out, S4, not_30_out, not_31_out, S1, S0);
  and and_13 (and_13_out, S4, not_32_out, S2, not_33_out, not_34_out);
  and and_14 (and_14_out, S4, not_35_out, S2, not_36_out, S0, IR);
  and and_15 (and_15_out, not_37_out, not_38_out, not_39_out, S1, S0, ADDI);
  and and_16 (and_16_out, S4, not_40_out, S2, S1, not_41_out);
  and and_17 (and_17_out, S4, not_42_out, S2, S1, S0);
  and and_18 (and_18_out, S4, S3, not_43_out, not_44_out, not_45_out, IR);
  and and_19 (and_19_out, not_46_out, not_47_out, not_48_out, S1, S0, ERET);
  and and_20 (and_20_out, S4, S3, not_49_out, not_50_out, S0, IR);
  and and_21 (and_21_out, not_51_out, not_52_out, S2, S1, S0);
  and and_22 (and_22_out, not_53_out, not_54_out, not_55_out, S1, S0, SW);
  and and_23 (and_23_out, not_56_out, S3, not_57_out, not_58_out, S0);
  and and_24 (and_24_out, not_59_out, S3, not_60_out, S1, not_61_out);
  and and_25 (and_25_out, not_62_out, S3, not_63_out, S1, S0);
  and and_26 (and_26_out, not_64_out, S3, S2, not_65_out, not_66_out);
  and and_27 (and_27_out, not_67_out, not_68_out, not_69_out, S1, S0, BEQ);
  and and_28 (and_28_out, not_70_out, S3, S2, S1, not_71_out);
  and and_29 (and_29_out, not_72_out, not_73_out, S2, S1, S0);
  and and_30 (and_30_out, not_74_out, S3, not_75_out, not_76_out, not_77_out, IR);
  and and_31 (and_31_out, S4, S3, not_78_out, S1, not_79_out);
  and and_32 (and_32_out, not_80_out, not_81_out, not_82_out, S1, S0, SW);
  and and_33 (and_33_out, not_83_out, S3, not_84_out, not_85_out, S0);
  and and_34 (and_34_out, not_86_out, S3, not_87_out, S1, not_88_out);
  and and_35 (and_35_out, not_89_out, S3, not_90_out, S1, S0);
  and and_36 (and_36_out, not_91_out, S3, S2, not_92_out, not_93_out);
  and and_37 (and_37_out, not_94_out, S3, S2, not_95_out, S0, IR);
  and and_38 (and_38_out, not_96_out, not_97_out, not_98_out, S1, S0, BEQ);
  and and_39 (and_39_out, not_99_out, S3, S2, S1, not_100_out);
  and and_40 (and_40_out, not_101_out, S3, S2, S1, S0, IR, not_102_out);
  and and_41 (and_41_out, S4, not_103_out, not_104_out, S1, not_105_out, IR);
  and and_42 (and_42_out, S4, not_106_out, S2, not_107_out, S0, IR);
  and and_43 (and_43_out, S4, not_108_out, S2, S1, S0);
  and and_44 (and_44_out, S4, S3, not_109_out, not_110_out, not_111_out, IR);
  and and_45 (and_45_out, not_112_out, not_113_out, not_114_out, S1, S0, ERET);
  and and_46 (and_46_out, S4, S3, not_115_out, not_116_out, S0, IR);
  and and_47 (and_47_out, not_117_out, not_118_out, not_119_out, S1, S0, LW);
  and and_48 (and_48_out, not_120_out, not_121_out, S2, not_122_out, not_123_out);
  and and_49 (and_49_out, not_124_out, not_125_out, S2, not_126_out, S0);
  and and_50 (and_50_out, not_127_out, not_128_out, S2, S1, not_129_out);
  and and_51 (and_51_out, not_130_out, S3, not_131_out, S1, S0);
  and and_52 (and_52_out, not_132_out, S3, S2, not_133_out, not_134_out);
  and and_53 (and_53_out, not_135_out, not_136_out, not_137_out, S1, S0, BEQ);
  and and_54 (and_54_out, not_138_out, S3, S2, S1, not_139_out);
  and and_55 (and_55_out, not_140_out, not_141_out, not_142_out, S1, S0, LW);
  and and_56 (and_56_out, not_143_out, not_144_out, S2, not_145_out, not_146_out);
  and and_57 (and_57_out, not_147_out, not_148_out, S2, not_149_out, S0);
  and and_58 (and_58_out, not_150_out, not_151_out, S2, S1, not_152_out);
  and and_59 (and_59_out, not_153_out, S3, not_154_out, S1, S0);
  and and_60 (and_60_out, not_155_out, S3, S2, not_156_out, not_157_out);
  and and_61 (and_61_out, not_158_out, not_159_out, not_160_out, S1, S0, BEQ);
  and and_62 (and_62_out, not_161_out, S3, S2, S1, not_162_out);
  and and_63 (and_63_out, S4, not_163_out, not_164_out, S1, S0);
  and and_64 (and_64_out, S4, not_165_out, S2, not_166_out, not_167_out);
  and and_65 (and_65_out, not_168_out, not_169_out, not_170_out, S1, S0, ADDI);
  and and_66 (and_66_out, S4, not_171_out, S2, S1, not_172_out);
  and and_67 (and_67_out, not_173_out, not_174_out, not_175_out, not_176_out, S0);
  and and_68 (and_68_out, not_177_out, not_178_out, not_179_out, S1, not_180_out);
  and and_69 (and_69_out, not_181_out, not_182_out, S2, not_183_out, S0);
  and and_70 (and_70_out, not_184_out, not_185_out, S2, S1, not_186_out);
  and and_71 (and_71_out, not_187_out, S3, not_188_out, not_189_out, S0);
  and and_72 (and_72_out, not_190_out, S3, not_191_out, S1, not_192_out);
  and and_73 (and_73_out, not_193_out, not_194_out, not_195_out, S1, S0, BEQ);
  and and_74 (and_74_out, not_196_out, S3, S2, S1, not_197_out);
  and and_75 (and_75_out, S4, not_198_out, not_199_out, not_200_out, S0);
  and and_76 (and_76_out, not_201_out, not_202_out, not_203_out, not_204_out, S0);
  and and_77 (and_77_out, not_205_out, not_206_out, not_207_out, S1, not_208_out);
  and and_78 (and_78_out, not_209_out, not_210_out, S2, not_211_out, S0);
  and and_79 (and_79_out, not_212_out, not_213_out, S2, S1, not_214_out);
  and and_80 (and_80_out, not_215_out, S3, not_216_out, not_217_out, not_218_out, IR);
  and and_81 (and_81_out, S4, S3, not_219_out, S1, not_220_out);
  and and_82 (and_82_out, not_221_out, S3, not_222_out, not_223_out, S0);
  and and_83 (and_83_out, not_224_out, S3, not_225_out, S1, not_226_out);
  and and_84 (and_84_out, not_227_out, S3, S2, not_228_out, S0, IR);
  and and_85 (and_85_out, not_229_out, not_230_out, not_231_out, S1, S0, BEQ);
  and and_86 (and_86_out, not_232_out, S3, S2, S1, not_233_out);
  and and_87 (and_87_out, not_234_out, S3, S2, S1, S0, IR, not_235_out);
  and and_88 (and_88_out, S4, not_236_out, not_237_out, S1, not_238_out, IR);
  and and_89 (and_89_out, not_239_out, not_240_out, not_241_out, S1, S0, SLT);
  and and_90 (and_90_out, S4, not_242_out, S2, not_243_out, S0, IR);
  and and_91 (and_91_out, not_244_out, not_245_out, not_246_out, S1, S0, ADDI);
  and and_92 (and_92_out, S4, not_247_out, S2, S1, not_248_out);
  and and_93 (and_93_out, S4, S3, not_249_out, not_250_out, not_251_out, IR);
  and and_94 (and_94_out, S4, S3, not_252_out, not_253_out, S0, IR);
  and and_95 (and_95_out, not_254_out, not_255_out, not_256_out, not_257_out, not_258_out);
  and and_96 (and_96_out, not_259_out, not_260_out, not_261_out, S1, not_262_out);
  and and_97 (and_97_out, not_263_out, not_264_out, S2, not_265_out, not_266_out);
  and and_98 (and_98_out, not_267_out, not_268_out, S2, S1, not_269_out);
  and and_99 (and_99_out, not_270_out, not_271_out, not_272_out, S1, S0, SW);
  and and_100 (and_100_out, not_273_out, S3, not_274_out, S1, not_275_out);
  and and_101 (and_101_out, not_276_out, S3, S2, not_277_out, not_278_out);
  and and_102 (and_102_out, not_279_out, S3, S2, S1, not_280_out);
  and and_103 (and_103_out, S4, not_281_out, not_282_out, not_283_out, not_284_out);
  and and_104 (and_104_out, not_285_out, not_286_out, not_287_out, not_288_out, not_289_out);
  and and_105 (and_105_out, not_290_out, not_291_out, not_292_out, S1, not_293_out);
  and and_106 (and_106_out, not_294_out, not_295_out, S2, not_296_out, not_297_out);
  and and_107 (and_107_out, not_298_out, not_299_out, S2, S1, not_300_out);
  and and_108 (and_108_out, S4, S3, not_301_out, S1, not_302_out);
  and and_109 (and_109_out, not_303_out, not_304_out, not_305_out, S1, S0, SW);
  and and_110 (and_110_out, not_306_out, S3, not_307_out, S1, not_308_out);
  and and_111 (and_111_out, not_309_out, S3, S2, not_310_out, not_311_out);
  and and_112 (and_112_out, not_312_out, S3, S2, S1, not_313_out);
  and and_113 (and_113_out, S4, not_314_out, not_315_out, not_316_out, not_317_out);
  and and_114 (and_114_out, not_318_out, not_319_out, not_320_out, S1, S0, SLT);
  and and_115 (and_115_out, S4, not_321_out, S2, not_322_out, not_323_out);
  and and_116 (and_116_out, S4, not_324_out, S2, S1, not_325_out);
  and and_117 (and_117_out, not_326_out, not_327_out, not_328_out, S1, S0, ERET);
  or or_1 (N4, and_1_out, and_2_out, and_3_out, and_4_out, and_5_out, and_6_out, and_7_out, and_8_out, and_9_out, and_10_out, and_11_out, and_12_out, and_13_out, and_14_out, and_15_out, and_16_out, and_17_out, and_18_out, and_19_out, and_20_out);
  or or_2 (N3, and_21_out, and_22_out, and_23_out, and_24_out, and_25_out, and_26_out, and_27_out, and_28_out, and_29_out, and_30_out, and_31_out, and_32_out, and_33_out, and_34_out, and_35_out, and_36_out, and_37_out, and_38_out, and_39_out, and_40_out, and_41_out, and_42_out, and_43_out, and_44_out, and_45_out, and_46_out);
  or or_3 (N2, and_47_out, and_48_out, and_49_out, and_50_out, and_51_out, and_52_out, and_53_out, and_54_out, and_55_out, and_56_out, and_57_out, and_58_out, and_59_out, and_60_out, and_61_out, and_62_out, and_63_out, and_64_out, and_65_out, and_66_out);
  or or_4 (N1, and_67_out, and_68_out, and_69_out, and_70_out, and_71_out, and_72_out, and_73_out, and_74_out, and_75_out, and_76_out, and_77_out, and_78_out, and_79_out, and_80_out, and_81_out, and_82_out, and_83_out, and_84_out, and_85_out, and_86_out, and_87_out, and_88_out, and_89_out, and_90_out, and_91_out, and_92_out, and_93_out, and_94_out);
  or or_5 (N0, and_95_out, and_96_out, and_97_out, and_98_out, and_99_out, and_100_out, and_101_out, and_102_out, and_103_out, and_104_out, and_105_out, and_106_out, and_107_out, and_108_out, and_109_out, and_110_out, and_111_out, and_112_out, and_113_out, and_114_out, and_115_out, and_116_out, and_117_out);
endmodule

// ALU
module RISC_V_ALU (
  input  ADD,
  input  ADD4,
  input  [31:0] X,
  input  [31:0] Y,
  input  SUB,
  input  SLT,
  output Equal,
  output [31:0] Result
);

  wire [0:0] comparator_1_lt;
  wire [1:0] priority_encoder_1_out;
  wire [31:0] adder_1_out, adder_2_out, subtractor_1_out;

  Pull_Resistor #(.pull(0)) pull_resistor_1 (.node(Y));
  Adder #(.width(32)) adder_1 (.a(X), .b(Y), .out(adder_1_out));  // open: cin, cout
  Adder #(.width(32)) adder_2 (.a(X), .b(32'h4), .out(adder_2_out));  // open: cin, cout
  Subtractor #(.width(32)) subtractor_1 (.a(X), .b(Y), .out(subtractor_1_out));  // open: bin, bout
  Comparator #(.width(32), .mode("twosComplement")) comparator_1 (
    .a(X), .b(Y), .eq(Equal), .lt(comparator_1_lt[0]));  // open: gt
  Priority_Encoder #(.select(2), .disabled("Z")) priority_encoder_1 (
    .in0(ADD), .in1(ADD4), .in2(SUB), .in3(SLT), .out(priority_encoder_1_out));  // open: gs, en_out, en_in
  Pull_Resistor #(.pull(0)) pull_resistor_2 (.node(priority_encoder_1_out));
  Multiplexer #(.select(2), .width(32), .disabled("Z"), .enable("false")) multiplexer_1 (
    .in0(adder_1_out), .in1(adder_2_out), .in2(subtractor_1_out), .in3({{31{1'b0}}, comparator_1_lt[0]}),
    .out(Result), .sel(priority_encoder_1_out));

  // Notes on the sheet:
  //   不要改变此引脚区域内容，也不要改变ALU封装形式
  //   输入引脚
  //   输出引脚
endmodule

// 中断控制器
module \中断控制器  (
  input  CLK,
  input  Key1,
  input  Key2,
  input  Key3,
  input  Clr,
  input  [1:0] EDU_TEST,
  output IR1W,
  output IR2W,
  output IR3W,
  output [1:0] IntNo,
  output IntR
);

  wire and_1_out, and_2_out, and_3_out, Clr0, Clr1, Clr2, Clr3, d_ff_1_q, d_ff_2_q, d_ff_3_q, IR1_q, IR2_q,
       IR3_q, or_1_out, or_3_out, or_6_out, or_7_out, or_8_out;

  or or_1 (or_1_out, Key1, EDU_TEST[0]);
  or or_2 (IR1W, IR1_q, d_ff_2_q);
  or or_3 (or_3_out, Key2, EDU_TEST[1]);
  or or_4 (IR2W, IR2_q, d_ff_3_q);
  D_Flip_Flop #(.trigger("rising"), .Pre_Clr_Positions("LEGACY"), .NegatePresetClear("false"), .enable("true"), .NewFFLayout("false")) d_ff_1 (
    .clk(Key3), .D(1'b1), .Q(d_ff_1_q), .reset(IR3_q));  // open: Qn, preset, en
  or or_5 (IR3W, IR3_q, d_ff_1_q);
  D_Flip_Flop #(.trigger("rising"), .Pre_Clr_Positions("LEGACY"), .NegatePresetClear("false"), .enable("true"), .NewFFLayout("false")) d_ff_2 (
    .clk(or_1_out), .D(1'b1), .Q(d_ff_2_q), .reset(IR1_q));  // open: Qn, preset, en
  D_Flip_Flop #(.trigger("rising"), .Pre_Clr_Positions("LEGACY"), .NegatePresetClear("false"), .enable("true"), .NewFFLayout("false")) d_ff_3 (
    .clk(or_3_out), .D(1'b1), .Q(d_ff_3_q), .reset(IR2_q));  // open: Qn, preset, en
  or or_6 (or_6_out, d_ff_2_q, IR1_q);
  and and_1 (and_1_out, or_6_out, ~Clr1);  // AND_Gate
  or or_7 (or_7_out, d_ff_3_q, IR2_q);
  and and_2 (and_2_out, or_7_out, ~Clr2);  // AND_Gate
  or or_8 (or_8_out, d_ff_1_q, IR3_q);
  and and_3 (and_3_out, or_8_out, ~Clr3);  // AND_Gate
  Pull_Resistor #(.pull(0)) pull_resistor_1 (.node(EDU_TEST));
  D_Flip_Flop #(.trigger("rising"), .Pre_Clr_Positions("LEGACY"), .NegatePresetClear("false"), .enable("true"), .NewFFLayout("false")) IR1 (
    .clk(CLK), .D(and_1_out), .Q(IR1_q));  // open: Qn, preset, en, reset
  D_Flip_Flop #(.trigger("rising"), .Pre_Clr_Positions("LEGACY"), .NegatePresetClear("false"), .enable("true"), .NewFFLayout("false")) IR2 (
    .clk(CLK), .D(and_2_out), .Q(IR2_q));  // open: Qn, preset, en, reset
  D_Flip_Flop #(.trigger("rising"), .Pre_Clr_Positions("LEGACY"), .NegatePresetClear("false"), .enable("true"), .NewFFLayout("false")) IR3 (
    .clk(CLK), .D(and_3_out), .Q(IR3_q));  // open: Qn, preset, en, reset
  Priority_Encoder #(.select(2), .disabled("Z")) priority_encoder_1 (
    .in1(IR1_q), .in2(IR2_q), .in3(IR3_q), .out(IntNo), .gs(IntR));  // open: in0, en_out, en_in
  Decoder #(.select(2), .tristate("false"), .disabled(0), .enable("true")) decoder_1 (
    .out0(Clr0), .out1(Clr1), .out2(Clr2), .out3(Clr3), .sel(IntNo), .en(Clr));

  // Other names for the same wires on the sheet: EDU_INT1 = EDU_TEST[0]; EDU_INT2 = EDU_TEST[1]

  // Notes on the sheet:
  //   中断等待
  //   中断等待
  //   中断等待
  //   中断信号采样参考电路
  //   Reset 
  //   Reset 
  //   Reset 
  //   中断优先编码器
endmodule
